// Logisim project 2BITMULTIPLIER.circ as structural Verilog: 1 circuit, main circuit main
// 1ST DEC
module main (
  input  A0,
  input  A1,
  input  B0,
  input  B1,
  output C0,
  output C1,
  output out_7,
  output out_8
);

  wire A0_B1_out, A1_B0_out, and_1_out, and_2_out;

  and A0_B1 (A0_B1_out, A0, B1);
  LED led_1 (.in(C0));
  and A0_B0 (C0, A0, B0);
  and A1_B0 (A1_B0_out, A1, B0);
  and and_1 (and_1_out, A1, B1);
  xor xor_1 (C1, A0_B1_out, A1_B0_out);
  and and_2 (and_2_out, A0_B1_out, A1_B0_out);
  xor xor_2 (out_7, and_2_out, and_1_out);
  and and_3 (out_8, and_2_out, and_1_out);
endmodule
