// Logisim project 4_8_15Test.circ as structural Verilog
module HalfAdder (
  input  A___INPUT,
  input  B___INPUT,
  output out_3,
  output out_4,
  output out_5,
  output out_6
);

  xor xor_1 (out_5, A___INPUT, B___INPUT);
  and and_1 (out_4, A___INPUT, B___INPUT);

  assign out_3 = A___INPUT;
  assign out_6 = B___INPUT;

  // Notes on the sheet:
  //   HALF ADDER 
  //   SUM
  //   CARRY
  //   RESULT OF ADDITION
endmodule

module FullAdder (
  input  in_1,
  input  in_2,
  output out_3,
  output out_4
);

  HalfAdder halfadder_1 (.A___INPUT(in_1), .B___INPUT(in_2), .out_4(out_3), .out_5(out_4));  // open: out_3, out_6

  // Notes on the sheet:
  //   Full Adder
endmodule
