// Logisim project AnkanBasu_Logisim_Working_Files_5_5_2015_8_00_pm.circ as structural Verilog: 16 circuits, main circuit main
module main (
  input  in_1,
  input  in_2,
  input  in_3,
  input  in_4,
  input  in_5,
  input  in_6,
  input  in_7,
  input  in_8,
  input  in_9,
  input  in_10,
  input  in_11,
  input  in_12,
  input  in_13,
  input  in_14,
  input  in_15,
  input  in_16,
  input  in_17,
  input  in_18,
  input  in_19,
  input  in_20,
  input  in_21,
  input  in_22,
  input  in_23,
  input  in_24,
  input  in_25,
  input  in_26,
  input  in_27,
  input  in_28,
  input  in_29,
  input  in_30,
  input  in_31,
  input  in_32,
  input  in_33,
  input  in_34,
  input  in_35,
  input  in_36,
  input  in_37,
  input  in_38,
  input  in_39,
  input  in_40,
  input  in_41,
  input  in_42,
  input  in_43,
  input  in_44,
  input  in_45,
  input  in_46,
  input  in_47,
  input  in_48,
  input  in_49,
  input  in_50,
  input  in_51,
  input  in_52,
  input  in_53,
  input  in_54,
  input  in_55,
  input  in_56,
  input  in_57,
  input  in_58,
  input  in_59,
  input  in_60,
  input  in_61,
  input  in_62,
  input  in_63,
  input  in_64,
  output [7:0] out_65,
  output [7:0] out_66,
  output [15:0] out_67,
  output [7:0] out_68,
  output [7:0] out_69,
  output [15:0] out_70
);

  wire addition_1_out_25, addition_2_out_25, and_1_out, and_2_out, and_3_out, and_4_out, and_5_out,
       and_6_out, and_7_out, and_8_out, and_9_out, and_10_out, and_11_out, and_12_out, and_13_out,
       and_14_out, and_15_out, and_16_out, and_17_out, and_18_out, and_19_out, and_20_out, and_21_out,
       and_22_out, and_23_out, and_24_out, and_25_out, and_26_out, and_27_out, and_28_out, and_29_out,
       and_30_out, and_31_out, and_32_out, and_33_out, and_34_out, and_35_out, and_36_out, and_37_out,
       and_38_out, and_39_out, and_40_out, and_41_out, and_42_out, and_43_out, and_44_out, and_45_out,
       and_46_out, and_47_out, and_48_out, and_49_out, and_50_out, and_51_out, and_52_out, and_53_out,
       and_54_out, and_55_out, and_56_out, and_57_out, and_58_out, and_59_out, and_60_out, and_61_out,
       and_62_out, and_63_out, and_64_out, mux_8_bit_chooser_circuit_1_div, mux_8_bit_chooser_circuit_1_mul,
       mux_8_bit_chooser_circuit_1_out_17, mux_8_bit_chooser_circuit_1_sub, mux_8_bit_chooser_circuit_2_div,
       mux_8_bit_chooser_circuit_2_mul, mux_8_bit_chooser_circuit_2_out_17, mux_8_bit_chooser_circuit_2_sub,
       undriven, undriven_2, undriven_3, undriven_4, undriven_5, undriven_6, undriven_7, undriven_8;

  MUX_8_BIT_CHOOSEr_CIRCUIT mux_8_bit_chooser_circuit_1 (
    .in_1(in_1), .in_2(in_2), .in_3(in_3), .in_4(in_4), .in_5(in_5), .in_6(in_6), .in_7(in_7), .in_8(in_8),
    .in_9(in_9), .in_10(in_10), .in_11(in_11), .in_12(in_12), .in_13(in_13), .in_14(in_14), .in_15(in_15),
    .in_16(in_16), .out_17(mux_8_bit_chooser_circuit_1_out_17), .SUB(mux_8_bit_chooser_circuit_1_sub),
    .MUL(mux_8_bit_chooser_circuit_1_mul), .DIV(mux_8_bit_chooser_circuit_1_div));
  MUX_8_BIT_CHOOSEr_CIRCUIT mux_8_bit_chooser_circuit_2 (
    .in_1(in_41), .in_2(in_42), .in_3(in_43), .in_4(in_44), .in_5(in_45), .in_6(in_46), .in_7(in_47),
    .in_8(in_48), .in_9(in_49), .in_10(in_50), .in_11(in_51), .in_12(in_52), .in_13(in_53), .in_14(in_54),
    .in_15(in_55), .in_16(in_56), .out_17(mux_8_bit_chooser_circuit_2_out_17),
    .SUB(mux_8_bit_chooser_circuit_2_sub), .MUL(mux_8_bit_chooser_circuit_2_mul),
    .DIV(mux_8_bit_chooser_circuit_2_div));
  MUX_to_SELECTOR mux_to_selector_1 (
    .InputFromMux(mux_8_bit_chooser_circuit_2_out_17), .in_8(in_33), .in_7(in_34), .in_6(in_35),
    .in_5(in_36), .in_4(in_37), .in_3(in_38), .in_2(in_39), .in_1(in_40));  // open: out_17, out_16, out_15, out_14, out_13, out_12, out_11, out_10
  and and_1 (and_1_out, mux_8_bit_chooser_circuit_1_out_17, in_18);
  and and_2 (and_2_out, mux_8_bit_chooser_circuit_1_out_17, in_17);
  and and_3 (and_3_out, mux_8_bit_chooser_circuit_1_sub, in_18);
  and and_4 (and_4_out, mux_8_bit_chooser_circuit_1_sub, in_17);
  and and_5 (and_5_out, mux_8_bit_chooser_circuit_1_mul, in_18);
  and and_6 (and_6_out, mux_8_bit_chooser_circuit_1_mul, in_17);
  and and_7 (and_7_out, mux_8_bit_chooser_circuit_1_div, in_17);
  and and_8 (and_8_out, mux_8_bit_chooser_circuit_1_div, in_18);
  MUX_to_SELECTOR mux_to_selector_2 (
    .InputFromMux(mux_8_bit_chooser_circuit_2_out_17), .in_8(in_57), .in_7(in_58), .in_6(in_59),
    .in_5(in_60), .in_4(in_61), .in_3(in_62), .in_2(in_63), .in_1(in_64));  // open: out_17, out_16, out_15, out_14, out_13, out_12, out_11, out_10
  and and_9 (and_9_out, mux_8_bit_chooser_circuit_1_out_17, in_20);
  and and_10 (and_10_out, mux_8_bit_chooser_circuit_1_out_17, in_19);
  and and_11 (and_11_out, mux_8_bit_chooser_circuit_1_sub, in_20);
  and and_12 (and_12_out, mux_8_bit_chooser_circuit_1_sub, in_19);
  and and_13 (and_13_out, mux_8_bit_chooser_circuit_1_mul, in_19);
  and and_14 (and_14_out, mux_8_bit_chooser_circuit_1_mul, in_20);
  and and_15 (and_15_out, mux_8_bit_chooser_circuit_1_div, in_19);
  and and_16 (and_16_out, mux_8_bit_chooser_circuit_1_div, in_20);
  MUX_to_SELECTOR mux_to_selector_3 (
    .InputFromMux(mux_8_bit_chooser_circuit_2_sub), .in_8(in_33), .in_7(in_34), .in_6(in_35), .in_5(in_36),
    .in_4(in_37), .in_3(in_38), .in_2(in_39), .in_1(in_40));  // open: out_17, out_16, out_15, out_14, out_13, out_12, out_11, out_10
  and and_17 (and_17_out, mux_8_bit_chooser_circuit_1_out_17, in_23);
  and and_18 (and_18_out, mux_8_bit_chooser_circuit_1_out_17, in_22);
  and and_19 (and_19_out, mux_8_bit_chooser_circuit_1_out_17, in_21);
  and and_20 (and_20_out, mux_8_bit_chooser_circuit_1_sub, in_22);
  and and_21 (and_21_out, mux_8_bit_chooser_circuit_1_sub, in_23);
  and and_22 (and_22_out, mux_8_bit_chooser_circuit_1_sub, in_21);
  and and_23 (and_23_out, mux_8_bit_chooser_circuit_1_mul, in_22);
  and and_24 (and_24_out, mux_8_bit_chooser_circuit_1_mul, in_21);
  and and_25 (and_25_out, mux_8_bit_chooser_circuit_1_mul, in_23);
  and and_26 (and_26_out, mux_8_bit_chooser_circuit_1_div, in_21);
  and and_27 (and_27_out, mux_8_bit_chooser_circuit_1_div, in_23);
  and and_28 (and_28_out, mux_8_bit_chooser_circuit_1_div, in_22);
  MUX_to_SELECTOR mux_to_selector_4 (
    .InputFromMux(mux_8_bit_chooser_circuit_2_sub), .in_8(in_57), .in_7(in_58), .in_6(in_59), .in_5(in_60),
    .in_4(in_61), .in_3(in_62), .in_2(in_63), .in_1(in_64));  // open: out_17, out_16, out_15, out_14, out_13, out_12, out_11, out_10
  and and_29 (and_29_out, mux_8_bit_chooser_circuit_1_out_17, in_24);
  and and_30 (and_30_out, mux_8_bit_chooser_circuit_1_sub, in_24);
  and and_31 (and_31_out, mux_8_bit_chooser_circuit_1_mul, in_24);
  and and_32 (and_32_out, mux_8_bit_chooser_circuit_1_div, in_24);
  MUX_to_SELECTOR mux_to_selector_5 (
    .InputFromMux(mux_8_bit_chooser_circuit_2_mul), .in_8(in_33), .in_7(in_34), .in_6(in_35), .in_5(in_36),
    .in_4(in_37), .in_3(in_38), .in_2(in_39), .in_1(in_40));  // open: out_17, out_16, out_15, out_14, out_13, out_12, out_11, out_10
  MUX_to_SELECTOR mux_to_selector_6 (
    .InputFromMux(mux_8_bit_chooser_circuit_2_mul), .in_8(in_57), .in_7(in_58), .in_6(in_59), .in_5(in_60),
    .in_4(in_61), .in_3(in_62), .in_2(in_63), .in_1(in_64));  // open: out_17, out_16, out_15, out_14, out_13, out_12, out_11, out_10
  MUX_to_SELECTOR mux_to_selector_7 (
    .InputFromMux(mux_8_bit_chooser_circuit_2_div), .in_8(in_33), .in_7(in_34), .in_6(in_35), .in_5(in_36),
    .in_4(in_37), .in_3(in_38), .in_2(in_39), .in_1(in_40));  // open: out_17, out_16, out_15, out_14, out_13, out_12, out_11, out_10
  MUX_to_SELECTOR mux_to_selector_8 (
    .InputFromMux(mux_8_bit_chooser_circuit_2_div), .in_8(in_57), .in_7(in_58), .in_6(in_59), .in_5(in_60),
    .in_4(in_61), .in_3(in_62), .in_2(in_63), .in_1(in_64));  // open: out_17, out_16, out_15, out_14, out_13, out_12, out_11, out_10
  and and_33 (and_33_out, mux_8_bit_chooser_circuit_1_out_17, in_25);
  and and_34 (and_34_out, mux_8_bit_chooser_circuit_1_out_17, in_26);
  and and_35 (and_35_out, mux_8_bit_chooser_circuit_1_out_17, in_27);
  and and_36 (and_36_out, mux_8_bit_chooser_circuit_1_sub, in_25);
  and and_37 (and_37_out, mux_8_bit_chooser_circuit_1_sub, in_26);
  and and_38 (and_38_out, mux_8_bit_chooser_circuit_1_sub, in_27);
  and and_39 (and_39_out, mux_8_bit_chooser_circuit_1_mul, in_25);
  and and_40 (and_40_out, mux_8_bit_chooser_circuit_1_mul, in_27);
  and and_41 (and_41_out, mux_8_bit_chooser_circuit_1_mul, in_26);
  and and_42 (and_42_out, mux_8_bit_chooser_circuit_1_div, in_27);
  and and_43 (and_43_out, mux_8_bit_chooser_circuit_1_div, in_26);
  and and_44 (and_44_out, mux_8_bit_chooser_circuit_1_div, in_25);
  and and_45 (and_45_out, mux_8_bit_chooser_circuit_1_out_17, in_30);
  and and_46 (and_46_out, mux_8_bit_chooser_circuit_1_out_17, in_28);
  and and_47 (and_47_out, mux_8_bit_chooser_circuit_1_out_17, in_29);
  and and_48 (and_48_out, mux_8_bit_chooser_circuit_1_sub, in_28);
  and and_49 (and_49_out, mux_8_bit_chooser_circuit_1_sub, in_29);
  and and_50 (and_50_out, mux_8_bit_chooser_circuit_1_sub, in_30);
  and and_51 (and_51_out, mux_8_bit_chooser_circuit_1_mul, in_29);
  and and_52 (and_52_out, mux_8_bit_chooser_circuit_1_mul, in_28);
  and and_53 (and_53_out, mux_8_bit_chooser_circuit_1_mul, in_30);
  and and_54 (and_54_out, mux_8_bit_chooser_circuit_1_div, in_30);
  and and_55 (and_55_out, mux_8_bit_chooser_circuit_1_div, in_28);
  and and_56 (and_56_out, mux_8_bit_chooser_circuit_1_div, in_29);
  and and_57 (and_57_out, mux_8_bit_chooser_circuit_1_out_17, in_32);
  and and_58 (and_58_out, mux_8_bit_chooser_circuit_1_out_17, in_31);
  and and_59 (and_59_out, mux_8_bit_chooser_circuit_1_sub, in_31);
  and and_60 (and_60_out, mux_8_bit_chooser_circuit_1_sub, in_32);
  and and_61 (and_61_out, mux_8_bit_chooser_circuit_1_mul, in_32);
  and and_62 (and_62_out, mux_8_bit_chooser_circuit_1_mul, in_31);
  and and_63 (and_63_out, mux_8_bit_chooser_circuit_1_div, in_31);
  and and_64 (and_64_out, mux_8_bit_chooser_circuit_1_div, in_32);
  Addition addition_1 (
    .B1(undriven), .B2(undriven_2), .B3(undriven_3), .B4(undriven_4), .B5(undriven_5), .B6(undriven_6),
    .B7(undriven_7), .B8(undriven_8), .out_17(out_68[0]), .out_18(out_68[1]), .out_19(out_68[2]),
    .out_20(out_68[3]), .out_21(out_68[4]), .out_22(out_68[5]), .out_23(out_68[6]), .out_24(out_68[7]),
    .out_25(addition_1_out_25));  // open: A1, A2, A3, A4, A5, A6, A7, A8
  Subtraction subtraction_1 (
    .out_17(out_69[0]), .out_18(out_69[1]), .out_19(out_69[2]), .out_20(out_69[3]), .out_21(out_69[4]),
    .out_22(out_69[5]), .out_23(out_69[6]), .out_24(out_69[7]));  // open: A1, A2, A3, A4, A5, A6, A7, A8, B1, B2, B3, B4, B5, B6, B7, B8
  Multiplication multiplication_1 (
    .out_17(out_70[0]), .out_18(out_70[1]), .out_19(out_70[2]), .out_20(out_70[3]), .out_21(out_70[4]),
    .out_22(out_70[5]), .out_23(out_70[6]), .out_24(out_70[7]), .out_25(out_70[8]), .out_26(out_70[9]),
    .out_27(out_70[10]), .out_28(out_70[11]), .out_29(out_70[12]), .out_30(out_70[13]), .out_31(out_70[14]),
    .out_32(out_70[15]));  // open: in_1, in_2, in_3, in_4, a5, a6, a7, a8, b1, b2, b3, b4, b5, b6, b7, b8
  Addition addition_2 (
    .A1(and_29_out), .A2(and_17_out), .A3(and_18_out), .A4(and_19_out), .A5(and_9_out), .A6(and_10_out),
    .A7(and_1_out), .A8(and_2_out), .B1(and_57_out), .B2(and_58_out), .B3(and_45_out), .B4(and_47_out),
    .B5(and_46_out), .B6(and_35_out), .B7(and_34_out), .B8(and_33_out), .out_17(out_65[0]),
    .out_18(out_65[1]), .out_19(out_65[2]), .out_20(out_65[3]), .out_21(out_65[4]), .out_22(out_65[5]),
    .out_23(out_65[6]), .out_24(out_65[7]), .out_25(addition_2_out_25));
  Subtraction subtraction_2 (
    .A1(and_30_out), .A2(and_21_out), .A3(and_20_out), .A4(and_22_out), .A5(and_11_out), .A6(and_12_out),
    .A7(and_3_out), .A8(and_4_out), .B1(and_60_out), .B2(and_59_out), .B3(and_50_out), .B4(and_49_out),
    .B5(and_48_out), .B6(and_38_out), .B7(and_37_out), .B8(and_36_out), .out_17(out_66[0]),
    .out_18(out_66[1]), .out_19(out_66[2]), .out_20(out_66[3]), .out_21(out_66[4]), .out_22(out_66[5]),
    .out_23(out_66[6]), .out_24(out_66[7]));
  Multiplication multiplication_2 (
    .in_1(and_31_out), .in_2(and_25_out), .in_3(and_23_out), .in_4(and_24_out), .a5(and_14_out),
    .a6(and_13_out), .a7(and_5_out), .a8(and_6_out), .b1(and_61_out), .b2(and_62_out), .b3(and_53_out),
    .b4(and_51_out), .b5(and_52_out), .b6(and_40_out), .b7(and_41_out), .b8(and_39_out), .out_17(out_67[0]),
    .out_18(out_67[1]), .out_19(out_67[2]), .out_20(out_67[3]), .out_21(out_67[4]), .out_22(out_67[5]),
    .out_23(out_67[6]), .out_24(out_67[7]), .out_25(out_67[8]), .out_26(out_67[9]), .out_27(out_67[10]),
    .out_28(out_67[11]), .out_29(out_67[12]), .out_30(out_67[13]), .out_31(out_67[14]), .out_32(out_67[15]));

  // Notes on the sheet:
  //   ADD: 1010  1110  1110  1101 
  //   SUB: 0000  1000  1111 1001
  //   MUL: 1100  0110  0001 1110
  //   DIV: 0100  1010 0101 0010 
  //   ADD: 1010  1110  1110  1101 
  //   SUB: 0000  1000  1111 1001
  //   MUL: 1100  0110  0001 1110
  //   DIV: 0100  1010 0101 0010 
  //   Cout
  //   Addition Answer
  //   Subtraction Answer
  //   Multiplication Answer
  //   Cout
  //   Addition Answer
  //   Subtraction Answer
  //   Multiplication Answer
endmodule

module FullAdder (
  input  A,
  input  B,
  input  Cin,
  output Cout,
  output S
);

  wire and_1_out, and_2_out, xor_2_out;

  or or_1 (Cout, and_1_out, and_2_out);
  and and_1 (and_1_out, Cin, B);
  and and_2 (and_2_out, A, xor_2_out);
  xor xor_1 (S, A, xor_2_out);
  xor xor_2 (xor_2_out, B, Cin);

  // Notes on the sheet:
  //   Full Adder
endmodule

// SUB
module Subtraction (
  input  A1,
  input  A2,
  input  A3,
  input  A4,
  input  A5,
  input  A6,
  input  A7,
  input  A8,
  input  B1,
  input  B2,
  input  B3,
  input  B4,
  input  B5,
  input  B6,
  input  B7,
  input  B8,
  output out_17,
  output out_18,
  output out_19,
  output out_20,
  output out_21,
  output out_22,
  output out_23,
  output out_24
);

  wire _001_1_2_out, _001_1_3_out, _001_1_4_out, _001_1_5_out, _001_1_6_out, _001_1_7_out, _001_1_out,
       _010_1_2_out, _010_1_3_out, _010_1_4_out, _010_1_5_out, _010_1_6_out, _010_1_7_out, _010_1_out,
       _011_2_2_out, _011_2_3_out, _011_2_4_out, _011_2_5_out, _011_2_6_out, _011_2_7_out, _011_2_out,
       _100_1_2_out, _100_1_3_out, _100_1_4_out, _100_1_5_out, _100_1_6_out, _100_1_7_out, _100_1_out,
       _101_2_2_out, _101_2_3_out, _101_2_4_out, _101_2_5_out, _101_2_6_out, _101_2_7_out, _101_2_out,
       _110_2_2_out, _110_2_3_out, _110_2_4_out, _110_2_5_out, _110_2_6_out, _110_2_7_out, _110_2_out,
       _111_3_2_out, _111_3_3_out, _111_3_4_out, _111_3_5_out, _111_3_6_out, _111_3_7_out, _111_3_out,
       Carry_1_out, Carry_2_out, Carry_2_out_2, Carry_3_out, Carry_3_out_2, Carry_4_out, Carry_4_out_2,
       Carry_5_out, Carry_5_out_2, Carry_6_out, Carry_6_out_2, Carry_7_out, Carry_7_out_2, Carry_8_out,
       Carry_8_out_2, Carry_out, not_1_out, not_2_out, not_3_out, not_4_out, not_5_out, not_6_out, not_7_out,
       not_8_out, not_9_out, not_10_out, not_11_out, not_12_out, not_13_out, not_14_out, not_15_out,
       not_16_out, not_17_out, not_18_out, not_19_out, not_20_out, not_21_out, not_22_out, not_23_out,
       not_24_out, not_25_out, not_26_out, not_27_out, not_28_out, not_29_out, not_30_out, not_31_out,
       not_32_out, not_33_out, not_34_out, not_35_out, not_36_out, not_37_out, not_38_out, not_39_out,
       not_40_out, not_41_out, not_42_out, not_43_out, not_44_out, not_45_out, not_46_out, not_47_out,
       not_48_out, not_49_out, not_50_out, not_51_out, not_52_out, not_53_out, not_54_out, not_55_out,
       not_56_out, not_57_out, not_58_out, not_59_out, not_60_out, not_61_out, not_62_out, not_63_out,
       not_64_out, not_65_out, not_66_out, not_67_out, not_68_out, not_69_out, not_70_out, not_71_out,
       Sum_2_out, Sum_3_out, Sum_4_out, Sum_5_out, Sum_6_out, Sum_7_out, Sum_8_out, Sum_out;

  not not_1 (not_1_out, B7);
  not not_2 (not_2_out, B8);
  not not_3 (not_3_out, B6);
  not not_4 (not_4_out, B5);
  and Carry (Carry_out, not_2_out, Carry_3_out);
  not not_5 (not_5_out, B4);
  and Carry_2 (Carry_2_out, not_3_out, Carry_4_out);
  and Carry_3 (Carry_3_out, not_1_out, Carry_2_out);
  xor Sum (Sum_out, not_1_out, Carry_2_out);
  xor Sum_2 (Sum_2_out, not_2_out, Carry_3_out);
  not not_6 (not_6_out, B3);
  and Carry_4 (Carry_4_out, not_4_out, Carry_6_out);
  xor Sum_3 (Sum_3_out, not_3_out, Carry_4_out);
  not not_7 (not_7_out, B1);
  not not_8 (not_8_out, B2);
  and Carry_5 (Carry_5_out, not_6_out, Carry_7_out);
  and Carry_6 (Carry_6_out, not_5_out, Carry_5_out);
  xor Sum_4 (Sum_4_out, not_5_out, Carry_5_out);
  xor Sum_5 (Sum_5_out, not_4_out, Carry_6_out);
  and Carry_7 (Carry_7_out, not_8_out, Carry_8_out);
  xor Sum_6 (Sum_6_out, not_6_out, Carry_7_out);
  and Carry_8 (Carry_8_out, not_7_out, 1'b1);
  xor Sum_7 (Sum_7_out, not_7_out, 1'b1);
  xor Sum_8 (Sum_8_out, not_8_out, Carry_8_out);
  and Carry_1 (Carry_1_out, A1, Sum_7_out);
  not not_9 (not_9_out, Sum_8_out);
  and _010_1 (_010_1_out, not_9_out, A2, not_10_out);
  not not_10 (not_10_out, Carry_1_out);
  not not_11 (not_11_out, Sum_8_out);
  and _001_1 (_001_1_out, not_11_out, not_12_out, Carry_1_out);
  not not_12 (not_12_out, A2);
  and _100_1 (_100_1_out, Sum_8_out, not_13_out, not_14_out);
  not not_13 (not_13_out, A2);
  not not_14 (not_14_out, Carry_1_out);
  and _111_3 (_111_3_out, Sum_8_out, A2, Carry_1_out);
  not not_15 (not_15_out, Sum_8_out);
  and _011_2 (_011_2_out, not_15_out, A2, Carry_1_out);
  and _110_2 (_110_2_out, Sum_8_out, A2, not_16_out);
  not not_16 (not_16_out, Carry_1_out);
  and _101_2 (_101_2_out, Sum_8_out, not_17_out, Carry_1_out);
  not not_17 (not_17_out, A2);
  not not_18 (not_18_out, Sum_6_out);
  and _010_1_2 (_010_1_2_out, not_18_out, A3, not_19_out);
  not not_19 (not_19_out, Carry_2_out_2);
  not not_20 (not_20_out, Sum_6_out);
  not not_21 (not_21_out, A3);
  and _001_1_2 (_001_1_2_out, not_20_out, not_21_out, Carry_2_out_2);
  not not_22 (not_22_out, A3);
  and _100_1_2 (_100_1_2_out, Sum_6_out, not_22_out, not_23_out);
  not not_23 (not_23_out, Carry_2_out_2);
  and _111_3_2 (_111_3_2_out, Sum_6_out, A3, Carry_2_out_2);
  not not_24 (not_24_out, Sum_6_out);
  and _011_2_2 (_011_2_2_out, not_24_out, A3, Carry_2_out_2);
  and _110_2_2 (_110_2_2_out, Sum_6_out, A3, not_25_out);
  not not_25 (not_25_out, Carry_2_out_2);
  and _101_2_2 (_101_2_2_out, Sum_6_out, not_26_out, Carry_2_out_2);
  not not_26 (not_26_out, A3);
  not not_27 (not_27_out, Sum_4_out);
  and _010_1_3 (_010_1_3_out, not_27_out, A4, not_28_out);
  not not_28 (not_28_out, Carry_3_out_2);
  not not_29 (not_29_out, Sum_4_out);
  and _001_1_3 (_001_1_3_out, not_29_out, not_30_out, Carry_3_out_2);
  not not_30 (not_30_out, A4);
  not not_31 (not_31_out, A4);
  and _100_1_3 (_100_1_3_out, Sum_4_out, not_31_out, not_32_out);
  not not_32 (not_32_out, Carry_3_out_2);
  and _111_3_3 (_111_3_3_out, Sum_4_out, A4, Carry_3_out_2);
  not not_33 (not_33_out, Sum_4_out);
  and _011_2_3 (_011_2_3_out, not_33_out, A4, Carry_3_out_2);
  and _110_2_3 (_110_2_3_out, Sum_4_out, A4, not_34_out);
  not not_34 (not_34_out, Carry_3_out_2);
  and _101_2_3 (_101_2_3_out, Sum_4_out, not_35_out, Carry_3_out_2);
  not not_35 (not_35_out, A4);
  not not_36 (not_36_out, Sum_5_out);
  and _010_1_4 (_010_1_4_out, not_36_out, A5, not_37_out);
  not not_37 (not_37_out, Carry_4_out_2);
  not not_38 (not_38_out, Sum_5_out);
  not not_39 (not_39_out, A5);
  and _001_1_4 (_001_1_4_out, not_38_out, not_39_out, Carry_4_out_2);
  not not_40 (not_40_out, A5);
  and _100_1_4 (_100_1_4_out, Sum_5_out, not_40_out, not_41_out);
  not not_41 (not_41_out, Carry_4_out_2);
  and _111_3_4 (_111_3_4_out, Sum_5_out, A5, Carry_4_out_2);
  not not_42 (not_42_out, Sum_5_out);
  and _011_2_4 (_011_2_4_out, not_42_out, A5, Carry_4_out_2);
  and _110_2_4 (_110_2_4_out, Sum_5_out, A5, not_43_out);
  not not_43 (not_43_out, Carry_4_out_2);
  not not_44 (not_44_out, A5);
  and _101_2_4 (_101_2_4_out, Sum_5_out, not_44_out, Carry_4_out_2);
  not not_45 (not_45_out, Sum_3_out);
  and _010_1_5 (_010_1_5_out, not_45_out, A6, not_46_out);
  not not_46 (not_46_out, Carry_5_out_2);
  not not_47 (not_47_out, Sum_3_out);
  not not_48 (not_48_out, Sum_3_out);
  and _001_1_5 (_001_1_5_out, not_47_out, not_48_out, Carry_5_out_2);
  not not_49 (not_49_out, A6);
  and _100_1_5 (_100_1_5_out, Sum_3_out, not_49_out, not_50_out);
  not not_50 (not_50_out, Carry_5_out_2);
  and _111_3_5 (_111_3_5_out, Sum_3_out, A6, Carry_5_out_2);
  not not_51 (not_51_out, Sum_3_out);
  and _011_2_5 (_011_2_5_out, not_51_out, A6, Carry_5_out_2);
  and _110_2_5 (_110_2_5_out, Sum_3_out, A6, not_52_out);
  not not_52 (not_52_out, Carry_5_out_2);
  not not_53 (not_53_out, A6);
  and _101_2_5 (_101_2_5_out, Sum_3_out, not_53_out, Carry_5_out_2);
  not not_54 (not_54_out, Sum_out);
  and _010_1_6 (_010_1_6_out, not_54_out, A7, not_55_out);
  not not_55 (not_55_out, Carry_6_out_2);
  not not_56 (not_56_out, Sum_out);
  not not_57 (not_57_out, A7);
  and _001_1_6 (_001_1_6_out, not_56_out, not_57_out, Carry_6_out_2);
  not not_58 (not_58_out, A7);
  and _100_1_6 (_100_1_6_out, Sum_out, not_58_out, not_59_out);
  not not_59 (not_59_out, Carry_6_out_2);
  and _111_3_6 (_111_3_6_out, Sum_out, A7, Carry_6_out_2);
  not not_60 (not_60_out, Sum_out);
  and _011_2_6 (_011_2_6_out, not_60_out, A7, Carry_6_out_2);
  and _110_2_6 (_110_2_6_out, Sum_out, A7, not_61_out);
  not not_61 (not_61_out, Carry_6_out_2);
  and _101_2_6 (_101_2_6_out, Sum_out, not_62_out, Carry_6_out_2);
  not not_62 (not_62_out, A7);
  not not_63 (not_63_out, Sum_2_out);
  and _010_1_7 (_010_1_7_out, not_63_out, A8, not_64_out);
  not not_64 (not_64_out, Carry_7_out_2);
  not not_65 (not_65_out, Sum_2_out);
  not not_66 (not_66_out, A8);
  and _001_1_7 (_001_1_7_out, not_65_out, not_66_out, Carry_7_out_2);
  and _100_1_7 (_100_1_7_out, Sum_2_out, not_67_out, not_68_out);
  not not_67 (not_67_out, A8);
  not not_68 (not_68_out, Carry_7_out_2);
  and _111_3_7 (_111_3_7_out, Sum_2_out, A8, Carry_7_out_2);
  not not_69 (not_69_out, Sum_2_out);
  and _011_2_7 (_011_2_7_out, not_69_out, A8, Carry_7_out_2);
  and _110_2_7 (_110_2_7_out, Sum_2_out, A8, not_70_out);
  not not_70 (not_70_out, Carry_7_out_2);
  and _101_2_7 (_101_2_7_out, Sum_2_out, not_71_out, Carry_7_out_2);
  not not_71 (not_71_out, A8);
  xor Output_1 (out_17, A1, Sum_7_out);
  or Output_2 (out_18, _010_1_out, _001_1_out, _100_1_out, _111_3_out);
  or Carry_2_dup2 (Carry_2_out_2, _111_3_out, _011_2_out, _110_2_out, _101_2_out);
  or Output_3 (out_19, _010_1_2_out, _001_1_2_out, _100_1_2_out, _111_3_2_out);
  or Carry_3_dup2 (Carry_3_out_2, _111_3_2_out, _011_2_2_out, _110_2_2_out, _101_2_2_out);
  or Output_4 (out_20, _010_1_3_out, _001_1_3_out, _100_1_3_out, _111_3_3_out);
  or Carry_4_dup2 (Carry_4_out_2, _111_3_3_out, _011_2_3_out, _110_2_3_out, _101_2_3_out);
  or Output_5 (out_21, _010_1_4_out, _001_1_4_out, _100_1_4_out, _111_3_4_out);
  or Carry_5_dup2 (Carry_5_out_2, _111_3_4_out, _011_2_4_out, _110_2_4_out, _101_2_4_out);
  or Output_6 (out_22, _010_1_5_out, _001_1_5_out, _100_1_5_out, _111_3_5_out);
  or Carry_6_dup2 (Carry_6_out_2, _111_3_5_out, _011_2_5_out, _110_2_5_out, _101_2_5_out);
  or Output_7 (out_23, _010_1_6_out, _001_1_6_out, _100_1_6_out, _111_3_6_out);
  or Carry_7_dup2 (Carry_7_out_2, _111_3_6_out, _011_2_6_out, _110_2_6_out, _101_2_6_out);
  or Output_8 (out_24, _010_1_7_out, _001_1_7_out, _100_1_7_out, _111_3_7_out);
  or Carry_8_dup2 (Carry_8_out_2, _111_3_7_out, _011_2_7_out, _110_2_7_out, _101_2_7_out);
endmodule

module Addition (
  input  A1,
  input  A2,
  input  A3,
  input  A4,
  input  A5,
  input  A6,
  input  A7,
  input  A8,
  input  B1,
  input  B2,
  input  B3,
  input  B4,
  input  B5,
  input  B6,
  input  B7,
  input  B8,
  output out_17,
  output out_18,
  output out_19,
  output out_20,
  output out_21,
  output out_22,
  output out_23,
  output out_24,
  output out_25
);

  wire _001_1_2_out, _001_1_3_out, _001_1_4_out, _001_1_5_out, _001_1_6_out, _001_1_7_out, _001_1_out,
       _010_1_2_out, _010_1_3_out, _010_1_4_out, _010_1_5_out, _010_1_6_out, _010_1_7_out, _010_1_out,
       _011_2_2_out, _011_2_3_out, _011_2_4_out, _011_2_5_out, _011_2_6_out, _011_2_7_out, _011_2_out,
       _100_1_2_out, _100_1_3_out, _100_1_4_out, _100_1_5_out, _100_1_6_out, _100_1_7_out, _100_1_out,
       _101_2_2_out, _101_2_3_out, _101_2_4_out, _101_2_5_out, _101_2_6_out, _101_2_7_out, _101_2_out,
       _110_2_2_out, _110_2_3_out, _110_2_4_out, _110_2_5_out, _110_2_6_out, _110_2_7_out, _110_2_out,
       _111_3_2_out, _111_3_3_out, _111_3_4_out, _111_3_5_out, _111_3_6_out, _111_3_7_out, _111_3_out,
       Carry_1_out, Carry_2_out, Carry_3_out, Carry_4_out, Carry_5_out, Carry_6_out, Carry_7_out, not_1_out,
       not_2_out, not_3_out, not_4_out, not_5_out, not_6_out, not_7_out, not_8_out, not_9_out, not_10_out,
       not_11_out, not_12_out, not_13_out, not_14_out, not_15_out, not_16_out, not_17_out, not_18_out,
       not_19_out, not_20_out, not_21_out, not_22_out, not_23_out, not_24_out, not_25_out, not_26_out,
       not_27_out, not_28_out, not_29_out, not_30_out, not_31_out, not_32_out, not_33_out, not_34_out,
       not_35_out, not_36_out, not_37_out, not_38_out, not_39_out, not_40_out, not_41_out, not_42_out,
       not_43_out, not_44_out, not_45_out, not_46_out, not_47_out, not_48_out, not_49_out, not_50_out,
       not_51_out, not_52_out, not_53_out, not_54_out, not_55_out, not_56_out, not_57_out, not_58_out,
       not_59_out, not_60_out, not_61_out, not_62_out, not_63_out;

  and Carry_1 (Carry_1_out, A1, B1);
  not not_1 (not_1_out, B2);
  and _010_1 (_010_1_out, not_1_out, A2, not_2_out);
  not not_2 (not_2_out, Carry_1_out);
  not not_3 (not_3_out, B2);
  and _001_1 (_001_1_out, not_3_out, not_4_out, Carry_1_out);
  not not_4 (not_4_out, A2);
  not not_5 (not_5_out, A2);
  and _100_1 (_100_1_out, B2, not_5_out, not_6_out);
  not not_6 (not_6_out, Carry_1_out);
  and _111_3 (_111_3_out, B2, A2, Carry_1_out);
  not not_7 (not_7_out, B2);
  and _011_2 (_011_2_out, not_7_out, A2, Carry_1_out);
  and _110_2 (_110_2_out, B2, A2, not_8_out);
  not not_8 (not_8_out, Carry_1_out);
  and _101_2 (_101_2_out, B2, not_9_out, Carry_1_out);
  not not_9 (not_9_out, A2);
  not not_10 (not_10_out, B3);
  and _010_1_2 (_010_1_2_out, not_10_out, A3, not_11_out);
  not not_11 (not_11_out, Carry_2_out);
  not not_12 (not_12_out, B3);
  not not_13 (not_13_out, A3);
  and _001_1_2 (_001_1_2_out, not_12_out, not_13_out, Carry_2_out);
  not not_14 (not_14_out, A3);
  and _100_1_2 (_100_1_2_out, B3, not_14_out, not_15_out);
  not not_15 (not_15_out, Carry_2_out);
  and _111_3_2 (_111_3_2_out, B3, A3, Carry_2_out);
  not not_16 (not_16_out, B3);
  and _011_2_2 (_011_2_2_out, not_16_out, A3, Carry_2_out);
  and _110_2_2 (_110_2_2_out, B3, A3, not_17_out);
  not not_17 (not_17_out, Carry_2_out);
  and _101_2_2 (_101_2_2_out, B3, not_18_out, Carry_2_out);
  not not_18 (not_18_out, A3);
  not not_19 (not_19_out, B4);
  and _010_1_3 (_010_1_3_out, not_19_out, A4, not_20_out);
  not not_20 (not_20_out, Carry_3_out);
  not not_21 (not_21_out, B4);
  and _001_1_3 (_001_1_3_out, not_21_out, not_22_out, Carry_3_out);
  not not_22 (not_22_out, A4);
  not not_23 (not_23_out, A4);
  and _100_1_3 (_100_1_3_out, B4, not_23_out, not_24_out);
  not not_24 (not_24_out, Carry_3_out);
  and _111_3_3 (_111_3_3_out, B4, A4, Carry_3_out);
  not not_25 (not_25_out, B4);
  and _011_2_3 (_011_2_3_out, not_25_out, A4, Carry_3_out);
  and _110_2_3 (_110_2_3_out, B4, A4, not_26_out);
  not not_26 (not_26_out, Carry_3_out);
  and _101_2_3 (_101_2_3_out, B4, not_27_out, Carry_3_out);
  not not_27 (not_27_out, A4);
  not not_28 (not_28_out, B5);
  and _010_1_4 (_010_1_4_out, not_28_out, A5, not_29_out);
  not not_29 (not_29_out, Carry_4_out);
  not not_30 (not_30_out, B5);
  and _001_1_4 (_001_1_4_out, not_30_out, not_31_out, Carry_4_out);
  not not_31 (not_31_out, A5);
  and _100_1_4 (_100_1_4_out, B5, not_32_out, not_33_out);
  not not_32 (not_32_out, A5);
  not not_33 (not_33_out, Carry_4_out);
  and _111_3_4 (_111_3_4_out, B5, A5, Carry_4_out);
  not not_34 (not_34_out, B5);
  and _011_2_4 (_011_2_4_out, not_34_out, A5, Carry_4_out);
  and _110_2_4 (_110_2_4_out, B5, A5, not_35_out);
  not not_35 (not_35_out, Carry_4_out);
  not not_36 (not_36_out, A5);
  and _101_2_4 (_101_2_4_out, B5, not_36_out, Carry_4_out);
  not not_37 (not_37_out, B6);
  and _010_1_5 (_010_1_5_out, not_37_out, A6, not_38_out);
  not not_38 (not_38_out, Carry_5_out);
  not not_39 (not_39_out, B6);
  not not_40 (not_40_out, B6);
  and _001_1_5 (_001_1_5_out, not_39_out, not_40_out, Carry_5_out);
  and _100_1_5 (_100_1_5_out, B6, not_41_out, not_42_out);
  not not_41 (not_41_out, A6);
  not not_42 (not_42_out, Carry_5_out);
  and _111_3_5 (_111_3_5_out, B6, A6, Carry_5_out);
  not not_43 (not_43_out, B6);
  and _011_2_5 (_011_2_5_out, not_43_out, A6, Carry_5_out);
  and _110_2_5 (_110_2_5_out, B6, A6, not_44_out);
  not not_44 (not_44_out, Carry_5_out);
  not not_45 (not_45_out, A6);
  and _101_2_5 (_101_2_5_out, B6, not_45_out, Carry_5_out);
  not not_46 (not_46_out, B7);
  and _010_1_6 (_010_1_6_out, not_46_out, A7, not_47_out);
  not not_47 (not_47_out, Carry_6_out);
  not not_48 (not_48_out, B7);
  and _001_1_6 (_001_1_6_out, not_48_out, not_49_out, Carry_6_out);
  not not_49 (not_49_out, A7);
  and _100_1_6 (_100_1_6_out, B7, not_50_out, not_51_out);
  not not_50 (not_50_out, A7);
  not not_51 (not_51_out, Carry_6_out);
  and _111_3_6 (_111_3_6_out, B7, A7, Carry_6_out);
  not not_52 (not_52_out, B7);
  and _011_2_6 (_011_2_6_out, not_52_out, A7, Carry_6_out);
  and _110_2_6 (_110_2_6_out, B7, A7, not_53_out);
  not not_53 (not_53_out, Carry_6_out);
  not not_54 (not_54_out, A7);
  and _101_2_6 (_101_2_6_out, B7, not_54_out, Carry_6_out);
  not not_55 (not_55_out, B8);
  not not_56 (not_56_out, Carry_7_out);
  not not_57 (not_57_out, B8);
  not not_58 (not_58_out, A8);
  not not_59 (not_59_out, A8);
  not not_60 (not_60_out, Carry_7_out);
  not not_61 (not_61_out, B8);
  not not_62 (not_62_out, Carry_7_out);
  not not_63 (not_63_out, A8);
  xor Output_1 (out_17, A1, B1);
  and _010_1_7 (_010_1_7_out, not_55_out, A8, not_56_out);
  and _001_1_7 (_001_1_7_out, not_57_out, not_58_out, Carry_7_out);
  and _100_1_7 (_100_1_7_out, B8, not_59_out, not_60_out);
  and _111_3_7 (_111_3_7_out, B8, A8, Carry_7_out);
  and _011_2_7 (_011_2_7_out, not_61_out, A8, Carry_7_out);
  and _110_2_7 (_110_2_7_out, B8, A8, not_62_out);
  and _101_2_7 (_101_2_7_out, B8, not_63_out, Carry_7_out);
  or Output_2 (out_18, _010_1_out, _001_1_out, _100_1_out, _111_3_out);
  or Carry_2 (Carry_2_out, _111_3_out, _011_2_out, _110_2_out, _101_2_out);
  or Output_3 (out_19, _010_1_2_out, _001_1_2_out, _100_1_2_out, _111_3_2_out);
  or Carry_3 (Carry_3_out, _111_3_2_out, _011_2_2_out, _110_2_2_out, _101_2_2_out);
  or Output_4 (out_20, _010_1_3_out, _001_1_3_out, _100_1_3_out, _111_3_3_out);
  or Carry_4 (Carry_4_out, _111_3_3_out, _011_2_3_out, _110_2_3_out, _101_2_3_out);
  or Output_5 (out_21, _010_1_4_out, _001_1_4_out, _100_1_4_out, _111_3_4_out);
  or Carry_5 (Carry_5_out, _111_3_4_out, _011_2_4_out, _110_2_4_out, _101_2_4_out);
  or Output_6 (out_22, _010_1_5_out, _001_1_5_out, _100_1_5_out, _111_3_5_out);
  or Carry_6 (Carry_6_out, _111_3_5_out, _011_2_5_out, _110_2_5_out, _101_2_5_out);
  or Output_7 (out_23, _010_1_6_out, _001_1_6_out, _100_1_6_out, _111_3_6_out);
  or Carry_7 (Carry_7_out, _111_3_6_out, _011_2_6_out, _110_2_6_out, _101_2_6_out);
  or Output_8 (out_24, _010_1_7_out, _001_1_7_out, _100_1_7_out, _111_3_7_out);
  or Carry_8 (out_25, _111_3_7_out, _011_2_7_out, _110_2_7_out, _101_2_7_out);
endmodule

module Multiplication (
  input  in_1,
  input  in_2,
  input  in_3,
  input  in_4,
  input  a5,
  input  a6,
  input  a7,
  input  a8,
  input  b1,
  input  b2,
  input  b3,
  input  b4,
  input  b5,
  input  b6,
  input  b7,
  input  b8,
  output out_17,
  output out_18,
  output out_19,
  output out_20,
  output out_21,
  output out_22,
  output out_23,
  output out_24,
  output out_25,
  output out_26,
  output out_27,
  output out_28,
  output out_29,
  output out_30,
  output out_31,
  output out_32
);

  wire a1_b2_out, a1_b3_out, a1_b4_out, a1_b5_out, a1_b6_out, a1_b7_out, a1_b8_out, a2_b1_out, a2_b2_out,
       a2_b3_out, a2_b4_out, a2_b5_out, a2_b6_out, a2_b7_out, a2_b8_out, a3b1_out, a3b2_out, a3b3_out,
       a3b4_out, a3b5_out, a3b6_out, a3b7_out, a3b8_out, a4b1_out, a4b2_out, a4b3_out, a4b4_out, a4b5_out,
       a4b6_out, a4b7_out, a4b8_out, a5b1_out, a5b2_out, a5b3_out, a5b4_out, a5b5_out, a5b6_out, a5b7_out,
       a5b8_out, a6b1_out, a6b2_out, a6b3_out, a6b4_out, a6b5_out, a6b6_out, a6b7_out, a6b8_out, a7b1_out,
       a7b2_out, a7b3_out, a7b4_out, a7b5_out, a7b6_out, a7b7_out, a7b8_out, a8b1_out, a8b2_out, a8b3_out,
       a8b4_out, a8b5_out, a8b6_out, a8b7_out, a8b8_out, fulladder_2_cout, fulladder_2_s, fulladder_3_cout,
       fulladder_4_cout, fulladder_4_s, fulladder_5_cout, fulladder_5_s, fulladder_6_cout, fulladder_7_cout,
       fulladder_7_s, fulladder_8_cout, fulladder_8_s, fulladder_9_cout, fulladder_9_s, fulladder_10_cout,
       fulladder_11_cout, fulladder_11_s, fulladder_12_cout, fulladder_12_s, fulladder_13_cout,
       fulladder_13_s, fulladder_14_cout, fulladder_14_s, fulladder_15_cout, fulladder_16_cout,
       fulladder_16_s, fulladder_17_cout, fulladder_17_s, fulladder_18_cout, fulladder_18_s,
       fulladder_19_cout, fulladder_19_s, fulladder_20_cout, fulladder_20_s, fulladder_21_cout,
       fulladder_21_s, fulladder_22_cout, fulladder_23_cout, fulladder_23_s, fulladder_24_cout,
       fulladder_24_s, fulladder_25_cout, fulladder_25_s, fulladder_26_cout, fulladder_26_s,
       fulladder_27_cout, fulladder_27_s, fulladder_28_cout, fulladder_28_s, fulladder_29_cout,
       fulladder_30_cout, fulladder_30_s, fulladder_31_cout, fulladder_31_s, fulladder_32_cout,
       fulladder_32_s, fulladder_33_cout, fulladder_33_s, fulladder_34_cout, fulladder_34_s,
       fulladder_35_cout, fulladder_36_cout, fulladder_36_s, fulladder_37_cout, fulladder_37_s,
       fulladder_38_cout, fulladder_38_s, fulladder_39_cout, fulladder_39_s, fulladder_40_cout,
       fulladder_40_s, fulladder_41_cout, fulladder_42_cout, fulladder_42_s, fulladder_43_cout,
       fulladder_43_s, fulladder_44_cout, fulladder_44_s, fulladder_45_cout, fulladder_45_s,
       fulladder_46_cout, fulladder_47_cout, fulladder_47_s, fulladder_48_cout, fulladder_48_s,
       fulladder_49_cout, fulladder_49_s, fulladder_50_cout, fulladder_51_cout, fulladder_51_s,
       fulladder_52_cout, fulladder_52_s, fulladder_53_cout, fulladder_54_cout, fulladder_54_s,
       fulladder_55_cout, fulladder_56_cout, not_1_out, not_2_out, not_3_out, not_4_out, not_5_out,
       not_6_out, not_7_out, not_8_out;

  and a8b8 (a8b8_out, a8, b8);
  LED led_1 (.in(out_32));
  and a8b7 (a8b7_out, a8, b7);
  LED led_2 (.in(fulladder_2_cout));
  FullAdder fulladder_1 (.Cout(out_32), .Cin(fulladder_3_cout), .A(fulladder_2_cout), .B(a8b8_out), .S(out_31));
  LED led_3 (.in(out_31));
  LED led_4 (.in(fulladder_4_cout));
  FullAdder fulladder_2 (
    .Cout(fulladder_2_cout), .Cin(fulladder_5_cout), .A(fulladder_4_cout), .B(a8b7_out), .S(fulladder_2_s));
  LED led_5 (.in(fulladder_2_s));
  and a7b8 (a7b8_out, a7, b8);
  FullAdder fulladder_3 (.Cout(fulladder_3_cout), .Cin(fulladder_6_cout), .A(fulladder_2_s), .B(a7b8_out), .S(out_30));
  LED led_6 (.in(out_30));
  and a8b5 (a8b5_out, a8, b5);
  LED led_7 (.in(fulladder_7_cout));
  and a8b6 (a8b6_out, a8, b6);
  FullAdder fulladder_4 (
    .Cout(fulladder_4_cout), .Cin(fulladder_8_cout), .A(fulladder_7_cout), .B(a8b6_out), .S(fulladder_4_s));
  LED led_8 (.in(fulladder_4_s));
  and a7b7 (a7b7_out, a7, b7);
  FullAdder fulladder_5 (
    .Cout(fulladder_5_cout), .Cin(fulladder_9_cout), .A(fulladder_4_s), .B(a7b7_out), .S(fulladder_5_s));
  LED led_9 (.in(fulladder_5_s));
  and a6b8 (a6b8_out, a6, b8);
  FullAdder fulladder_6 (.Cout(fulladder_6_cout), .Cin(fulladder_10_cout), .A(fulladder_5_s), .B(a6b8_out), .S(out_29));
  LED led_10 (.in(out_29));
  and a8b4 (a8b4_out, a8, b4);
  LED led_11 (.in(fulladder_11_cout));
  FullAdder fulladder_7 (
    .Cout(fulladder_7_cout), .Cin(fulladder_12_cout), .A(fulladder_11_cout), .B(a8b5_out), .S(fulladder_7_s));
  LED led_12 (.in(fulladder_7_s));
  and a7b6 (a7b6_out, a7, b6);
  FullAdder fulladder_8 (
    .Cout(fulladder_8_cout), .Cin(fulladder_13_cout), .A(fulladder_7_s), .B(a7b6_out), .S(fulladder_8_s));
  LED led_13 (.in(fulladder_8_s));
  and a6b7 (a6b7_out, a6, b7);
  FullAdder fulladder_9 (
    .Cout(fulladder_9_cout), .Cin(fulladder_14_cout), .A(fulladder_8_s), .B(a6b7_out), .S(fulladder_9_s));
  LED led_14 (.in(fulladder_9_s));
  and a5b8 (a5b8_out, a5, b8);
  FullAdder fulladder_10 (
    .Cout(fulladder_10_cout), .Cin(fulladder_15_cout), .A(fulladder_9_s), .B(a5b8_out), .S(out_28));
  LED led_15 (.in(out_28));
  not not_1 (not_1_out, 1'b1);
  LED led_16 (.in(fulladder_16_cout));
  LED led_17 (.in(fulladder_16_cout));
  LED led_18 (.in(fulladder_17_cout));
  FullAdder fulladder_11 (
    .Cout(fulladder_11_cout), .Cin(fulladder_18_cout), .A(fulladder_17_cout), .B(a8b4_out), .S(fulladder_11_s));
  LED led_19 (.in(fulladder_11_s));
  and a7b5 (a7b5_out, a7, b5);
  FullAdder fulladder_12 (
    .Cout(fulladder_12_cout), .Cin(fulladder_19_cout), .A(fulladder_11_s), .B(a7b5_out), .S(fulladder_12_s));
  LED led_20 (.in(fulladder_12_s));
  and a6b6 (a6b6_out, a6, b6);
  FullAdder fulladder_13 (
    .Cout(fulladder_13_cout), .Cin(fulladder_20_cout), .A(fulladder_12_s), .B(a6b6_out), .S(fulladder_13_s));
  LED led_21 (.in(fulladder_13_s));
  and a5b7 (a5b7_out, a5, b7);
  FullAdder fulladder_14 (
    .Cout(fulladder_14_cout), .Cin(fulladder_21_cout), .A(fulladder_13_s), .B(a5b7_out), .S(fulladder_14_s));
  LED led_22 (.in(fulladder_14_s));
  and a4b8 (a4b8_out, in_4, b8);
  FullAdder fulladder_15 (
    .Cout(fulladder_15_cout), .Cin(fulladder_22_cout), .A(fulladder_14_s), .B(a4b8_out), .S(out_27));
  LED led_23 (.in(out_27));
  and a8b2 (a8b2_out, a8, b2);
  FullAdder fulladder_16 (
    .Cout(fulladder_16_cout), .Cin(fulladder_23_cout), .A(not_1_out), .B(a8b2_out), .S(fulladder_16_s));
  LED led_24 (.in(fulladder_16_cout));
  LED led_25 (.in(fulladder_16_s));
  and a8b3 (a8b3_out, a8, b3);
  FullAdder fulladder_17 (
    .Cout(fulladder_17_cout), .Cin(fulladder_24_cout), .A(fulladder_16_cout), .B(a8b3_out), .S(fulladder_17_s));
  LED led_26 (.in(fulladder_17_s));
  and a7b4 (a7b4_out, a7, b4);
  FullAdder fulladder_18 (
    .Cout(fulladder_18_cout), .Cin(fulladder_25_cout), .A(fulladder_17_s), .B(a7b4_out), .S(fulladder_18_s));
  LED led_27 (.in(fulladder_18_s));
  and a6b5 (a6b5_out, a6, b5);
  FullAdder fulladder_19 (
    .Cout(fulladder_19_cout), .Cin(fulladder_26_cout), .A(fulladder_18_s), .B(a6b5_out), .S(fulladder_19_s));
  LED led_28 (.in(fulladder_19_s));
  and a5b6 (a5b6_out, a5, b6);
  FullAdder fulladder_20 (
    .Cout(fulladder_20_cout), .Cin(fulladder_27_cout), .A(fulladder_19_s), .B(a5b6_out), .S(fulladder_20_s));
  LED led_29 (.in(fulladder_20_s));
  and a4b7 (a4b7_out, in_4, b7);
  FullAdder fulladder_21 (
    .Cout(fulladder_21_cout), .Cin(fulladder_28_cout), .A(fulladder_20_s), .B(a4b7_out), .S(fulladder_21_s));
  LED led_30 (.in(fulladder_21_s));
  and a3b8 (a3b8_out, in_3, b8);
  FullAdder fulladder_22 (
    .Cout(fulladder_22_cout), .Cin(fulladder_29_cout), .A(fulladder_21_s), .B(a3b8_out), .S(out_26));
  LED led_31 (.in(out_26));
  and a8b1 (a8b1_out, a8, b1);
  and a7b2 (a7b2_out, a7, b2);
  FullAdder fulladder_23 (
    .Cout(fulladder_23_cout), .Cin(fulladder_36_cout), .A(a8b1_out), .B(a7b2_out), .S(fulladder_23_s));
  and a7b3 (a7b3_out, a7, b3);
  FullAdder fulladder_24 (
    .Cout(fulladder_24_cout), .Cin(fulladder_30_cout), .A(fulladder_16_s), .B(a7b3_out), .S(fulladder_24_s));
  LED led_32 (.in(fulladder_24_s));
  and a6b4 (a6b4_out, a6, b4);
  FullAdder fulladder_25 (
    .Cout(fulladder_25_cout), .Cin(fulladder_31_cout), .A(fulladder_24_s), .B(a6b4_out), .S(fulladder_25_s));
  LED led_33 (.in(fulladder_25_s));
  and a5b5 (a5b5_out, a5, b5);
  FullAdder fulladder_26 (
    .Cout(fulladder_26_cout), .Cin(fulladder_32_cout), .A(fulladder_25_s), .B(a5b5_out), .S(fulladder_26_s));
  LED led_34 (.in(fulladder_26_s));
  and a4b6 (a4b6_out, in_4, b6);
  FullAdder fulladder_27 (
    .Cout(fulladder_27_cout), .Cin(fulladder_33_cout), .A(fulladder_26_s), .B(a4b6_out), .S(fulladder_27_s));
  LED led_35 (.in(fulladder_27_s));
  and a3b7 (a3b7_out, in_3, b7);
  FullAdder fulladder_28 (
    .Cout(fulladder_28_cout), .Cin(fulladder_34_cout), .A(fulladder_27_s), .B(a3b7_out), .S(fulladder_28_s));
  LED led_36 (.in(fulladder_28_s));
  and a2_b8 (a2_b8_out, in_2, b8);
  FullAdder fulladder_29 (
    .Cout(fulladder_29_cout), .Cin(fulladder_35_cout), .A(fulladder_28_s), .B(a2_b8_out), .S(out_25));
  and a7b1 (a7b1_out, a7, b1);
  LED led_37 (.in(fulladder_23_s));
  and a6b3 (a6b3_out, a6, b3);
  FullAdder fulladder_30 (
    .Cout(fulladder_30_cout), .Cin(fulladder_37_cout), .A(fulladder_23_s), .B(a6b3_out), .S(fulladder_30_s));
  LED led_38 (.in(fulladder_30_s));
  and a5b4 (a5b4_out, a5, b4);
  FullAdder fulladder_31 (
    .Cout(fulladder_31_cout), .Cin(fulladder_38_cout), .A(fulladder_30_s), .B(a5b4_out), .S(fulladder_31_s));
  LED led_39 (.in(fulladder_31_s));
  and a4b5 (a4b5_out, in_4, b5);
  FullAdder fulladder_32 (
    .Cout(fulladder_32_cout), .Cin(fulladder_39_cout), .A(fulladder_31_s), .B(a4b5_out), .S(fulladder_32_s));
  LED led_40 (.in(fulladder_32_s));
  and a3b6 (a3b6_out, in_3, b6);
  FullAdder fulladder_33 (
    .Cout(fulladder_33_cout), .Cin(fulladder_40_cout), .A(fulladder_32_s), .B(a3b6_out), .S(fulladder_33_s));
  LED led_41 (.in(fulladder_33_s));
  and a2_b7 (a2_b7_out, in_2, b7);
  FullAdder fulladder_34 (
    .Cout(fulladder_34_cout), .Cin(fulladder_41_cout), .A(fulladder_33_s), .B(a2_b7_out), .S(fulladder_34_s));
  and a1_b8 (a1_b8_out, in_1, b8);
  FullAdder fulladder_35 (.Cout(fulladder_35_cout), .Cin(not_2_out), .A(fulladder_34_s), .B(a1_b8_out), .S(out_24));
  LED led_42 (.in(out_25));
  and a6b2 (a6b2_out, a6, b2);
  FullAdder fulladder_36 (
    .Cout(fulladder_36_cout), .Cin(fulladder_42_cout), .A(a7b1_out), .B(a6b2_out), .S(fulladder_36_s));
  LED led_43 (.in(fulladder_36_s));
  and a5b3 (a5b3_out, a5, b3);
  FullAdder fulladder_37 (
    .Cout(fulladder_37_cout), .Cin(fulladder_43_cout), .A(fulladder_36_s), .B(a5b3_out), .S(fulladder_37_s));
  LED led_44 (.in(fulladder_37_s));
  and a4b4 (a4b4_out, in_4, b4);
  FullAdder fulladder_38 (
    .Cout(fulladder_38_cout), .Cin(fulladder_44_cout), .A(fulladder_37_s), .B(a4b4_out), .S(fulladder_38_s));
  LED led_45 (.in(fulladder_38_s));
  and a3b5 (a3b5_out, in_3, b5);
  FullAdder fulladder_39 (
    .Cout(fulladder_39_cout), .Cin(fulladder_45_cout), .A(fulladder_38_s), .B(a3b5_out), .S(fulladder_39_s));
  LED led_46 (.in(fulladder_39_s));
  FullAdder fulladder_40 (
    .Cout(fulladder_40_cout), .Cin(fulladder_46_cout), .A(fulladder_39_s), .B(a2_b6_out), .S(fulladder_40_s));
  and a1_b7 (a1_b7_out, in_1, b7);
  FullAdder fulladder_41 (.Cout(fulladder_41_cout), .Cin(not_3_out), .A(fulladder_40_s), .B(a1_b7_out), .S(out_23));
  LED led_47 (.in(fulladder_34_s));
  not not_2 (not_2_out, 1'b1);
  LED led_48 (.in(out_24));
  and a6b1 (a6b1_out, a6, b1);
  and a5b2 (a5b2_out, a5, b2);
  FullAdder fulladder_42 (
    .Cout(fulladder_42_cout), .Cin(fulladder_47_cout), .A(a6b1_out), .B(a5b2_out), .S(fulladder_42_s));
  LED led_49 (.in(fulladder_42_s));
  and a4b3 (a4b3_out, in_4, in_4, b3);
  FullAdder fulladder_43 (
    .Cout(fulladder_43_cout), .Cin(fulladder_48_cout), .A(fulladder_42_s), .B(a4b3_out), .S(fulladder_43_s));
  LED led_50 (.in(fulladder_43_s));
  and a3b4 (a3b4_out, in_3, b4);
  FullAdder fulladder_44 (
    .Cout(fulladder_44_cout), .Cin(fulladder_49_cout), .A(fulladder_43_s), .B(a3b4_out), .S(fulladder_44_s));
  LED led_51 (.in(fulladder_44_s));
  and a2_b5 (a2_b5_out, in_2, b5);
  FullAdder fulladder_45 (
    .Cout(fulladder_45_cout), .Cin(fulladder_50_cout), .A(fulladder_44_s), .B(a2_b5_out), .S(fulladder_45_s));
  and a2_b6 (a2_b6_out, in_2, b6);
  FullAdder fulladder_46 (.Cout(fulladder_46_cout), .Cin(not_4_out), .A(fulladder_45_s), .B(a1_b6_out), .S(out_22));
  LED led_52 (.in(fulladder_40_s));
  not not_3 (not_3_out, 1'b1);
  LED led_53 (.in(out_23));
  LED led_54 (.in(out_23));
  and a5b1 (a5b1_out, a5, b1);
  and a4b2 (a4b2_out, in_4, b2);
  FullAdder fulladder_47 (
    .Cout(fulladder_47_cout), .Cin(fulladder_51_cout), .A(a5b1_out), .B(a4b2_out), .S(fulladder_47_s));
  LED led_55 (.in(fulladder_47_s));
  and a3b3 (a3b3_out, in_3, b3);
  FullAdder fulladder_48 (
    .Cout(fulladder_48_cout), .Cin(fulladder_52_cout), .A(fulladder_47_s), .B(a3b3_out), .S(fulladder_48_s));
  LED led_56 (.in(fulladder_48_s));
  and a2_b4 (a2_b4_out, in_2, in_2, in_2, b4);
  FullAdder fulladder_49 (
    .Cout(fulladder_49_cout), .Cin(fulladder_53_cout), .A(fulladder_48_s), .B(a2_b4_out), .S(fulladder_49_s));
  and a1_b5 (a1_b5_out, in_1, b5);
  FullAdder fulladder_50 (.Cout(fulladder_50_cout), .Cin(not_5_out), .A(fulladder_49_s), .B(a1_b5_out), .S(out_21));
  LED led_57 (.in(fulladder_45_s));
  and a1_b6 (a1_b6_out, in_1, b6);
  not not_4 (not_4_out, 1'b1);
  LED led_58 (.in(out_22));
  LED led_59 (.in(out_22));
  LED led_60 (.in(out_22));
  and a4b1 (a4b1_out, in_4, b1);
  and a3b2 (a3b2_out, in_3, b2);
  FullAdder fulladder_51 (
    .Cout(fulladder_51_cout), .Cin(fulladder_54_cout), .A(a4b1_out), .B(a3b2_out), .S(fulladder_51_s));
  LED led_61 (.in(fulladder_51_s));
  and a2_b3 (a2_b3_out, in_2, in_2, b3);
  FullAdder fulladder_52 (
    .Cout(fulladder_52_cout), .Cin(fulladder_55_cout), .A(fulladder_51_s), .B(a2_b3_out), .S(fulladder_52_s));
  and a1_b4 (a1_b4_out, in_1, b4);
  FullAdder fulladder_53 (.Cout(fulladder_53_cout), .Cin(not_6_out), .A(fulladder_52_s), .B(a1_b4_out), .S(out_20));
  LED led_62 (.in(fulladder_49_s));
  not not_5 (not_5_out, 1'b1);
  LED led_63 (.in(out_21));
  LED led_64 (.in(out_21));
  LED led_65 (.in(out_21));
  LED led_66 (.in(out_21));
  and a3b1 (a3b1_out, in_3, b1, b1);
  and a2_b2 (a2_b2_out, in_2, b2);
  FullAdder fulladder_54 (
    .Cout(fulladder_54_cout), .Cin(fulladder_56_cout), .A(a3b1_out), .B(a2_b2_out), .S(fulladder_54_s));
  LED led_67 (.in(fulladder_54_s));
  FullAdder fulladder_55 (.Cout(fulladder_55_cout), .Cin(not_7_out), .A(fulladder_54_s), .B(a1_b3_out), .S(out_19));
  LED led_68 (.in(fulladder_52_s));
  not not_6 (not_6_out, 1'b1);
  LED led_69 (.in(out_20));
  LED led_70 (.in(out_20));
  LED led_71 (.in(out_20));
  LED led_72 (.in(out_20));
  LED led_73 (.in(out_20));
  and a2_b1 (a2_b1_out, b1, in_2);
  and a1_b2 (a1_b2_out, in_1, b2);
  FullAdder fulladder_56 (.Cout(fulladder_56_cout), .Cin(not_8_out), .A(a2_b1_out), .B(a1_b2_out), .S(out_18));
  LED led_74 (.in(out_18));
  and a1_b3 (a1_b3_out, in_1, b3);
  not not_7 (not_7_out, 1'b1);
  LED led_75 (.in(out_19));
  LED led_76 (.in(out_19));
  LED led_77 (.in(out_19));
  LED led_78 (.in(out_19));
  LED led_79 (.in(out_19));
  LED led_80 (.in(out_19));
  and a1_b1 (out_17, in_1, b1);
  not not_8 (not_8_out, 1'b1);
  LED led_81 (.in(out_17));
  LED led_82 (.in(out_17));
  LED led_83 (.in(out_18));
  LED led_84 (.in(out_17));
  LED led_85 (.in(out_18));
  LED led_86 (.in(out_17));
  LED led_87 (.in(out_18));
  LED led_88 (.in(out_18));
  LED led_89 (.in(out_17));
  LED led_90 (.in(out_17));
  LED led_91 (.in(out_18));
  LED led_92 (.in(out_17));
  LED led_93 (.in(out_18));
  LED led_94 (.in(out_18));
  LED led_95 (.in(out_17));

  // Notes on the sheet:
  //   b2
  //   e
  //   b1
  //   a4
  //   a3
  //   a2
  //   a1
endmodule

module Division (
  input  A8,
  input  A7,
  input  A6,
  input  A5,
  input  A4,
  input  A3,
  input  A2,
  input  A1,
  input  in_9,
  input  in_10,
  input  in_11,
  input  in_12,
  input  in_13,
  input  in_14,
  input  in_15,
  input  in_16,
  input  in_17,
  input  in_18,
  input  in_19,
  input  in_20,
  input  in_21,
  input  in_22,
  input  in_23,
  input  in_24,
  input  B8,
  input  B7,
  input  B6,
  input  B5,
  input  B4,
  input  B3,
  input  B2,
  input  B1,
  input  in_33,
  input  in_34,
  input  A8_2,
  input  A7_2,
  input  A6_2,
  input  A5_2,
  input  A4_2,
  input  A3_2,
  input  A2_2,
  input  A1_2,
  input  in_43,
  input  in_44,
  input  in_45,
  input  in_46,
  input  in_47,
  input  in_48,
  input  in_49,
  input  in_50,
  input  in_51,
  input  in_52,
  input  in_53,
  input  in_54,
  input  in_55,
  input  in_56,
  input  in_57,
  input  in_58,
  input  B8_2,
  input  B7_2,
  input  B6_2,
  input  B5_2,
  input  B4_2,
  input  B3_2,
  input  B2_2,
  input  B1_2,
  output [15:0] out_67,
  output out_68,
  output [15:0] out_69,
  output out_70
);

  Subtractor #(.width(16)) subtractor_1 (
    .a({in_17, in_18, in_19, in_20, in_21, in_22, in_23, in_24, B8, B7, B6, B5, B4, B3, B2, B1}),
    .b({A8, A7, A6, A5, A4, A3, A2, A1, in_9, in_10, in_11, in_12, in_13, in_14, in_15, in_16}),
    .out(out_67), .bin(in_33), .bout(out_68));
  Subtractor #(.width(16)) subtractor_2 (
    .a({in_51, in_52, in_53, in_54, in_55, in_56, in_57, in_58, B8_2, B7_2, B6_2, B5_2, B4_2, B3_2, B2_2, B1_2}),
    .b({A8_2, A7_2, A6_2, A5_2, A4_2, A3_2, A2_2, A1_2, in_43, in_44, in_45, in_46, in_47, in_48, in_49, in_50}),
    .out(out_69), .bin(in_34), .bout(out_70));
endmodule

module div2 (
  input  in_1,
  input  x,
  input  y,
  input  in_4,
  output out_5,
  output out_6
);

  wire and_1_out, and_2_out, and_3_out, and_4_out, and_5_out, not_1_out, not_2_out, xor_1_out;

  not not_1 (not_1_out, x);
  not not_2 (not_2_out, in_1);
  ExactlyOne xor_1 (.out(xor_1_out), .in0(x), .in2(y), .in4(in_4));
  and and_1 (and_1_out, in_4, y);
  and and_2 (and_2_out, in_4, not_1_out);
  and and_3 (and_3_out, y, not_1_out);
  and and_4 (and_4_out, x, in_1);
  and and_5 (and_5_out, not_2_out, xor_1_out);
  or or_1 (out_6, and_1_out, and_2_out, and_3_out);
  or or_2 (out_5, and_4_out, and_5_out);
endmodule

module div4 (
  input  a4,
  input  a3,
  input  a2,
  input  a1,
  input  in_5,
  input  in_6,
  input  in_7,
  input  in_8,
  input  in_9,
  input  in_10,
  input  in_11,
  input  in_12,
  input  b4,
  input  b3,
  input  b2,
  input  b1,
  input  in_17,
  input  in_18,
  input  in_19,
  input  in_20,
  input  in_21,
  input  in_22,
  input  in_23,
  input  in_24,
  input  in_25,
  input  in_26,
  input  in_27,
  input  in_28,
  input  in_29,
  input  in_30,
  input  in_31,
  input  in_32,
  input  in_33,
  input  in_34,
  input  in_35,
  input  in_36,
  input  in_37,
  input  in_38,
  input  in_39,
  input  in_40,
  input  in_41,
  input  in_42,
  input  in_43,
  input  in_44,
  input  in_45,
  input  in_46,
  input  in_47,
  input  in_48,
  input  in_49,
  input  in_50,
  input  in_51,
  input  in_52,
  input  in_53,
  output out_54,
  output out_55,
  output out_56,
  output out_57,
  output out_58,
  output out_59,
  output out_60,
  output [7:0] out_61,
  output q4,
  output out_63,
  output [7:0] out_64,
  output [7:0] out_65,
  output q3,
  output [7:0] out_67,
  output out_68,
  output out_69,
  output out_70,
  output out_71,
  output out_72,
  output out_73,
  output out_74,
  output [7:0] out_75,
  output [7:0] out_76,
  output [7:0] remainder,
  output q2,
  output out_79,
  output out_80,
  output out_81,
  output out_82,
  output out_83,
  output out_84,
  output [7:0] out_85,
  output [7:0] out_86,
  output [7:0] out_87,
  output q1,
  output out_89,
  output out_90,
  output out_91,
  output out_92,
  output out_93,
  output [7:0] out_94,
  output [7:0] out_95,
  output [7:0] remainder_2,
  output q4_2,
  output out_98,
  output out_99,
  output out_100,
  output out_101,
  output [7:0] remainder_3,
  output [7:0] out_103,
  output [7:0] out_104,
  output q4_3,
  output out_106,
  output out_107,
  output out_108,
  output [7:0] out_109,
  output q4_4,
  output out_111,
  output out_112,
  output [7:0] out_113,
  output q4_5,
  output out_115
);

  wire [7:0] and_6_out, and_7_out;

  assign out_64 = {in_9, in_10, in_11, in_12, b4, b3, b2, b1} & out_61;  // AND_Gate and_1, 8 bits wide
  assign out_75 = out_64 & out_65;  // AND_Gate and_2, 8 bits wide
  assign out_85 = out_75 & remainder;  // AND_Gate and_3, 8 bits wide
  assign out_94 = out_85 & out_87;  // AND_Gate and_4, 8 bits wide
  assign remainder_3 = out_94 & remainder_2;  // AND_Gate and_5, 8 bits wide
  assign and_6_out = remainder_3 & out_104;  // AND_Gate and_6, 8 bits wide
  assign and_7_out = and_6_out & out_109;  // AND_Gate and_7, 8 bits wide
  Subtractor subtractor_1 (
    .a({in_9, in_10, in_11, in_12, b4, b3, b2, b1}), .b({a4, a3, a2, a1, in_5, in_6, in_7, in_8}),
    .out(out_61), .bin(in_17), .bout(out_63));
  Subtractor subtractor_2 (
    .a(out_64), .b({in_18, a4, a3, a2, a1, in_5, in_6, in_7}), .out(out_65), .bin(in_19), .bout(out_68));
  Subtractor subtractor_3 (
    .a(out_75), .b({in_21, in_22, a4, a3, a2, a1, in_5, in_6}), .out(remainder), .bin(in_23), .bout(out_79));
  Subtractor subtractor_4 (
    .a(out_85), .b({in_24, in_25, in_26, a4, a3, a2, a1, in_5}), .out(out_87), .bin(in_27), .bout(out_89));
  Subtractor subtractor_5 (
    .a(out_94), .b({in_28, in_29, in_30, in_31, a4, a3, a2, a1}), .out(remainder_2), .bin(in_32),
    .bout(out_98));
  Subtractor subtractor_6 (
    .a(remainder_3), .b({in_33, in_34, in_35, in_36, in_37, a4, a3, a2}), .out(out_104), .bin(in_38),
    .bout(out_106));
  Subtractor subtractor_7 (
    .a(and_6_out), .b({in_39, in_40, in_41, in_42, in_43, in_44, a4, a3}), .out(out_109), .bin(in_45),
    .bout(out_111));
  Subtractor subtractor_8 (
    .a(and_7_out), .b({in_47, in_48, in_49, in_50, in_51, in_52, in_53, a4}), .out(out_113), .bin(in_46),
    .bout(out_115));
  not not_1 (q4, out_63);
  not not_2 (q3, out_68);
  not not_3 (q2, out_79);
  not not_4 (q1, out_89);
  not not_5 (q4_2, out_98);
  not not_6 (q4_3, out_106);
  not not_7 (q4_4, out_111);
  not not_8 (q4_5, out_115);

  assign out_54 = a4;
  assign out_55 = a3;
  assign out_56 = a2;
  assign out_57 = a1;
  assign out_58 = in_5;
  assign out_59 = in_6;
  assign out_60 = in_7;
  assign out_67 = {in_18, a4, a3, a2, a1, in_5, in_6, in_7};
  assign out_69 = a4;
  assign out_70 = a3;
  assign out_71 = a2;
  assign out_72 = a1;
  assign out_73 = in_5;
  assign out_74 = in_6;
  assign out_76 = {in_21, in_22, a4, a3, a2, a1, in_5, in_6};
  assign out_80 = a4;
  assign out_81 = a3;
  assign out_82 = a2;
  assign out_83 = a1;
  assign out_84 = in_5;
  assign out_86 = {in_24, in_25, in_26, a4, a3, a2, a1, in_5};
  assign out_90 = a4;
  assign out_91 = a3;
  assign out_92 = a2;
  assign out_93 = a1;
  assign out_95 = {in_28, in_29, in_30, in_31, a4, a3, a2, a1};
  assign out_99 = a4;
  assign out_100 = a3;
  assign out_101 = a2;
  assign out_103 = {in_33, in_34, in_35, in_36, in_37, a4, a3, a2};
  assign out_107 = a4;
  assign out_108 = a3;
  assign out_112 = a4;

  // Notes on the sheet:
  //   divisor
  //   dividend
  //   remainder
  //   remainder
  //   remainder
endmodule

module testMuxForDiv (
  input  [7:0] in_1,
  input  [7:0] in_2,
  input  in_3,
  output [7:0] out_4
);

  Multiplexer #(.width(8)) multiplexer_1 (.in0(in_1), .in1(in_2), .out(out_4), .sel(in_3));  // open: en
endmodule

module Div4withMux (
  input  a4,
  input  a3,
  input  a2,
  input  a1,
  input  in_5,
  input  in_6,
  input  in_7,
  input  in_8,
  input  in_9,
  input  in_10,
  input  in_11,
  input  in_12,
  input  b4,
  input  b3,
  input  b2,
  input  b1,
  input  in_17,
  input  in_18,
  input  in_19,
  input  in_20,
  input  in_21,
  input  in_22,
  input  in_23,
  input  in_24,
  input  in_25,
  input  in_26,
  input  in_27,
  input  in_28,
  input  in_29,
  input  in_30,
  input  in_31,
  input  in_32,
  input  in_33,
  input  in_34,
  input  in_35,
  input  in_36,
  input  in_37,
  input  in_38,
  input  in_39,
  input  in_40,
  input  in_41,
  input  in_42,
  input  in_43,
  input  in_44,
  input  in_45,
  input  in_46,
  input  in_47,
  input  in_48,
  input  in_49,
  input  in_50,
  input  in_51,
  input  in_52,
  input  in_53,
  output out_54,
  output out_55,
  output out_56,
  output out_57,
  output out_58,
  output out_59,
  output out_60,
  output [7:0] out_61,
  output q4,
  output out_63,
  output out_64,
  output [7:0] out_65,
  output out_66,
  output [7:0] out_67,
  output [7:0] out_68,
  output q3,
  output [7:0] out_70,
  output out_71,
  output out_72,
  output out_73,
  output out_74,
  output out_75,
  output out_76,
  output out_77,
  output out_78,
  output out_79,
  output [7:0] out_80,
  output [7:0] out_81,
  output [7:0] out_82,
  output [7:0] remainder,
  output q2,
  output out_85,
  output out_86,
  output out_87,
  output out_88,
  output out_89,
  output out_90,
  output out_91,
  output out_92,
  output [7:0] out_93,
  output [7:0] out_94,
  output [7:0] out_95,
  output q1,
  output out_97,
  output out_98,
  output out_99,
  output out_100,
  output out_101,
  output out_102,
  output out_103,
  output [7:0] out_104,
  output [7:0] out_105,
  output [7:0] remainder_2,
  output q4_2,
  output out_108,
  output out_109,
  output out_110,
  output out_111,
  output out_112,
  output out_113,
  output [7:0] remainder_3,
  output [7:0] out_115,
  output [7:0] out_116,
  output q4_3,
  output out_118,
  output out_119,
  output out_120,
  output out_121,
  output [7:0] out_122,
  output [7:0] out_123,
  output q4_4,
  output out_125,
  output out_126,
  output out_127,
  output [7:0] out_128,
  output q4_5,
  output out_130,
  output out_131
);

  wire or_5_out, or_6_out, or_8_out;
  wire [7:0] testmuxfordiv_5_out_4;

  testMuxForDiv testmuxfordiv_1 (.in_1(remainder), .in_2(out_80), .in_3(out_85), .out_4(out_93));
  testMuxForDiv testmuxfordiv_2 (.in_1(out_95), .in_2(out_93), .in_3(out_97), .out_4(out_104));
  testMuxForDiv testmuxfordiv_3 (.in_1(remainder_2), .in_2(out_104), .in_3(out_108), .out_4(remainder_3));
  testMuxForDiv testmuxfordiv_4 (.in_1(out_116), .in_2(remainder_3), .in_3(out_118), .out_4(out_122));
  testMuxForDiv testmuxfordiv_5 (.in_1(out_123), .in_2(out_122), .in_3(out_125), .out_4(testmuxfordiv_5_out_4));
  testMuxForDiv testmuxfordiv_6 (
    .in_1(out_61), .in_2({in_9, in_10, in_11, in_12, b4, b3, b2, b1}), .in_3(out_63), .out_4(out_65));
  testMuxForDiv testmuxfordiv_7 (.in_1(out_68), .in_2(out_65), .in_3(out_71), .out_4(out_80));
  Subtractor subtractor_1 (
    .a({in_9, in_10, in_11, in_12, b4, b3, b2, b1}), .b({a4, a3, a2, a1, in_5, in_6, in_7, in_8}),
    .out(out_61), .bin(in_17), .bout(out_63));
  Subtractor subtractor_2 (
    .a(out_65), .b({in_18, a4, a3, a2, a1, in_5, in_6, in_7}), .out(out_68), .bin(in_19), .bout(out_71));
  Subtractor subtractor_3 (
    .a(out_80), .b({in_21, in_22, a4, a3, a2, a1, in_5, in_6}), .out(remainder), .bin(in_23), .bout(out_85));
  Subtractor subtractor_4 (
    .a(out_93), .b({in_24, in_25, in_26, a4, a3, a2, a1, in_5}), .out(out_95), .bin(in_27), .bout(out_97));
  Subtractor subtractor_5 (
    .a(out_104), .b({in_28, in_29, in_30, in_31, a4, a3, a2, a1}), .out(remainder_2), .bin(in_32),
    .bout(out_108));
  Subtractor subtractor_6 (
    .a(remainder_3), .b({in_33, in_34, in_35, in_36, in_37, a4, a3, a2}), .out(out_116), .bin(in_38),
    .bout(out_118));
  Subtractor subtractor_7 (
    .a(out_122), .b({in_39, in_40, in_41, in_42, in_43, in_44, a4, a3}), .out(out_123), .bin(in_45),
    .bout(out_125));
  Subtractor subtractor_8 (
    .a(testmuxfordiv_5_out_4), .b({in_47, in_48, in_49, in_50, in_51, in_52, in_53, a4}), .out(out_128),
    .bin(in_46), .bout(out_130));
  not not_1 (q4, out_63);
  not not_2 (q3, out_71);
  not not_3 (q2, out_85);
  not not_4 (q1, out_97);
  not not_5 (q4_2, out_108);
  not not_6 (q4_3, out_118);
  not not_7 (q4_4, out_125);
  not not_8 (q4_5, out_130);
  or or_1 (out_64, out_61[0], out_61[1], out_61[2], out_61[3], out_61[5], out_61[6], out_61[7]);
  or or_2 (out_72, out_68[0], out_68[1], out_68[2], out_68[3], out_68[5], out_68[6], out_68[7]);
  or or_3 (out_86, remainder[0], remainder[1], remainder[2], remainder[3], remainder[5], remainder[6], remainder[7]);
  or or_4 (out_98, out_95[0], out_95[1], out_95[2], out_95[3], out_95[5], out_95[6], out_95[7]);
  or or_5 (or_5_out, out_116[0], out_116[1], out_116[2], out_116[4], out_116[5], out_116[6], out_116[7]);
  or or_6 (or_6_out, out_128[0], out_128[1], out_128[2], out_128[4], out_128[5], out_128[6], out_128[7]);
  or or_7 (out_109, remainder_2[0], remainder_2[1], remainder_2[2], remainder_2[3], remainder_2[5], remainder_2[6], remainder_2[7]);
  and and_1 (out_119, or_5_out, q4_3);
  or or_8 (or_8_out, out_123[0], out_123[1], out_123[2], out_123[4], out_123[5], out_123[6], out_123[7]);
  and and_2 (out_66, out_64, q4);
  and and_3 (out_79, out_72, q3);
  and and_4 (out_92, out_86, q2);
  and and_5 (out_103, out_98, q1);
  and and_6 (out_113, out_109, q4_2);
  and and_7 (out_126, or_8_out, q4_4);
  and and_8 (out_131, or_6_out, q4_5);

  assign out_54 = a4;
  assign out_55 = a3;
  assign out_56 = a2;
  assign out_57 = a1;
  assign out_58 = in_5;
  assign out_59 = in_6;
  assign out_60 = in_7;
  assign out_67 = out_65;
  assign out_70 = {in_18, a4, a3, a2, a1, in_5, in_6, in_7};
  assign out_73 = a4;
  assign out_74 = a3;
  assign out_75 = a2;
  assign out_76 = a1;
  assign out_77 = in_5;
  assign out_78 = in_6;
  assign out_81 = out_80;
  assign out_82 = {in_21, in_22, a4, a3, a2, a1, in_5, in_6};
  assign out_87 = a4;
  assign out_88 = a3;
  assign out_89 = a2;
  assign out_90 = a1;
  assign out_91 = in_5;
  assign out_94 = {in_24, in_25, in_26, a4, a3, a2, a1, in_5};
  assign out_99 = a4;
  assign out_100 = a3;
  assign out_101 = a2;
  assign out_102 = a1;
  assign out_105 = {in_28, in_29, in_30, in_31, a4, a3, a2, a1};
  assign out_110 = a4;
  assign out_111 = a3;
  assign out_112 = a2;
  assign out_115 = {in_33, in_34, in_35, in_36, in_37, a4, a3, a2};
  assign out_120 = a4;
  assign out_121 = a3;
  assign out_127 = a4;

  // Notes on the sheet:
  //   divisor
  //   dividend
  //   remainder
  //   remainder
  //   remainder
endmodule

module Div8BitWithMux (
  input  A1,
  input  a2,
  input  a3,
  input  a4,
  input  a5,
  input  a6,
  input  a7,
  input  a8,
  input  A1_2,
  input  a2_2,
  input  a3_2,
  input  a4_2,
  input  a5_2,
  input  a6_2,
  input  a7_2,
  input  a8_2,
  output out_17,
  output [15:0] out_18,
  output [15:0] out_19,
  output [15:0] out_20,
  output out_21,
  output [15:0] out_22,
  output out_23,
  output [15:0] out_24,
  output [15:0] out_25,
  output out_26,
  output [15:0] out_27,
  output [15:0] out_28,
  output out_29,
  output [15:0] out_30,
  output [15:0] out_31,
  output out_32,
  output [15:0] out_33,
  output [15:0] out_34,
  output [15:0] out_35,
  output out_36,
  output [15:0] out_37,
  output [15:0] out_38,
  output out_39,
  output [15:0] out_40,
  output [15:0] out_41,
  output out_42,
  output [15:0] out_43,
  output [15:0] out_44,
  output out_45,
  output [15:0] out_46,
  output [15:0] out_47,
  output out_48,
  output [15:0] out_49,
  output [15:0] out_50,
  output out_51,
  output [15:0] out_52,
  output [15:0] out_53,
  output out_54,
  output [15:0] out_55,
  output [15:0] out_56,
  output out_57,
  output [15:0] out_58,
  output [15:0] out_59,
  output out_60,
  output [15:0] out_61,
  output [15:0] out_62,
  output out_63
);

  wire not_137_out, not_138_out, not_139_out, not_140_out, not_141_out, not_142_out, not_143_out,
       not_144_out, not_145_out, not_146_out, not_147_out, not_148_out, not_149_out, not_150_out,
       not_151_out, not_152_out, not_153_out, not_154_out, not_155_out, not_156_out, not_157_out,
       not_158_out, not_159_out, not_160_out, not_161_out, not_162_out, not_163_out, not_164_out,
       not_165_out, not_166_out, not_167_out, not_168_out, or_1_out, or_2_out, or_3_out, or_4_out, or_5_out,
       or_6_out, or_7_out, or_8_out, or_9_out, or_10_out, or_11_out, or_12_out, or_13_out, or_14_out,
       or_15_out, or_16_out, subtractor_1_bout, subtractor_2_bout, subtractor_3_bout, subtractor_4_bout,
       subtractor_5_bout, subtractor_6_bout, subtractor_7_bout, subtractor_8_bout, subtractor_9_bout,
       subtractor_10_bout, subtractor_11_bout, subtractor_12_bout, subtractor_13_bout, subtractor_14_bout,
       subtractor_15_bout, subtractor_16_bout;
  wire [15:0] subtractor_1_out, subtractor_2_out, subtractor_3_out, subtractor_4_out, subtractor_5_out,
       subtractor_6_out, subtractor_7_out, subtractor_8_out, subtractor_9_out, subtractor_10_out,
       subtractor_11_out, subtractor_12_out, subtractor_13_out, subtractor_14_out, subtractor_15_out,
       subtractor_16_out;
  wire [15:8] not_135_out;

  not not_1 (out_30[12], 1'b1);
  not not_2 (out_30[14], 1'b1);
  not not_3 (out_33[12], 1'b1);
  not not_4 (out_33[14], 1'b1);
  not not_5 (out_35[10], 1'b1);
  not not_6 (out_35[12], 1'b1);
  not not_7 (out_35[14], 1'b1);
  not not_8 (out_38[12], 1'b1);
  not not_9 (out_38[14], 1'b1);
  not not_10 (out_41[12], 1'b1);
  not not_11 (out_41[14], 1'b1);
  not not_12 (out_44[12], 1'b1);
  not not_13 (out_44[14], 1'b1);
  not not_14 (out_47[8], 1'b1);
  not not_15 (out_47[10], 1'b1);
  not not_16 (out_47[12], 1'b1);
  not not_17 (out_47[14], 1'b1);
  not not_18 (out_50[8], 1'b1);
  not not_19 (out_50[10], 1'b1);
  not not_20 (out_50[12], 1'b1);
  not not_21 (out_50[14], 1'b1);
  not not_22 (out_53[8], 1'b1);
  not not_23 (out_53[10], 1'b1);
  not not_24 (out_53[12], 1'b1);
  not not_25 (out_53[14], 1'b1);
  not not_26 (out_56[8], 1'b1);
  not not_27 (out_56[10], 1'b1);
  not not_28 (out_56[12], 1'b1);
  not not_29 (out_56[14], 1'b1);
  not not_30 (out_59[8], 1'b1);
  not not_31 (out_59[10], 1'b1);
  not not_32 (out_59[12], 1'b1);
  not not_33 (out_59[14], 1'b1);
  not not_34 (out_62[8], 1'b1);
  not not_35 (out_62[10], 1'b1);
  not not_36 (out_62[12], 1'b1);
  not not_37 (out_62[14], 1'b1);
  not not_38 (out_24[14], 1'b1);
  not not_39 (out_27[14], 1'b1);
  not not_40 (out_27[15], 1'b1);
  not not_41 (out_30[13], 1'b1);
  not not_42 (out_30[15], 1'b1);
  not not_43 (out_33[11], 1'b1);
  not not_44 (out_33[13], 1'b1);
  not not_45 (out_33[15], 1'b1);
  not not_46 (out_35[11], 1'b1);
  not not_47 (out_35[13], 1'b1);
  not not_48 (out_35[15], 1'b1);
  not not_49 (out_38[9], 1'b1);
  not not_50 (out_38[10], 1'b1);
  not not_51 (out_38[11], 1'b1);
  not not_52 (out_38[13], 1'b1);
  not not_53 (out_38[15], 1'b1);
  not not_54 (out_41[8], 1'b1);
  not not_55 (out_41[9], 1'b1);
  not not_56 (out_41[10], 1'b1);
  not not_57 (out_41[11], 1'b1);
  not not_58 (out_41[13], 1'b1);
  not not_59 (out_41[15], 1'b1);
  not not_60 (out_44[7], 1'b1);
  not not_61 (out_44[8], 1'b1);
  not not_62 (out_44[9], 1'b1);
  not not_63 (out_44[10], 1'b1);
  not not_64 (out_44[11], 1'b1);
  not not_65 (out_44[13], 1'b1);
  not not_66 (out_44[15], 1'b1);
  not not_67 (out_47[6], 1'b1);
  not not_68 (out_47[7], 1'b1);
  not not_69 (out_47[9], 1'b1);
  not not_70 (out_47[11], 1'b1);
  not not_71 (out_47[13], 1'b1);
  not not_72 (out_47[15], 1'b1);
  not not_73 (out_50[5], 1'b1);
  not not_74 (out_50[6], 1'b1);
  not not_75 (out_50[7], 1'b1);
  not not_76 (out_50[9], 1'b1);
  not not_77 (out_50[11], 1'b1);
  not not_78 (out_50[13], 1'b1);
  not not_79 (out_50[15], 1'b1);
  not not_80 (out_53[4], 1'b1);
  not not_81 (out_53[5], 1'b1);
  not not_82 (out_53[6], 1'b1);
  not not_83 (out_53[7], 1'b1);
  not not_84 (out_53[9], 1'b1);
  not not_85 (out_53[11], 1'b1);
  not not_86 (out_53[13], 1'b1);
  not not_87 (out_53[15], 1'b1);
  not not_88 (out_56[3], 1'b1);
  not not_89 (out_56[4], 1'b1);
  not not_90 (out_56[5], 1'b1);
  not not_91 (out_56[6], 1'b1);
  not not_92 (out_56[7], 1'b1);
  not not_93 (out_56[9], 1'b1);
  not not_94 (out_56[11], 1'b1);
  not not_95 (out_56[13], 1'b1);
  not not_96 (out_56[15], 1'b1);
  not not_97 (out_59[2], 1'b1);
  not not_98 (out_59[3], 1'b1);
  not not_99 (out_59[4], 1'b1);
  not not_100 (out_59[5], 1'b1);
  not not_101 (out_59[6], 1'b1);
  not not_102 (out_59[7], 1'b1);
  not not_103 (out_59[9], 1'b1);
  not not_104 (out_59[11], 1'b1);
  not not_105 (out_59[13], 1'b1);
  not not_106 (out_59[15], 1'b1);
  not not_107 (out_62[1], 1'b1);
  not not_108 (out_62[2], 1'b1);
  not not_109 (out_62[3], 1'b1);
  not not_110 (out_62[4], 1'b1);
  not not_111 (out_62[5], 1'b1);
  not not_112 (out_62[6], 1'b1);
  not not_113 (out_62[7], 1'b1);
  not not_114 (out_62[9], 1'b1);
  not not_115 (out_62[11], 1'b1);
  not not_116 (out_62[13], 1'b1);
  not not_117 (out_62[15], 1'b1);
  not not_118 (out_20[15], 1'b1);
  not not_119 (out_24[15], 1'b1);
  not not_120 (out_27[13], 1'b1);
  not not_121 (out_18[7], 1'b1);
  not not_122 (out_18[6], 1'b1);
  not not_123 (out_18[4], 1'b1);
  not not_124 (out_18[5], 1'b1);
  not not_125 (out_18[2], 1'b1);
  not not_126 (out_18[0], 1'b1);
  not not_127 (out_18[1], 1'b1);
  not not_128 (out_18[3], 1'b1);
  not not_129 (not_135_out[15], 1'b1);
  not not_130 (not_135_out[12], 1'b1);
  not not_131 (not_135_out[13], 1'b1);
  not not_132 (not_135_out[11], 1'b1);
  not not_133 (not_135_out[14], 1'b1);
  MuxFor8BitDivision muxfor8bitdivision_1 (
    .in_1(subtractor_1_out), .in_2({not_135_out, a8_2, a7_2, a6_2, a5_2, a4_2, a3_2, a2_2, A1_2}),
    .in_3(subtractor_1_bout), .out_4(out_19));
  MuxFor8BitDivision muxfor8bitdivision_2 (
    .in_1(subtractor_2_out), .in_2(out_19), .in_3(subtractor_2_bout), .out_4(out_22));
  MuxFor8BitDivision muxfor8bitdivision_3 (
    .in_1(subtractor_3_out), .in_2(out_22), .in_3(subtractor_3_bout), .out_4(out_25));
  MuxFor8BitDivision muxfor8bitdivision_4 (
    .in_1(subtractor_4_out), .in_2(out_25), .in_3(subtractor_4_bout), .out_4(out_28));
  MuxFor8BitDivision muxfor8bitdivision_5 (
    .in_1(subtractor_5_out), .in_2(out_28), .in_3(subtractor_5_bout), .out_4(out_31));
  MuxFor8BitDivision muxfor8bitdivision_6 (
    .in_1(subtractor_6_out), .in_2(out_31), .in_3(subtractor_6_bout), .out_4(out_34));
  MuxFor8BitDivision muxfor8bitdivision_7 (
    .in_1(subtractor_7_out), .in_2(out_34), .in_3(subtractor_7_bout), .out_4(out_37));
  MuxFor8BitDivision muxfor8bitdivision_8 (
    .in_1(subtractor_8_out), .in_2(out_37), .in_3(subtractor_8_bout), .out_4(out_40));
  MuxFor8BitDivision muxfor8bitdivision_9 (
    .in_1(subtractor_9_out), .in_2(out_40), .in_3(subtractor_9_bout), .out_4(out_43));
  MuxFor8BitDivision muxfor8bitdivision_10 (
    .in_1(subtractor_10_out), .in_2(out_43), .in_3(subtractor_10_bout), .out_4(out_46));
  MuxFor8BitDivision muxfor8bitdivision_11 (
    .in_1(subtractor_11_out), .in_2(out_46), .in_3(subtractor_11_bout), .out_4(out_49));
  MuxFor8BitDivision muxfor8bitdivision_12 (
    .in_1(subtractor_12_out), .in_2(out_49), .in_3(subtractor_12_bout), .out_4(out_52));
  MuxFor8BitDivision muxfor8bitdivision_13 (
    .in_1(subtractor_13_out), .in_2(out_52), .in_3(subtractor_13_bout), .out_4(out_55));
  MuxFor8BitDivision muxfor8bitdivision_14 (
    .in_1(subtractor_14_out), .in_2(out_55), .in_3(subtractor_14_bout), .out_4(out_58));
  MuxFor8BitDivision muxfor8bitdivision_15 (
    .in_1(subtractor_15_out), .in_2(out_58), .in_3(subtractor_15_bout), .out_4(out_61));
  not not_134 (not_135_out[10], 1'b1);
  not not_135 (not_135_out[8], 1'b1);
  not not_136 (not_135_out[9], 1'b1);
  not not_137 (not_137_out, 1'b1);
  LED led_1 (.in(subtractor_1_bout));
  Subtractor #(.width(16)) subtractor_1 (
    .a({not_135_out, a8_2, a7_2, a6_2, a5_2, a4_2, a3_2, a2_2, A1_2}),
    .b({a8, a7, a6, a5, a4, a3, a2, A1, out_18[7:0]}), .out(subtractor_1_out), .bin(not_137_out),
    .bout(subtractor_1_bout));
  not not_138 (not_138_out, 1'b1);
  Subtractor #(.width(16)) subtractor_2 (
    .a(out_19), .b({out_20[15], a8, a7, a6, a5, a4, a3, a2, A1, out_18[7:1]}), .out(subtractor_2_out),
    .bin(not_138_out), .bout(subtractor_2_bout));
  LED led_2 (.in(subtractor_2_bout));
  not not_139 (not_139_out, 1'b1);
  Subtractor #(.width(16)) subtractor_3 (
    .a(out_22), .b({out_24[15:14], a8, a7, a6, a5, a4, a3, a2, A1, out_18[7:2]}), .out(subtractor_3_out),
    .bin(not_139_out), .bout(subtractor_3_bout));
  LED led_3 (.in(subtractor_3_bout));
  not not_140 (not_140_out, 1'b1);
  Subtractor #(.width(16)) subtractor_4 (
    .a(out_25), .b({out_27[15:13], a8, a7, a6, a5, a4, a3, a2, A1, out_18[7:3]}), .out(subtractor_4_out),
    .bin(not_140_out), .bout(subtractor_4_bout));
  LED led_4 (.in(subtractor_4_bout));
  not not_141 (not_141_out, 1'b1);
  Subtractor #(.width(16)) subtractor_5 (
    .a(out_28), .b({out_30[15:12], a8, a7, a6, a5, a4, a3, a2, A1, out_18[7:4]}), .out(subtractor_5_out),
    .bin(not_141_out), .bout(subtractor_5_bout));
  LED led_5 (.in(subtractor_5_bout));
  not not_142 (not_142_out, 1'b1);
  Subtractor #(.width(16)) subtractor_6 (
    .a(out_31), .b({out_33[15:11], a8, a7, a6, a5, a4, a3, a2, A1, out_18[7:5]}), .out(subtractor_6_out),
    .bin(not_142_out), .bout(subtractor_6_bout));
  LED led_6 (.in(subtractor_6_bout));
  not not_143 (not_143_out, 1'b1);
  Subtractor #(.width(16)) subtractor_7 (
    .a(out_34), .b({out_35[15:10], a8, a7, a6, a5, a4, a3, a2, A1, out_18[7:6]}), .out(subtractor_7_out),
    .bin(not_143_out), .bout(subtractor_7_bout));
  LED led_7 (.in(subtractor_7_bout));
  not not_144 (not_144_out, 1'b1);
  Subtractor #(.width(16)) subtractor_8 (
    .a(out_37), .b({out_38[15:9], a8, a7, a6, a5, a4, a3, a2, A1, out_18[7]}), .out(subtractor_8_out),
    .bin(not_144_out), .bout(subtractor_8_bout));
  LED led_8 (.in(subtractor_8_bout));
  not not_145 (not_145_out, 1'b1);
  Subtractor #(.width(16)) subtractor_9 (
    .a(out_40), .b({out_41[15:8], a8, a7, a6, a5, a4, a3, a2, A1}), .out(subtractor_9_out),
    .bin(not_145_out), .bout(subtractor_9_bout));
  LED led_9 (.in(subtractor_9_bout));
  not not_146 (not_146_out, 1'b1);
  Subtractor #(.width(16)) subtractor_10 (
    .a(out_43), .b({out_44[15:7], a8, a7, a6, a5, a4, a3, a2}), .out(subtractor_10_out), .bin(not_146_out),
    .bout(subtractor_10_bout));
  LED led_10 (.in(subtractor_10_bout));
  not not_147 (not_147_out, 1'b1);
  Subtractor #(.width(16)) subtractor_11 (
    .a(out_46), .b({out_47[15:6], a8, a7, a6, a5, a4, a3}), .out(subtractor_11_out), .bin(not_147_out),
    .bout(subtractor_11_bout));
  LED led_11 (.in(subtractor_11_bout));
  not not_148 (not_148_out, 1'b1);
  Subtractor #(.width(16)) subtractor_12 (
    .a(out_49), .b({out_50[15:5], a8, a7, a6, a5, a4}), .out(subtractor_12_out), .bin(not_148_out),
    .bout(subtractor_12_bout));
  LED led_12 (.in(subtractor_12_bout));
  not not_149 (not_149_out, 1'b1);
  Subtractor #(.width(16)) subtractor_13 (
    .a(out_52), .b({out_53[15:4], a8, a7, a6, a5}), .out(subtractor_13_out), .bin(not_149_out),
    .bout(subtractor_13_bout));
  LED led_13 (.in(subtractor_13_bout));
  not not_150 (not_150_out, 1'b1);
  Subtractor #(.width(16)) subtractor_14 (
    .a(out_55), .b({out_56[15:3], a8, a7, a6}), .out(subtractor_14_out), .bin(not_150_out),
    .bout(subtractor_14_bout));
  LED led_14 (.in(subtractor_14_bout));
  not not_151 (not_151_out, 1'b1);
  Subtractor #(.width(16)) subtractor_15 (
    .a(out_58), .b({out_59[15:2], a8, a7}), .out(subtractor_15_out), .bin(not_151_out),
    .bout(subtractor_15_bout));
  LED led_15 (.in(subtractor_15_bout));
  not not_152 (not_152_out, 1'b1);
  LED led_16 (.in(subtractor_16_bout));
  or or_1 (or_1_out, subtractor_1_out[0], subtractor_1_out[1], subtractor_1_out[2], subtractor_1_out[3], subtractor_1_out[4], subtractor_1_out[5], subtractor_1_out[6], subtractor_1_out[7], subtractor_1_out[9], subtractor_1_out[10], subtractor_1_out[11], subtractor_1_out[12], subtractor_1_out[13], subtractor_1_out[14], subtractor_1_out[15]);
  not not_153 (not_153_out, subtractor_1_bout);
  or or_2 (or_2_out, subtractor_2_out[0], subtractor_2_out[1], subtractor_2_out[2], subtractor_2_out[3], subtractor_2_out[4], subtractor_2_out[5], subtractor_2_out[6], subtractor_2_out[7], subtractor_2_out[9], subtractor_2_out[10], subtractor_2_out[11], subtractor_2_out[12], subtractor_2_out[13], subtractor_2_out[14], subtractor_2_out[15]);
  not not_154 (not_154_out, subtractor_2_bout);
  or or_3 (or_3_out, subtractor_3_out[0], subtractor_3_out[1], subtractor_3_out[2], subtractor_3_out[3], subtractor_3_out[4], subtractor_3_out[5], subtractor_3_out[6], subtractor_3_out[7], subtractor_3_out[9], subtractor_3_out[10], subtractor_3_out[11], subtractor_3_out[12], subtractor_3_out[13], subtractor_3_out[14], subtractor_3_out[15]);
  not not_155 (not_155_out, subtractor_3_bout);
  or or_4 (or_4_out, subtractor_4_out[0], subtractor_4_out[1], subtractor_4_out[2], subtractor_4_out[3], subtractor_4_out[4], subtractor_4_out[5], subtractor_4_out[6], subtractor_4_out[7], subtractor_4_out[9], subtractor_4_out[10], subtractor_4_out[11], subtractor_4_out[12], subtractor_4_out[13], subtractor_4_out[14], subtractor_4_out[15]);
  not not_156 (not_156_out, subtractor_4_bout);
  not not_157 (not_157_out, subtractor_5_bout);
  not not_158 (not_158_out, subtractor_6_bout);
  not not_159 (not_159_out, subtractor_7_bout);
  Subtractor #(.width(16)) subtractor_16 (
    .a(out_61), .b({out_62[15:1], a8}), .out(subtractor_16_out), .bin(not_152_out), .bout(subtractor_16_bout));
  and and_1 (out_17, or_1_out, not_153_out);
  and and_2 (out_21, or_2_out, not_154_out);
  and and_3 (out_23, or_3_out, not_155_out);
  and and_4 (out_26, or_4_out, not_156_out);
  or or_5 (or_5_out, subtractor_5_out[0], subtractor_5_out[1], subtractor_5_out[2], subtractor_5_out[3], subtractor_5_out[4], subtractor_5_out[5], subtractor_5_out[6], subtractor_5_out[7], subtractor_5_out[9], subtractor_5_out[10], subtractor_5_out[11], subtractor_5_out[12], subtractor_5_out[13], subtractor_5_out[14], subtractor_5_out[15]);
  and and_5 (out_29, or_5_out, not_157_out);
  or or_6 (or_6_out, subtractor_6_out[0], subtractor_6_out[1], subtractor_6_out[2], subtractor_6_out[3], subtractor_6_out[4], subtractor_6_out[5], subtractor_6_out[6], subtractor_6_out[7], subtractor_6_out[9], subtractor_6_out[10], subtractor_6_out[11], subtractor_6_out[12], subtractor_6_out[13], subtractor_6_out[14], subtractor_6_out[15]);
  and and_6 (out_32, or_6_out, not_158_out);
  or or_7 (or_7_out, subtractor_7_out[0], subtractor_7_out[1], subtractor_7_out[2], subtractor_7_out[3], subtractor_7_out[4], subtractor_7_out[5], subtractor_7_out[6], subtractor_7_out[7], subtractor_7_out[9], subtractor_7_out[10], subtractor_7_out[11], subtractor_7_out[12], subtractor_7_out[13], subtractor_7_out[14], subtractor_7_out[15]);
  and and_7 (out_36, or_7_out, not_159_out);
  or or_8 (or_8_out, subtractor_8_out[0], subtractor_8_out[1], subtractor_8_out[2], subtractor_8_out[3], subtractor_8_out[4], subtractor_8_out[5], subtractor_8_out[6], subtractor_8_out[7], subtractor_8_out[9], subtractor_8_out[10], subtractor_8_out[11], subtractor_8_out[12], subtractor_8_out[13], subtractor_8_out[14], subtractor_8_out[15]);
  not not_160 (not_160_out, subtractor_8_bout);
  or or_9 (or_9_out, subtractor_9_out[0], subtractor_9_out[1], subtractor_9_out[2], subtractor_9_out[3], subtractor_9_out[4], subtractor_9_out[5], subtractor_9_out[6], subtractor_9_out[7], subtractor_9_out[9], subtractor_9_out[10], subtractor_9_out[11], subtractor_9_out[12], subtractor_9_out[13], subtractor_9_out[14], subtractor_9_out[15]);
  not not_161 (not_161_out, subtractor_9_bout);
  or or_10 (or_10_out, subtractor_10_out[0], subtractor_10_out[1], subtractor_10_out[2], subtractor_10_out[3], subtractor_10_out[4], subtractor_10_out[5], subtractor_10_out[6], subtractor_10_out[7], subtractor_10_out[9], subtractor_10_out[10], subtractor_10_out[11], subtractor_10_out[12], subtractor_10_out[13], subtractor_10_out[14], subtractor_10_out[15]);
  not not_162 (not_162_out, subtractor_10_bout);
  or or_11 (or_11_out, subtractor_11_out[0], subtractor_11_out[1], subtractor_11_out[2], subtractor_11_out[3], subtractor_11_out[4], subtractor_11_out[5], subtractor_11_out[6], subtractor_11_out[7], subtractor_11_out[9], subtractor_11_out[10], subtractor_11_out[11], subtractor_11_out[12], subtractor_11_out[13], subtractor_11_out[14], subtractor_11_out[15]);
  not not_163 (not_163_out, subtractor_11_bout);
  or or_12 (or_12_out, subtractor_12_out[0], subtractor_12_out[1], subtractor_12_out[2], subtractor_12_out[3], subtractor_12_out[4], subtractor_12_out[5], subtractor_12_out[6], subtractor_12_out[7], subtractor_12_out[9], subtractor_12_out[10], subtractor_12_out[11], subtractor_12_out[12], subtractor_12_out[13], subtractor_12_out[14], subtractor_12_out[15]);
  not not_164 (not_164_out, subtractor_12_bout);
  or or_13 (or_13_out, subtractor_13_out[0], subtractor_13_out[1], subtractor_13_out[2], subtractor_13_out[3], subtractor_13_out[4], subtractor_13_out[5], subtractor_13_out[6], subtractor_13_out[7], subtractor_13_out[9], subtractor_13_out[10], subtractor_13_out[11], subtractor_13_out[12], subtractor_13_out[13], subtractor_13_out[14], subtractor_13_out[15]);
  not not_165 (not_165_out, subtractor_13_bout);
  or or_14 (or_14_out, subtractor_14_out[0], subtractor_14_out[1], subtractor_14_out[2], subtractor_14_out[3], subtractor_14_out[4], subtractor_14_out[5], subtractor_14_out[6], subtractor_14_out[7], subtractor_14_out[9], subtractor_14_out[10], subtractor_14_out[11], subtractor_14_out[12], subtractor_14_out[13], subtractor_14_out[14], subtractor_14_out[15]);
  not not_166 (not_166_out, subtractor_14_bout);
  or or_15 (or_15_out, subtractor_15_out[0], subtractor_15_out[1], subtractor_15_out[2], subtractor_15_out[3], subtractor_15_out[4], subtractor_15_out[5], subtractor_15_out[6], subtractor_15_out[7], subtractor_15_out[9], subtractor_15_out[10], subtractor_15_out[11], subtractor_15_out[12], subtractor_15_out[13], subtractor_15_out[14], subtractor_15_out[15]);
  not not_167 (not_167_out, subtractor_15_bout);
  or or_16 (or_16_out, subtractor_16_out[0], subtractor_16_out[1], subtractor_16_out[2], subtractor_16_out[3], subtractor_16_out[4], subtractor_16_out[5], subtractor_16_out[6], subtractor_16_out[7], subtractor_16_out[9], subtractor_16_out[10], subtractor_16_out[11], subtractor_16_out[12], subtractor_16_out[13], subtractor_16_out[14], subtractor_16_out[15]);
  not not_168 (not_168_out, subtractor_16_bout);
  and and_8 (out_39, or_8_out, not_160_out);
  and and_9 (out_42, or_9_out, not_161_out);
  LED led_17 (.in(out_45));
  and and_10 (out_45, or_10_out, not_162_out);
  LED led_18 (.in(out_48));
  and and_11 (out_48, or_11_out, not_163_out);
  LED led_19 (.in(out_51));
  and and_12 (out_51, or_12_out, not_164_out);
  LED led_20 (.in(out_54));
  and and_13 (out_54, or_13_out, not_165_out);
  LED led_21 (.in(out_57));
  and and_14 (out_57, or_14_out, not_166_out);
  LED led_22 (.in(out_60));
  and and_15 (out_60, or_15_out, not_167_out);
  LED led_23 (.in(out_63));
  and and_16 (out_63, or_16_out, not_168_out);

  assign out_18[15:8] = {a8, a7, a6, a5, a4, a3, a2, A1};
  assign out_20[14:0] = {a8, a7, a6, a5, a4, a3, a2, A1, out_18[7:1]};
  assign out_24[13:0] = {a8, a7, a6, a5, a4, a3, a2, A1, out_18[7:2]};
  assign out_27[12:0] = {a8, a7, a6, a5, a4, a3, a2, A1, out_18[7:3]};
  assign out_30[11:0] = {a8, a7, a6, a5, a4, a3, a2, A1, out_18[7:4]};
  assign out_33[10:0] = {a8, a7, a6, a5, a4, a3, a2, A1, out_18[7:5]};
  assign out_35[9:0] = {a8, a7, a6, a5, a4, a3, a2, A1, out_18[7:6]};
  assign out_38[8:0] = {a8, a7, a6, a5, a4, a3, a2, A1, out_18[7]};
  assign out_41[7:0] = {a8, a7, a6, a5, a4, a3, a2, A1};
  assign out_44[6:0] = {a8, a7, a6, a5, a4, a3, a2};
  assign out_47[5:0] = {a8, a7, a6, a5, a4, a3};
  assign out_50[4:0] = {a8, a7, a6, a5, a4};
  assign out_53[3:0] = {a8, a7, a6, a5};
  assign out_56[2:0] = {a8, a7, a6};
  assign out_59[1:0] = {a8, a7};
  assign out_62[0] = a8;

  // Notes on the sheet:
  //   divisor
  //   Right Shift
  //   Left Shift
  //   dividend
endmodule

module MuxFor8BitDivision (
  input  [15:0] in_1,
  input  [15:0] in_2,
  input  in_3,
  output [15:0] out_4
);

  Multiplexer #(.width(16)) multiplexer_1 (.in0(in_1), .in1(in_2), .out(out_4), .sel(in_3));  // open: en
endmodule
module Div8BitForCircuitDesign (
  input  A1,
  input  a2,
  input  a3,
  input  a4,
  input  a5,
  input  a6,
  input  a7,
  input  a8,
  input  A1_2,
  input  a2_2,
  input  a3_2,
  input  a4_2,
  input  a5_2,
  input  a6_2,
  input  a7_2,
  input  a8_2,
  output [7:0] out_17,
  output [7:0] out_18,
  output [15:0] out_19,
  output [15:0] out_20,
  output [15:0] out_21,
  output [15:0] out_22,
  output [15:0] out_23,
  output [15:0] out_24,
  output [15:0] out_25,
  output [15:0] out_26,
  output [15:0] out_27,
  output [15:0] out_28,
  output [15:0] out_29,
  output [15:0] out_30,
  output [15:0] out_31,
  output [15:0] out_32,
  output [15:0] out_33,
  output [15:0] out_34,
  output out_35,
  output [15:0] out_36,
  output [15:0] out_37,
  output [15:0] out_38,
  output [15:0] out_39,
  output [15:0] out_40,
  output [15:0] out_41,
  output [15:0] out_42,
  output [15:0] out_43,
  output [15:0] out_44,
  output [15:0] out_45,
  output [15:0] out_46,
  output [15:0] out_47
);

  wire not_153_out, not_154_out, not_155_out, not_156_out, not_157_out, not_158_out, not_159_out,
       not_160_out, not_161_out, not_162_out, not_163_out, not_164_out, not_165_out, not_166_out,
       not_167_out, not_168_out, not_169_out, not_170_out, subtractor_1_bout, subtractor_2_bout,
       subtractor_3_bout, subtractor_4_bout, subtractor_5_bout, subtractor_6_bout, subtractor_7_bout,
       subtractor_8_bout, subtractor_9_bout, subtractor_10_bout, subtractor_11_bout, subtractor_12_bout,
       subtractor_13_bout, subtractor_14_bout, subtractor_15_bout, subtractor_16_bout, subtractor_17_bout;
  wire [15:0] not_122_out, subtractor_1_out, subtractor_2_out, subtractor_3_out, subtractor_4_out,
       subtractor_5_out, subtractor_6_out, subtractor_7_out, subtractor_8_out, subtractor_9_out,
       subtractor_10_out, subtractor_11_out, subtractor_12_out, subtractor_13_out, subtractor_14_out,
       subtractor_15_out, subtractor_16_out, subtractor_17_out;
  wire [15:1] not_111_out;
  wire [15:2] not_101_out;
  wire [15:3] not_92_out;
  wire [15:4] not_84_out;
  wire [15:5] not_77_out;
  wire [15:6] not_71_out;
  wire [15:8] not_151_out;

  not not_1 (out_28[12], 1'b1);
  not not_2 (out_28[14], 1'b1);
  not not_3 (out_30[12], 1'b1);
  not not_4 (out_30[14], 1'b1);
  not not_5 (out_32[10], 1'b1);
  not not_6 (out_32[12], 1'b1);
  not not_7 (out_32[14], 1'b1);
  not not_8 (out_34[12], 1'b1);
  not not_9 (out_34[14], 1'b1);
  not not_10 (out_37[12], 1'b1);
  not not_11 (out_37[14], 1'b1);
  not not_12 (out_39[12], 1'b1);
  not not_13 (out_39[14], 1'b1);
  not not_14 (not_71_out[8], 1'b1);
  not not_15 (not_71_out[10], 1'b1);
  not not_16 (not_71_out[12], 1'b1);
  not not_17 (not_71_out[14], 1'b1);
  not not_18 (not_77_out[8], 1'b1);
  not not_19 (not_77_out[10], 1'b1);
  not not_20 (not_77_out[12], 1'b1);
  not not_21 (not_77_out[14], 1'b1);
  not not_22 (not_84_out[8], 1'b1);
  not not_23 (not_84_out[10], 1'b1);
  not not_24 (not_84_out[12], 1'b1);
  not not_25 (not_84_out[14], 1'b1);
  not not_26 (not_92_out[8], 1'b1);
  not not_27 (not_92_out[10], 1'b1);
  not not_28 (not_92_out[12], 1'b1);
  not not_29 (not_92_out[14], 1'b1);
  not not_30 (not_101_out[8], 1'b1);
  not not_31 (not_101_out[10], 1'b1);
  not not_32 (not_101_out[12], 1'b1);
  not not_33 (not_101_out[14], 1'b1);
  not not_34 (not_111_out[8], 1'b1);
  not not_35 (not_111_out[10], 1'b1);
  not not_36 (not_111_out[12], 1'b1);
  not not_37 (not_111_out[14], 1'b1);
  not not_38 (not_122_out[8], 1'b1);
  not not_39 (not_122_out[10], 1'b1);
  not not_40 (not_122_out[12], 1'b1);
  not not_41 (not_122_out[14], 1'b1);
  not not_42 (out_24[14], 1'b1);
  not not_43 (out_26[14], 1'b1);
  not not_44 (out_26[15], 1'b1);
  not not_45 (out_28[13], 1'b1);
  not not_46 (out_28[15], 1'b1);
  not not_47 (out_30[11], 1'b1);
  not not_48 (out_30[13], 1'b1);
  not not_49 (out_30[15], 1'b1);
  not not_50 (out_32[11], 1'b1);
  not not_51 (out_32[13], 1'b1);
  not not_52 (out_32[15], 1'b1);
  not not_53 (out_34[9], 1'b1);
  not not_54 (out_34[10], 1'b1);
  not not_55 (out_34[11], 1'b1);
  not not_56 (out_34[13], 1'b1);
  not not_57 (out_34[15], 1'b1);
  not not_58 (out_37[8], 1'b1);
  not not_59 (out_37[9], 1'b1);
  not not_60 (out_37[10], 1'b1);
  not not_61 (out_37[11], 1'b1);
  not not_62 (out_37[13], 1'b1);
  not not_63 (out_37[15], 1'b1);
  not not_64 (out_39[7], 1'b1);
  not not_65 (out_39[8], 1'b1);
  not not_66 (out_39[9], 1'b1);
  not not_67 (out_39[10], 1'b1);
  not not_68 (out_39[11], 1'b1);
  not not_69 (out_39[13], 1'b1);
  not not_70 (out_39[15], 1'b1);
  not not_71 (not_71_out[6], 1'b1);
  not not_72 (not_71_out[7], 1'b1);
  not not_73 (not_71_out[9], 1'b1);
  not not_74 (not_71_out[11], 1'b1);
  not not_75 (not_71_out[13], 1'b1);
  not not_76 (not_71_out[15], 1'b1);
  not not_77 (not_77_out[5], 1'b1);
  not not_78 (not_77_out[6], 1'b1);
  not not_79 (not_77_out[7], 1'b1);
  not not_80 (not_77_out[9], 1'b1);
  not not_81 (not_77_out[11], 1'b1);
  not not_82 (not_77_out[13], 1'b1);
  not not_83 (not_77_out[15], 1'b1);
  not not_84 (not_84_out[4], 1'b1);
  not not_85 (not_84_out[5], 1'b1);
  not not_86 (not_84_out[6], 1'b1);
  not not_87 (not_84_out[7], 1'b1);
  not not_88 (not_84_out[9], 1'b1);
  not not_89 (not_84_out[11], 1'b1);
  not not_90 (not_84_out[13], 1'b1);
  not not_91 (not_84_out[15], 1'b1);
  not not_92 (not_92_out[3], 1'b1);
  not not_93 (not_92_out[4], 1'b1);
  not not_94 (not_92_out[5], 1'b1);
  not not_95 (not_92_out[6], 1'b1);
  not not_96 (not_92_out[7], 1'b1);
  not not_97 (not_92_out[9], 1'b1);
  not not_98 (not_92_out[11], 1'b1);
  not not_99 (not_92_out[13], 1'b1);
  not not_100 (not_92_out[15], 1'b1);
  not not_101 (not_101_out[2], 1'b1);
  not not_102 (not_101_out[3], 1'b1);
  not not_103 (not_101_out[4], 1'b1);
  not not_104 (not_101_out[5], 1'b1);
  not not_105 (not_101_out[6], 1'b1);
  not not_106 (not_101_out[7], 1'b1);
  not not_107 (not_101_out[9], 1'b1);
  not not_108 (not_101_out[11], 1'b1);
  not not_109 (not_101_out[13], 1'b1);
  not not_110 (not_101_out[15], 1'b1);
  not not_111 (not_111_out[1], 1'b1);
  not not_112 (not_111_out[2], 1'b1);
  not not_113 (not_111_out[3], 1'b1);
  not not_114 (not_111_out[4], 1'b1);
  not not_115 (not_111_out[5], 1'b1);
  not not_116 (not_111_out[6], 1'b1);
  not not_117 (not_111_out[7], 1'b1);
  not not_118 (not_111_out[9], 1'b1);
  not not_119 (not_111_out[11], 1'b1);
  not not_120 (not_111_out[13], 1'b1);
  not not_121 (not_111_out[15], 1'b1);
  not not_122 (not_122_out[0], 1'b1);
  not not_123 (not_122_out[1], 1'b1);
  not not_124 (not_122_out[3], 1'b1);
  not not_125 (not_122_out[3], 1'b1);
  not not_126 (not_122_out[4], 1'b1);
  not not_127 (not_122_out[5], 1'b1);
  not not_128 (not_122_out[6], 1'b1);
  not not_129 (not_122_out[7], 1'b1);
  not not_130 (not_122_out[9], 1'b1);
  not not_131 (not_122_out[11], 1'b1);
  not not_132 (not_122_out[13], 1'b1);
  not not_133 (not_122_out[15], 1'b1);
  not not_134 (out_22[15], 1'b1);
  not not_135 (out_24[15], 1'b1);
  not not_136 (out_26[13], 1'b1);
  not not_137 (out_20[4], 1'b1);
  not not_138 (out_20[7], 1'b1);
  not not_139 (out_20[5], 1'b1);
  not not_140 (out_20[6], 1'b1);
  not not_141 (out_20[1], 1'b1);
  not not_142 (out_20[0], 1'b1);
  not not_143 (out_20[2], 1'b1);
  not not_144 (out_20[3], 1'b1);
  not not_145 (not_151_out[15], 1'b1);
  not not_146 (not_151_out[14], 1'b1);
  not not_147 (not_151_out[13], 1'b1);
  not not_148 (not_151_out[11], 1'b1);
  not not_149 (not_151_out[12], 1'b1);
  MuxFor8BitDivision muxfor8bitdivision_1 (
    .in_1(subtractor_1_out), .in_2({not_151_out, a8_2, a7_2, a6_2, a5_2, a4_2, a3_2, a2_2, A1_2}),
    .in_3(subtractor_1_bout), .out_4(out_21));
  MuxFor8BitDivision muxfor8bitdivision_2 (
    .in_1(subtractor_2_out), .in_2(out_21), .in_3(subtractor_2_bout), .out_4(out_23));
  MuxFor8BitDivision muxfor8bitdivision_3 (
    .in_1(subtractor_3_out), .in_2(out_23), .in_3(subtractor_3_bout), .out_4(out_25));
  MuxFor8BitDivision muxfor8bitdivision_4 (
    .in_1(subtractor_4_out), .in_2(out_25), .in_3(subtractor_4_bout), .out_4(out_27));
  MuxFor8BitDivision muxfor8bitdivision_5 (
    .in_1(subtractor_5_out), .in_2(out_27), .in_3(subtractor_5_bout), .out_4(out_29));
  MuxFor8BitDivision muxfor8bitdivision_6 (
    .in_1(subtractor_6_out), .in_2(out_29), .in_3(subtractor_6_bout), .out_4(out_31));
  MuxFor8BitDivision muxfor8bitdivision_7 (
    .in_1(subtractor_7_out), .in_2(out_31), .in_3(subtractor_7_bout), .out_4(out_33));
  MuxFor8BitDivision muxfor8bitdivision_8 (
    .in_1(subtractor_8_out), .in_2(out_33), .in_3(subtractor_8_bout), .out_4(out_36));
  MuxFor8BitDivision muxfor8bitdivision_9 (
    .in_1(subtractor_9_out), .in_2(out_36), .in_3(subtractor_9_bout), .out_4(out_38));
  MuxFor8BitDivision muxfor8bitdivision_10 (
    .in_1(subtractor_10_out), .in_2(out_38), .in_3(subtractor_10_bout), .out_4(out_40));
  MuxFor8BitDivision muxfor8bitdivision_11 (
    .in_1(subtractor_11_out), .in_2(out_40), .in_3(subtractor_11_bout), .out_4(out_41));
  MuxFor8BitDivision muxfor8bitdivision_12 (
    .in_1(subtractor_12_out), .in_2(out_41), .in_3(subtractor_12_bout), .out_4(out_42));
  MuxFor8BitDivision muxfor8bitdivision_13 (
    .in_1(subtractor_13_out), .in_2(out_42), .in_3(subtractor_13_bout), .out_4(out_43));
  MuxFor8BitDivision muxfor8bitdivision_14 (
    .in_1(subtractor_14_out), .in_2(out_43), .in_3(subtractor_14_bout), .out_4(out_44));
  MuxFor8BitDivision muxfor8bitdivision_15 (
    .in_1(subtractor_15_out), .in_2(out_44), .in_3(subtractor_15_bout), .out_4(out_45));
  not not_150 (not_151_out[9], 1'b1);
  not not_151 (not_151_out[8], 1'b1);
  not not_152 (not_151_out[10], 1'b1);
  MuxFor8BitDivision muxfor8bitdivision_16 (
    .in_1(subtractor_16_out), .in_2(out_45), .in_3(subtractor_16_bout), .out_4(out_46));
  MuxFor8BitDivision muxfor8bitdivision_17 (
    .in_1(subtractor_17_out), .in_2(out_46), .in_3(subtractor_17_bout), .out_4(out_47));
  not not_153 (not_153_out, 1'b1);
  LED led_1 (.in(subtractor_1_bout));
  Subtractor #(.width(16)) subtractor_1 (
    .a({not_151_out, a8_2, a7_2, a6_2, a5_2, a4_2, a3_2, a2_2, A1_2}),
    .b({a8, a7, a6, a5, a4, a3, a2, A1, out_20[7:0]}), .out(subtractor_1_out), .bin(not_153_out),
    .bout(subtractor_1_bout));
  not not_154 (not_154_out, 1'b1);
  Subtractor #(.width(16)) subtractor_2 (
    .a(out_21), .b({out_22[15], a8, a7, a6, a5, a4, a3, a2, A1, out_20[7:1]}), .out(subtractor_2_out),
    .bin(not_154_out), .bout(subtractor_2_bout));
  LED led_2 (.in(subtractor_2_bout));
  not not_155 (not_155_out, 1'b1);
  Subtractor #(.width(16)) subtractor_3 (
    .a(out_23), .b({out_24[15:14], a8, a7, a6, a5, a4, a3, a2, A1, out_20[7:2]}), .out(subtractor_3_out),
    .bin(not_155_out), .bout(subtractor_3_bout));
  LED led_3 (.in(subtractor_3_bout));
  not not_156 (not_156_out, 1'b1);
  Subtractor #(.width(16)) subtractor_4 (
    .a(out_25), .b({out_26[15:13], a8, a7, a6, a5, a4, a3, a2, A1, out_20[7:3]}), .out(subtractor_4_out),
    .bin(not_156_out), .bout(subtractor_4_bout));
  LED led_4 (.in(subtractor_4_bout));
  not not_157 (not_157_out, 1'b1);
  Subtractor #(.width(16)) subtractor_5 (
    .a(out_27), .b({out_28[15:12], a8, a7, a6, a5, a4, a3, a2, A1, out_20[7:4]}), .out(subtractor_5_out),
    .bin(not_157_out), .bout(subtractor_5_bout));
  LED led_5 (.in(subtractor_5_bout));
  not not_158 (not_158_out, 1'b1);
  Subtractor #(.width(16)) subtractor_6 (
    .a(out_29), .b({out_30[15:11], a8, a7, a6, a5, a4, a3, a2, A1, out_20[7:5]}), .out(subtractor_6_out),
    .bin(not_158_out), .bout(subtractor_6_bout));
  LED led_6 (.in(subtractor_6_bout));
  not not_159 (not_159_out, 1'b1);
  Subtractor #(.width(16)) subtractor_7 (
    .a(out_31), .b({out_32[15:10], a8, a7, a6, a5, a4, a3, a2, A1, out_20[7:6]}), .out(subtractor_7_out),
    .bin(not_159_out), .bout(subtractor_7_bout));
  LED led_7 (.in(subtractor_7_bout));
  not not_160 (not_160_out, 1'b1);
  Subtractor #(.width(16)) subtractor_8 (
    .a(out_33), .b({out_34[15:9], a8, a7, a6, a5, a4, a3, a2, A1, out_20[7]}), .out(subtractor_8_out),
    .bin(not_160_out), .bout(subtractor_8_bout));
  LED led_8 (.in(subtractor_8_bout));
  not not_161 (not_161_out, 1'b1);
  Subtractor #(.width(16)) subtractor_9 (
    .a(out_36), .b({out_37[15:8], a8, a7, a6, a5, a4, a3, a2, A1}), .out(subtractor_9_out),
    .bin(not_161_out), .bout(subtractor_9_bout));
  LED led_9 (.in(subtractor_9_bout));
  not not_162 (not_162_out, 1'b1);
  Subtractor #(.width(16)) subtractor_10 (
    .a(out_38), .b({out_39[15:7], a8, a7, a6, a5, a4, a3, a2}), .out(subtractor_10_out), .bin(not_162_out),
    .bout(subtractor_10_bout));
  LED led_10 (.in(subtractor_10_bout));
  not not_163 (not_163_out, 1'b1);
  Subtractor #(.width(16)) subtractor_11 (
    .a(out_40), .b({not_71_out, a8, a7, a6, a5, a4, a3}), .out(subtractor_11_out), .bin(not_163_out),
    .bout(subtractor_11_bout));
  LED led_11 (.in(subtractor_11_bout));
  not not_164 (not_164_out, 1'b1);
  Subtractor #(.width(16)) subtractor_12 (
    .a(out_41), .b({not_77_out, a8, a7, a6, a5, a4}), .out(subtractor_12_out), .bin(not_164_out),
    .bout(subtractor_12_bout));
  LED led_12 (.in(subtractor_12_bout));
  not not_165 (not_165_out, 1'b1);
  Subtractor #(.width(16)) subtractor_13 (
    .a(out_42), .b({not_84_out, a8, a7, a6, a5}), .out(subtractor_13_out), .bin(not_165_out),
    .bout(subtractor_13_bout));
  LED led_13 (.in(subtractor_13_bout));
  not not_166 (not_166_out, 1'b1);
  Subtractor #(.width(16)) subtractor_14 (
    .a(out_43), .b({not_92_out, a8, a7, a6}), .out(subtractor_14_out), .bin(not_166_out),
    .bout(subtractor_14_bout));
  LED led_14 (.in(subtractor_14_bout));
  not not_167 (not_167_out, 1'b1);
  Subtractor #(.width(16)) subtractor_15 (
    .a(out_44), .b({not_101_out, a8, a7}), .out(subtractor_15_out), .bin(not_167_out),
    .bout(subtractor_15_bout));
  LED led_15 (.in(subtractor_15_bout));
  not not_168 (not_168_out, 1'b1);
  LED led_16 (.in(subtractor_16_bout));
  not not_169 (not_169_out, 1'b1);
  LED led_17 (.in(subtractor_17_bout));
  not not_170 (not_170_out, subtractor_1_bout);
  not not_171 (out_17[7], subtractor_2_bout);
  not not_172 (out_17[6], subtractor_3_bout);
  not not_173 (out_17[5], subtractor_4_bout);
  not not_174 (out_17[4], subtractor_5_bout);
  not not_175 (out_17[3], subtractor_6_bout);
  not not_176 (out_17[2], subtractor_7_bout);
  Subtractor #(.width(16)) subtractor_16 (
    .a(out_45), .b({not_111_out, a8}), .out(subtractor_16_out), .bin(not_168_out), .bout(subtractor_16_bout));
  Subtractor #(.width(16)) subtractor_17 (
    .a(out_46), .b({not_122_out[15:3], not_122_out[3], not_122_out[1:0]}), .out(subtractor_17_out),
    .bin(not_169_out), .bout(subtractor_17_bout));
  not not_177 (out_17[1], subtractor_8_bout);
  not not_178 (out_17[0], subtractor_9_bout);
  not not_179 (out_18[7], subtractor_10_bout);
  not not_180 (out_18[6], subtractor_11_bout);
  not not_181 (out_18[5], subtractor_12_bout);
  not not_182 (out_18[4], subtractor_13_bout);
  not not_183 (out_18[3], subtractor_14_bout);
  not not_184 (out_18[2], subtractor_15_bout);
  not not_185 (out_18[1], subtractor_16_bout);
  not not_186 (out_18[0], subtractor_17_bout);
  // NOT_Gate not_187 is placed but not wired

  assign out_19 = {out_17, out_18};
  assign out_20[15:8] = {a8, a7, a6, a5, a4, a3, a2, A1};
  assign out_22[14:0] = {a8, a7, a6, a5, a4, a3, a2, A1, out_20[7:1]};
  assign out_24[13:0] = {a8, a7, a6, a5, a4, a3, a2, A1, out_20[7:2]};
  assign out_26[12:0] = {a8, a7, a6, a5, a4, a3, a2, A1, out_20[7:3]};
  assign out_28[11:0] = {a8, a7, a6, a5, a4, a3, a2, A1, out_20[7:4]};
  assign out_30[10:0] = {a8, a7, a6, a5, a4, a3, a2, A1, out_20[7:5]};
  assign out_32[9:0] = {a8, a7, a6, a5, a4, a3, a2, A1, out_20[7:6]};
  assign out_34[8:0] = {a8, a7, a6, a5, a4, a3, a2, A1, out_20[7]};
  assign out_35 = out_17[1];
  assign out_37[7:0] = {a8, a7, a6, a5, a4, a3, a2, A1};
  assign out_39[6:0] = {a8, a7, a6, a5, a4, a3, a2};

  // Notes on the sheet:
  //   divisor
  //   Right Shift
  //   Left Shift
  //   dividend
  //   logic breaks
endmodule

module Populate (
  input  in_1,
  input  in_2,
  input  in_3,
  input  in_4,
  input  in_5,
  input  in_6,
  input  in_7,
  input  in_8,
  input  in_9,
  input  in_10,
  input  in_11,
  input  in_12,
  input  in_13,
  input  in_14,
  input  in_15,
  input  in_16,
  output out_17
);

  not not_1 (out_17, in_1);
endmodule

module MUX_8_BIT_CHOOSEr_CIRCUIT (
  input  in_1,
  input  in_2,
  input  in_3,
  input  in_4,
  input  in_5,
  input  in_6,
  input  in_7,
  input  in_8,
  input  in_9,
  input  in_10,
  input  in_11,
  input  in_12,
  input  in_13,
  input  in_14,
  input  in_15,
  input  in_16,
  output out_17,
  output SUB,
  output MUL,
  output DIV
);

  wire not_1_out, not_2_out, not_3_out, not_4_out, not_5_out, not_6_out, not_7_out, not_8_out, not_9_out,
       not_10_out, not_11_out, not_12_out, not_13_out, not_14_out, not_15_out, not_16_out, not_17_out,
       not_18_out, not_19_out, not_20_out, not_21_out, not_22_out, not_23_out, not_24_out, not_25_out,
       not_26_out, not_27_out, not_28_out, not_29_out, not_30_out, not_31_out, not_32_out;

  LED led_1 (.in(in_1));
  LED led_2 (.in(in_9));
  not not_1 (not_1_out, in_2);
  not not_2 (not_2_out, in_4);
  not not_3 (not_3_out, in_8);
  not not_4 (not_4_out, in_12);
  not not_5 (not_5_out, in_15);
  not not_6 (not_6_out, in_1);
  not not_7 (not_7_out, in_2);
  not not_8 (not_8_out, in_3);
  not not_9 (not_9_out, in_4);
  not not_10 (not_10_out, in_6);
  not not_11 (not_11_out, in_7);
  not not_12 (not_12_out, in_8);
  not not_13 (not_13_out, in_14);
  not not_14 (not_14_out, in_15);
  not not_15 (not_15_out, in_3);
  not not_16 (not_16_out, in_4);
  not not_17 (not_17_out, in_5);
  not not_18 (not_18_out, in_8);
  not not_19 (not_19_out, in_9);
  not not_20 (not_20_out, in_10);
  not not_21 (not_21_out, in_11);
  not not_22 (not_22_out, in_16);
  not not_23 (not_23_out, in_1);
  not not_24 (not_24_out, in_3);
  not not_25 (not_25_out, in_4);
  not not_26 (not_26_out, in_6);
  not not_27 (not_27_out, in_8);
  not not_28 (not_28_out, in_9);
  not not_29 (not_29_out, in_11);
  not not_30 (not_30_out, in_13);
  not not_31 (not_31_out, in_14);
  not not_32 (not_32_out, in_16);
  and and_1 (out_17, in_1, not_1_out, in_3, not_2_out, in_5, in_6, in_7, not_3_out, in_10, in_11, not_4_out, in_13, in_14, not_5_out, in_16);
  LED led_3 (.in(out_17));
  LED led_4 (.in(SUB));
  and and_2 (SUB, not_6_out, not_7_out, not_8_out, not_9_out, in_5, not_10_out, not_11_out, not_12_out, in_10, in_11, in_12, in_13, not_13_out, not_14_out, in_16);
  LED led_5 (.in(MUL));
  and and_3 (MUL, in_1, in_2, not_15_out, not_16_out, not_17_out, in_6, in_7, not_18_out, not_20_out, not_21_out, in_12, in_13, in_14, in_15, not_22_out);
  and and_4 (DIV, not_23_out, in_2, not_24_out, not_25_out, in_5, not_26_out, in_7, not_27_out, in_10, not_29_out, in_12, not_30_out, not_31_out, in_15, not_32_out);
  LED led_6 (.in(DIV));

  // Notes on the sheet:
  //   ADD: 1010  1110  1110  1101 
  //   SUB: 0000  1000  1111 1001
  //   MUL: 1100  0110  0001 1110
  //   DIV: 0100  1010 0101 0010 
  //   ADD
endmodule

module MUX_to_SELECTOR (
  input  in_1,
  input  in_2,
  input  in_3,
  input  in_4,
  input  in_5,
  input  in_6,
  input  in_7,
  input  in_8,
  input  InputFromMux,
  output out_10,
  output out_11,
  output out_12,
  output out_13,
  output out_14,
  output out_15,
  output out_16,
  output out_17
);

  and and_1 (out_16, InputFromMux, in_7);
  and and_2 (out_17, InputFromMux, in_8);
  and and_3 (out_13, InputFromMux, in_4);
  and and_4 (out_14, InputFromMux, in_5);
  and and_5 (out_15, InputFromMux, in_6);
  and and_6 (out_12, InputFromMux, in_3);
  and and_7 (out_11, InputFromMux, in_2);
  and and_8 (out_10, InputFromMux, in_1);
endmodule
