// Logisim project Div_4_28_15.circ as structural Verilog: 1 circuit, main circuit main
module main (
  input  in_1,
  input  in_2,
  input  in_3,
  input  in_4,
  input  in_5,
  input  in_6,
  input  in_7,
  input  in_8,
  input  in_9,
  input  in_10,
  input  in_11,
  input  in_12,
  input  in_13,
  input  in_14,
  input  in_15,
  input  in_16,
  input  [15:0] in_17,
  input  [15:0] in_18,
  input  [15:0] in_19,
  output [15:0] out_20
);

  wire or_2_out;
  wire [5:0] undriven;
  wire [7:0] multiplier_2_cout;

  // OR_Gate or_1 is placed but not wired
  Multiplier #(.width(16)) multiplier_1 (.a(in_19), .b(in_18));  // open: out, cin, cout
  Multiplier multiplier_2 (.cin({in_1, in_2, undriven}), .cout(multiplier_2_cout));  // open: a, b, out
  Multiplier #(.width(16)) multiplier_3 (.a(in_17), .b(in_18), .out(out_20));  // open: cin, cout
  or or_2 (or_2_out, out_20[8], out_20[9], out_20[10], out_20[11], out_20[12], out_20[13], out_20[14], out_20[15]);
  LED led_1 (.in(or_2_out));
endmodule
