// Logisim project DoivisionUsingGates.circ as structural Verilog: 2 circuits, main circuit main
module main (
  input  in_1,
  input  in_2,
  input  in_3,
  input  in_4,
  input  in_5,
  input  in_6,
  input  in_7,
  input  As,
  input  in_9,
  input  in_10,
  input  in_11,
  input  in_12,
  input  in_13,
  input  in_14,
  input  in_15,
  input  Bs,
  input  in_17,
  input  in_18,
  input  in_19,
  input  in_20,
  input  in_21,
  input  in_22,
  input  in_23,
  input  in_24,
  input  in_25,
  input  in_26,
  input  in_27,
  output out_28,
  output out_29,
  output out_30,
  output out_31,
  output out_32,
  output out_33,
  output _1_C,
  output out_35,
  output out_36,
  output out_37,
  output out_38,
  output out_39,
  output out_40,
  output out_41,
  output out_42,
  output out_43,
  output out_44,
  output Quot_1,
  output out_46,
  output out_47,
  output out_48,
  output out_49,
  output out_50,
  output out_51,
  output out_52,
  output out_53,
  output out_54,
  output out_55,
  output out_56,
  output out_57,
  output out_58,
  output out_59,
  output out_60,
  output out_61,
  output out_62
);

  wire fa_sub_4_cout, fa_sub_5_cout, fa_sub_6_cout, fa_sub_7_cout, fa_sub_8_cout, fa_sub_9_cout,
       fa_sub_10_cout, fa_sub_11_cout, fa_sub_12_cout, fa_sub_13_cout, fa_sub_14_cout, fa_sub_15_cout,
       fa_sub_16_cout, fa_sub_17_cout, fa_sub_18_cout, fa_sub_19_cout, fa_sub_20_cout, fa_sub_21_cout,
       fa_sub_22_cout, fa_sub_23_cout, fa_sub_24_cout;

  not not_1 (out_35, in_9);
  FA_sub fa_sub_1 (.Cout(out_36), .Cin(fa_sub_4_cout), .A(out_35), .B(in_17), .S(out_41));
  FA_sub fa_sub_2 (.Cout(Quot_1), .Cin(fa_sub_5_cout), .A(in_1), .B(out_41), .S(out_50));
  FA_sub fa_sub_3 (.Cout(out_54), .Cin(fa_sub_6_cout), .A(out_41), .B(out_50), .S(out_59));
  not not_2 (out_30, in_10);
  FA_sub fa_sub_4 (.Cout(fa_sub_4_cout), .Cin(fa_sub_7_cout), .A(out_30), .B(in_18), .S(out_42));
  FA_sub fa_sub_5 (.Cout(fa_sub_5_cout), .Cin(fa_sub_8_cout), .A(in_2), .B(out_42), .S(out_51));
  FA_sub fa_sub_6 (.Cout(fa_sub_6_cout), .Cin(fa_sub_9_cout), .A(out_42), .B(out_51), .S(out_60));
  not not_3 (out_31, in_11);
  FA_sub fa_sub_7 (.Cout(fa_sub_7_cout), .Cin(fa_sub_10_cout), .A(out_31), .B(in_19), .S(out_37));
  FA_sub fa_sub_8 (.Cout(fa_sub_8_cout), .Cin(fa_sub_11_cout), .A(in_3), .B(out_37), .S(out_46));
  FA_sub fa_sub_9 (.Cout(fa_sub_9_cout), .Cin(fa_sub_12_cout), .A(out_37), .B(out_46), .S(out_55));
  not not_4 (out_28, in_12);
  FA_sub fa_sub_10 (.Cout(fa_sub_10_cout), .Cin(fa_sub_13_cout), .A(out_28), .B(in_20), .S(out_38));
  FA_sub fa_sub_11 (.Cout(fa_sub_11_cout), .Cin(fa_sub_14_cout), .A(in_4), .B(out_38), .S(out_47));
  FA_sub fa_sub_12 (.Cout(fa_sub_12_cout), .Cin(fa_sub_15_cout), .A(out_38), .B(out_47), .S(out_56));
  not not_5 (out_29, in_13);
  FA_sub fa_sub_13 (.Cout(fa_sub_13_cout), .Cin(fa_sub_16_cout), .A(out_29), .B(in_21), .S(out_39));
  FA_sub fa_sub_14 (.Cout(fa_sub_14_cout), .Cin(fa_sub_17_cout), .A(in_5), .B(out_39), .S(out_48));
  FA_sub fa_sub_15 (.Cout(fa_sub_15_cout), .Cin(fa_sub_18_cout), .A(out_39), .B(out_48), .S(out_57));
  not not_6 (out_32, in_14);
  FA_sub fa_sub_16 (.Cout(fa_sub_16_cout), .Cin(fa_sub_19_cout), .A(out_32), .B(in_22), .S(out_40));
  FA_sub fa_sub_17 (.Cout(fa_sub_17_cout), .Cin(fa_sub_20_cout), .A(in_6), .B(out_40), .S(out_49));
  FA_sub fa_sub_18 (.Cout(fa_sub_18_cout), .Cin(fa_sub_21_cout), .A(out_40), .B(out_49), .S(out_58));
  not not_7 (out_33, in_15);
  FA_sub fa_sub_19 (.Cout(fa_sub_19_cout), .Cin(fa_sub_22_cout), .A(out_33), .B(in_23), .S(out_43));
  FA_sub fa_sub_20 (.Cout(fa_sub_20_cout), .Cin(fa_sub_24_cout), .A(in_7), .B(out_43), .S(out_52));
  FA_sub fa_sub_21 (.Cout(fa_sub_21_cout), .Cin(fa_sub_23_cout), .A(out_43), .B(out_52), .S(out_61));
  not not_8 (_1_C, Bs);
  LED led_1 (.in(in_24));
  FA_sub fa_sub_22 (.Cout(fa_sub_22_cout), .Cin(in_25), .A(_1_C), .B(in_24), .S(out_44));
  FA_sub fa_sub_23 (.Cout(fa_sub_23_cout), .Cin(in_27), .A(out_44), .B(out_53), .S(out_62));
  FA_sub fa_sub_24 (.Cout(fa_sub_24_cout), .Cin(in_26), .A(As), .B(out_44), .S(out_53));

  // Notes on the sheet:
  //   Add 1
  //   2 C
  //   DIVIDENT
  //   DIVISOR
  //   DIVISOR
  //   Remainder1
  //   A-B step 1
  //   DIVISOR
endmodule

module FA_sub (
  input  A,
  input  B,
  input  Cin,
  output Cout,
  output S
);

  wire and_1_out, and_2_out, xor_2_out;

  or or_1 (Cout, and_1_out, and_2_out);
  and and_1 (and_1_out, Cin, B);
  and and_2 (and_2_out, A, xor_2_out);
  xor xor_1 (S, A, xor_2_out);
  xor xor_2 (xor_2_out, B, Cin);

  // Notes on the sheet:
  //   Full Adder
endmodule
