// Logisim project FullAdder_latest.circ as structural Verilog
module main (
  input  A,
  input  B,
  input  Cin,
  output Cout,
  output S
);

  wire and_1_out, and_2_out, xor_2_out;

  or or_1 (Cout, and_1_out, and_2_out);
  and and_1 (and_1_out, Cin, B);
  and and_2 (and_2_out, A, xor_2_out);
  xor xor_1 (S, A, xor_2_out);
  xor xor_2 (xor_2_out, B, Cin);

  // Notes on the sheet:
  //   Full Adder
endmodule

module FullAdder (
  input  A,
  input  B,
  input  Cin,
  output Cout,
  output S
);

  wire and_1_out, and_2_out, xor_2_out;

  or or_1 (Cout, and_1_out, and_2_out);
  and and_1 (and_1_out, Cin, B);
  and and_2 (and_2_out, A, xor_2_out);
  xor xor_1 (S, A, xor_2_out);
  xor xor_2 (xor_2_out, B, Cin);

  // Notes on the sheet:
  //   Full Adder
endmodule

module _2_bit_adder (
  input  A2,
  input  A1,
  input  B2,
  input  B1,
  input  in_5,
  output Flag,
  output S2,
  output S1
);

  wire fulladder_1_cout;

  FullAdder fulladder_1 (.Cout(fulladder_1_cout), .Cin(in_5), .A(A1), .B(B1), .S(S1));
  FullAdder fulladder_2 (.Cout(Flag), .Cin(fulladder_1_cout), .A(A2), .B(B2), .S(S2));
endmodule

module _4_BIT_ADDER (
  input  in_1,
  input  in_2,
  input  in_3,
  input  in_4,
  input  in_5,
  input  in_6,
  input  in_7,
  input  in_8,
  input  in_9,
  output _4S5,
  output _4S4,
  output _4S3,
  output _4S2,
  output _4S1
);

  wire n2_bit_adder_1_flag;

  _2_bit_adder u_2_bit_adder_1 (
    .Flag(n2_bit_adder_1_flag), .S2(_4S2), .S1(_4S1), .A2(in_3), .B2(in_7), .in_5(in_9), .A1(in_4), .B1(in_8));
  _2_bit_adder u_2_bit_adder_2 (
    .Flag(_4S5), .S2(_4S4), .S1(_4S3), .A2(in_1), .B2(in_5), .in_5(n2_bit_adder_1_flag), .A1(in_2), .B1(in_6));
endmodule

module _8_BIT_ADDER (
  input  in_1,
  input  in_2,
  input  in_3,
  input  in_4,
  input  in_5,
  input  in_6,
  input  in_7,
  input  in_8,
  input  in_9,
  input  in_10,
  input  in_11,
  input  in_12,
  input  in_13,
  input  in_14,
  input  in_15,
  input  in_16,
  input  in_17,
  output out_18,
  output out_19,
  output out_20,
  output out_21,
  output out_22,
  output out_23,
  output out_24,
  output out_25,
  output out_26
);

  wire n4_bit_adder_1__4s5;

  _4_BIT_ADDER u_4_bit_adder_1 (
    ._4S5(n4_bit_adder_1__4s5), ._4S4(out_23), ._4S3(out_24), ._4S2(out_25), ._4S1(out_26), .in_9(in_17),
    .in_3(in_15), .in_4(in_16), .in_5(in_5), .in_6(in_6), .in_7(in_7), .in_8(in_8), .in_1(in_13), .in_2(in_14));
  _4_BIT_ADDER u_4_bit_adder_2 (
    ._4S5(out_18), ._4S4(out_19), ._4S3(out_20), ._4S2(out_21), ._4S1(out_22), .in_9(n4_bit_adder_1__4s5),
    .in_3(in_11), .in_4(in_12), .in_5(in_1), .in_6(in_2), .in_7(in_3), .in_8(in_4), .in_1(in_9), .in_2(in_10));
endmodule

module FAforMul (
  input  A,
  input  B,
  input  Cin,
  output Cout,
  output S
);

  wire and_1_out, and_2_out, xor_2_out;

  or or_1 (Cout, and_1_out, and_2_out);
  and and_1 (and_1_out, Cin, B);
  and and_2 (and_2_out, A, xor_2_out);
  xor xor_1 (S, A, xor_2_out);
  xor xor_2 (xor_2_out, B, Cin);

  // Notes on the sheet:
  //   Full Adder
endmodule

module _4BIT_MUL (
  input  B3,
  input  A3,
  input  B2,
  input  A2,
  input  B1,
  input  A1,
  input  B0,
  input  A0,
  input  in_9
);

  wire faformul_2_cout, faformul_3_cout, faformul_4_cout;

  FAforMul faformul_1 (.Cin(faformul_2_cout), .A(A3), .B(B3));  // open: Cout, S
  FAforMul faformul_2 (.Cout(faformul_2_cout), .Cin(faformul_3_cout), .A(A2), .B(B2));  // open: S
  FAforMul faformul_3 (.Cout(faformul_3_cout), .Cin(faformul_4_cout), .A(A1), .B(B1));  // open: S
  FAforMul faformul_4 (.Cout(faformul_4_cout), .Cin(in_9), .A(A0), .B(B0));  // open: S
endmodule

module _4BitT2 (
  input  A0,
  input  B0,
  input  in_3,
  input  _0,
  output out_5,
  output out_6
);

  wire and_1_out;

  FAforMul faformul_1 (.Cout(out_5), .Cin(_0), .A(and_1_out), .B(in_3), .S(out_6));
  and and_1 (and_1_out, A0, B0);
endmodule
