// Logisim project Gated_D_Latch_4_21_2015.circ as structural Verilog: 1 circuit, main circuit main
module main (
  input  Data,
  input  Enable,
  input  Y,
  input  _31,
  input  _30,
  input  _29,
  input  _28,
  input  _27,
  input  _26,
  input  _25,
  input  in_11,
  input  in_12,
  input  in_13,
  input  in_14,
  input  in_15,
  input  in_16,
  input  in_17,
  input  in_18,
  input  in_19,
  input  in_20,
  input  in_21,
  input  in_22,
  input  in_23,
  input  in_24,
  input  in_25,
  input  in_26,
  input  in_27,
  input  in_28,
  input  in_29,
  input  in_30,
  input  in_31,
  input  in_32,
  input  in_33,
  input  in_34,
  input  in_35,
  input  A1,
  input  A0,
  output X,
  output out_39,
  output Data_8,
  output Data_6,
  output out_42,
  output Data_7,
  output Data_2,
  output X_2,
  output X_3,
  output X_4,
  output X_5,
  output X_6,
  output X_7,
  output X_8,
  output Enable_2,
  output Y_2,
  output Y_3,
  output Y_4,
  output Y_5,
  output Y_6,
  output Y_7,
  output Y_8,
  output Y_9,
  output Data_3,
  output X_9,
  output Enable_3,
  output X_10,
  output X_11,
  output X_12,
  output X_13,
  output X_14,
  output X_15,
  output Y_10,
  output Y_11,
  output Y_12,
  output Y_13,
  output Y_14,
  output Y_15,
  output Y_16,
  output Y_17,
  output out_78,
  output Data_4,
  output X_16,
  output X_17,
  output X_18,
  output X_19,
  output X_20,
  output X_21,
  output X_22,
  output Enable_4,
  output Y_18,
  output Y_19,
  output Y_20,
  output Y_21,
  output Y_22,
  output Y_23,
  output Y_24,
  output Y_25,
  output Data_5,
  output X_23,
  output Enable_5,
  output X_24,
  output Y_26,
  output X_25,
  output X_26,
  output Y_27,
  output X_27,
  output X_28,
  output X_29,
  output Y_28,
  output Y_29,
  output Y_30,
  output Y_31,
  output Y_32,
  output Y_33
);

  wire _0_0_out, _0_1_2_out, _1_1_out, and_5_out, and_6_out, and_7_out, and_8_out, and_9_out, and_10_out,
       and_11_out, and_12_out, and_13_out, and_14_out, and_15_out, and_16_out, and_17_out, and_18_out,
       and_19_out, and_20_out, and_21_out, and_22_out, and_23_out, and_24_out, and_25_out, and_26_out,
       and_27_out, and_28_out, and_29_out, and_30_out, and_31_out, and_32_out, and_33_out, and_34_out,
       and_35_out, and_36_out, nand_1_out, nand_2_out, nand_5_out, nand_6_out, nand_7_out, nand_8_out,
       nand_9_out, nand_10_out, nand_11_out, nand_12_out, nand_13_out, nand_15_out, nand_17_out, nand_19_out,
       nand_21_out, nand_22_out, nand_23_out, nand_24_out, nand_25_out, nand_26_out, nand_27_out,
       nand_28_out, nand_37_out, nand_38_out, nand_39_out, nand_40_out, nand_41_out, nand_42_out,
       nand_43_out, nand_44_out, nand_53_out, nand_54_out, nand_55_out, nand_56_out, nand_57_out,
       nand_58_out, nand_59_out, nand_60_out, nand_69_out, nand_70_out, nand_71_out, nand_72_out,
       nand_73_out, nand_74_out, nand_75_out, nand_76_out, nand_85_out, nand_86_out, nand_87_out,
       nand_88_out, nand_89_out, nand_90_out, nand_91_out, nand_92_out, nand_101_out, nand_102_out,
       nand_103_out, nand_104_out, nand_105_out, nand_106_out, nand_107_out, nand_108_out, nand_117_out,
       nand_118_out, nand_119_out, nand_120_out, nand_121_out, nand_122_out, nand_123_out, nand_124_out,
       not_1_out, not_2_out, not_3_out, not_4_out, not_5_out, not_6_out, not_7_out, not_8_out, not_9_out,
       not_10_out, not_11_out, not_12_out, not_13_out, not_14_out, not_15_out, not_16_out, not_17_out,
       not_18_out, not_19_out, not_20_out, not_21_out, not_22_out, not_23_out, not_24_out, not_25_out,
       not_26_out, not_27_out, not_28_out, not_29_out, not_30_out, not_31_out, not_32_out, not_33_out,
       not_34_out, not_35_out, not_36_out, not_37_out, or_1_out, or_2_out, or_3_out, or_4_out, or_5_out,
       or_6_out, or_7_out, or_8_out;

  not not_1 (not_1_out, Data);
  nand nand_1 (nand_1_out, Data, Enable);
  nand nand_2 (nand_2_out, Enable, not_1_out);
  not not_2 (not_2_out, A0);
  not not_3 (not_3_out, A1);
  not not_4 (not_4_out, A1);
  not not_5 (not_5_out, A0);
  and _0_1 (out_78, not_5_out, A1);
  and _1_1 (_1_1_out, A0, A1);
  and _0_0 (_0_0_out, not_2_out, not_3_out);
  and _0_1_2 (_0_1_2_out, A0, not_4_out);
  nand nand_3 (X, nand_1_out, out_39);
  nand nand_4 (out_39, X, nand_2_out);
  and and_1 (Enable_2, _0_0_out, in_35);
  and and_2 (Enable_3, _0_1_2_out, in_35);
  and and_3 (Enable_4, out_78, in_35);
  and and_4 (Enable_5, _1_1_out, in_35);
  not not_6 (not_6_out, Y);
  nand nand_5 (nand_5_out, Y, Enable_2);
  nand nand_6 (nand_6_out, Enable_2, not_7_out);
  not not_7 (not_7_out, Y);
  nand nand_7 (nand_7_out, Y, Enable_3);
  nand nand_8 (nand_8_out, Enable_3, not_8_out);
  not not_8 (not_8_out, Y);
  nand nand_9 (nand_9_out, Y, Enable_4);
  nand nand_10 (nand_10_out, Enable_4, not_9_out);
  not not_9 (not_9_out, Y);
  nand nand_11 (nand_11_out, Y, Enable_5);
  nand nand_12 (nand_12_out, Enable_5, not_6_out);
  nand nand_13 (nand_13_out, nand_11_out, Y_26);
  nand nand_14 (Y_26, nand_13_out, nand_12_out);
  nand nand_15 (nand_15_out, nand_5_out, Y_2);
  nand nand_16 (Y_2, nand_15_out, nand_6_out);
  nand nand_17 (nand_17_out, nand_7_out, Y_10);
  nand nand_18 (Y_10, nand_17_out, nand_8_out);
  nand nand_19 (nand_19_out, nand_9_out, Y_21);
  nand nand_20 (Y_21, nand_19_out, nand_10_out);
  and and_5 (and_5_out, nand_15_out, _0_0_out);
  and and_6 (and_6_out, nand_17_out, _0_1_2_out);
  and and_7 (and_7_out, nand_19_out, out_78);
  and and_8 (and_8_out, nand_13_out, _1_1_out);
  or or_1 (or_1_out, and_8_out, and_7_out, and_6_out, and_5_out);
  not not_10 (not_10_out, _31);
  not not_11 (not_11_out, _31);
  not not_12 (not_12_out, _31);
  not not_13 (not_13_out, _31);
  nand nand_21 (nand_21_out, _31, Enable_2);
  nand nand_22 (nand_22_out, Enable_2, not_10_out);
  nand nand_23 (nand_23_out, _31, Enable_3);
  nand nand_24 (nand_24_out, Enable_3, not_11_out);
  nand nand_25 (nand_25_out, _31, Enable_4);
  nand nand_26 (nand_26_out, Enable_4, not_12_out);
  nand nand_27 (nand_27_out, _31, Enable_5);
  nand nand_28 (nand_28_out, Enable_5, not_13_out);
  nand nand_29 (X_2, nand_21_out, Y_3);
  nand nand_30 (Y_3, X_2, nand_22_out);
  nand nand_31 (X_9, nand_23_out, Y_11);
  nand nand_32 (Y_11, X_9, nand_24_out);
  nand nand_33 (X_16, nand_25_out, Y_18);
  nand nand_34 (Y_18, X_16, nand_26_out);
  nand nand_35 (X_23, nand_27_out, Y_27);
  nand nand_36 (Y_27, X_23, nand_28_out);
  and and_9 (and_9_out, X_2, _0_0_out);
  and and_10 (and_10_out, X_9, _0_1_2_out);
  and and_11 (and_11_out, X_16, out_78);
  and and_12 (and_12_out, X_23, _1_1_out);
  or or_2 (or_2_out, and_12_out, and_11_out, and_10_out, and_9_out);
  not not_14 (not_14_out, _30);
  not not_15 (not_15_out, _30);
  not not_16 (not_16_out, _30);
  not not_17 (not_17_out, _30);
  nand nand_37 (nand_37_out, _30, Enable_2);
  nand nand_38 (nand_38_out, Enable_2, not_14_out);
  nand nand_39 (nand_39_out, _30, Enable_3);
  nand nand_40 (nand_40_out, Enable_3, not_15_out);
  nand nand_41 (nand_41_out, _30, Enable_4);
  nand nand_42 (nand_42_out, Enable_4, not_16_out);
  nand nand_43 (nand_43_out, _30, Enable_5);
  nand nand_44 (nand_44_out, Enable_5, not_17_out);
  nand nand_45 (X_8, nand_37_out, Y_9);
  nand nand_46 (Y_9, X_8, nand_38_out);
  nand nand_47 (X_10, nand_39_out, Y_12);
  nand nand_48 (Y_12, X_10, nand_40_out);
  nand nand_49 (X_22, nand_41_out, Y_25);
  nand nand_50 (Y_25, X_22, nand_42_out);
  nand nand_51 (X_24, nand_43_out, Y_28);
  nand nand_52 (Y_28, X_24, nand_44_out);
  and and_13 (and_13_out, X_8, _0_0_out);
  and and_14 (and_14_out, X_10, _0_1_2_out);
  and and_15 (and_15_out, X_22, out_78);
  and and_16 (and_16_out, X_24, _1_1_out);
  or or_3 (or_3_out, and_16_out, and_15_out, and_14_out, and_13_out);
  not not_18 (not_18_out, _29);
  not not_19 (not_19_out, _29);
  not not_20 (not_20_out, _29);
  not not_21 (not_21_out, _29);
  nand nand_53 (nand_53_out, _29, Enable_2);
  nand nand_54 (nand_54_out, Enable_2, not_18_out);
  nand nand_55 (nand_55_out, _29, Enable_3);
  nand nand_56 (nand_56_out, Enable_3, not_19_out);
  nand nand_57 (nand_57_out, _29, Enable_4);
  nand nand_58 (nand_58_out, Enable_4, not_20_out);
  nand nand_59 (nand_59_out, _29, Enable_5);
  nand nand_60 (nand_60_out, Enable_5, not_21_out);
  nand nand_61 (X_5, nand_53_out, Y_6);
  nand nand_62 (Y_6, X_5, nand_54_out);
  nand nand_63 (X_13, nand_55_out, Y_15);
  nand nand_64 (Y_15, X_13, nand_56_out);
  nand nand_65 (X_19, nand_57_out, Y_22);
  nand nand_66 (Y_22, X_19, nand_58_out);
  nand nand_67 (X_27, nand_59_out, Y_31);
  nand nand_68 (Y_31, X_27, nand_60_out);
  and and_17 (and_17_out, X_5, _0_0_out);
  and and_18 (and_18_out, X_13, Enable_3);
  and and_19 (and_19_out, X_19, out_78);
  and and_20 (and_20_out, X_27, _1_1_out);
  or or_4 (or_4_out, and_20_out, and_19_out, and_18_out, and_17_out);
  not not_22 (not_22_out, _28);
  not not_23 (not_23_out, _28);
  not not_24 (not_24_out, _28);
  not not_25 (not_25_out, _28);
  nand nand_69 (nand_69_out, _28, Enable_2);
  nand nand_70 (nand_70_out, Enable_2, not_22_out);
  nand nand_71 (nand_71_out, _28, Enable_3);
  nand nand_72 (nand_72_out, Enable_3, not_23_out);
  nand nand_73 (nand_73_out, _28, Enable_4);
  nand nand_74 (nand_74_out, Enable_4, not_24_out);
  nand nand_75 (nand_75_out, _28, Enable_5);
  nand nand_76 (nand_76_out, Enable_5, not_25_out);
  nand nand_77 (X_6, nand_69_out, Y_7);
  nand nand_78 (Y_7, X_6, nand_70_out);
  nand nand_79 (X_14, nand_71_out, Y_16);
  nand nand_80 (Y_16, X_14, nand_72_out);
  nand nand_81 (X_20, nand_73_out, Y_23);
  nand nand_82 (Y_23, X_20, nand_74_out);
  nand nand_83 (X_28, nand_75_out, Y_32);
  nand nand_84 (Y_32, X_28, nand_76_out);
  and and_21 (and_21_out, X_6, _0_0_out);
  and and_22 (and_22_out, X_14, _0_1_2_out);
  and and_23 (and_23_out, X_20, out_78);
  and and_24 (and_24_out, X_28, _1_1_out);
  or or_5 (or_5_out, and_24_out, and_23_out, and_22_out, and_21_out);
  not not_26 (not_26_out, _27);
  not not_27 (not_27_out, _27);
  not not_28 (not_28_out, _27);
  not not_29 (not_29_out, _27);
  nand nand_85 (nand_85_out, _27, Enable_2);
  nand nand_86 (nand_86_out, Enable_2, not_26_out);
  nand nand_87 (nand_87_out, _27, Enable_3);
  nand nand_88 (nand_88_out, Enable_3, not_27_out);
  nand nand_89 (nand_89_out, _27, Enable_4);
  nand nand_90 (nand_90_out, Enable_4, not_28_out);
  nand nand_91 (nand_91_out, _27, Enable_5);
  nand nand_92 (nand_92_out, Enable_5, not_29_out);
  nand nand_93 (X_3, nand_85_out, Y_4);
  nand nand_94 (Y_4, X_3, nand_86_out);
  nand nand_95 (X_11, nand_87_out, Y_13);
  nand nand_96 (Y_13, X_11, nand_88_out);
  nand nand_97 (X_17, nand_89_out, Y_19);
  nand nand_98 (Y_19, X_17, nand_90_out);
  nand nand_99 (X_25, nand_91_out, Y_29);
  nand nand_100 (Y_29, X_25, nand_92_out);
  and and_25 (and_25_out, X_3, _0_0_out);
  and and_26 (and_26_out, X_11, _0_1_2_out);
  and and_27 (and_27_out, X_17, out_78);
  and and_28 (and_28_out, X_25, _1_1_out);
  or or_6 (or_6_out, and_28_out, and_27_out, and_26_out, and_25_out);
  not not_30 (not_30_out, _26);
  not not_31 (not_31_out, _26);
  not not_32 (not_32_out, _26);
  not not_33 (not_33_out, _26);
  nand nand_101 (nand_101_out, _26, Enable_2);
  nand nand_102 (nand_102_out, Enable_2, not_30_out);
  nand nand_103 (nand_103_out, _26, Enable_3);
  nand nand_104 (nand_104_out, Enable_3, not_31_out);
  nand nand_105 (nand_105_out, _26, Enable_4);
  nand nand_106 (nand_106_out, Enable_4, not_32_out);
  nand nand_107 (nand_107_out, _26, Enable_5);
  nand nand_108 (nand_108_out, Enable_5, not_33_out);
  nand nand_109 (X_4, nand_101_out, Y_5);
  nand nand_110 (Y_5, X_4, nand_102_out);
  nand nand_111 (X_12, nand_103_out, Y_14);
  nand nand_112 (Y_14, X_12, nand_104_out);
  nand nand_113 (X_18, nand_105_out, Y_20);
  nand nand_114 (Y_20, X_18, nand_106_out);
  nand nand_115 (X_26, nand_107_out, Y_30);
  nand nand_116 (Y_30, X_26, nand_108_out);
  and and_29 (and_29_out, X_4, _0_0_out);
  and and_30 (and_30_out, X_12, _0_1_2_out);
  and and_31 (and_31_out, X_18, out_78);
  and and_32 (and_32_out, X_26, _1_1_out);
  or or_7 (or_7_out, and_32_out, and_31_out, and_30_out, and_29_out);
  not not_34 (not_34_out, _25);
  nand nand_117 (nand_117_out, _25, Enable_2);
  nand nand_118 (nand_118_out, Enable_2, not_35_out);
  not not_35 (not_35_out, _25);
  nand nand_119 (nand_119_out, _25, Enable_3);
  nand nand_120 (nand_120_out, Enable_3, not_36_out);
  not not_36 (not_36_out, _25);
  nand nand_121 (nand_121_out, _25, Enable_4);
  nand nand_122 (nand_122_out, Enable_4, not_37_out);
  not not_37 (not_37_out, _25);
  nand nand_123 (nand_123_out, _25, Enable_5);
  nand nand_124 (nand_124_out, Enable_5, not_34_out);
  nand nand_125 (X_29, nand_123_out, Y_33);
  nand nand_126 (Y_33, X_29, nand_124_out);
  nand nand_127 (X_7, nand_117_out, Y_8);
  nand nand_128 (Y_8, X_7, nand_118_out);
  nand nand_129 (X_15, nand_119_out, Y_17);
  nand nand_130 (Y_17, X_15, nand_120_out);
  nand nand_131 (X_21, nand_121_out, Y_24);
  nand nand_132 (Y_24, X_21, nand_122_out);
  and and_33 (and_33_out, X_7, _0_0_out);
  and and_34 (and_34_out, X_15, _0_1_2_out);
  and and_35 (and_35_out, X_21, out_78);
  and and_36 (and_36_out, X_29, _1_1_out);
  or or_8 (or_8_out, and_36_out, and_35_out, and_34_out, and_33_out);

  assign Data_2 = Y;
  assign Data_3 = Y;
  assign Data_4 = Y;
  assign Data_5 = Y;
  assign Data_6 = _30;
  assign Data_7 = _31;
  assign Data_8 = Y;
  assign out_42 = _29;

  // Notes on the sheet:
  //   Address
  //   Circuit - Gated D Latch
  //   Write Enabled
  //   32
  //   X
  //   X
  //   X
  //   X
  //   Data
  //   Data
  //   Data
  //   Data
  //   Enable
  //   Enable
  //   Enable
  //   Enable
  //   Data
  //   Data
  //   Data
  //   Enable
  //   Enable
  //   Data
  //   Enable
  //   Enable
  //   Data 5
  //   Data
  //   Data
  //   Data
  //   Data
  //   Enable
  //   Enable
  //   Enable
  //   Enable
  //   Data 4
  //   Enable
  //   Enable
  //   Enable
  //   Data 3
  //   Data 2
  //   Data 1
endmodule
