// Logisim project LogisimLab.circ as structural Verilog: 1 circuit, main circuit main
module main (
  input  B1,
  input  B8,
  input  B7,
  input  B6,
  input  B5,
  input  B4,
  input  B3,
  input  B2,
  input  A8,
  input  A7,
  input  A6,
  input  A5,
  input  A4,
  input  A3,
  input  A2,
  input  A1,
  output out_17,
  output out_18,
  output out_19,
  output out_20,
  output out_21,
  output out_22,
  output out_23,
  output out_24,
  output out_25
);

  wire _001_1_2_out, _001_1_3_out, _001_1_4_out, _001_1_5_out, _001_1_6_out, _001_1_7_out, _001_1_out,
       _010_1_2_out, _010_1_3_out, _010_1_4_out, _010_1_5_out, _010_1_6_out, _010_1_7_out, _010_1_out,
       _011_2_2_out, _011_2_3_out, _011_2_4_out, _011_2_5_out, _011_2_6_out, _011_2_7_out, _011_2_out,
       _100_1_2_out, _100_1_3_out, _100_1_4_out, _100_1_5_out, _100_1_6_out, _100_1_7_out, _100_1_out,
       _101_2_2_out, _101_2_3_out, _101_2_4_out, _101_2_5_out, _101_2_6_out, _101_2_7_out, _101_2_out,
       _110_2_2_out, _110_2_3_out, _110_2_4_out, _110_2_5_out, _110_2_6_out, _110_2_7_out, _110_2_out,
       _111_3_2_out, _111_3_3_out, _111_3_4_out, _111_3_5_out, _111_3_6_out, _111_3_7_out, _111_3_out,
       Carry_1_out, Carry_2_out, Carry_3_out, Carry_4_out, Carry_5_out, Carry_6_out, Carry_7_out, not_1_out,
       not_2_out, not_3_out, not_4_out, not_5_out, not_6_out, not_7_out, not_8_out, not_9_out, not_10_out,
       not_11_out, not_12_out, not_13_out, not_14_out, not_15_out, not_16_out, not_17_out, not_18_out,
       not_19_out, not_20_out, not_21_out, not_22_out, not_23_out, not_24_out, not_25_out, not_26_out,
       not_27_out, not_28_out, not_29_out, not_30_out, not_31_out, not_32_out, not_33_out, not_34_out,
       not_35_out, not_36_out, not_37_out, not_38_out, not_39_out, not_40_out, not_41_out, not_42_out,
       not_43_out, not_44_out, not_45_out, not_46_out, not_47_out, not_48_out, not_49_out, not_50_out,
       not_51_out, not_52_out, not_53_out, not_54_out, not_55_out, not_56_out, not_57_out, not_58_out,
       not_59_out, not_60_out, not_61_out, not_62_out, not_63_out;

  and Carry_1 (Carry_1_out, B1, A1);
  not not_1 (not_1_out, A2);
  and _010_1 (_010_1_out, not_1_out, B2, not_2_out);
  not not_2 (not_2_out, Carry_1_out);
  not not_3 (not_3_out, A2);
  not not_4 (not_4_out, B2);
  and _001_1 (_001_1_out, not_3_out, not_4_out, Carry_1_out);
  and _100_1 (_100_1_out, A2, not_5_out, not_6_out);
  not not_5 (not_5_out, B2);
  not not_6 (not_6_out, Carry_1_out);
  and _111_3 (_111_3_out, A2, B2, Carry_1_out);
  not not_7 (not_7_out, A2);
  and _011_2 (_011_2_out, not_7_out, B2, Carry_1_out);
  and _110_2 (_110_2_out, A2, B2, not_8_out);
  not not_8 (not_8_out, Carry_1_out);
  and _101_2 (_101_2_out, A2, not_9_out, Carry_1_out);
  not not_9 (not_9_out, B2);
  not not_10 (not_10_out, A3);
  not not_11 (not_11_out, Carry_2_out);
  not not_12 (not_12_out, A3);
  not not_13 (not_13_out, B3);
  not not_14 (not_14_out, B3);
  not not_15 (not_15_out, Carry_2_out);
  not not_16 (not_16_out, A3);
  not not_17 (not_17_out, Carry_2_out);
  not not_18 (not_18_out, B3);
  not not_19 (not_19_out, A4);
  not not_20 (not_20_out, Carry_3_out);
  not not_21 (not_21_out, A4);
  not not_22 (not_22_out, B4);
  not not_23 (not_23_out, B4);
  not not_24 (not_24_out, Carry_3_out);
  not not_25 (not_25_out, A4);
  not not_26 (not_26_out, Carry_3_out);
  not not_27 (not_27_out, B4);
  not not_28 (not_28_out, A5);
  not not_29 (not_29_out, Carry_4_out);
  not not_30 (not_30_out, A5);
  not not_31 (not_31_out, B5);
  not not_32 (not_32_out, B5);
  not not_33 (not_33_out, Carry_4_out);
  not not_34 (not_34_out, A5);
  not not_35 (not_35_out, Carry_4_out);
  not not_36 (not_36_out, B5);
  not not_37 (not_37_out, A6);
  not not_38 (not_38_out, Carry_5_out);
  not not_39 (not_39_out, A6);
  not not_40 (not_40_out, A6);
  not not_41 (not_41_out, B6);
  not not_42 (not_42_out, Carry_5_out);
  not not_43 (not_43_out, A6);
  not not_44 (not_44_out, Carry_5_out);
  not not_45 (not_45_out, B6);
  not not_46 (not_46_out, A7);
  not not_47 (not_47_out, Carry_6_out);
  not not_48 (not_48_out, A7);
  not not_49 (not_49_out, B7);
  not not_50 (not_50_out, B7);
  not not_51 (not_51_out, Carry_6_out);
  not not_52 (not_52_out, A7);
  not not_53 (not_53_out, Carry_6_out);
  not not_54 (not_54_out, B7);
  not not_55 (not_55_out, A8);
  not not_56 (not_56_out, Carry_7_out);
  not not_57 (not_57_out, A8);
  not not_58 (not_58_out, B8);
  not not_59 (not_59_out, B8);
  not not_60 (not_60_out, Carry_7_out);
  not not_61 (not_61_out, A8);
  not not_62 (not_62_out, Carry_7_out);
  not not_63 (not_63_out, B8);
  xor Output_1 (out_25, B1, A1);
  and _010_1_2 (_010_1_2_out, not_10_out, B3, not_11_out);
  and _001_1_2 (_001_1_2_out, not_12_out, not_13_out, Carry_2_out);
  and _100_1_2 (_100_1_2_out, A3, not_14_out, not_15_out);
  and _111_3_2 (_111_3_2_out, A3, B3, Carry_2_out);
  and _011_2_2 (_011_2_2_out, not_16_out, B3, Carry_2_out);
  and _110_2_2 (_110_2_2_out, A3, B3, not_17_out);
  and _101_2_2 (_101_2_2_out, A3, not_18_out, Carry_2_out);
  and _010_1_3 (_010_1_3_out, not_19_out, B4, not_20_out);
  and _001_1_3 (_001_1_3_out, not_21_out, not_22_out, Carry_3_out);
  and _100_1_3 (_100_1_3_out, A4, not_23_out, not_24_out);
  and _111_3_3 (_111_3_3_out, A4, B4, Carry_3_out);
  and _011_2_3 (_011_2_3_out, not_25_out, B4, Carry_3_out);
  and _110_2_3 (_110_2_3_out, A4, B4, not_26_out);
  and _101_2_3 (_101_2_3_out, A4, not_27_out, Carry_3_out);
  and _010_1_4 (_010_1_4_out, not_28_out, B5, not_29_out);
  and _001_1_4 (_001_1_4_out, not_30_out, not_31_out, Carry_4_out);
  and _100_1_4 (_100_1_4_out, A5, not_32_out, not_33_out);
  and _111_3_4 (_111_3_4_out, A5, B5, Carry_4_out);
  and _011_2_4 (_011_2_4_out, not_34_out, B5, Carry_4_out);
  and _110_2_4 (_110_2_4_out, A5, B5, not_35_out);
  and _101_2_4 (_101_2_4_out, A5, not_36_out, Carry_4_out);
  and _010_1_5 (_010_1_5_out, not_37_out, B6, not_38_out);
  and _001_1_5 (_001_1_5_out, not_39_out, not_40_out, Carry_5_out);
  and _100_1_5 (_100_1_5_out, A6, not_41_out, not_42_out);
  and _111_3_5 (_111_3_5_out, A6, B6, Carry_5_out);
  and _011_2_5 (_011_2_5_out, not_43_out, B6, Carry_5_out);
  and _110_2_5 (_110_2_5_out, A6, B6, not_44_out);
  and _101_2_5 (_101_2_5_out, A6, not_45_out, Carry_5_out);
  and _010_1_6 (_010_1_6_out, not_46_out, B7, not_47_out);
  and _001_1_6 (_001_1_6_out, not_48_out, not_49_out, Carry_6_out);
  and _100_1_6 (_100_1_6_out, A7, not_50_out, not_51_out);
  and _111_3_6 (_111_3_6_out, A7, B7, Carry_6_out);
  and _011_2_6 (_011_2_6_out, not_52_out, B7, Carry_6_out);
  and _110_2_6 (_110_2_6_out, A7, B7, not_53_out);
  and _101_2_6 (_101_2_6_out, A7, not_54_out, Carry_6_out);
  and _010_1_7 (_010_1_7_out, not_55_out, B8, not_56_out);
  and _001_1_7 (_001_1_7_out, not_57_out, not_58_out, Carry_7_out);
  and _100_1_7 (_100_1_7_out, A8, not_59_out, not_60_out);
  and _111_3_7 (_111_3_7_out, A8, B8, Carry_7_out);
  and _011_2_7 (_011_2_7_out, not_61_out, B8, Carry_7_out);
  and _110_2_7 (_110_2_7_out, A8, B8, not_62_out);
  and _101_2_7 (_101_2_7_out, A8, not_63_out, Carry_7_out);
  or Output_2 (out_24, _010_1_out, _001_1_out, _100_1_out, _111_3_out);
  or Carry_2 (Carry_2_out, _111_3_out, _011_2_out, _110_2_out, _101_2_out);
  or Output_3 (out_23, _010_1_2_out, _001_1_2_out, _100_1_2_out, _111_3_2_out);
  or Carry_3 (Carry_3_out, _111_3_2_out, _011_2_2_out, _110_2_2_out, _101_2_2_out);
  or Output_4 (out_22, _010_1_3_out, _001_1_3_out, _100_1_3_out, _111_3_3_out);
  or Carry_4 (Carry_4_out, _111_3_3_out, _011_2_3_out, _110_2_3_out, _101_2_3_out);
  or Output_5 (out_21, _010_1_4_out, _001_1_4_out, _100_1_4_out, _111_3_4_out);
  or Carry_5 (Carry_5_out, _111_3_4_out, _011_2_4_out, _110_2_4_out, _101_2_4_out);
  or Output_6 (out_20, _010_1_5_out, _001_1_5_out, _100_1_5_out, _111_3_5_out);
  or Carry_6 (Carry_6_out, _111_3_5_out, _011_2_5_out, _110_2_5_out, _101_2_5_out);
  or Output_7 (out_19, _010_1_6_out, _001_1_6_out, _100_1_6_out, _111_3_6_out);
  or Carry_7 (Carry_7_out, _111_3_6_out, _011_2_6_out, _110_2_6_out, _101_2_6_out);
  or Output_8 (out_18, _010_1_7_out, _001_1_7_out, _100_1_7_out, _111_3_7_out);
  or Carry_8 (out_17, _111_3_7_out, _011_2_7_out, _110_2_7_out, _101_2_7_out);
endmodule
