// Logisim project LogisimLab_3_24_2015.circ as structural Verilog: 1 circuit, main circuit main
module main (
  input  A8,
  input  A7,
  input  A6,
  input  A5,
  input  A4,
  input  A3,
  input  A2,
  input  A1,
  input  B8,
  input  B7,
  input  B6,
  input  B5,
  input  B4,
  input  B3,
  input  B2,
  input  B1,
  output out_17,
  output out_18,
  output out_19,
  output out_20,
  output out_21,
  output out_22
);

  wire _001_1_2_out, _001_1_3_out, _001_1_out, _010_1_2_out, _010_1_3_out, _010_1_out, _011_2_2_out,
       _011_2_3_out, _011_2_out, _100_1_2_out, _100_1_3_out, _100_1_out, _101_2_2_out, _101_2_3_out,
       _101_2_out, _110_2_2_out, _110_2_3_out, _110_2_out, _111_3_2_out, _111_3_3_out, _111_3_out,
       Carry_1_out, Carry_2_out, Carry_3_out, not_1_out, not_2_out, not_3_out, not_4_out, not_5_out,
       not_6_out, not_7_out, not_8_out, not_9_out, not_10_out, not_11_out, not_12_out, not_13_out,
       not_14_out, not_15_out, not_16_out, not_17_out, not_18_out, not_19_out, not_20_out, not_21_out,
       not_22_out, not_23_out, not_24_out, not_25_out, not_26_out, not_27_out;

  and Carry_1 (Carry_1_out, B1, A1, A1, A1);
  and _111_3 (_111_3_out, A2, B2, Carry_1_out);
  not not_1 (not_1_out, A2);
  and _011_2 (_011_2_out, not_1_out, Carry_1_out);
  and _101_2 (_101_2_out, A2, not_2_out, Carry_1_out);
  not not_2 (not_2_out, B2);
  and _110_2 (_110_2_out, A2, B2, not_3_out);
  not not_3 (not_3_out, Carry_1_out);
  not not_4 (not_4_out, A2);
  not not_5 (not_5_out, B2);
  and _001_1 (_001_1_out, not_4_out, not_5_out, Carry_1_out);
  not not_6 (not_6_out, A2);
  and _010_1 (_010_1_out, not_6_out, B2, not_7_out);
  not not_7 (not_7_out, Carry_1_out);
  and _100_1 (_100_1_out, A2, not_8_out, not_9_out);
  not not_8 (not_8_out, B2);
  not not_9 (not_9_out, Carry_1_out);
  and _111_3_2 (_111_3_2_out, A3, B3, Carry_2_out);
  not not_10 (not_10_out, A3);
  and _011_2_2 (_011_2_2_out, not_10_out, B3, Carry_2_out);
  and _101_2_2 (_101_2_2_out, A3, not_11_out, Carry_2_out);
  not not_11 (not_11_out, B3);
  and _110_2_2 (_110_2_2_out, A3, B3, not_12_out);
  not not_12 (not_12_out, Carry_2_out);
  not not_13 (not_13_out, A3);
  and _001_1_2 (_001_1_2_out, not_13_out, not_14_out, Carry_2_out);
  not not_14 (not_14_out, B3);
  not not_15 (not_15_out, A3);
  and _010_1_2 (_010_1_2_out, not_15_out, B3, not_16_out);
  not not_16 (not_16_out, Carry_2_out);
  and _100_1_2 (_100_1_2_out, A3, not_17_out, not_18_out);
  not not_17 (not_17_out, B3);
  not not_18 (not_18_out, Carry_2_out);
  and _111_3_3 (_111_3_3_out, A4, B4, Carry_3_out);
  not not_19 (not_19_out, A4);
  and _011_2_3 (_011_2_3_out, not_19_out, B4, Carry_3_out);
  and _101_2_3 (_101_2_3_out, A4, not_20_out, Carry_3_out);
  not not_20 (not_20_out, B4);
  and _110_2_3 (_110_2_3_out, A4, B4, not_21_out);
  not not_21 (not_21_out, Carry_3_out);
  not not_22 (not_22_out, A4);
  and _001_1_3 (_001_1_3_out, not_22_out, not_23_out, Carry_3_out);
  not not_23 (not_23_out, B4);
  not not_24 (not_24_out, A4);
  and _010_1_3 (_010_1_3_out, not_24_out, B4, not_25_out);
  not not_25 (not_25_out, Carry_3_out);
  not not_26 (not_26_out, B4);
  and _100_1_3 (_100_1_3_out, A4, not_26_out, not_27_out);
  not not_27 (not_27_out, Carry_3_out);
  xor Output_1 (out_17, B1, A1);
  or Carry_2 (Carry_2_out, _111_3_out, _011_2_out, _101_2_out, _110_2_out);
  or Output_2 (out_18, _111_3_out, _010_1_out, _001_1_out, _100_1_out);
  or Carry_3 (Carry_3_out, _111_3_2_out, _011_2_2_out, _101_2_2_out, _110_2_2_out);
  or Output_3 (out_19, _111_3_2_out, _010_1_2_out, _001_1_2_out, _100_1_2_out);
  // OR_Gate Carry_4 has open pins: in0=_111_3_3_out, in1=_011_2_3_out, in2=_101_2_3_out, in3=_110_2_3_out, out=open
  or Output_4 (out_20, _111_3_3_out, _010_1_3_out, _001_1_3_out, _100_1_3_out);
endmodule
