// Logisim project AnkanBasu_Logisim_Working_Files_5_5_2015_8_00_pm.circ as structural Verilog: 20 circuits, main circuit main
module main (
  input  [15:0] in_1,
  input  [7:0] _8_bit_Number_A,
  input  [7:0] _8_bit_Number_B,
  output [15:0] out_4,
  output [7:0] out_5,
  output [7:0] out_6,
  output [7:0] out_7
);

  wire Addition_Module_out_25, Instruction_Set_div, Instruction_Set_mul, Instruction_Set_out_17,
       Instruction_Set_sub;
  wire [7:0] Control_2_out_10, Control_3_out_10, Control_4_out_10, Control_5_out_10, Control_6_out_10,
       Control_7_out_10, Control_8_out_10, Control_out_10;

  MUX_16_bit_direction Instruction_Set (
    .LS(in_1[0]), .in_2(in_1[1]), .in_3(in_1[2]), .in_4(in_1[3]), .in_5(in_1[4]), .in_6(in_1[5]),
    .in_7(in_1[6]), .in_8(in_1[7]), .in_9(in_1[8]), .in_10(in_1[9]), .in_11(in_1[10]), .in_12(in_1[11]),
    .in_13(in_1[12]), .in_14(in_1[13]), .in_15(in_1[14]), .MS(in_1[15]), .out_17(Instruction_Set_out_17),
    .SUB(Instruction_Set_sub), .MUL(Instruction_Set_mul), .DIV(Instruction_Set_div));
  Control_8_bit Control (
    .in_1(_8_bit_Number_A[0]), .in_2(_8_bit_Number_A[1]), .in_3(_8_bit_Number_A[2]),
    .in_4(_8_bit_Number_A[3]), .in_5(_8_bit_Number_A[4]), .in_6(_8_bit_Number_A[5]),
    .in_7(_8_bit_Number_A[6]), .in_8(_8_bit_Number_A[7]), .InputFromMux(Instruction_Set_out_17),
    .out_10(Control_out_10[0]), .out_11(Control_out_10[1]), .out_12(Control_out_10[2]),
    .out_13(Control_out_10[3]), .out_14(Control_out_10[4]), .out_15(Control_out_10[5]),
    .out_16(Control_out_10[6]), .out_17(Control_out_10[7]));
  Control_8_bit Control_2 (
    .in_1(_8_bit_Number_B[0]), .in_2(_8_bit_Number_B[1]), .in_3(_8_bit_Number_B[2]),
    .in_4(_8_bit_Number_B[3]), .in_5(_8_bit_Number_B[4]), .in_6(_8_bit_Number_B[5]),
    .in_7(_8_bit_Number_B[6]), .in_8(_8_bit_Number_B[7]), .InputFromMux(Instruction_Set_out_17),
    .out_10(Control_2_out_10[0]), .out_11(Control_2_out_10[1]), .out_12(Control_2_out_10[2]),
    .out_13(Control_2_out_10[3]), .out_14(Control_2_out_10[4]), .out_15(Control_2_out_10[5]),
    .out_16(Control_2_out_10[6]), .out_17(Control_2_out_10[7]));
  Addition Addition_Module (
    .A1(Control_out_10[0]), .A2(Control_out_10[1]), .A3(Control_out_10[2]), .A4(Control_out_10[3]),
    .A5(Control_out_10[4]), .A6(Control_out_10[5]), .A7(Control_out_10[6]), .A8(Control_out_10[7]),
    .B1(Control_2_out_10[0]), .B2(Control_2_out_10[1]), .B3(Control_2_out_10[2]), .B4(Control_2_out_10[3]),
    .B5(Control_2_out_10[4]), .B6(Control_2_out_10[5]), .B7(Control_2_out_10[6]), .B8(Control_2_out_10[7]),
    .out_17(out_6[0]), .out_18(out_6[1]), .out_19(out_6[2]), .out_20(out_6[3]), .out_21(out_6[4]),
    .out_22(out_6[5]), .out_23(out_6[6]), .out_24(out_6[7]), .out_25(Addition_Module_out_25));
  Control_8_bit Control_3 (
    .in_1(_8_bit_Number_A[0]), .in_2(_8_bit_Number_A[1]), .in_3(_8_bit_Number_A[2]),
    .in_4(_8_bit_Number_A[3]), .in_5(_8_bit_Number_A[4]), .in_6(_8_bit_Number_A[5]),
    .in_7(_8_bit_Number_A[6]), .in_8(_8_bit_Number_A[7]), .InputFromMux(Instruction_Set_sub),
    .out_10(Control_3_out_10[0]), .out_11(Control_3_out_10[1]), .out_12(Control_3_out_10[2]),
    .out_13(Control_3_out_10[3]), .out_14(Control_3_out_10[4]), .out_15(Control_3_out_10[5]),
    .out_16(Control_3_out_10[6]), .out_17(Control_3_out_10[7]));
  Control_8_bit Control_4 (
    .in_1(_8_bit_Number_B[0]), .in_2(_8_bit_Number_B[1]), .in_3(_8_bit_Number_B[2]),
    .in_4(_8_bit_Number_B[3]), .in_5(_8_bit_Number_B[4]), .in_6(_8_bit_Number_B[5]),
    .in_7(_8_bit_Number_B[6]), .in_8(_8_bit_Number_B[7]), .InputFromMux(Instruction_Set_sub),
    .out_10(Control_4_out_10[0]), .out_11(Control_4_out_10[1]), .out_12(Control_4_out_10[2]),
    .out_13(Control_4_out_10[3]), .out_14(Control_4_out_10[4]), .out_15(Control_4_out_10[5]),
    .out_16(Control_4_out_10[6]), .out_17(Control_4_out_10[7]));
  Subtraction Subtraction_Module (
    .A1(Control_3_out_10[0]), .A2(Control_3_out_10[1]), .A3(Control_3_out_10[2]), .A4(Control_3_out_10[3]),
    .A5(Control_3_out_10[4]), .A6(Control_3_out_10[5]), .A7(Control_3_out_10[6]), .A8(Control_3_out_10[7]),
    .B1(Control_4_out_10[0]), .B2(Control_4_out_10[1]), .B3(Control_4_out_10[2]), .B4(Control_4_out_10[3]),
    .B5(Control_4_out_10[4]), .B6(Control_4_out_10[5]), .B7(Control_4_out_10[6]), .B8(Control_4_out_10[7]),
    .out_17(out_7[0]), .out_18(out_7[1]), .out_19(out_7[2]), .out_20(out_7[3]), .out_21(out_7[4]),
    .out_22(out_7[5]), .out_23(out_7[6]), .out_24(out_7[7]));
  Control_8_bit Control_5 (
    .in_1(_8_bit_Number_A[0]), .in_2(_8_bit_Number_A[1]), .in_3(_8_bit_Number_A[2]),
    .in_4(_8_bit_Number_A[3]), .in_5(_8_bit_Number_A[4]), .in_6(_8_bit_Number_A[5]),
    .in_7(_8_bit_Number_A[6]), .in_8(_8_bit_Number_A[7]), .InputFromMux(Instruction_Set_mul),
    .out_10(Control_5_out_10[0]), .out_11(Control_5_out_10[1]), .out_12(Control_5_out_10[2]),
    .out_13(Control_5_out_10[3]), .out_14(Control_5_out_10[4]), .out_15(Control_5_out_10[5]),
    .out_16(Control_5_out_10[6]), .out_17(Control_5_out_10[7]));
  Control_8_bit Control_6 (
    .in_1(_8_bit_Number_B[0]), .in_2(_8_bit_Number_B[1]), .in_3(_8_bit_Number_B[2]),
    .in_4(_8_bit_Number_B[3]), .in_5(_8_bit_Number_B[4]), .in_6(_8_bit_Number_B[5]),
    .in_7(_8_bit_Number_B[6]), .in_8(_8_bit_Number_B[7]), .InputFromMux(Instruction_Set_mul),
    .out_10(Control_6_out_10[0]), .out_11(Control_6_out_10[1]), .out_12(Control_6_out_10[2]),
    .out_13(Control_6_out_10[3]), .out_14(Control_6_out_10[4]), .out_15(Control_6_out_10[5]),
    .out_16(Control_6_out_10[6]), .out_17(Control_6_out_10[7]));
  Multiplication Multiplication_Module (
    .in_1(Control_5_out_10[0]), .in_2(Control_5_out_10[1]), .in_3(Control_5_out_10[2]),
    .in_4(Control_5_out_10[3]), .a5(Control_5_out_10[4]), .a6(Control_5_out_10[5]), .a7(Control_5_out_10[6]),
    .a8(Control_5_out_10[7]), .b1(Control_6_out_10[0]), .b2(Control_6_out_10[1]), .b3(Control_6_out_10[2]),
    .b4(Control_6_out_10[3]), .b5(Control_6_out_10[4]), .b6(Control_6_out_10[5]), .b7(Control_6_out_10[6]),
    .b8(Control_6_out_10[7]), .out_17(out_4[0]), .out_18(out_4[1]), .out_19(out_4[2]), .out_20(out_4[3]),
    .out_21(out_4[4]), .out_22(out_4[5]), .out_23(out_4[6]), .out_24(out_4[7]), .out_25(out_4[8]),
    .out_26(out_4[9]), .out_27(out_4[10]), .out_28(out_4[11]), .out_29(out_4[12]), .out_30(out_4[13]),
    .out_31(out_4[14]), .out_32(out_4[15]));
  Control_8_bit Control_7 (
    .in_1(_8_bit_Number_A[0]), .in_2(_8_bit_Number_A[1]), .in_3(_8_bit_Number_A[2]),
    .in_4(_8_bit_Number_A[3]), .in_5(_8_bit_Number_A[4]), .in_6(_8_bit_Number_A[5]),
    .in_7(_8_bit_Number_A[6]), .in_8(_8_bit_Number_A[7]), .InputFromMux(Instruction_Set_div),
    .out_10(Control_7_out_10[0]), .out_11(Control_7_out_10[1]), .out_12(Control_7_out_10[2]),
    .out_13(Control_7_out_10[3]), .out_14(Control_7_out_10[4]), .out_15(Control_7_out_10[5]),
    .out_16(Control_7_out_10[6]), .out_17(Control_7_out_10[7]));
  Control_8_bit Control_8 (
    .in_1(_8_bit_Number_B[0]), .in_2(_8_bit_Number_B[1]), .in_3(_8_bit_Number_B[2]),
    .in_4(_8_bit_Number_B[3]), .in_5(_8_bit_Number_B[4]), .in_6(_8_bit_Number_B[5]),
    .in_7(_8_bit_Number_B[6]), .in_8(_8_bit_Number_B[7]), .InputFromMux(Instruction_Set_div),
    .out_10(Control_8_out_10[0]), .out_11(Control_8_out_10[1]), .out_12(Control_8_out_10[2]),
    .out_13(Control_8_out_10[3]), .out_14(Control_8_out_10[4]), .out_15(Control_8_out_10[5]),
    .out_16(Control_8_out_10[6]), .out_17(Control_8_out_10[7]));
  Div_8_bit_circuit div_8_bit_circuit_1 (
    .A1(Control_7_out_10[0]), .a2(Control_7_out_10[1]), .a3(Control_7_out_10[2]), .a4(Control_7_out_10[3]),
    .a5(Control_7_out_10[4]), .a6(Control_7_out_10[5]), .a7(Control_7_out_10[6]), .a8(Control_7_out_10[7]),
    .A1_2(Control_8_out_10[0]), .a2_2(Control_8_out_10[1]), .a3_2(Control_8_out_10[2]),
    .a4_2(Control_8_out_10[3]), .a5_2(Control_8_out_10[4]), .a6_2(Control_8_out_10[5]),
    .a7_2(Control_8_out_10[6]), .a8_2(Control_8_out_10[7]), .Final_Answer(out_5));  // open: out_18

  // Notes on the sheet:
  //   A
  //   B
  //   ADD: 1010  1110  1110  1101 
  //   SUB: 0000  1000  1111 1001
  //   MUL: 1100  0110  0001 1110
  //   DIV: 0100  1010 0101 0010 
  //   Instruction Set
  //   A+B
  //   Cout
  //   Addition Answer
  //   A-B
  //   Subtraction Answer
  //   A*B
  //   Multiplication Answer
  //   A/B
  //   Division Answer
endmodule

module FullAdder (
  input  A,
  input  B,
  input  Cin,
  output Cout,
  output S
);

  wire and_1_out, and_2_out, xor_2_out;

  or or_1 (Cout, and_1_out, and_2_out);
  and and_1 (and_1_out, Cin, B);
  and and_2 (and_2_out, A, xor_2_out);
  xor xor_1 (S, A, xor_2_out);
  xor xor_2 (xor_2_out, B, Cin);

  // Notes on the sheet:
  //   Full Adder
endmodule

module Subtraction (
  input  A1,
  input  A2,
  input  A3,
  input  A4,
  input  A5,
  input  A6,
  input  A7,
  input  A8,
  input  B1,
  input  B2,
  input  B3,
  input  B4,
  input  B5,
  input  B6,
  input  B7,
  input  B8,
  output out_17,
  output out_18,
  output out_19,
  output out_20,
  output out_21,
  output out_22,
  output out_23,
  output out_24
);

  wire _001_1_2_out, _001_1_3_out, _001_1_4_out, _001_1_5_out, _001_1_6_out, _001_1_7_out, _001_1_out,
       _010_1_2_out, _010_1_3_out, _010_1_4_out, _010_1_5_out, _010_1_6_out, _010_1_7_out, _010_1_out,
       _011_2_2_out, _011_2_3_out, _011_2_4_out, _011_2_5_out, _011_2_6_out, _011_2_7_out, _011_2_out,
       _100_1_2_out, _100_1_3_out, _100_1_4_out, _100_1_5_out, _100_1_6_out, _100_1_7_out, _100_1_out,
       _101_2_2_out, _101_2_3_out, _101_2_4_out, _101_2_5_out, _101_2_6_out, _101_2_7_out, _101_2_out,
       _110_2_2_out, _110_2_3_out, _110_2_4_out, _110_2_5_out, _110_2_6_out, _110_2_7_out, _110_2_out,
       _111_3_2_out, _111_3_3_out, _111_3_4_out, _111_3_5_out, _111_3_6_out, _111_3_7_out, _111_3_out,
       Carry_1_out, Carry_2_out, Carry_2_out_2, Carry_3_out, Carry_3_out_2, Carry_4_out, Carry_4_out_2,
       Carry_5_out, Carry_5_out_2, Carry_6_out, Carry_6_out_2, Carry_7_out, Carry_7_out_2, Carry_8_out,
       Carry_8_out_2, Carry_out, not_1_out, not_2_out, not_3_out, not_4_out, not_5_out, not_6_out, not_7_out,
       not_8_out, not_9_out, not_10_out, not_11_out, not_12_out, not_13_out, not_14_out, not_15_out,
       not_16_out, not_17_out, not_18_out, not_19_out, not_20_out, not_21_out, not_22_out, not_23_out,
       not_24_out, not_25_out, not_26_out, not_27_out, not_28_out, not_29_out, not_30_out, not_31_out,
       not_32_out, not_33_out, not_34_out, not_35_out, not_36_out, not_37_out, not_38_out, not_39_out,
       not_40_out, not_41_out, not_42_out, not_43_out, not_44_out, not_45_out, not_46_out, not_47_out,
       not_48_out, not_49_out, not_50_out, not_51_out, not_52_out, not_53_out, not_54_out, not_55_out,
       not_56_out, not_57_out, not_58_out, not_59_out, not_60_out, not_61_out, not_62_out, not_63_out,
       not_64_out, not_65_out, not_66_out, not_67_out, not_68_out, not_69_out, not_70_out, not_71_out,
       Sum_2_out, Sum_3_out, Sum_4_out, Sum_5_out, Sum_6_out, Sum_7_out, Sum_8_out, Sum_out;

  not not_1 (not_1_out, B7);
  not not_2 (not_2_out, B8);
  not not_3 (not_3_out, B6);
  not not_4 (not_4_out, B5);
  and Carry (Carry_out, not_2_out, Carry_3_out);
  not not_5 (not_5_out, B4);
  and Carry_2 (Carry_2_out, not_3_out, Carry_4_out);
  and Carry_3 (Carry_3_out, not_1_out, Carry_2_out);
  xor Sum (Sum_out, not_1_out, Carry_2_out);
  xor Sum_2 (Sum_2_out, not_2_out, Carry_3_out);
  not not_6 (not_6_out, B3);
  and Carry_4 (Carry_4_out, not_4_out, Carry_6_out);
  xor Sum_3 (Sum_3_out, not_3_out, Carry_4_out);
  not not_7 (not_7_out, B1);
  not not_8 (not_8_out, B2);
  and Carry_5 (Carry_5_out, not_6_out, Carry_7_out);
  and Carry_6 (Carry_6_out, not_5_out, Carry_5_out);
  xor Sum_4 (Sum_4_out, not_5_out, Carry_5_out);
  xor Sum_5 (Sum_5_out, not_4_out, Carry_6_out);
  and Carry_7 (Carry_7_out, not_8_out, Carry_8_out);
  xor Sum_6 (Sum_6_out, not_6_out, Carry_7_out);
  and Carry_8 (Carry_8_out, not_7_out, 1'b1);
  xor Sum_7 (Sum_7_out, not_7_out, 1'b1);
  xor Sum_8 (Sum_8_out, not_8_out, Carry_8_out);
  and Carry_1 (Carry_1_out, A1, Sum_7_out);
  not not_9 (not_9_out, Sum_8_out);
  and _010_1 (_010_1_out, not_9_out, A2, not_10_out);
  not not_10 (not_10_out, Carry_1_out);
  not not_11 (not_11_out, Sum_8_out);
  not not_12 (not_12_out, A2);
  and _001_1 (_001_1_out, not_11_out, not_12_out, Carry_1_out);
  not not_13 (not_13_out, A2);
  and _100_1 (_100_1_out, Sum_8_out, not_13_out, not_14_out);
  not not_14 (not_14_out, Carry_1_out);
  and _111_3 (_111_3_out, Sum_8_out, A2, Carry_1_out);
  not not_15 (not_15_out, Sum_8_out);
  and _011_2 (_011_2_out, not_15_out, A2, Carry_1_out);
  and _110_2 (_110_2_out, Sum_8_out, A2, not_16_out);
  not not_16 (not_16_out, Carry_1_out);
  not not_17 (not_17_out, A2);
  and _101_2 (_101_2_out, Sum_8_out, not_17_out, Carry_1_out);
  not not_18 (not_18_out, Sum_6_out);
  and _010_1_2 (_010_1_2_out, not_18_out, A3, not_19_out);
  not not_19 (not_19_out, Carry_2_out_2);
  not not_20 (not_20_out, Sum_6_out);
  not not_21 (not_21_out, A3);
  and _001_1_2 (_001_1_2_out, not_20_out, not_21_out, Carry_2_out_2);
  and _100_1_2 (_100_1_2_out, Sum_6_out, not_22_out, not_23_out);
  not not_22 (not_22_out, A3);
  not not_23 (not_23_out, Carry_2_out_2);
  and _111_3_2 (_111_3_2_out, Sum_6_out, A3, Carry_2_out_2);
  not not_24 (not_24_out, Sum_6_out);
  and _011_2_2 (_011_2_2_out, not_24_out, A3, Carry_2_out_2);
  and _110_2_2 (_110_2_2_out, Sum_6_out, A3, not_25_out);
  not not_25 (not_25_out, Carry_2_out_2);
  and _101_2_2 (_101_2_2_out, Sum_6_out, not_26_out, Carry_2_out_2);
  not not_26 (not_26_out, A3);
  not not_27 (not_27_out, Sum_4_out);
  and _010_1_3 (_010_1_3_out, not_27_out, A4, not_28_out);
  not not_28 (not_28_out, Carry_3_out_2);
  not not_29 (not_29_out, Sum_4_out);
  not not_30 (not_30_out, A4);
  and _001_1_3 (_001_1_3_out, not_29_out, not_30_out, Carry_3_out_2);
  and _100_1_3 (_100_1_3_out, Sum_4_out, not_31_out, not_32_out);
  not not_31 (not_31_out, A4);
  not not_32 (not_32_out, Carry_3_out_2);
  and _111_3_3 (_111_3_3_out, Sum_4_out, A4, Carry_3_out_2);
  not not_33 (not_33_out, Sum_4_out);
  and _011_2_3 (_011_2_3_out, not_33_out, A4, Carry_3_out_2);
  and _110_2_3 (_110_2_3_out, Sum_4_out, A4, not_34_out);
  not not_34 (not_34_out, Carry_3_out_2);
  and _101_2_3 (_101_2_3_out, Sum_4_out, not_35_out, Carry_3_out_2);
  not not_35 (not_35_out, A4);
  not not_36 (not_36_out, Sum_5_out);
  and _010_1_4 (_010_1_4_out, not_36_out, A5, not_37_out);
  not not_37 (not_37_out, Carry_4_out_2);
  not not_38 (not_38_out, Sum_5_out);
  and _001_1_4 (_001_1_4_out, not_38_out, not_39_out, Carry_4_out_2);
  not not_39 (not_39_out, A5);
  not not_40 (not_40_out, A5);
  and _100_1_4 (_100_1_4_out, Sum_5_out, not_40_out, not_41_out);
  not not_41 (not_41_out, Carry_4_out_2);
  and _111_3_4 (_111_3_4_out, Sum_5_out, A5, Carry_4_out_2);
  not not_42 (not_42_out, Sum_5_out);
  and _011_2_4 (_011_2_4_out, not_42_out, A5, Carry_4_out_2);
  and _110_2_4 (_110_2_4_out, Sum_5_out, A5, not_43_out);
  not not_43 (not_43_out, Carry_4_out_2);
  and _101_2_4 (_101_2_4_out, Sum_5_out, not_44_out, Carry_4_out_2);
  not not_44 (not_44_out, A5);
  not not_45 (not_45_out, Sum_3_out);
  and _010_1_5 (_010_1_5_out, not_45_out, A6, not_46_out);
  not not_46 (not_46_out, Carry_5_out_2);
  not not_47 (not_47_out, Sum_3_out);
  and _001_1_5 (_001_1_5_out, not_47_out, not_48_out, Carry_5_out_2);
  not not_48 (not_48_out, A7);
  and _100_1_5 (_100_1_5_out, Sum_3_out, not_49_out, not_50_out);
  not not_49 (not_49_out, A6);
  not not_50 (not_50_out, Carry_5_out_2);
  and _111_3_5 (_111_3_5_out, Sum_3_out, A6, Carry_5_out_2);
  not not_51 (not_51_out, Sum_3_out);
  and _011_2_5 (_011_2_5_out, not_51_out, A6, Carry_5_out_2);
  and _110_2_5 (_110_2_5_out, Sum_3_out, A6, not_52_out);
  not not_52 (not_52_out, Carry_5_out_2);
  and _101_2_5 (_101_2_5_out, Sum_3_out, not_53_out, Carry_5_out_2);
  not not_53 (not_53_out, A6);
  not not_54 (not_54_out, Sum_out);
  and _010_1_6 (_010_1_6_out, not_54_out, A7, not_55_out);
  not not_55 (not_55_out, Carry_6_out_2);
  not not_56 (not_56_out, Sum_out);
  and _001_1_6 (_001_1_6_out, not_56_out, not_57_out, Carry_6_out_2);
  not not_57 (not_57_out, A7);
  not not_58 (not_58_out, A7);
  and _100_1_6 (_100_1_6_out, Sum_out, not_58_out, not_59_out);
  not not_59 (not_59_out, Carry_6_out_2);
  and _111_3_6 (_111_3_6_out, Sum_out, A7, Carry_6_out_2);
  not not_60 (not_60_out, Sum_out);
  and _011_2_6 (_011_2_6_out, not_60_out, A7, Carry_6_out_2);
  and _110_2_6 (_110_2_6_out, Sum_out, A7, not_61_out);
  not not_61 (not_61_out, Carry_6_out_2);
  not not_62 (not_62_out, A7);
  and _101_2_6 (_101_2_6_out, Sum_out, not_62_out, Carry_6_out_2);
  not not_63 (not_63_out, Sum_2_out);
  and _010_1_7 (_010_1_7_out, not_63_out, A8, not_64_out);
  not not_64 (not_64_out, Carry_7_out_2);
  not not_65 (not_65_out, Sum_2_out);
  and _001_1_7 (_001_1_7_out, not_65_out, not_66_out, Carry_7_out_2);
  not not_66 (not_66_out, A8);
  and _100_1_7 (_100_1_7_out, Sum_2_out, not_67_out, not_68_out);
  not not_67 (not_67_out, A8);
  not not_68 (not_68_out, Carry_7_out_2);
  and _111_3_7 (_111_3_7_out, Sum_2_out, A8, Carry_7_out_2);
  not not_69 (not_69_out, Sum_2_out);
  and _011_2_7 (_011_2_7_out, not_69_out, A8, Carry_7_out_2);
  and _110_2_7 (_110_2_7_out, Sum_2_out, A8, not_70_out);
  not not_70 (not_70_out, Carry_7_out_2);
  not not_71 (not_71_out, A8);
  and _101_2_7 (_101_2_7_out, Sum_2_out, not_71_out, Carry_7_out_2);
  xor Output_1 (out_17, A1, Sum_7_out);
  or Output_2 (out_18, _010_1_out, _001_1_out, _100_1_out, _111_3_out);
  or Carry_2_dup2 (Carry_2_out_2, _111_3_out, _011_2_out, _110_2_out, _101_2_out);
  or Output_3 (out_19, _010_1_2_out, _001_1_2_out, _100_1_2_out, _111_3_2_out);
  or Carry_3_dup2 (Carry_3_out_2, _111_3_2_out, _011_2_2_out, _110_2_2_out, _101_2_2_out);
  or Output_4 (out_20, _010_1_3_out, _001_1_3_out, _100_1_3_out, _111_3_3_out);
  or Carry_4_dup2 (Carry_4_out_2, _111_3_3_out, _011_2_3_out, _110_2_3_out, _101_2_3_out);
  or Output_5 (out_21, _010_1_4_out, _001_1_4_out, _100_1_4_out, _111_3_4_out);
  or Carry_5_dup2 (Carry_5_out_2, _111_3_4_out, _011_2_4_out, _110_2_4_out, _101_2_4_out);
  or Output_6 (out_22, _010_1_5_out, _001_1_5_out, _100_1_5_out, _111_3_5_out);
  or Carry_6_dup2 (Carry_6_out_2, _111_3_5_out, _011_2_5_out, _110_2_5_out, _101_2_5_out);
  or Output_7 (out_23, _010_1_6_out, _001_1_6_out, _100_1_6_out, _111_3_6_out);
  or Carry_7_dup2 (Carry_7_out_2, _111_3_6_out, _011_2_6_out, _110_2_6_out, _101_2_6_out);
  or Output_8 (out_24, _010_1_7_out, _001_1_7_out, _100_1_7_out, _111_3_7_out);
  or Carry_8_dup2 (Carry_8_out_2, _111_3_7_out, _011_2_7_out, _110_2_7_out, _101_2_7_out);

  // Notes on the sheet:
  //   B
  //   A
  //   A-B
endmodule

module Addition (
  input  A1,
  input  A2,
  input  A3,
  input  A4,
  input  A5,
  input  A6,
  input  A7,
  input  A8,
  input  B1,
  input  B2,
  input  B3,
  input  B4,
  input  B5,
  input  B6,
  input  B7,
  input  B8,
  output out_17,
  output out_18,
  output out_19,
  output out_20,
  output out_21,
  output out_22,
  output out_23,
  output out_24,
  output out_25
);

  wire _001_1_2_out, _001_1_3_out, _001_1_4_out, _001_1_5_out, _001_1_6_out, _001_1_7_out, _001_1_out,
       _010_1_2_out, _010_1_3_out, _010_1_4_out, _010_1_5_out, _010_1_6_out, _010_1_7_out, _010_1_out,
       _011_2_2_out, _011_2_3_out, _011_2_4_out, _011_2_5_out, _011_2_6_out, _011_2_7_out, _011_2_out,
       _100_1_2_out, _100_1_3_out, _100_1_4_out, _100_1_5_out, _100_1_6_out, _100_1_7_out, _100_1_out,
       _101_2_2_out, _101_2_3_out, _101_2_4_out, _101_2_5_out, _101_2_6_out, _101_2_7_out, _101_2_out,
       _110_2_2_out, _110_2_3_out, _110_2_4_out, _110_2_5_out, _110_2_6_out, _110_2_7_out, _110_2_out,
       _111_3_2_out, _111_3_3_out, _111_3_4_out, _111_3_5_out, _111_3_6_out, _111_3_7_out, _111_3_out,
       Carry_1_out, Carry_2_out, Carry_3_out, Carry_4_out, Carry_5_out, Carry_6_out, Carry_7_out, not_1_out,
       not_2_out, not_3_out, not_4_out, not_5_out, not_6_out, not_7_out, not_8_out, not_9_out, not_10_out,
       not_11_out, not_12_out, not_13_out, not_14_out, not_15_out, not_16_out, not_17_out, not_18_out,
       not_19_out, not_20_out, not_21_out, not_22_out, not_23_out, not_24_out, not_25_out, not_26_out,
       not_27_out, not_28_out, not_29_out, not_30_out, not_31_out, not_32_out, not_33_out, not_34_out,
       not_35_out, not_36_out, not_37_out, not_38_out, not_39_out, not_40_out, not_41_out, not_42_out,
       not_43_out, not_44_out, not_45_out, not_46_out, not_47_out, not_48_out, not_49_out, not_50_out,
       not_51_out, not_52_out, not_53_out, not_54_out, not_55_out, not_56_out, not_57_out, not_58_out,
       not_59_out, not_60_out, not_61_out, not_62_out, not_63_out;

  and Carry_1 (Carry_1_out, A1, B1);
  not not_1 (not_1_out, B2);
  and _010_1 (_010_1_out, not_1_out, A2, not_2_out);
  not not_2 (not_2_out, Carry_1_out);
  not not_3 (not_3_out, B2);
  and _001_1 (_001_1_out, not_3_out, not_4_out, Carry_1_out);
  not not_4 (not_4_out, A2);
  not not_5 (not_5_out, A2);
  and _100_1 (_100_1_out, B2, not_5_out, not_6_out);
  not not_6 (not_6_out, Carry_1_out);
  and _111_3 (_111_3_out, B2, A2, Carry_1_out);
  not not_7 (not_7_out, B2);
  and _011_2 (_011_2_out, not_7_out, A2, Carry_1_out);
  and _110_2 (_110_2_out, B2, A2, not_8_out);
  not not_8 (not_8_out, Carry_1_out);
  and _101_2 (_101_2_out, B2, not_9_out, Carry_1_out);
  not not_9 (not_9_out, A2);
  not not_10 (not_10_out, B3);
  and _010_1_2 (_010_1_2_out, not_10_out, A3, not_11_out);
  not not_11 (not_11_out, Carry_2_out);
  not not_12 (not_12_out, B3);
  and _001_1_2 (_001_1_2_out, not_12_out, not_13_out, Carry_2_out);
  not not_13 (not_13_out, A3);
  and _100_1_2 (_100_1_2_out, B3, not_14_out, not_15_out);
  not not_14 (not_14_out, A3);
  not not_15 (not_15_out, Carry_2_out);
  and _111_3_2 (_111_3_2_out, B3, A3, Carry_2_out);
  not not_16 (not_16_out, B3);
  and _011_2_2 (_011_2_2_out, not_16_out, A3, Carry_2_out);
  and _110_2_2 (_110_2_2_out, B3, A3, not_17_out);
  not not_17 (not_17_out, Carry_2_out);
  not not_18 (not_18_out, A3);
  and _101_2_2 (_101_2_2_out, B3, not_18_out, Carry_2_out);
  not not_19 (not_19_out, B4);
  and _010_1_3 (_010_1_3_out, not_19_out, A4, not_20_out);
  not not_20 (not_20_out, Carry_3_out);
  not not_21 (not_21_out, B4);
  not not_22 (not_22_out, A4);
  and _001_1_3 (_001_1_3_out, not_21_out, not_22_out, Carry_3_out);
  not not_23 (not_23_out, A4);
  and _100_1_3 (_100_1_3_out, B4, not_23_out, not_24_out);
  not not_24 (not_24_out, Carry_3_out);
  and _111_3_3 (_111_3_3_out, B4, A4, Carry_3_out);
  not not_25 (not_25_out, B4);
  and _011_2_3 (_011_2_3_out, not_25_out, A4, Carry_3_out);
  and _110_2_3 (_110_2_3_out, B4, A4, not_26_out);
  not not_26 (not_26_out, Carry_3_out);
  not not_27 (not_27_out, A4);
  and _101_2_3 (_101_2_3_out, B4, not_27_out, Carry_3_out);
  not not_28 (not_28_out, B5);
  and _010_1_4 (_010_1_4_out, not_28_out, A5, not_29_out);
  not not_29 (not_29_out, Carry_4_out);
  not not_30 (not_30_out, B5);
  not not_31 (not_31_out, A5);
  and _001_1_4 (_001_1_4_out, not_30_out, not_31_out, Carry_4_out);
  and _100_1_4 (_100_1_4_out, B5, not_32_out, not_33_out);
  not not_32 (not_32_out, A5);
  not not_33 (not_33_out, Carry_4_out);
  and _111_3_4 (_111_3_4_out, B5, A5, Carry_4_out);
  not not_34 (not_34_out, B5);
  and _011_2_4 (_011_2_4_out, not_34_out, A5, Carry_4_out);
  and _110_2_4 (_110_2_4_out, B5, A5, not_35_out);
  not not_35 (not_35_out, Carry_4_out);
  and _101_2_4 (_101_2_4_out, B5, not_36_out, Carry_4_out);
  not not_36 (not_36_out, A5);
  not not_37 (not_37_out, B6);
  and _010_1_5 (_010_1_5_out, not_37_out, A6, not_38_out);
  not not_38 (not_38_out, Carry_5_out);
  not not_39 (not_39_out, B6);
  not not_40 (not_40_out, B6);
  and _001_1_5 (_001_1_5_out, not_39_out, not_40_out, Carry_5_out);
  and _100_1_5 (_100_1_5_out, B6, not_41_out, not_42_out);
  not not_41 (not_41_out, A6);
  not not_42 (not_42_out, Carry_5_out);
  and _111_3_5 (_111_3_5_out, B6, A6, Carry_5_out);
  not not_43 (not_43_out, B6);
  and _011_2_5 (_011_2_5_out, not_43_out, A6, Carry_5_out);
  and _110_2_5 (_110_2_5_out, B6, A6, not_44_out);
  not not_44 (not_44_out, Carry_5_out);
  not not_45 (not_45_out, A6);
  and _101_2_5 (_101_2_5_out, B6, not_45_out, Carry_5_out);
  not not_46 (not_46_out, B7);
  and _010_1_6 (_010_1_6_out, not_46_out, A7, not_47_out);
  not not_47 (not_47_out, Carry_6_out);
  not not_48 (not_48_out, B7);
  not not_49 (not_49_out, A7);
  and _001_1_6 (_001_1_6_out, not_48_out, not_49_out, Carry_6_out);
  not not_50 (not_50_out, A7);
  and _100_1_6 (_100_1_6_out, B7, not_50_out, not_51_out);
  not not_51 (not_51_out, Carry_6_out);
  and _111_3_6 (_111_3_6_out, B7, A7, Carry_6_out);
  not not_52 (not_52_out, B7);
  and _011_2_6 (_011_2_6_out, not_52_out, A7, Carry_6_out);
  and _110_2_6 (_110_2_6_out, B7, A7, not_53_out);
  not not_53 (not_53_out, Carry_6_out);
  and _101_2_6 (_101_2_6_out, B7, not_54_out, Carry_6_out);
  not not_54 (not_54_out, A7);
  not not_55 (not_55_out, B8);
  not not_56 (not_56_out, Carry_7_out);
  not not_57 (not_57_out, B8);
  not not_58 (not_58_out, A8);
  not not_59 (not_59_out, A8);
  not not_60 (not_60_out, Carry_7_out);
  not not_61 (not_61_out, B8);
  not not_62 (not_62_out, Carry_7_out);
  not not_63 (not_63_out, A8);
  xor Output_1 (out_17, A1, B1);
  and _010_1_7 (_010_1_7_out, not_55_out, A8, not_56_out);
  and _001_1_7 (_001_1_7_out, not_57_out, not_58_out, Carry_7_out);
  and _100_1_7 (_100_1_7_out, B8, not_59_out, not_60_out);
  and _111_3_7 (_111_3_7_out, B8, A8, Carry_7_out);
  and _011_2_7 (_011_2_7_out, not_61_out, A8, Carry_7_out);
  and _110_2_7 (_110_2_7_out, B8, A8, not_62_out);
  and _101_2_7 (_101_2_7_out, B8, not_63_out, Carry_7_out);
  or Output_2 (out_18, _010_1_out, _001_1_out, _100_1_out, _111_3_out);
  or Carry_2 (Carry_2_out, _111_3_out, _011_2_out, _110_2_out, _101_2_out);
  or Output_3 (out_19, _010_1_2_out, _001_1_2_out, _100_1_2_out, _111_3_2_out);
  or Carry_3 (Carry_3_out, _111_3_2_out, _011_2_2_out, _110_2_2_out, _101_2_2_out);
  or Output_4 (out_20, _010_1_3_out, _001_1_3_out, _100_1_3_out, _111_3_3_out);
  or Carry_4 (Carry_4_out, _111_3_3_out, _011_2_3_out, _110_2_3_out, _101_2_3_out);
  or Output_5 (out_21, _010_1_4_out, _001_1_4_out, _100_1_4_out, _111_3_4_out);
  or Carry_5 (Carry_5_out, _111_3_4_out, _011_2_4_out, _110_2_4_out, _101_2_4_out);
  or Output_6 (out_22, _010_1_5_out, _001_1_5_out, _100_1_5_out, _111_3_5_out);
  or Carry_6 (Carry_6_out, _111_3_5_out, _011_2_5_out, _110_2_5_out, _101_2_5_out);
  or Output_7 (out_23, _010_1_6_out, _001_1_6_out, _100_1_6_out, _111_3_6_out);
  or Carry_7 (Carry_7_out, _111_3_6_out, _011_2_6_out, _110_2_6_out, _101_2_6_out);
  or Output_8 (out_24, _010_1_7_out, _001_1_7_out, _100_1_7_out, _111_3_7_out);
  or Carry_8 (out_25, _111_3_7_out, _011_2_7_out, _110_2_7_out, _101_2_7_out);
endmodule

module Multiplication (
  input  in_1,
  input  in_2,
  input  in_3,
  input  in_4,
  input  a5,
  input  a6,
  input  a7,
  input  a8,
  input  b1,
  input  b2,
  input  b3,
  input  b4,
  input  b5,
  input  b6,
  input  b7,
  input  b8,
  output out_17,
  output out_18,
  output out_19,
  output out_20,
  output out_21,
  output out_22,
  output out_23,
  output out_24,
  output out_25,
  output out_26,
  output out_27,
  output out_28,
  output out_29,
  output out_30,
  output out_31,
  output out_32
);

  wire a1_b2_out, a1_b3_out, a1_b4_out, a1_b5_out, a1_b6_out, a1_b7_out, a1_b8_out, a2_b1_out, a2_b2_out,
       a2_b3_out, a2_b4_out, a2_b5_out, a2_b6_out, a2_b7_out, a2_b8_out, a3b1_out, a3b2_out, a3b3_out,
       a3b4_out, a3b5_out, a3b6_out, a3b7_out, a3b8_out, a4b1_out, a4b2_out, a4b3_out, a4b4_out, a4b5_out,
       a4b6_out, a4b7_out, a4b8_out, a5b1_out, a5b2_out, a5b3_out, a5b4_out, a5b5_out, a5b6_out, a5b7_out,
       a5b8_out, a6b1_out, a6b2_out, a6b3_out, a6b4_out, a6b5_out, a6b6_out, a6b7_out, a6b8_out, a7b1_out,
       a7b2_out, a7b3_out, a7b4_out, a7b5_out, a7b6_out, a7b7_out, a7b8_out, a8b1_out, a8b2_out, a8b3_out,
       a8b4_out, a8b5_out, a8b6_out, a8b7_out, a8b8_out, fulladder_2_cout, fulladder_2_s, fulladder_3_cout,
       fulladder_4_cout, fulladder_4_s, fulladder_5_cout, fulladder_5_s, fulladder_6_cout, fulladder_7_cout,
       fulladder_7_s, fulladder_8_cout, fulladder_8_s, fulladder_9_cout, fulladder_9_s, fulladder_10_cout,
       fulladder_11_cout, fulladder_11_s, fulladder_12_cout, fulladder_12_s, fulladder_13_cout,
       fulladder_13_s, fulladder_14_cout, fulladder_14_s, fulladder_15_cout, fulladder_16_cout,
       fulladder_16_s, fulladder_17_cout, fulladder_17_s, fulladder_18_cout, fulladder_18_s,
       fulladder_19_cout, fulladder_19_s, fulladder_20_cout, fulladder_20_s, fulladder_21_cout,
       fulladder_21_s, fulladder_22_cout, fulladder_23_cout, fulladder_23_s, fulladder_24_cout,
       fulladder_24_s, fulladder_25_cout, fulladder_25_s, fulladder_26_cout, fulladder_26_s,
       fulladder_27_cout, fulladder_27_s, fulladder_28_cout, fulladder_28_s, fulladder_29_cout,
       fulladder_30_cout, fulladder_30_s, fulladder_31_cout, fulladder_31_s, fulladder_32_cout,
       fulladder_32_s, fulladder_33_cout, fulladder_33_s, fulladder_34_cout, fulladder_34_s,
       fulladder_35_cout, fulladder_36_cout, fulladder_36_s, fulladder_37_cout, fulladder_37_s,
       fulladder_38_cout, fulladder_38_s, fulladder_39_cout, fulladder_39_s, fulladder_40_cout,
       fulladder_40_s, fulladder_41_cout, fulladder_42_cout, fulladder_42_s, fulladder_43_cout,
       fulladder_43_s, fulladder_44_cout, fulladder_44_s, fulladder_45_cout, fulladder_45_s,
       fulladder_46_cout, fulladder_47_cout, fulladder_47_s, fulladder_48_cout, fulladder_48_s,
       fulladder_49_cout, fulladder_49_s, fulladder_50_cout, fulladder_51_cout, fulladder_51_s,
       fulladder_52_cout, fulladder_52_s, fulladder_53_cout, fulladder_54_cout, fulladder_54_s,
       fulladder_55_cout, fulladder_56_cout, not_1_out, not_2_out, not_3_out, not_4_out, not_5_out,
       not_6_out, not_7_out, not_8_out;

  and a8b8 (a8b8_out, a8, b8);
  LED led_1 (.in(out_32));
  and a8b7 (a8b7_out, a8, b7);
  LED led_2 (.in(fulladder_2_cout));
  FullAdder fulladder_1 (.Cout(out_32), .Cin(fulladder_3_cout), .A(fulladder_2_cout), .B(a8b8_out), .S(out_31));
  LED led_3 (.in(out_31));
  LED led_4 (.in(fulladder_4_cout));
  FullAdder fulladder_2 (
    .Cout(fulladder_2_cout), .Cin(fulladder_5_cout), .A(fulladder_4_cout), .B(a8b7_out), .S(fulladder_2_s));
  LED led_5 (.in(fulladder_2_s));
  and a7b8 (a7b8_out, a7, b8);
  FullAdder fulladder_3 (.Cout(fulladder_3_cout), .Cin(fulladder_6_cout), .A(fulladder_2_s), .B(a7b8_out), .S(out_30));
  LED led_6 (.in(out_30));
  and a8b5 (a8b5_out, a8, b5);
  LED led_7 (.in(fulladder_7_cout));
  and a8b6 (a8b6_out, a8, b6);
  FullAdder fulladder_4 (
    .Cout(fulladder_4_cout), .Cin(fulladder_8_cout), .A(fulladder_7_cout), .B(a8b6_out), .S(fulladder_4_s));
  LED led_8 (.in(fulladder_4_s));
  and a7b7 (a7b7_out, a7, b7);
  FullAdder fulladder_5 (
    .Cout(fulladder_5_cout), .Cin(fulladder_9_cout), .A(fulladder_4_s), .B(a7b7_out), .S(fulladder_5_s));
  LED led_9 (.in(fulladder_5_s));
  and a6b8 (a6b8_out, a6, b8);
  FullAdder fulladder_6 (.Cout(fulladder_6_cout), .Cin(fulladder_10_cout), .A(fulladder_5_s), .B(a6b8_out), .S(out_29));
  LED led_10 (.in(out_29));
  and a8b4 (a8b4_out, a8, b4);
  LED led_11 (.in(fulladder_11_cout));
  FullAdder fulladder_7 (
    .Cout(fulladder_7_cout), .Cin(fulladder_12_cout), .A(fulladder_11_cout), .B(a8b5_out), .S(fulladder_7_s));
  LED led_12 (.in(fulladder_7_s));
  and a7b6 (a7b6_out, a7, b6);
  FullAdder fulladder_8 (
    .Cout(fulladder_8_cout), .Cin(fulladder_13_cout), .A(fulladder_7_s), .B(a7b6_out), .S(fulladder_8_s));
  LED led_13 (.in(fulladder_8_s));
  and a6b7 (a6b7_out, a6, b7);
  FullAdder fulladder_9 (
    .Cout(fulladder_9_cout), .Cin(fulladder_14_cout), .A(fulladder_8_s), .B(a6b7_out), .S(fulladder_9_s));
  LED led_14 (.in(fulladder_9_s));
  and a5b8 (a5b8_out, a5, b8);
  FullAdder fulladder_10 (
    .Cout(fulladder_10_cout), .Cin(fulladder_15_cout), .A(fulladder_9_s), .B(a5b8_out), .S(out_28));
  LED led_15 (.in(out_28));
  not not_1 (not_1_out, 1'b1);
  LED led_16 (.in(fulladder_16_cout));
  LED led_17 (.in(fulladder_16_cout));
  LED led_18 (.in(fulladder_17_cout));
  FullAdder fulladder_11 (
    .Cout(fulladder_11_cout), .Cin(fulladder_18_cout), .A(fulladder_17_cout), .B(a8b4_out), .S(fulladder_11_s));
  LED led_19 (.in(fulladder_11_s));
  and a7b5 (a7b5_out, a7, b5);
  FullAdder fulladder_12 (
    .Cout(fulladder_12_cout), .Cin(fulladder_19_cout), .A(fulladder_11_s), .B(a7b5_out), .S(fulladder_12_s));
  LED led_20 (.in(fulladder_12_s));
  and a6b6 (a6b6_out, a6, b6);
  FullAdder fulladder_13 (
    .Cout(fulladder_13_cout), .Cin(fulladder_20_cout), .A(fulladder_12_s), .B(a6b6_out), .S(fulladder_13_s));
  LED led_21 (.in(fulladder_13_s));
  and a5b7 (a5b7_out, a5, b7);
  FullAdder fulladder_14 (
    .Cout(fulladder_14_cout), .Cin(fulladder_21_cout), .A(fulladder_13_s), .B(a5b7_out), .S(fulladder_14_s));
  LED led_22 (.in(fulladder_14_s));
  and a4b8 (a4b8_out, in_4, b8);
  FullAdder fulladder_15 (
    .Cout(fulladder_15_cout), .Cin(fulladder_22_cout), .A(fulladder_14_s), .B(a4b8_out), .S(out_27));
  LED led_23 (.in(out_27));
  and a8b2 (a8b2_out, a8, b2);
  FullAdder fulladder_16 (
    .Cout(fulladder_16_cout), .Cin(fulladder_23_cout), .A(not_1_out), .B(a8b2_out), .S(fulladder_16_s));
  LED led_24 (.in(fulladder_16_cout));
  LED led_25 (.in(fulladder_16_s));
  and a8b3 (a8b3_out, a8, b3);
  FullAdder fulladder_17 (
    .Cout(fulladder_17_cout), .Cin(fulladder_24_cout), .A(fulladder_16_cout), .B(a8b3_out), .S(fulladder_17_s));
  LED led_26 (.in(fulladder_17_s));
  and a7b4 (a7b4_out, a7, b4);
  FullAdder fulladder_18 (
    .Cout(fulladder_18_cout), .Cin(fulladder_25_cout), .A(fulladder_17_s), .B(a7b4_out), .S(fulladder_18_s));
  LED led_27 (.in(fulladder_18_s));
  and a6b5 (a6b5_out, a6, b5);
  FullAdder fulladder_19 (
    .Cout(fulladder_19_cout), .Cin(fulladder_26_cout), .A(fulladder_18_s), .B(a6b5_out), .S(fulladder_19_s));
  LED led_28 (.in(fulladder_19_s));
  and a5b6 (a5b6_out, a5, b6);
  FullAdder fulladder_20 (
    .Cout(fulladder_20_cout), .Cin(fulladder_27_cout), .A(fulladder_19_s), .B(a5b6_out), .S(fulladder_20_s));
  LED led_29 (.in(fulladder_20_s));
  and a4b7 (a4b7_out, in_4, b7);
  FullAdder fulladder_21 (
    .Cout(fulladder_21_cout), .Cin(fulladder_28_cout), .A(fulladder_20_s), .B(a4b7_out), .S(fulladder_21_s));
  LED led_30 (.in(fulladder_21_s));
  and a3b8 (a3b8_out, in_3, b8);
  FullAdder fulladder_22 (
    .Cout(fulladder_22_cout), .Cin(fulladder_29_cout), .A(fulladder_21_s), .B(a3b8_out), .S(out_26));
  LED led_31 (.in(out_26));
  and a8b1 (a8b1_out, a8, b1);
  and a7b2 (a7b2_out, a7, b2);
  FullAdder fulladder_23 (
    .Cout(fulladder_23_cout), .Cin(fulladder_36_cout), .A(a8b1_out), .B(a7b2_out), .S(fulladder_23_s));
  and a7b3 (a7b3_out, a7, b3);
  FullAdder fulladder_24 (
    .Cout(fulladder_24_cout), .Cin(fulladder_30_cout), .A(fulladder_16_s), .B(a7b3_out), .S(fulladder_24_s));
  LED led_32 (.in(fulladder_24_s));
  and a6b4 (a6b4_out, a6, b4);
  FullAdder fulladder_25 (
    .Cout(fulladder_25_cout), .Cin(fulladder_31_cout), .A(fulladder_24_s), .B(a6b4_out), .S(fulladder_25_s));
  LED led_33 (.in(fulladder_25_s));
  and a5b5 (a5b5_out, a5, b5);
  FullAdder fulladder_26 (
    .Cout(fulladder_26_cout), .Cin(fulladder_32_cout), .A(fulladder_25_s), .B(a5b5_out), .S(fulladder_26_s));
  LED led_34 (.in(fulladder_26_s));
  and a4b6 (a4b6_out, in_4, b6);
  FullAdder fulladder_27 (
    .Cout(fulladder_27_cout), .Cin(fulladder_33_cout), .A(fulladder_26_s), .B(a4b6_out), .S(fulladder_27_s));
  LED led_35 (.in(fulladder_27_s));
  and a3b7 (a3b7_out, in_3, b7);
  FullAdder fulladder_28 (
    .Cout(fulladder_28_cout), .Cin(fulladder_34_cout), .A(fulladder_27_s), .B(a3b7_out), .S(fulladder_28_s));
  LED led_36 (.in(fulladder_28_s));
  and a2_b8 (a2_b8_out, in_2, b8);
  FullAdder fulladder_29 (
    .Cout(fulladder_29_cout), .Cin(fulladder_35_cout), .A(fulladder_28_s), .B(a2_b8_out), .S(out_25));
  and a7b1 (a7b1_out, a7, b1);
  LED led_37 (.in(fulladder_23_s));
  and a6b3 (a6b3_out, a6, b3);
  FullAdder fulladder_30 (
    .Cout(fulladder_30_cout), .Cin(fulladder_37_cout), .A(fulladder_23_s), .B(a6b3_out), .S(fulladder_30_s));
  LED led_38 (.in(fulladder_30_s));
  and a5b4 (a5b4_out, a5, b4);
  FullAdder fulladder_31 (
    .Cout(fulladder_31_cout), .Cin(fulladder_38_cout), .A(fulladder_30_s), .B(a5b4_out), .S(fulladder_31_s));
  LED led_39 (.in(fulladder_31_s));
  and a4b5 (a4b5_out, in_4, b5);
  FullAdder fulladder_32 (
    .Cout(fulladder_32_cout), .Cin(fulladder_39_cout), .A(fulladder_31_s), .B(a4b5_out), .S(fulladder_32_s));
  LED led_40 (.in(fulladder_32_s));
  and a3b6 (a3b6_out, in_3, b6);
  FullAdder fulladder_33 (
    .Cout(fulladder_33_cout), .Cin(fulladder_40_cout), .A(fulladder_32_s), .B(a3b6_out), .S(fulladder_33_s));
  LED led_41 (.in(fulladder_33_s));
  and a2_b7 (a2_b7_out, in_2, b7);
  FullAdder fulladder_34 (
    .Cout(fulladder_34_cout), .Cin(fulladder_41_cout), .A(fulladder_33_s), .B(a2_b7_out), .S(fulladder_34_s));
  and a1_b8 (a1_b8_out, in_1, b8);
  FullAdder fulladder_35 (.Cout(fulladder_35_cout), .Cin(not_2_out), .A(fulladder_34_s), .B(a1_b8_out), .S(out_24));
  LED led_42 (.in(out_25));
  and a6b2 (a6b2_out, a6, b2);
  FullAdder fulladder_36 (
    .Cout(fulladder_36_cout), .Cin(fulladder_42_cout), .A(a7b1_out), .B(a6b2_out), .S(fulladder_36_s));
  LED led_43 (.in(fulladder_36_s));
  and a5b3 (a5b3_out, a5, b3);
  FullAdder fulladder_37 (
    .Cout(fulladder_37_cout), .Cin(fulladder_43_cout), .A(fulladder_36_s), .B(a5b3_out), .S(fulladder_37_s));
  LED led_44 (.in(fulladder_37_s));
  and a4b4 (a4b4_out, in_4, b4);
  FullAdder fulladder_38 (
    .Cout(fulladder_38_cout), .Cin(fulladder_44_cout), .A(fulladder_37_s), .B(a4b4_out), .S(fulladder_38_s));
  LED led_45 (.in(fulladder_38_s));
  and a3b5 (a3b5_out, in_3, b5);
  FullAdder fulladder_39 (
    .Cout(fulladder_39_cout), .Cin(fulladder_45_cout), .A(fulladder_38_s), .B(a3b5_out), .S(fulladder_39_s));
  LED led_46 (.in(fulladder_39_s));
  FullAdder fulladder_40 (
    .Cout(fulladder_40_cout), .Cin(fulladder_46_cout), .A(fulladder_39_s), .B(a2_b6_out), .S(fulladder_40_s));
  and a1_b7 (a1_b7_out, in_1, b7);
  FullAdder fulladder_41 (.Cout(fulladder_41_cout), .Cin(not_3_out), .A(fulladder_40_s), .B(a1_b7_out), .S(out_23));
  LED led_47 (.in(fulladder_34_s));
  not not_2 (not_2_out, 1'b1);
  LED led_48 (.in(out_24));
  and a6b1 (a6b1_out, a6, b1);
  and a5b2 (a5b2_out, a5, b2);
  FullAdder fulladder_42 (
    .Cout(fulladder_42_cout), .Cin(fulladder_47_cout), .A(a6b1_out), .B(a5b2_out), .S(fulladder_42_s));
  LED led_49 (.in(fulladder_42_s));
  and a4b3 (a4b3_out, in_4, in_4, b3);
  FullAdder fulladder_43 (
    .Cout(fulladder_43_cout), .Cin(fulladder_48_cout), .A(fulladder_42_s), .B(a4b3_out), .S(fulladder_43_s));
  LED led_50 (.in(fulladder_43_s));
  and a3b4 (a3b4_out, in_3, b4);
  FullAdder fulladder_44 (
    .Cout(fulladder_44_cout), .Cin(fulladder_49_cout), .A(fulladder_43_s), .B(a3b4_out), .S(fulladder_44_s));
  LED led_51 (.in(fulladder_44_s));
  and a2_b5 (a2_b5_out, in_2, b5);
  FullAdder fulladder_45 (
    .Cout(fulladder_45_cout), .Cin(fulladder_50_cout), .A(fulladder_44_s), .B(a2_b5_out), .S(fulladder_45_s));
  and a2_b6 (a2_b6_out, in_2, b6);
  FullAdder fulladder_46 (.Cout(fulladder_46_cout), .Cin(not_4_out), .A(fulladder_45_s), .B(a1_b6_out), .S(out_22));
  LED led_52 (.in(fulladder_40_s));
  not not_3 (not_3_out, 1'b1);
  LED led_53 (.in(out_23));
  LED led_54 (.in(out_23));
  and a5b1 (a5b1_out, a5, b1);
  and a4b2 (a4b2_out, in_4, b2);
  FullAdder fulladder_47 (
    .Cout(fulladder_47_cout), .Cin(fulladder_51_cout), .A(a5b1_out), .B(a4b2_out), .S(fulladder_47_s));
  LED led_55 (.in(fulladder_47_s));
  and a3b3 (a3b3_out, in_3, b3);
  FullAdder fulladder_48 (
    .Cout(fulladder_48_cout), .Cin(fulladder_52_cout), .A(fulladder_47_s), .B(a3b3_out), .S(fulladder_48_s));
  LED led_56 (.in(fulladder_48_s));
  and a2_b4 (a2_b4_out, in_2, in_2, in_2, b4);
  FullAdder fulladder_49 (
    .Cout(fulladder_49_cout), .Cin(fulladder_53_cout), .A(fulladder_48_s), .B(a2_b4_out), .S(fulladder_49_s));
  and a1_b5 (a1_b5_out, in_1, b5);
  FullAdder fulladder_50 (.Cout(fulladder_50_cout), .Cin(not_5_out), .A(fulladder_49_s), .B(a1_b5_out), .S(out_21));
  LED led_57 (.in(fulladder_45_s));
  and a1_b6 (a1_b6_out, in_1, b6);
  not not_4 (not_4_out, 1'b1);
  LED led_58 (.in(out_22));
  LED led_59 (.in(out_22));
  LED led_60 (.in(out_22));
  and a4b1 (a4b1_out, in_4, b1);
  and a3b2 (a3b2_out, in_3, b2);
  FullAdder fulladder_51 (
    .Cout(fulladder_51_cout), .Cin(fulladder_54_cout), .A(a4b1_out), .B(a3b2_out), .S(fulladder_51_s));
  LED led_61 (.in(fulladder_51_s));
  and a2_b3 (a2_b3_out, in_2, in_2, b3);
  FullAdder fulladder_52 (
    .Cout(fulladder_52_cout), .Cin(fulladder_55_cout), .A(fulladder_51_s), .B(a2_b3_out), .S(fulladder_52_s));
  and a1_b4 (a1_b4_out, in_1, b4);
  FullAdder fulladder_53 (.Cout(fulladder_53_cout), .Cin(not_6_out), .A(fulladder_52_s), .B(a1_b4_out), .S(out_20));
  LED led_62 (.in(fulladder_49_s));
  not not_5 (not_5_out, 1'b1);
  LED led_63 (.in(out_21));
  LED led_64 (.in(out_21));
  LED led_65 (.in(out_21));
  LED led_66 (.in(out_21));
  and a3b1 (a3b1_out, in_3, b1, b1);
  and a2_b2 (a2_b2_out, in_2, b2);
  FullAdder fulladder_54 (
    .Cout(fulladder_54_cout), .Cin(fulladder_56_cout), .A(a3b1_out), .B(a2_b2_out), .S(fulladder_54_s));
  LED led_67 (.in(fulladder_54_s));
  FullAdder fulladder_55 (.Cout(fulladder_55_cout), .Cin(not_7_out), .A(fulladder_54_s), .B(a1_b3_out), .S(out_19));
  LED led_68 (.in(fulladder_52_s));
  not not_6 (not_6_out, 1'b1);
  LED led_69 (.in(out_20));
  LED led_70 (.in(out_20));
  LED led_71 (.in(out_20));
  LED led_72 (.in(out_20));
  LED led_73 (.in(out_20));
  and a2_b1 (a2_b1_out, b1, in_2);
  and a1_b2 (a1_b2_out, in_1, b2);
  FullAdder fulladder_56 (.Cout(fulladder_56_cout), .Cin(not_8_out), .A(a2_b1_out), .B(a1_b2_out), .S(out_18));
  LED led_74 (.in(out_18));
  and a1_b3 (a1_b3_out, in_1, b3);
  not not_7 (not_7_out, 1'b1);
  LED led_75 (.in(out_19));
  LED led_76 (.in(out_19));
  LED led_77 (.in(out_19));
  LED led_78 (.in(out_19));
  LED led_79 (.in(out_19));
  LED led_80 (.in(out_19));
  and a1_b1 (out_17, in_1, b1);
  not not_8 (not_8_out, 1'b1);
  LED led_81 (.in(out_17));
  LED led_82 (.in(out_17));
  LED led_83 (.in(out_18));
  LED led_84 (.in(out_18));
  LED led_85 (.in(out_17));
  LED led_86 (.in(out_17));
  LED led_87 (.in(out_18));
  LED led_88 (.in(out_17));
  LED led_89 (.in(out_18));
  LED led_90 (.in(out_17));
  LED led_91 (.in(out_18));
  LED led_92 (.in(out_17));
  LED led_93 (.in(out_18));
  LED led_94 (.in(out_18));
  LED led_95 (.in(out_17));

  // Notes on the sheet:
  //   b2
  //   e
  //   b1
  //   a4
  //   a3
  //   a2
  //   a1
endmodule

module MuxFor8BitDivision (
  input  [15:0] in_1,
  input  [15:0] in_2,
  input  in_3,
  output [15:0] out_4
);

  Multiplexer #(.width(16)) multiplexer_1 (.in0(in_1), .in1(in_2), .out(out_4), .sel(in_3));  // open: en
endmodule

module Div8BitForCircuitDesign (
  input  A1,
  input  a2,
  input  a3,
  input  a4,
  input  a5,
  input  a6,
  input  a7,
  input  a8,
  input  A1_2,
  input  a2_2,
  input  a3_2,
  input  a4_2,
  input  a5_2,
  input  a6_2,
  input  a7_2,
  input  a8_2,
  output [7:0] Final_Answer,
  output [7:0] out_18,
  output [15:0] out_19,
  output [15:0] out_20,
  output [15:0] out_21,
  output [15:0] out_22,
  output [15:0] out_23,
  output [15:0] out_24,
  output [15:0] out_25,
  output [15:0] out_26,
  output [15:0] out_27,
  output [15:0] out_28,
  output [15:0] out_29,
  output [15:0] out_30,
  output [15:0] out_31,
  output [15:0] out_32,
  output [15:0] out_33,
  output [15:0] out_34,
  output out_35,
  output [15:0] out_36,
  output [15:0] out_37,
  output [15:0] out_38,
  output [15:0] out_39,
  output [15:0] out_40,
  output [15:0] out_41,
  output [15:0] out_42,
  output [15:0] out_43,
  output [15:0] out_44,
  output [15:0] out_45,
  output [15:0] out_46,
  output [15:0] out_47
);

  wire not_153_out, not_154_out, not_155_out, not_156_out, not_157_out, not_158_out, not_159_out,
       not_160_out, not_161_out, not_162_out, not_163_out, not_164_out, not_165_out, not_166_out,
       not_167_out, not_168_out, not_169_out, not_170_out, subtractor_1_bout, subtractor_2_bout,
       subtractor_3_bout, subtractor_4_bout, subtractor_5_bout, subtractor_6_bout, subtractor_7_bout,
       subtractor_8_bout, subtractor_9_bout, subtractor_10_bout, subtractor_11_bout, subtractor_12_bout,
       subtractor_13_bout, subtractor_14_bout, subtractor_15_bout, subtractor_16_bout, subtractor_17_bout;
  wire [15:0] not_122_out, subtractor_1_out, subtractor_2_out, subtractor_3_out, subtractor_4_out,
       subtractor_5_out, subtractor_6_out, subtractor_7_out, subtractor_8_out, subtractor_9_out,
       subtractor_10_out, subtractor_11_out, subtractor_12_out, subtractor_13_out, subtractor_14_out,
       subtractor_15_out, subtractor_16_out, subtractor_17_out;
  wire [15:1] not_111_out;
  wire [15:2] not_101_out;
  wire [15:3] not_92_out;
  wire [15:4] not_84_out;
  wire [15:5] not_77_out;
  wire [15:6] not_71_out;
  wire [15:8] not_152_out;

  not not_1 (out_28[12], 1'b1);
  not not_2 (out_28[14], 1'b1);
  not not_3 (out_30[12], 1'b1);
  not not_4 (out_30[14], 1'b1);
  not not_5 (out_32[10], 1'b1);
  not not_6 (out_32[12], 1'b1);
  not not_7 (out_32[14], 1'b1);
  not not_8 (out_34[12], 1'b1);
  not not_9 (out_34[14], 1'b1);
  not not_10 (out_37[12], 1'b1);
  not not_11 (out_37[14], 1'b1);
  not not_12 (out_39[12], 1'b1);
  not not_13 (out_39[14], 1'b1);
  not not_14 (not_71_out[8], 1'b1);
  not not_15 (not_71_out[10], 1'b1);
  not not_16 (not_71_out[12], 1'b1);
  not not_17 (not_71_out[14], 1'b1);
  not not_18 (not_77_out[8], 1'b1);
  not not_19 (not_77_out[10], 1'b1);
  not not_20 (not_77_out[12], 1'b1);
  not not_21 (not_77_out[14], 1'b1);
  not not_22 (not_84_out[8], 1'b1);
  not not_23 (not_84_out[10], 1'b1);
  not not_24 (not_84_out[12], 1'b1);
  not not_25 (not_84_out[14], 1'b1);
  not not_26 (not_92_out[8], 1'b1);
  not not_27 (not_92_out[10], 1'b1);
  not not_28 (not_92_out[12], 1'b1);
  not not_29 (not_92_out[14], 1'b1);
  not not_30 (not_101_out[8], 1'b1);
  not not_31 (not_101_out[10], 1'b1);
  not not_32 (not_101_out[12], 1'b1);
  not not_33 (not_101_out[14], 1'b1);
  not not_34 (not_111_out[8], 1'b1);
  not not_35 (not_111_out[10], 1'b1);
  not not_36 (not_111_out[12], 1'b1);
  not not_37 (not_111_out[14], 1'b1);
  not not_38 (not_122_out[8], 1'b1);
  not not_39 (not_122_out[10], 1'b1);
  not not_40 (not_122_out[12], 1'b1);
  not not_41 (not_122_out[14], 1'b1);
  not not_42 (out_24[14], 1'b1);
  not not_43 (out_26[14], 1'b1);
  not not_44 (out_26[15], 1'b1);
  not not_45 (out_28[13], 1'b1);
  not not_46 (out_28[15], 1'b1);
  not not_47 (out_30[11], 1'b1);
  not not_48 (out_30[13], 1'b1);
  not not_49 (out_30[15], 1'b1);
  not not_50 (out_32[11], 1'b1);
  not not_51 (out_32[13], 1'b1);
  not not_52 (out_32[15], 1'b1);
  not not_53 (out_34[9], 1'b1);
  not not_54 (out_34[10], 1'b1);
  not not_55 (out_34[11], 1'b1);
  not not_56 (out_34[13], 1'b1);
  not not_57 (out_34[15], 1'b1);
  not not_58 (out_37[8], 1'b1);
  not not_59 (out_37[9], 1'b1);
  not not_60 (out_37[10], 1'b1);
  not not_61 (out_37[11], 1'b1);
  not not_62 (out_37[13], 1'b1);
  not not_63 (out_37[15], 1'b1);
  not not_64 (out_39[7], 1'b1);
  not not_65 (out_39[8], 1'b1);
  not not_66 (out_39[9], 1'b1);
  not not_67 (out_39[10], 1'b1);
  not not_68 (out_39[11], 1'b1);
  not not_69 (out_39[13], 1'b1);
  not not_70 (out_39[15], 1'b1);
  not not_71 (not_71_out[6], 1'b1);
  not not_72 (not_71_out[7], 1'b1);
  not not_73 (not_71_out[9], 1'b1);
  not not_74 (not_71_out[11], 1'b1);
  not not_75 (not_71_out[13], 1'b1);
  not not_76 (not_71_out[15], 1'b1);
  not not_77 (not_77_out[5], 1'b1);
  not not_78 (not_77_out[6], 1'b1);
  not not_79 (not_77_out[7], 1'b1);
  not not_80 (not_77_out[9], 1'b1);
  not not_81 (not_77_out[11], 1'b1);
  not not_82 (not_77_out[13], 1'b1);
  not not_83 (not_77_out[15], 1'b1);
  not not_84 (not_84_out[4], 1'b1);
  not not_85 (not_84_out[5], 1'b1);
  not not_86 (not_84_out[6], 1'b1);
  not not_87 (not_84_out[7], 1'b1);
  not not_88 (not_84_out[9], 1'b1);
  not not_89 (not_84_out[11], 1'b1);
  not not_90 (not_84_out[13], 1'b1);
  not not_91 (not_84_out[15], 1'b1);
  not not_92 (not_92_out[3], 1'b1);
  not not_93 (not_92_out[4], 1'b1);
  not not_94 (not_92_out[5], 1'b1);
  not not_95 (not_92_out[6], 1'b1);
  not not_96 (not_92_out[7], 1'b1);
  not not_97 (not_92_out[9], 1'b1);
  not not_98 (not_92_out[11], 1'b1);
  not not_99 (not_92_out[13], 1'b1);
  not not_100 (not_92_out[15], 1'b1);
  not not_101 (not_101_out[2], 1'b1);
  not not_102 (not_101_out[3], 1'b1);
  not not_103 (not_101_out[4], 1'b1);
  not not_104 (not_101_out[5], 1'b1);
  not not_105 (not_101_out[6], 1'b1);
  not not_106 (not_101_out[7], 1'b1);
  not not_107 (not_101_out[9], 1'b1);
  not not_108 (not_101_out[11], 1'b1);
  not not_109 (not_101_out[13], 1'b1);
  not not_110 (not_101_out[15], 1'b1);
  not not_111 (not_111_out[1], 1'b1);
  not not_112 (not_111_out[2], 1'b1);
  not not_113 (not_111_out[3], 1'b1);
  not not_114 (not_111_out[4], 1'b1);
  not not_115 (not_111_out[5], 1'b1);
  not not_116 (not_111_out[6], 1'b1);
  not not_117 (not_111_out[7], 1'b1);
  not not_118 (not_111_out[9], 1'b1);
  not not_119 (not_111_out[11], 1'b1);
  not not_120 (not_111_out[13], 1'b1);
  not not_121 (not_111_out[15], 1'b1);
  not not_122 (not_122_out[0], 1'b1);
  not not_123 (not_122_out[1], 1'b1);
  not not_124 (not_122_out[3], 1'b1);
  not not_125 (not_122_out[3], 1'b1);
  not not_126 (not_122_out[4], 1'b1);
  not not_127 (not_122_out[5], 1'b1);
  not not_128 (not_122_out[6], 1'b1);
  not not_129 (not_122_out[7], 1'b1);
  not not_130 (not_122_out[9], 1'b1);
  not not_131 (not_122_out[11], 1'b1);
  not not_132 (not_122_out[13], 1'b1);
  not not_133 (not_122_out[15], 1'b1);
  not not_134 (out_22[15], 1'b1);
  not not_135 (out_24[15], 1'b1);
  not not_136 (out_26[13], 1'b1);
  not not_137 (out_20[4], 1'b1);
  not not_138 (out_20[5], 1'b1);
  not not_139 (out_20[7], 1'b1);
  not not_140 (out_20[6], 1'b1);
  not not_141 (out_20[3], 1'b1);
  not not_142 (out_20[0], 1'b1);
  not not_143 (out_20[1], 1'b1);
  not not_144 (out_20[2], 1'b1);
  not not_145 (not_152_out[15], 1'b1);
  not not_146 (not_152_out[14], 1'b1);
  not not_147 (not_152_out[12], 1'b1);
  not not_148 (not_152_out[11], 1'b1);
  not not_149 (not_152_out[13], 1'b1);
  MuxFor8BitDivision muxfor8bitdivision_1 (
    .in_1(subtractor_1_out), .in_2({not_152_out, a8_2, a7_2, a6_2, a5_2, a4_2, a3_2, a2_2, A1_2}),
    .in_3(subtractor_1_bout), .out_4(out_21));
  MuxFor8BitDivision muxfor8bitdivision_2 (
    .in_1(subtractor_2_out), .in_2(out_21), .in_3(subtractor_2_bout), .out_4(out_23));
  MuxFor8BitDivision muxfor8bitdivision_3 (
    .in_1(subtractor_3_out), .in_2(out_23), .in_3(subtractor_3_bout), .out_4(out_25));
  MuxFor8BitDivision muxfor8bitdivision_4 (
    .in_1(subtractor_4_out), .in_2(out_25), .in_3(subtractor_4_bout), .out_4(out_27));
  MuxFor8BitDivision muxfor8bitdivision_5 (
    .in_1(subtractor_5_out), .in_2(out_27), .in_3(subtractor_5_bout), .out_4(out_29));
  MuxFor8BitDivision muxfor8bitdivision_6 (
    .in_1(subtractor_6_out), .in_2(out_29), .in_3(subtractor_6_bout), .out_4(out_31));
  MuxFor8BitDivision muxfor8bitdivision_7 (
    .in_1(subtractor_7_out), .in_2(out_31), .in_3(subtractor_7_bout), .out_4(out_33));
  MuxFor8BitDivision muxfor8bitdivision_8 (
    .in_1(subtractor_8_out), .in_2(out_33), .in_3(subtractor_8_bout), .out_4(out_36));
  MuxFor8BitDivision muxfor8bitdivision_9 (
    .in_1(subtractor_9_out), .in_2(out_36), .in_3(subtractor_9_bout), .out_4(out_38));
  MuxFor8BitDivision muxfor8bitdivision_10 (
    .in_1(subtractor_10_out), .in_2(out_38), .in_3(subtractor_10_bout), .out_4(out_40));
  MuxFor8BitDivision muxfor8bitdivision_11 (
    .in_1(subtractor_11_out), .in_2(out_40), .in_3(subtractor_11_bout), .out_4(out_41));
  MuxFor8BitDivision muxfor8bitdivision_12 (
    .in_1(subtractor_12_out), .in_2(out_41), .in_3(subtractor_12_bout), .out_4(out_42));
  MuxFor8BitDivision muxfor8bitdivision_13 (
    .in_1(subtractor_13_out), .in_2(out_42), .in_3(subtractor_13_bout), .out_4(out_43));
  MuxFor8BitDivision muxfor8bitdivision_14 (
    .in_1(subtractor_14_out), .in_2(out_43), .in_3(subtractor_14_bout), .out_4(out_44));
  MuxFor8BitDivision muxfor8bitdivision_15 (
    .in_1(subtractor_15_out), .in_2(out_44), .in_3(subtractor_15_bout), .out_4(out_45));
  not not_150 (not_152_out[9], 1'b1);
  not not_151 (not_152_out[10], 1'b1);
  not not_152 (not_152_out[8], 1'b1);
  MuxFor8BitDivision muxfor8bitdivision_16 (
    .in_1(subtractor_16_out), .in_2(out_45), .in_3(subtractor_16_bout), .out_4(out_46));
  MuxFor8BitDivision muxfor8bitdivision_17 (
    .in_1(subtractor_17_out), .in_2(out_46), .in_3(subtractor_17_bout), .out_4(out_47));
  not not_153 (not_153_out, 1'b1);
  LED led_1 (.in(subtractor_1_bout));
  Subtractor #(.width(16)) subtractor_1 (
    .a({not_152_out, a8_2, a7_2, a6_2, a5_2, a4_2, a3_2, a2_2, A1_2}),
    .b({a8, a7, a6, a5, a4, a3, a2, A1, out_20[7:0]}), .out(subtractor_1_out), .bin(not_153_out),
    .bout(subtractor_1_bout));
  not not_154 (not_154_out, 1'b1);
  Subtractor #(.width(16)) subtractor_2 (
    .a(out_21), .b({out_22[15], a8, a7, a6, a5, a4, a3, a2, A1, out_20[7:1]}), .out(subtractor_2_out),
    .bin(not_154_out), .bout(subtractor_2_bout));
  LED led_2 (.in(subtractor_2_bout));
  not not_155 (not_155_out, 1'b1);
  Subtractor #(.width(16)) subtractor_3 (
    .a(out_23), .b({out_24[15:14], a8, a7, a6, a5, a4, a3, a2, A1, out_20[7:2]}), .out(subtractor_3_out),
    .bin(not_155_out), .bout(subtractor_3_bout));
  LED led_3 (.in(subtractor_3_bout));
  not not_156 (not_156_out, 1'b1);
  Subtractor #(.width(16)) subtractor_4 (
    .a(out_25), .b({out_26[15:13], a8, a7, a6, a5, a4, a3, a2, A1, out_20[7:3]}), .out(subtractor_4_out),
    .bin(not_156_out), .bout(subtractor_4_bout));
  LED led_4 (.in(subtractor_4_bout));
  not not_157 (not_157_out, 1'b1);
  Subtractor #(.width(16)) subtractor_5 (
    .a(out_27), .b({out_28[15:12], a8, a7, a6, a5, a4, a3, a2, A1, out_20[7:4]}), .out(subtractor_5_out),
    .bin(not_157_out), .bout(subtractor_5_bout));
  LED led_5 (.in(subtractor_5_bout));
  not not_158 (not_158_out, 1'b1);
  Subtractor #(.width(16)) subtractor_6 (
    .a(out_29), .b({out_30[15:11], a8, a7, a6, a5, a4, a3, a2, A1, out_20[7:5]}), .out(subtractor_6_out),
    .bin(not_158_out), .bout(subtractor_6_bout));
  LED led_6 (.in(subtractor_6_bout));
  not not_159 (not_159_out, 1'b1);
  Subtractor #(.width(16)) subtractor_7 (
    .a(out_31), .b({out_32[15:10], a8, a7, a6, a5, a4, a3, a2, A1, out_20[7:6]}), .out(subtractor_7_out),
    .bin(not_159_out), .bout(subtractor_7_bout));
  LED led_7 (.in(subtractor_7_bout));
  not not_160 (not_160_out, 1'b1);
  Subtractor #(.width(16)) subtractor_8 (
    .a(out_33), .b({out_34[15:9], a8, a7, a6, a5, a4, a3, a2, A1, out_20[7]}), .out(subtractor_8_out),
    .bin(not_160_out), .bout(subtractor_8_bout));
  LED led_8 (.in(subtractor_8_bout));
  not not_161 (not_161_out, 1'b1);
  Subtractor #(.width(16)) subtractor_9 (
    .a(out_36), .b({out_37[15:8], a8, a7, a6, a5, a4, a3, a2, A1}), .out(subtractor_9_out),
    .bin(not_161_out), .bout(subtractor_9_bout));
  LED led_9 (.in(subtractor_9_bout));
  not not_162 (not_162_out, 1'b1);
  Subtractor #(.width(16)) subtractor_10 (
    .a(out_38), .b({out_39[15:7], a8, a7, a6, a5, a4, a3, a2}), .out(subtractor_10_out), .bin(not_162_out),
    .bout(subtractor_10_bout));
  LED led_10 (.in(subtractor_10_bout));
  not not_163 (not_163_out, 1'b1);
  Subtractor #(.width(16)) subtractor_11 (
    .a(out_40), .b({not_71_out, a8, a7, a6, a5, a4, a3}), .out(subtractor_11_out), .bin(not_163_out),
    .bout(subtractor_11_bout));
  LED led_11 (.in(subtractor_11_bout));
  not not_164 (not_164_out, 1'b1);
  Subtractor #(.width(16)) subtractor_12 (
    .a(out_41), .b({not_77_out, a8, a7, a6, a5, a4}), .out(subtractor_12_out), .bin(not_164_out),
    .bout(subtractor_12_bout));
  LED led_12 (.in(subtractor_12_bout));
  not not_165 (not_165_out, 1'b1);
  Subtractor #(.width(16)) subtractor_13 (
    .a(out_42), .b({not_84_out, a8, a7, a6, a5}), .out(subtractor_13_out), .bin(not_165_out),
    .bout(subtractor_13_bout));
  LED led_13 (.in(subtractor_13_bout));
  not not_166 (not_166_out, 1'b1);
  Subtractor #(.width(16)) subtractor_14 (
    .a(out_43), .b({not_92_out, a8, a7, a6}), .out(subtractor_14_out), .bin(not_166_out),
    .bout(subtractor_14_bout));
  LED led_14 (.in(subtractor_14_bout));
  not not_167 (not_167_out, 1'b1);
  Subtractor #(.width(16)) subtractor_15 (
    .a(out_44), .b({not_101_out, a8, a7}), .out(subtractor_15_out), .bin(not_167_out),
    .bout(subtractor_15_bout));
  LED led_15 (.in(subtractor_15_bout));
  not not_168 (not_168_out, 1'b1);
  LED led_16 (.in(subtractor_16_bout));
  not not_169 (not_169_out, 1'b1);
  LED led_17 (.in(subtractor_17_bout));
  not not_170 (not_170_out, subtractor_1_bout);
  not not_171 (Final_Answer[7], subtractor_2_bout);
  not not_172 (Final_Answer[6], subtractor_3_bout);
  not not_173 (Final_Answer[5], subtractor_4_bout);
  not not_174 (Final_Answer[4], subtractor_5_bout);
  not not_175 (Final_Answer[3], subtractor_6_bout);
  not not_176 (Final_Answer[2], subtractor_7_bout);
  Subtractor #(.width(16)) subtractor_16 (
    .a(out_45), .b({not_111_out, a8}), .out(subtractor_16_out), .bin(not_168_out), .bout(subtractor_16_bout));
  Subtractor #(.width(16)) subtractor_17 (
    .a(out_46), .b({not_122_out[15:3], not_122_out[3], not_122_out[1:0]}), .out(subtractor_17_out),
    .bin(not_169_out), .bout(subtractor_17_bout));
  not not_177 (Final_Answer[1], subtractor_8_bout);
  not not_178 (Final_Answer[0], subtractor_9_bout);
  not not_179 (out_18[7], subtractor_10_bout);
  not not_180 (out_18[6], subtractor_11_bout);
  not not_181 (out_18[5], subtractor_12_bout);
  not not_182 (out_18[4], subtractor_13_bout);
  not not_183 (out_18[3], subtractor_14_bout);
  not not_184 (out_18[2], subtractor_15_bout);
  not not_185 (out_18[1], subtractor_16_bout);
  not not_186 (out_18[0], subtractor_17_bout);
  // NOT_Gate not_187 is placed but not wired

  assign out_19 = {Final_Answer, out_18};
  assign out_20[15:8] = {a8, a7, a6, a5, a4, a3, a2, A1};
  assign out_22[14:0] = {a8, a7, a6, a5, a4, a3, a2, A1, out_20[7:1]};
  assign out_24[13:0] = {a8, a7, a6, a5, a4, a3, a2, A1, out_20[7:2]};
  assign out_26[12:0] = {a8, a7, a6, a5, a4, a3, a2, A1, out_20[7:3]};
  assign out_28[11:0] = {a8, a7, a6, a5, a4, a3, a2, A1, out_20[7:4]};
  assign out_30[10:0] = {a8, a7, a6, a5, a4, a3, a2, A1, out_20[7:5]};
  assign out_32[9:0] = {a8, a7, a6, a5, a4, a3, a2, A1, out_20[7:6]};
  assign out_34[8:0] = {a8, a7, a6, a5, a4, a3, a2, A1, out_20[7]};
  assign out_35 = Final_Answer[1];
  assign out_37[7:0] = {a8, a7, a6, a5, a4, a3, a2, A1};
  assign out_39[6:0] = {a8, a7, a6, a5, a4, a3, a2};

  // Notes on the sheet:
  //   divisor
  //   Right Shift
  //   Don't use output
  //   Left Shift
  //   dividend
  //   logic breaks
endmodule

module MUX_8_BIT_CHOOSEr_CIRCUIT (
  input  LS,
  input  in_2,
  input  in_3,
  input  in_4,
  input  in_5,
  input  in_6,
  input  in_7,
  input  in_8,
  input  in_9,
  input  in_10,
  input  in_11,
  input  in_12,
  input  in_13,
  input  in_14,
  input  in_15,
  input  MS,
  output out_17,
  output SUB,
  output MUL,
  output DIV
);

  wire not_1_out, not_2_out, not_3_out, not_4_out, not_5_out, not_6_out, not_7_out, not_8_out, not_9_out,
       not_10_out, not_11_out, not_12_out, not_13_out, not_14_out, not_15_out, not_16_out, not_17_out,
       not_18_out, not_19_out, not_20_out, not_21_out, not_22_out, not_23_out, not_24_out, not_25_out,
       not_26_out, not_27_out, not_28_out, not_29_out, not_30_out, not_31_out, not_32_out;

  LED led_1 (.in(MS));
  LED led_2 (.in(in_8));
  not not_1 (not_1_out, in_15);
  not not_2 (not_2_out, in_13);
  not not_3 (not_3_out, in_9);
  not not_4 (not_4_out, in_5);
  not not_5 (not_5_out, in_2);
  not not_6 (not_6_out, MS);
  not not_7 (not_7_out, in_15);
  not not_8 (not_8_out, in_14);
  not not_9 (not_9_out, in_13);
  not not_10 (not_10_out, in_11);
  not not_11 (not_11_out, in_10);
  not not_12 (not_12_out, in_9);
  not not_13 (not_13_out, in_3);
  not not_14 (not_14_out, in_2);
  not not_15 (not_15_out, in_14);
  not not_16 (not_16_out, in_13);
  not not_17 (not_17_out, in_12);
  not not_18 (not_18_out, in_9);
  not not_19 (not_19_out, in_8);
  not not_20 (not_20_out, in_7);
  not not_21 (not_21_out, in_6);
  not not_22 (not_22_out, LS);
  not not_23 (not_23_out, MS);
  not not_24 (not_24_out, in_14);
  not not_25 (not_25_out, in_13);
  not not_26 (not_26_out, in_11);
  not not_27 (not_27_out, in_9);
  not not_28 (not_28_out, in_8);
  not not_29 (not_29_out, in_6);
  not not_30 (not_30_out, in_4);
  not not_31 (not_31_out, in_3);
  not not_32 (not_32_out, LS);
  LED led_3 (.in(out_17));
  and and_1 (out_17, MS, not_1_out, in_14, not_2_out, in_12, in_11, in_10, not_3_out, in_7, in_6, not_4_out, in_4, in_3, not_5_out, LS);
  and and_2 (SUB, not_6_out, not_7_out, not_8_out, not_9_out, in_12, not_10_out, not_11_out, not_12_out, in_7, in_6, in_5, in_4, not_13_out, not_14_out, LS);
  LED led_4 (.in(SUB));
  and and_3 (MUL, MS, in_15, not_15_out, not_16_out, not_17_out, in_11, in_10, not_18_out, not_20_out, not_21_out, in_5, in_4, in_3, in_2, not_22_out);
  LED led_5 (.in(MUL));
  LED led_6 (.in(DIV));
  and and_4 (DIV, not_23_out, in_15, not_24_out, not_25_out, in_12, not_26_out, in_10, not_27_out, in_7, not_29_out, in_5, not_30_out, not_31_out, in_2, not_32_out);

  // Notes on the sheet:
  //   ADD: 1010  1110  1110  1101 
  //   SUB: 0000  1000  1111 1001
  //   MUL: 1100  0110  0001 1110
  //   DIV: 0100  1010 0101 0010 
  //   ADD
endmodule

module MUX_to_SELECTOR (
  input  in_1,
  input  in_2,
  input  in_3,
  input  in_4,
  input  in_5,
  input  in_6,
  input  in_7,
  input  in_8,
  input  InputFromMux,
  output out_10,
  output out_11,
  output out_12,
  output out_13,
  output out_14,
  output out_15,
  output out_16,
  output out_17
);

  and and_1 (out_16, InputFromMux, in_7);
  and and_2 (out_17, InputFromMux, in_8);
  and and_3 (out_13, InputFromMux, in_4);
  and and_4 (out_15, InputFromMux, in_6);
  and and_5 (out_14, InputFromMux, in_5);
  and and_6 (out_12, InputFromMux, in_3);
  and and_7 (out_11, InputFromMux, in_2);
  and and_8 (out_10, InputFromMux, in_1);
endmodule

// Division
module Div_8_bit_circuit (
  input  A1,
  input  a2,
  input  a3,
  input  a4,
  input  a5,
  input  a6,
  input  a7,
  input  a8,
  input  A1_2,
  input  a2_2,
  input  a3_2,
  input  a4_2,
  input  a5_2,
  input  a6_2,
  input  a7_2,
  input  a8_2,
  output [7:0] Final_Answer,
  output out_18
);

  wire not_153_out, not_154_out, not_155_out, not_156_out, not_157_out, not_158_out, not_159_out,
       not_160_out, not_161_out, not_162_out, not_163_out, not_164_out, not_165_out, not_166_out,
       not_167_out, not_168_out, not_169_out, not_170_out, subtractor_1_bout, subtractor_2_bout,
       subtractor_3_bout, subtractor_4_bout, subtractor_5_bout, subtractor_6_bout, subtractor_7_bout,
       subtractor_8_bout, subtractor_9_bout, subtractor_10_bout, subtractor_11_bout, subtractor_12_bout,
       subtractor_13_bout, subtractor_14_bout, subtractor_15_bout, subtractor_16_bout, subtractor_17_bout;
  wire [0:0] not_143_out;
  wire [7:0] not_186_out;
  wire [15:0] muxfor8bitdivision_1_out_4, muxfor8bitdivision_2_out_4, muxfor8bitdivision_3_out_4,
       muxfor8bitdivision_4_out_4, muxfor8bitdivision_5_out_4, muxfor8bitdivision_6_out_4,
       muxfor8bitdivision_7_out_4, muxfor8bitdivision_8_out_4, muxfor8bitdivision_9_out_4,
       muxfor8bitdivision_10_out_4, muxfor8bitdivision_11_out_4, muxfor8bitdivision_12_out_4,
       muxfor8bitdivision_13_out_4, muxfor8bitdivision_14_out_4, muxfor8bitdivision_15_out_4,
       muxfor8bitdivision_16_out_4, muxfor8bitdivision_17_out_4, not_122_out, not_138_out, not_141_out,
       not_142_out, subtractor_1_out, subtractor_2_out, subtractor_3_out, subtractor_4_out, subtractor_5_out,
       subtractor_6_out, subtractor_7_out, subtractor_8_out, subtractor_9_out, subtractor_10_out,
       subtractor_11_out, subtractor_12_out, subtractor_13_out, subtractor_14_out, subtractor_15_out,
       subtractor_16_out, subtractor_17_out;
  wire [15:1] not_111_out;
  wire [15:2] not_101_out;
  wire [15:3] not_92_out;
  wire [15:4] not_84_out;
  wire [15:5] not_77_out;
  wire [15:6] not_71_out;
  wire [15:7] not_64_out;
  wire [15:8] not_58_out, not_151_out;
  wire [15:9] not_53_out;
  wire [15:10] not_5_out;
  wire [15:12] not_1_out;
  wire [15:14] not_42_out;

  not not_1 (not_1_out[12], 1'b1);
  not not_2 (not_1_out[14], 1'b1);
  not not_3 (not_138_out[12], 1'b1);
  not not_4 (not_138_out[14], 1'b1);
  not not_5 (not_5_out[10], 1'b1);
  not not_6 (not_5_out[12], 1'b1);
  not not_7 (not_5_out[14], 1'b1);
  not not_8 (not_53_out[12], 1'b1);
  not not_9 (not_53_out[14], 1'b1);
  not not_10 (not_58_out[12], 1'b1);
  not not_11 (not_58_out[14], 1'b1);
  not not_12 (not_64_out[12], 1'b1);
  not not_13 (not_64_out[14], 1'b1);
  not not_14 (not_71_out[8], 1'b1);
  not not_15 (not_71_out[10], 1'b1);
  not not_16 (not_71_out[12], 1'b1);
  not not_17 (not_71_out[14], 1'b1);
  not not_18 (not_77_out[8], 1'b1);
  not not_19 (not_77_out[10], 1'b1);
  not not_20 (not_77_out[12], 1'b1);
  not not_21 (not_77_out[14], 1'b1);
  not not_22 (not_84_out[8], 1'b1);
  not not_23 (not_84_out[10], 1'b1);
  not not_24 (not_84_out[12], 1'b1);
  not not_25 (not_84_out[14], 1'b1);
  not not_26 (not_92_out[8], 1'b1);
  not not_27 (not_92_out[10], 1'b1);
  not not_28 (not_92_out[12], 1'b1);
  not not_29 (not_92_out[14], 1'b1);
  not not_30 (not_101_out[8], 1'b1);
  not not_31 (not_101_out[10], 1'b1);
  not not_32 (not_101_out[12], 1'b1);
  not not_33 (not_101_out[14], 1'b1);
  not not_34 (not_111_out[8], 1'b1);
  not not_35 (not_111_out[10], 1'b1);
  not not_36 (not_111_out[12], 1'b1);
  not not_37 (not_111_out[14], 1'b1);
  not not_38 (not_122_out[8], 1'b1);
  not not_39 (not_122_out[10], 1'b1);
  not not_40 (not_122_out[12], 1'b1);
  not not_41 (not_122_out[14], 1'b1);
  not not_42 (not_42_out[14], 1'b1);
  not not_43 (not_142_out[14], 1'b1);
  not not_44 (not_142_out[15], 1'b1);
  not not_45 (not_1_out[13], 1'b1);
  not not_46 (not_1_out[15], 1'b1);
  not not_47 (not_138_out[11], 1'b1);
  not not_48 (not_138_out[13], 1'b1);
  not not_49 (not_138_out[15], 1'b1);
  not not_50 (not_5_out[11], 1'b1);
  not not_51 (not_5_out[13], 1'b1);
  not not_52 (not_5_out[15], 1'b1);
  not not_53 (not_53_out[9], 1'b1);
  not not_54 (not_53_out[10], 1'b1);
  not not_55 (not_53_out[11], 1'b1);
  not not_56 (not_53_out[13], 1'b1);
  not not_57 (not_53_out[15], 1'b1);
  not not_58 (not_58_out[8], 1'b1);
  not not_59 (not_58_out[9], 1'b1);
  not not_60 (not_58_out[10], 1'b1);
  not not_61 (not_58_out[11], 1'b1);
  not not_62 (not_58_out[13], 1'b1);
  not not_63 (not_58_out[15], 1'b1);
  not not_64 (not_64_out[7], 1'b1);
  not not_65 (not_64_out[8], 1'b1);
  not not_66 (not_64_out[9], 1'b1);
  not not_67 (not_64_out[10], 1'b1);
  not not_68 (not_64_out[11], 1'b1);
  not not_69 (not_64_out[13], 1'b1);
  not not_70 (not_64_out[15], 1'b1);
  not not_71 (not_71_out[6], 1'b1);
  not not_72 (not_71_out[7], 1'b1);
  not not_73 (not_71_out[9], 1'b1);
  not not_74 (not_71_out[11], 1'b1);
  not not_75 (not_71_out[13], 1'b1);
  not not_76 (not_71_out[15], 1'b1);
  not not_77 (not_77_out[5], 1'b1);
  not not_78 (not_77_out[6], 1'b1);
  not not_79 (not_77_out[7], 1'b1);
  not not_80 (not_77_out[9], 1'b1);
  not not_81 (not_77_out[11], 1'b1);
  not not_82 (not_77_out[13], 1'b1);
  not not_83 (not_77_out[15], 1'b1);
  not not_84 (not_84_out[4], 1'b1);
  not not_85 (not_84_out[5], 1'b1);
  not not_86 (not_84_out[6], 1'b1);
  not not_87 (not_84_out[7], 1'b1);
  not not_88 (not_84_out[9], 1'b1);
  not not_89 (not_84_out[11], 1'b1);
  not not_90 (not_84_out[13], 1'b1);
  not not_91 (not_84_out[15], 1'b1);
  not not_92 (not_92_out[3], 1'b1);
  not not_93 (not_92_out[4], 1'b1);
  not not_94 (not_92_out[5], 1'b1);
  not not_95 (not_92_out[6], 1'b1);
  not not_96 (not_92_out[7], 1'b1);
  not not_97 (not_92_out[9], 1'b1);
  not not_98 (not_92_out[11], 1'b1);
  not not_99 (not_92_out[13], 1'b1);
  not not_100 (not_92_out[15], 1'b1);
  not not_101 (not_101_out[2], 1'b1);
  not not_102 (not_101_out[3], 1'b1);
  not not_103 (not_101_out[4], 1'b1);
  not not_104 (not_101_out[5], 1'b1);
  not not_105 (not_101_out[6], 1'b1);
  not not_106 (not_101_out[7], 1'b1);
  not not_107 (not_101_out[9], 1'b1);
  not not_108 (not_101_out[11], 1'b1);
  not not_109 (not_101_out[13], 1'b1);
  not not_110 (not_101_out[15], 1'b1);
  not not_111 (not_111_out[1], 1'b1);
  not not_112 (not_111_out[2], 1'b1);
  not not_113 (not_111_out[3], 1'b1);
  not not_114 (not_111_out[4], 1'b1);
  not not_115 (not_111_out[5], 1'b1);
  not not_116 (not_111_out[6], 1'b1);
  not not_117 (not_111_out[7], 1'b1);
  not not_118 (not_111_out[9], 1'b1);
  not not_119 (not_111_out[11], 1'b1);
  not not_120 (not_111_out[13], 1'b1);
  not not_121 (not_111_out[15], 1'b1);
  not not_122 (not_122_out[0], 1'b1);
  not not_123 (not_122_out[1], 1'b1);
  not not_124 (not_122_out[3], 1'b1);
  not not_125 (not_122_out[3], 1'b1);
  not not_126 (not_122_out[4], 1'b1);
  not not_127 (not_122_out[5], 1'b1);
  not not_128 (not_122_out[6], 1'b1);
  not not_129 (not_122_out[7], 1'b1);
  not not_130 (not_122_out[9], 1'b1);
  not not_131 (not_122_out[11], 1'b1);
  not not_132 (not_122_out[13], 1'b1);
  not not_133 (not_122_out[15], 1'b1);
  not not_134 (not_141_out[15], 1'b1);
  not not_135 (not_42_out[15], 1'b1);
  not not_136 (not_142_out[13], 1'b1);
  not not_137 (not_138_out[1], 1'b1);
  not not_138 (not_138_out[0], 1'b1);
  not not_139 (not_138_out[2], 1'b1);
  not not_140 (not_142_out[1], 1'b1);
  not not_141 (not_141_out[0], 1'b1);
  not not_142 (not_142_out[0], 1'b1);
  not not_143 (not_143_out[0], 1'b1);
  not not_144 (not_141_out[1], 1'b1);
  not not_145 (not_151_out[15], 1'b1);
  not not_146 (not_151_out[14], 1'b1);
  not not_147 (not_151_out[12], 1'b1);
  not not_148 (not_151_out[13], 1'b1);
  not not_149 (not_151_out[11], 1'b1);
  MuxFor8BitDivision muxfor8bitdivision_1 (
    .in_1(subtractor_1_out), .in_2({not_151_out, a8, a7, a6, a5, a4, a3, a2, A1}), .in_3(subtractor_1_bout),
    .out_4(muxfor8bitdivision_1_out_4));
  MuxFor8BitDivision muxfor8bitdivision_2 (
    .in_1(subtractor_2_out), .in_2(muxfor8bitdivision_1_out_4), .in_3(subtractor_2_bout),
    .out_4(muxfor8bitdivision_2_out_4));
  MuxFor8BitDivision muxfor8bitdivision_3 (
    .in_1(subtractor_3_out), .in_2(muxfor8bitdivision_2_out_4), .in_3(subtractor_3_bout),
    .out_4(muxfor8bitdivision_3_out_4));
  MuxFor8BitDivision muxfor8bitdivision_4 (
    .in_1(subtractor_4_out), .in_2(muxfor8bitdivision_3_out_4), .in_3(subtractor_4_bout),
    .out_4(muxfor8bitdivision_4_out_4));
  MuxFor8BitDivision muxfor8bitdivision_5 (
    .in_1(subtractor_5_out), .in_2(muxfor8bitdivision_4_out_4), .in_3(subtractor_5_bout),
    .out_4(muxfor8bitdivision_5_out_4));
  MuxFor8BitDivision muxfor8bitdivision_6 (
    .in_1(subtractor_6_out), .in_2(muxfor8bitdivision_5_out_4), .in_3(subtractor_6_bout),
    .out_4(muxfor8bitdivision_6_out_4));
  MuxFor8BitDivision muxfor8bitdivision_7 (
    .in_1(subtractor_7_out), .in_2(muxfor8bitdivision_6_out_4), .in_3(subtractor_7_bout),
    .out_4(muxfor8bitdivision_7_out_4));
  MuxFor8BitDivision muxfor8bitdivision_8 (
    .in_1(subtractor_8_out), .in_2(muxfor8bitdivision_7_out_4), .in_3(subtractor_8_bout),
    .out_4(muxfor8bitdivision_8_out_4));
  MuxFor8BitDivision muxfor8bitdivision_9 (
    .in_1(subtractor_9_out), .in_2(muxfor8bitdivision_8_out_4), .in_3(subtractor_9_bout),
    .out_4(muxfor8bitdivision_9_out_4));
  MuxFor8BitDivision muxfor8bitdivision_10 (
    .in_1(subtractor_10_out), .in_2(muxfor8bitdivision_9_out_4), .in_3(subtractor_10_bout),
    .out_4(muxfor8bitdivision_10_out_4));
  MuxFor8BitDivision muxfor8bitdivision_11 (
    .in_1(subtractor_11_out), .in_2(muxfor8bitdivision_10_out_4), .in_3(subtractor_11_bout),
    .out_4(muxfor8bitdivision_11_out_4));
  MuxFor8BitDivision muxfor8bitdivision_12 (
    .in_1(subtractor_12_out), .in_2(muxfor8bitdivision_11_out_4), .in_3(subtractor_12_bout),
    .out_4(muxfor8bitdivision_12_out_4));
  MuxFor8BitDivision muxfor8bitdivision_13 (
    .in_1(subtractor_13_out), .in_2(muxfor8bitdivision_12_out_4), .in_3(subtractor_13_bout),
    .out_4(muxfor8bitdivision_13_out_4));
  MuxFor8BitDivision muxfor8bitdivision_14 (
    .in_1(subtractor_14_out), .in_2(muxfor8bitdivision_13_out_4), .in_3(subtractor_14_bout),
    .out_4(muxfor8bitdivision_14_out_4));
  MuxFor8BitDivision muxfor8bitdivision_15 (
    .in_1(subtractor_15_out), .in_2(muxfor8bitdivision_14_out_4), .in_3(subtractor_15_bout),
    .out_4(muxfor8bitdivision_15_out_4));
  not not_150 (not_151_out[10], 1'b1);
  not not_151 (not_151_out[8], 1'b1);
  not not_152 (not_151_out[9], 1'b1);
  MuxFor8BitDivision muxfor8bitdivision_16 (
    .in_1(subtractor_16_out), .in_2(muxfor8bitdivision_15_out_4), .in_3(subtractor_16_bout),
    .out_4(muxfor8bitdivision_16_out_4));
  MuxFor8BitDivision muxfor8bitdivision_17 (
    .in_1(subtractor_17_out), .in_2(muxfor8bitdivision_16_out_4), .in_3(subtractor_17_bout),
    .out_4(muxfor8bitdivision_17_out_4));
  not not_153 (not_153_out, 1'b1);
  LED led_1 (.in(subtractor_1_bout));
  Subtractor #(.width(16)) subtractor_1 (
    .a({not_151_out, a8, a7, a6, a5, a4, a3, a2, A1}),
    .b({a8_2, a7_2, a6_2, a5_2, a4_2, a3_2, a2_2, A1_2, not_138_out[2:0], not_142_out[1:0], not_141_out[1:0], not_143_out[0]}),
    .out(subtractor_1_out), .bin(not_153_out), .bout(subtractor_1_bout));
  not not_154 (not_154_out, 1'b1);
  Subtractor #(.width(16)) subtractor_2 (
    .a(muxfor8bitdivision_1_out_4),
    .b({not_141_out[15], a8_2, a7_2, a6_2, a5_2, a4_2, a3_2, a2_2, A1_2, not_138_out[2:0], not_142_out[1:0], not_141_out[1:0]}),
    .out(subtractor_2_out), .bin(not_154_out), .bout(subtractor_2_bout));
  LED led_2 (.in(subtractor_2_bout));
  not not_155 (not_155_out, 1'b1);
  Subtractor #(.width(16)) subtractor_3 (
    .a(muxfor8bitdivision_2_out_4),
    .b({not_42_out, a8_2, a7_2, a6_2, a5_2, a4_2, a3_2, a2_2, A1_2, not_138_out[2:0], not_142_out[1:0], not_141_out[1]}),
    .out(subtractor_3_out), .bin(not_155_out), .bout(subtractor_3_bout));
  LED led_3 (.in(subtractor_3_bout));
  not not_156 (not_156_out, 1'b1);
  Subtractor #(.width(16)) subtractor_4 (
    .a(muxfor8bitdivision_3_out_4),
    .b({not_142_out[15:13], a8_2, a7_2, a6_2, a5_2, a4_2, a3_2, a2_2, A1_2, not_138_out[2:0], not_142_out[1:0]}),
    .out(subtractor_4_out), .bin(not_156_out), .bout(subtractor_4_bout));
  LED led_4 (.in(subtractor_4_bout));
  not not_157 (not_157_out, 1'b1);
  Subtractor #(.width(16)) subtractor_5 (
    .a(muxfor8bitdivision_4_out_4),
    .b({not_1_out, a8_2, a7_2, a6_2, a5_2, a4_2, a3_2, a2_2, A1_2, not_138_out[2:0], not_142_out[1]}),
    .out(subtractor_5_out), .bin(not_157_out), .bout(subtractor_5_bout));
  LED led_5 (.in(subtractor_5_bout));
  not not_158 (not_158_out, 1'b1);
  Subtractor #(.width(16)) subtractor_6 (
    .a(muxfor8bitdivision_5_out_4),
    .b({not_138_out[15:11], a8_2, a7_2, a6_2, a5_2, a4_2, a3_2, a2_2, A1_2, not_138_out[2:0]}),
    .out(subtractor_6_out), .bin(not_158_out), .bout(subtractor_6_bout));
  LED led_6 (.in(subtractor_6_bout));
  not not_159 (not_159_out, 1'b1);
  Subtractor #(.width(16)) subtractor_7 (
    .a(muxfor8bitdivision_6_out_4),
    .b({not_5_out, a8_2, a7_2, a6_2, a5_2, a4_2, a3_2, a2_2, A1_2, not_138_out[2:1]}),
    .out(subtractor_7_out), .bin(not_159_out), .bout(subtractor_7_bout));
  LED led_7 (.in(subtractor_7_bout));
  not not_160 (not_160_out, 1'b1);
  Subtractor #(.width(16)) subtractor_8 (
    .a(muxfor8bitdivision_7_out_4),
    .b({not_53_out, a8_2, a7_2, a6_2, a5_2, a4_2, a3_2, a2_2, A1_2, not_138_out[2]}), .out(subtractor_8_out),
    .bin(not_160_out), .bout(subtractor_8_bout));
  LED led_8 (.in(subtractor_8_bout));
  not not_161 (not_161_out, 1'b1);
  Subtractor #(.width(16)) subtractor_9 (
    .a(muxfor8bitdivision_8_out_4), .b({not_58_out, a8_2, a7_2, a6_2, a5_2, a4_2, a3_2, a2_2, A1_2}),
    .out(subtractor_9_out), .bin(not_161_out), .bout(subtractor_9_bout));
  LED led_9 (.in(subtractor_9_bout));
  not not_162 (not_162_out, 1'b1);
  Subtractor #(.width(16)) subtractor_10 (
    .a(muxfor8bitdivision_9_out_4), .b({not_64_out, a8_2, a7_2, a6_2, a5_2, a4_2, a3_2, a2_2}),
    .out(subtractor_10_out), .bin(not_162_out), .bout(subtractor_10_bout));
  LED led_10 (.in(subtractor_10_bout));
  not not_163 (not_163_out, 1'b1);
  Subtractor #(.width(16)) subtractor_11 (
    .a(muxfor8bitdivision_10_out_4), .b({not_71_out, a8_2, a7_2, a6_2, a5_2, a4_2, a3_2}),
    .out(subtractor_11_out), .bin(not_163_out), .bout(subtractor_11_bout));
  LED led_11 (.in(subtractor_11_bout));
  not not_164 (not_164_out, 1'b1);
  Subtractor #(.width(16)) subtractor_12 (
    .a(muxfor8bitdivision_11_out_4), .b({not_77_out, a8_2, a7_2, a6_2, a5_2, a4_2}), .out(subtractor_12_out),
    .bin(not_164_out), .bout(subtractor_12_bout));
  LED led_12 (.in(subtractor_12_bout));
  not not_165 (not_165_out, 1'b1);
  Subtractor #(.width(16)) subtractor_13 (
    .a(muxfor8bitdivision_12_out_4), .b({not_84_out, a8_2, a7_2, a6_2, a5_2}), .out(subtractor_13_out),
    .bin(not_165_out), .bout(subtractor_13_bout));
  LED led_13 (.in(subtractor_13_bout));
  not not_166 (not_166_out, 1'b1);
  Subtractor #(.width(16)) subtractor_14 (
    .a(muxfor8bitdivision_13_out_4), .b({not_92_out, a8_2, a7_2, a6_2}), .out(subtractor_14_out),
    .bin(not_166_out), .bout(subtractor_14_bout));
  LED led_14 (.in(subtractor_14_bout));
  not not_167 (not_167_out, 1'b1);
  Subtractor #(.width(16)) subtractor_15 (
    .a(muxfor8bitdivision_14_out_4), .b({not_101_out, a8_2, a7_2}), .out(subtractor_15_out),
    .bin(not_167_out), .bout(subtractor_15_bout));
  LED led_15 (.in(subtractor_15_bout));
  not not_168 (not_168_out, 1'b1);
  LED led_16 (.in(subtractor_16_bout));
  not not_169 (not_169_out, 1'b1);
  LED led_17 (.in(subtractor_17_bout));
  not not_170 (not_170_out, subtractor_1_bout);
  not not_171 (Final_Answer[7], subtractor_2_bout);
  not not_172 (Final_Answer[6], subtractor_3_bout);
  not not_173 (Final_Answer[5], subtractor_4_bout);
  not not_174 (Final_Answer[4], subtractor_5_bout);
  not not_175 (Final_Answer[3], subtractor_6_bout);
  not not_176 (Final_Answer[2], subtractor_7_bout);
  Subtractor #(.width(16)) subtractor_16 (
    .a(muxfor8bitdivision_15_out_4), .b({not_111_out, a8_2}), .out(subtractor_16_out), .bin(not_168_out),
    .bout(subtractor_16_bout));
  Subtractor #(.width(16)) subtractor_17 (
    .a(muxfor8bitdivision_16_out_4), .b({not_122_out[15:3], not_122_out[3], not_122_out[1:0]}),
    .out(subtractor_17_out), .bin(not_169_out), .bout(subtractor_17_bout));
  not not_177 (Final_Answer[1], subtractor_8_bout);
  not not_178 (Final_Answer[0], subtractor_9_bout);
  not not_179 (not_186_out[7], subtractor_10_bout);
  not not_180 (not_186_out[6], subtractor_11_bout);
  not not_181 (not_186_out[5], subtractor_12_bout);
  not not_182 (not_186_out[4], subtractor_13_bout);
  not not_183 (not_186_out[3], subtractor_14_bout);
  not not_184 (not_186_out[2], subtractor_15_bout);
  not not_185 (not_186_out[1], subtractor_16_bout);
  not not_186 (not_186_out[0], subtractor_17_bout);
  // NOT_Gate not_187 is placed but not wired

  assign out_18 = Final_Answer[1];

  // Notes on the sheet:
  //   divisor
  //   Right Shift
  //   Don't use output
  //   Left Shift
  //   dividend
  //   logic breaks
endmodule

// Control
module Control_8_bit (
  input  in_1,
  input  in_2,
  input  in_3,
  input  in_4,
  input  in_5,
  input  in_6,
  input  in_7,
  input  in_8,
  input  InputFromMux,
  output out_10,
  output out_11,
  output out_12,
  output out_13,
  output out_14,
  output out_15,
  output out_16,
  output out_17
);

  and and_1 (out_17, InputFromMux, in_8);
  and and_2 (out_16, InputFromMux, in_7);
  and and_3 (out_15, InputFromMux, in_6);
  and and_4 (out_14, InputFromMux, in_5);
  and and_5 (out_13, InputFromMux, in_4);
  and and_6 (out_11, InputFromMux, in_2);
  and and_7 (out_12, InputFromMux, in_3);
  and and_8 (out_10, InputFromMux, in_1);
endmodule

// MUX by BASU
module MUX_16_bit_direction (
  input  LS,
  input  in_2,
  input  in_3,
  input  in_4,
  input  in_5,
  input  in_6,
  input  in_7,
  input  in_8,
  input  in_9,
  input  in_10,
  input  in_11,
  input  in_12,
  input  in_13,
  input  in_14,
  input  in_15,
  input  MS,
  output out_17,
  output SUB,
  output MUL,
  output DIV
);

  wire not_1_out, not_2_out, not_3_out, not_4_out, not_5_out, not_6_out, not_7_out, not_8_out, not_9_out,
       not_10_out, not_11_out, not_12_out, not_13_out, not_14_out, not_15_out, not_16_out, not_17_out,
       not_18_out, not_19_out, not_20_out, not_21_out, not_22_out, not_23_out, not_24_out, not_25_out,
       not_26_out, not_27_out, not_28_out, not_29_out, not_30_out, not_31_out, not_32_out;

  LED led_1 (.in(MS));
  LED led_2 (.in(in_8));
  not not_1 (not_1_out, in_15);
  not not_2 (not_2_out, in_13);
  not not_3 (not_3_out, in_9);
  not not_4 (not_4_out, in_5);
  not not_5 (not_5_out, in_2);
  not not_6 (not_6_out, MS);
  not not_7 (not_7_out, in_15);
  not not_8 (not_8_out, in_14);
  not not_9 (not_9_out, in_13);
  not not_10 (not_10_out, in_11);
  not not_11 (not_11_out, in_10);
  not not_12 (not_12_out, in_9);
  not not_13 (not_13_out, in_3);
  not not_14 (not_14_out, in_2);
  not not_15 (not_15_out, in_14);
  not not_16 (not_16_out, in_13);
  not not_17 (not_17_out, in_12);
  not not_18 (not_18_out, in_9);
  not not_19 (not_19_out, in_8);
  not not_20 (not_20_out, in_7);
  not not_21 (not_21_out, in_6);
  not not_22 (not_22_out, LS);
  not not_23 (not_23_out, MS);
  not not_24 (not_24_out, in_14);
  not not_25 (not_25_out, in_13);
  not not_26 (not_26_out, in_11);
  not not_27 (not_27_out, in_9);
  not not_28 (not_28_out, in_8);
  not not_29 (not_29_out, in_6);
  not not_30 (not_30_out, in_4);
  not not_31 (not_31_out, in_3);
  not not_32 (not_32_out, LS);
  LED led_3 (.in(out_17));
  and and_1 (out_17, MS, not_1_out, in_14, not_2_out, in_12, in_11, in_10, not_3_out, in_7, in_6, not_4_out, in_4, in_3, not_5_out, LS);
  and and_2 (SUB, not_6_out, not_7_out, not_8_out, not_9_out, in_12, not_10_out, not_11_out, not_12_out, in_7, in_6, in_5, in_4, not_13_out, not_14_out, LS);
  LED led_4 (.in(SUB));
  and and_3 (MUL, MS, in_15, not_15_out, not_16_out, not_17_out, in_11, in_10, not_18_out, not_20_out, not_21_out, in_5, in_4, in_3, in_2, not_22_out);
  LED led_5 (.in(MUL));
  and and_4 (DIV, not_23_out, in_15, not_24_out, not_25_out, in_12, not_26_out, in_10, not_27_out, in_7, not_29_out, in_5, not_30_out, not_31_out, in_2, not_32_out);
  LED led_6 (.in(DIV));

  // Notes on the sheet:
  //   ADD: 1010  1110  1110  1101 
  //   SUB: 0000  1000  1111 1001
  //   MUL: 1100  0110  0001 1110
  //   DIV: 0100  1010 0101 0010 
  //   ADD
endmodule

module ALU_without_D_Latch (
  input  [15:0] in_1,
  input  [7:0] _8_bit_Number_A,
  input  [7:0] _8_bit_Number_B,
  output [15:0] out_4,
  output [7:0] out_5,
  output [7:0] out_6,
  output [7:0] out_7,
  output [15:0] out_8
);

  wire Addition_Module_out_25, Instruction_Set_div, Instruction_Set_mul, Instruction_Set_out_17,
       Instruction_Set_sub;
  wire [7:0] Control_2_out_10, Control_3_out_10, Control_4_out_10, Control_5_out_10, Control_6_out_10,
       Control_7_out_10, Control_8_out_10, Control_out_10;

  MUX_16_bit_direction Instruction_Set (
    .LS(in_1[0]), .in_2(in_1[1]), .in_3(in_1[2]), .in_4(in_1[3]), .in_5(in_1[4]), .in_6(in_1[5]),
    .in_7(in_1[6]), .in_8(in_1[7]), .in_9(in_1[8]), .in_10(in_1[9]), .in_11(in_1[10]), .in_12(in_1[11]),
    .in_13(in_1[12]), .in_14(in_1[13]), .in_15(in_1[14]), .MS(in_1[15]), .out_17(Instruction_Set_out_17),
    .SUB(Instruction_Set_sub), .MUL(Instruction_Set_mul), .DIV(Instruction_Set_div));
  Control_8_bit Control (
    .in_1(_8_bit_Number_A[0]), .in_2(_8_bit_Number_A[1]), .in_3(_8_bit_Number_A[2]),
    .in_4(_8_bit_Number_A[3]), .in_5(_8_bit_Number_A[4]), .in_6(_8_bit_Number_A[5]),
    .in_7(_8_bit_Number_A[6]), .in_8(_8_bit_Number_A[7]), .InputFromMux(Instruction_Set_out_17),
    .out_10(Control_out_10[0]), .out_11(Control_out_10[1]), .out_12(Control_out_10[2]),
    .out_13(Control_out_10[3]), .out_14(Control_out_10[4]), .out_15(Control_out_10[5]),
    .out_16(Control_out_10[6]), .out_17(Control_out_10[7]));
  Control_8_bit Control_2 (
    .in_1(_8_bit_Number_B[0]), .in_2(_8_bit_Number_B[1]), .in_3(_8_bit_Number_B[2]),
    .in_4(_8_bit_Number_B[3]), .in_5(_8_bit_Number_B[4]), .in_6(_8_bit_Number_B[5]),
    .in_7(_8_bit_Number_B[6]), .in_8(_8_bit_Number_B[7]), .InputFromMux(Instruction_Set_out_17),
    .out_10(Control_2_out_10[0]), .out_11(Control_2_out_10[1]), .out_12(Control_2_out_10[2]),
    .out_13(Control_2_out_10[3]), .out_14(Control_2_out_10[4]), .out_15(Control_2_out_10[5]),
    .out_16(Control_2_out_10[6]), .out_17(Control_2_out_10[7]));
  Addition Addition_Module (
    .A1(Control_out_10[0]), .A2(Control_out_10[1]), .A3(Control_out_10[2]), .A4(Control_out_10[3]),
    .A5(Control_out_10[4]), .A6(Control_out_10[5]), .A7(Control_out_10[6]), .A8(Control_out_10[7]),
    .B1(Control_2_out_10[0]), .B2(Control_2_out_10[1]), .B3(Control_2_out_10[2]), .B4(Control_2_out_10[3]),
    .B5(Control_2_out_10[4]), .B6(Control_2_out_10[5]), .B7(Control_2_out_10[6]), .B8(Control_2_out_10[7]),
    .out_17(out_6[0]), .out_18(out_6[1]), .out_19(out_6[2]), .out_20(out_6[3]), .out_21(out_6[4]),
    .out_22(out_6[5]), .out_23(out_6[6]), .out_24(out_6[7]), .out_25(Addition_Module_out_25));
  Control_8_bit Control_3 (
    .in_1(_8_bit_Number_A[0]), .in_2(_8_bit_Number_A[1]), .in_3(_8_bit_Number_A[2]),
    .in_4(_8_bit_Number_A[3]), .in_5(_8_bit_Number_A[4]), .in_6(_8_bit_Number_A[5]),
    .in_7(_8_bit_Number_A[6]), .in_8(_8_bit_Number_A[7]), .InputFromMux(Instruction_Set_sub),
    .out_10(Control_3_out_10[0]), .out_11(Control_3_out_10[1]), .out_12(Control_3_out_10[2]),
    .out_13(Control_3_out_10[3]), .out_14(Control_3_out_10[4]), .out_15(Control_3_out_10[5]),
    .out_16(Control_3_out_10[6]), .out_17(Control_3_out_10[7]));
  Control_8_bit Control_4 (
    .in_1(_8_bit_Number_B[0]), .in_2(_8_bit_Number_B[1]), .in_3(_8_bit_Number_B[2]),
    .in_4(_8_bit_Number_B[3]), .in_5(_8_bit_Number_B[4]), .in_6(_8_bit_Number_B[5]),
    .in_7(_8_bit_Number_B[6]), .in_8(_8_bit_Number_B[7]), .InputFromMux(Instruction_Set_sub),
    .out_10(Control_4_out_10[0]), .out_11(Control_4_out_10[1]), .out_12(Control_4_out_10[2]),
    .out_13(Control_4_out_10[3]), .out_14(Control_4_out_10[4]), .out_15(Control_4_out_10[5]),
    .out_16(Control_4_out_10[6]), .out_17(Control_4_out_10[7]));
  Subtraction Subtraction_Module (
    .A1(Control_3_out_10[0]), .A2(Control_3_out_10[1]), .A3(Control_3_out_10[2]), .A4(Control_3_out_10[3]),
    .A5(Control_3_out_10[4]), .A6(Control_3_out_10[5]), .A7(Control_3_out_10[6]), .A8(Control_3_out_10[7]),
    .B1(Control_4_out_10[0]), .B2(Control_4_out_10[1]), .B3(Control_4_out_10[2]), .B4(Control_4_out_10[3]),
    .B5(Control_4_out_10[4]), .B6(Control_4_out_10[5]), .B7(Control_4_out_10[6]), .B8(Control_4_out_10[7]),
    .out_17(out_7[0]), .out_18(out_7[1]), .out_19(out_7[2]), .out_20(out_7[3]), .out_21(out_7[4]),
    .out_22(out_7[5]), .out_23(out_7[6]), .out_24(out_7[7]));
  Control_8_bit Control_5 (
    .in_1(_8_bit_Number_A[0]), .in_2(_8_bit_Number_A[1]), .in_3(_8_bit_Number_A[2]),
    .in_4(_8_bit_Number_A[3]), .in_5(_8_bit_Number_A[4]), .in_6(_8_bit_Number_A[5]),
    .in_7(_8_bit_Number_A[6]), .in_8(_8_bit_Number_A[7]), .InputFromMux(Instruction_Set_mul),
    .out_10(Control_5_out_10[0]), .out_11(Control_5_out_10[1]), .out_12(Control_5_out_10[2]),
    .out_13(Control_5_out_10[3]), .out_14(Control_5_out_10[4]), .out_15(Control_5_out_10[5]),
    .out_16(Control_5_out_10[6]), .out_17(Control_5_out_10[7]));
  Control_8_bit Control_6 (
    .in_1(_8_bit_Number_B[0]), .in_2(_8_bit_Number_B[1]), .in_3(_8_bit_Number_B[2]),
    .in_4(_8_bit_Number_B[3]), .in_5(_8_bit_Number_B[4]), .in_6(_8_bit_Number_B[5]),
    .in_7(_8_bit_Number_B[6]), .in_8(_8_bit_Number_B[7]), .InputFromMux(Instruction_Set_mul),
    .out_10(Control_6_out_10[0]), .out_11(Control_6_out_10[1]), .out_12(Control_6_out_10[2]),
    .out_13(Control_6_out_10[3]), .out_14(Control_6_out_10[4]), .out_15(Control_6_out_10[5]),
    .out_16(Control_6_out_10[6]), .out_17(Control_6_out_10[7]));
  Multiplication Multiplication_Module (
    .in_1(Control_5_out_10[0]), .in_2(Control_5_out_10[1]), .in_3(Control_5_out_10[2]),
    .in_4(Control_5_out_10[3]), .a5(Control_5_out_10[4]), .a6(Control_5_out_10[5]), .a7(Control_5_out_10[6]),
    .a8(Control_5_out_10[7]), .b1(Control_6_out_10[0]), .b2(Control_6_out_10[1]), .b3(Control_6_out_10[2]),
    .b4(Control_6_out_10[3]), .b5(Control_6_out_10[4]), .b6(Control_6_out_10[5]), .b7(Control_6_out_10[6]),
    .b8(Control_6_out_10[7]), .out_17(out_4[0]), .out_18(out_4[1]), .out_19(out_4[2]), .out_20(out_4[3]),
    .out_21(out_4[4]), .out_22(out_4[5]), .out_23(out_4[6]), .out_24(out_4[7]), .out_25(out_4[8]),
    .out_26(out_4[9]), .out_27(out_4[10]), .out_28(out_4[11]), .out_29(out_4[12]), .out_30(out_4[13]),
    .out_31(out_4[14]), .out_32(out_4[15]));
  assign out_8 = out_4 | {{8{1'b0}}, out_7} | {{8{1'b0}}, out_5} | {{8{1'b0}}, out_6};  // OR_Gate or_1, 16 bits wide
  Control_8_bit Control_7 (
    .in_1(_8_bit_Number_A[0]), .in_2(_8_bit_Number_A[1]), .in_3(_8_bit_Number_A[2]),
    .in_4(_8_bit_Number_A[3]), .in_5(_8_bit_Number_A[4]), .in_6(_8_bit_Number_A[5]),
    .in_7(_8_bit_Number_A[6]), .in_8(_8_bit_Number_A[7]), .InputFromMux(Instruction_Set_div),
    .out_10(Control_7_out_10[0]), .out_11(Control_7_out_10[1]), .out_12(Control_7_out_10[2]),
    .out_13(Control_7_out_10[3]), .out_14(Control_7_out_10[4]), .out_15(Control_7_out_10[5]),
    .out_16(Control_7_out_10[6]), .out_17(Control_7_out_10[7]));
  Control_8_bit Control_8 (
    .in_1(_8_bit_Number_B[0]), .in_2(_8_bit_Number_B[1]), .in_3(_8_bit_Number_B[2]),
    .in_4(_8_bit_Number_B[3]), .in_5(_8_bit_Number_B[4]), .in_6(_8_bit_Number_B[5]),
    .in_7(_8_bit_Number_B[6]), .in_8(_8_bit_Number_B[7]), .InputFromMux(Instruction_Set_div),
    .out_10(Control_8_out_10[0]), .out_11(Control_8_out_10[1]), .out_12(Control_8_out_10[2]),
    .out_13(Control_8_out_10[3]), .out_14(Control_8_out_10[4]), .out_15(Control_8_out_10[5]),
    .out_16(Control_8_out_10[6]), .out_17(Control_8_out_10[7]));
  Div_8_bit_circuit div_8_bit_circuit_1 (
    .A1(Control_7_out_10[0]), .a2(Control_7_out_10[1]), .a3(Control_7_out_10[2]), .a4(Control_7_out_10[3]),
    .a5(Control_7_out_10[4]), .a6(Control_7_out_10[5]), .a7(Control_7_out_10[6]), .a8(Control_7_out_10[7]),
    .A1_2(Control_8_out_10[0]), .a2_2(Control_8_out_10[1]), .a3_2(Control_8_out_10[2]),
    .a4_2(Control_8_out_10[3]), .a5_2(Control_8_out_10[4]), .a6_2(Control_8_out_10[5]),
    .a7_2(Control_8_out_10[6]), .a8_2(Control_8_out_10[7]), .Final_Answer(out_5));  // open: out_18

  // Notes on the sheet:
  //   A
  //   B
  //   ADD: 1010  1110  1110  1101 
  //   SUB: 0000  1000  1111 1001
  //   MUL: 1100  0110  0001 1110
  //   DIV: 0100  1010 0101 0010 
  //   Instruction Set
  //   A+B
  //   Cout
  //   Addition Answer
  //   A-B
  //   Subtraction Answer
  //   A*B
  //   Multiplication Answer
  //   A/B
  //   Division Answer
endmodule
module FinalExam (
  input  [31:0] _32_Bit_Input,
  input  [31:0] _32_Bit_Input_2,
  input  [15:0] _16_BIT_BUS,
  input  [4:0] _00000__0,
  input  [4:0] _00001__1,
  input  [4:0] _10_2,
  input  [4:0] _11__3,
  input  [4:0] _100__4,
  input  [4:0] _101__5,
  input  [4:0] _110__6,
  input  [4:0] _111__7,
  input  [4:0] _1000__8,
  input  [4:0] _1001__9,
  input  [4:0] _1010__10,
  input  [4:0] _1011__11,
  input  [4:0] _1100__12,
  input  [4:0] _1101__13,
  input  [4:0] _1110__14,
  input  [4:0] _1111__15,
  input  [4:0] _10000__16,
  input  [4:0] _10001__17,
  input  [4:0] _10010__18,
  input  [4:0] _10011__19,
  input  [4:0] _10100__20,
  input  [4:0] _10101__21,
  input  [4:0] _10110__22,
  input  [4:0] _11000__23,
  input  [4:0] _11000__24,
  input  [4:0] _11001__25,
  input  [4:0] _11010__26,
  input  [4:0] _11011__27,
  input  [4:0] _11100__28,
  input  [4:0] _11101__29,
  input  [4:0] _11110__30,
  input  [4:0] _11111__31,
  output [31:0] _32_BIT_OUTPUT,
  output [4:0] out_37,
  output [31:0] out_38,
  output [4:0] LAST_5_BITS,
  output out_40,
  output [31:0] out_41,
  output out_42,
  output [31:0] out_43,
  output out_44,
  output [31:0] out_45,
  output out_46,
  output [31:0] out_47,
  output out_48,
  output [31:0] out_49,
  output out_50,
  output [31:0] out_51,
  output out_52,
  output [31:0] out_53,
  output out_54,
  output [31:0] out_55,
  output out_56,
  output [31:0] out_57,
  output out_58,
  output [31:0] out_59,
  output out_60,
  output [31:0] out_61,
  output out_62,
  output [31:0] out_63,
  output out_64,
  output [31:0] out_65,
  output out_66,
  output [31:0] out_67,
  output out_68,
  output [31:0] out_69,
  output out_70,
  output [31:0] out_71,
  output out_72,
  output [31:0] out_73,
  output out_74,
  output [31:0] out_75,
  output out_76,
  output [31:0] out_77,
  output out_78,
  output [31:0] out_79,
  output out_80,
  output [31:0] out_81,
  output out_82,
  output [31:0] out_83,
  output out_84,
  output [31:0] out_85,
  output out_86,
  output [31:0] out_87,
  output out_88,
  output [31:0] out_89,
  output out_90,
  output [31:0] out_91,
  output out_92,
  output [31:0] out_93,
  output out_94,
  output [31:0] out_95,
  output out_96,
  output [31:0] out_97,
  output out_98,
  output [31:0] out_99,
  output out_100,
  output [31:0] out_101,
  output out_102,
  output [31:0] out_103
);

  wire mux_for_finalexam_1_out_17;
  wire [31:0] rotateleft_1_rorated_output, rotateleft_2_rorated_output, rotateleft_3_rorated_output,
       rotateleft_4_rorated_output, rotateleft_5_rorated_output, rotateleft_6_rorated_output,
       rotateleft_7_rorated_output, rotateleft_8_rorated_output, rotateleft_9_rorated_output,
       rotateleft_10_rorated_output, rotateleft_11_rorated_output, rotateleft_12_rorated_output,
       rotateleft_13_rorated_output, rotateleft_14_rorated_output, rotateleft_15_rorated_output,
       rotateleft_16_rorated_output, rotateleft_17_rorated_output, rotateleft_18_rorated_output,
       rotateleft_19_rorated_output, rotateleft_20_rorated_output, rotateleft_21_rorated_output,
       rotateleft_22_rorated_output, rotateleft_23_rorated_output, rotateleft_24_rorated_output,
       rotateleft_25_rorated_output, rotateleft_26_rorated_output, rotateleft_27_rorated_output,
       rotateleft_28_rorated_output, rotateleft_29_rorated_output, rotateleft_30_rorated_output,
       rotateleft_31_rorated_output, rotateleft_32_rorated_output;
  wire [31:5] n32bitcontrol_34_out_39;

  MUX_FOR_FINALEXAM mux_for_finalexam_1 (
    .LS(_16_BIT_BUS[0]), .in_2(_16_BIT_BUS[1]), .in_3(_16_BIT_BUS[2]), .in_4(_16_BIT_BUS[3]),
    .in_5(_16_BIT_BUS[4]), .in_6(_16_BIT_BUS[5]), .in_7(_16_BIT_BUS[6]), .in_8(_16_BIT_BUS[7]),
    .in_9(_16_BIT_BUS[8]), .in_10(_16_BIT_BUS[9]), .in_11(_16_BIT_BUS[10]), .in_12(_16_BIT_BUS[11]),
    .in_13(_16_BIT_BUS[12]), .in_14(_16_BIT_BUS[13]), .in_15(_16_BIT_BUS[14]), .MS(_16_BIT_BUS[15]),
    .out_17(mux_for_finalexam_1_out_17));
  RotateLeft rotateleft_1 (.INPUT(out_38), .Rorated_Output(rotateleft_1_rorated_output));
  RotateLeft rotateleft_2 (.INPUT(rotateleft_1_rorated_output), .Rorated_Output(rotateleft_2_rorated_output));
  RotateLeft rotateleft_3 (.INPUT(rotateleft_2_rorated_output), .Rorated_Output(rotateleft_3_rorated_output));
  RotateLeft rotateleft_4 (.INPUT(rotateleft_3_rorated_output), .Rorated_Output(rotateleft_4_rorated_output));
  RotateLeft rotateleft_5 (.INPUT(rotateleft_4_rorated_output), .Rorated_Output(rotateleft_5_rorated_output));
  RotateLeft rotateleft_6 (.INPUT(rotateleft_5_rorated_output), .Rorated_Output(rotateleft_6_rorated_output));
  RotateLeft rotateleft_7 (.INPUT(rotateleft_6_rorated_output), .Rorated_Output(rotateleft_7_rorated_output));
  RotateLeft rotateleft_8 (.INPUT(rotateleft_7_rorated_output), .Rorated_Output(rotateleft_8_rorated_output));
  RotateLeft rotateleft_9 (.INPUT(rotateleft_8_rorated_output), .Rorated_Output(rotateleft_9_rorated_output));
  RotateLeft rotateleft_10 (.INPUT(rotateleft_9_rorated_output), .Rorated_Output(rotateleft_10_rorated_output));
  RotateLeft rotateleft_11 (.INPUT(rotateleft_10_rorated_output), .Rorated_Output(rotateleft_11_rorated_output));
  RotateLeft rotateleft_12 (.INPUT(rotateleft_11_rorated_output), .Rorated_Output(rotateleft_12_rorated_output));
  RotateLeft rotateleft_13 (.INPUT(rotateleft_12_rorated_output), .Rorated_Output(rotateleft_13_rorated_output));
  RotateLeft rotateleft_14 (.INPUT(rotateleft_13_rorated_output), .Rorated_Output(rotateleft_14_rorated_output));
  RotateLeft rotateleft_15 (.INPUT(rotateleft_14_rorated_output), .Rorated_Output(rotateleft_15_rorated_output));
  RotateLeft rotateleft_16 (.INPUT(rotateleft_15_rorated_output), .Rorated_Output(rotateleft_16_rorated_output));
  RotateLeft rotateleft_17 (.INPUT(rotateleft_16_rorated_output), .Rorated_Output(rotateleft_17_rorated_output));
  RotateLeft rotateleft_18 (.INPUT(rotateleft_17_rorated_output), .Rorated_Output(rotateleft_18_rorated_output));
  RotateLeft rotateleft_19 (.INPUT(rotateleft_18_rorated_output), .Rorated_Output(rotateleft_19_rorated_output));
  RotateLeft rotateleft_20 (.INPUT(rotateleft_19_rorated_output), .Rorated_Output(rotateleft_20_rorated_output));
  RotateLeft rotateleft_21 (.INPUT(rotateleft_20_rorated_output), .Rorated_Output(rotateleft_21_rorated_output));
  RotateLeft rotateleft_22 (.INPUT(rotateleft_21_rorated_output), .Rorated_Output(rotateleft_22_rorated_output));
  RotateLeft rotateleft_23 (.INPUT(rotateleft_22_rorated_output), .Rorated_Output(rotateleft_23_rorated_output));
  RotateLeft rotateleft_24 (.INPUT(rotateleft_23_rorated_output), .Rorated_Output(rotateleft_24_rorated_output));
  RotateLeft rotateleft_25 (.INPUT(rotateleft_24_rorated_output), .Rorated_Output(rotateleft_25_rorated_output));
  RotateLeft rotateleft_26 (.INPUT(rotateleft_25_rorated_output), .Rorated_Output(rotateleft_26_rorated_output));
  RotateLeft rotateleft_27 (.INPUT(rotateleft_26_rorated_output), .Rorated_Output(rotateleft_27_rorated_output));
  RotateLeft rotateleft_28 (.INPUT(rotateleft_27_rorated_output), .Rorated_Output(rotateleft_28_rorated_output));
  RotateLeft rotateleft_29 (.INPUT(rotateleft_28_rorated_output), .Rorated_Output(rotateleft_29_rorated_output));
  RotateLeft rotateleft_30 (.INPUT(rotateleft_29_rorated_output), .Rorated_Output(rotateleft_30_rorated_output));
  RotateLeft rotateleft_31 (.INPUT(rotateleft_30_rorated_output), .Rorated_Output(rotateleft_31_rorated_output));
  RotateLeft rotateleft_32 (.INPUT(rotateleft_31_rorated_output), .Rorated_Output(rotateleft_32_rorated_output));
  _32BITCONTROL u_32bitcontrol_1 (
    .in_1(_32_Bit_Input[0]), .in_2(_32_Bit_Input[1]), .in_3(_32_Bit_Input[2]), .in_4(_32_Bit_Input[3]),
    .in_5(_32_Bit_Input[4]), .in_6(_32_Bit_Input[5]), .in_7(_32_Bit_Input[6]), .in_8(_32_Bit_Input[7]),
    .in_9(_32_Bit_Input[8]), .in_10(_32_Bit_Input[9]), .in_11(_32_Bit_Input[10]), .in_12(_32_Bit_Input[11]),
    .in_13(_32_Bit_Input[12]), .in_14(_32_Bit_Input[13]), .in_15(_32_Bit_Input[14]),
    .in_16(_32_Bit_Input[15]), .in_17(_32_Bit_Input[16]), .in_18(_32_Bit_Input[17]),
    .in_19(_32_Bit_Input[18]), .in_20(_32_Bit_Input[19]), .in_21(_32_Bit_Input[20]),
    .in_22(_32_Bit_Input[21]), .in_23(_32_Bit_Input[22]), .in_24(_32_Bit_Input[23]),
    .in_25(_32_Bit_Input[24]), .in_26(_32_Bit_Input[25]), .in_27(_32_Bit_Input[26]),
    .in_28(_32_Bit_Input[27]), .in_29(_32_Bit_Input[28]), .in_30(_32_Bit_Input[29]),
    .in_31(_32_Bit_Input[30]), .in_32(_32_Bit_Input[31]), .InputFromMux(mux_for_finalexam_1_out_17),
    .out_34(out_38[0]), .out_35(out_38[1]), .out_36(out_38[2]), .out_37(out_38[3]), .out_38(out_38[4]),
    .out_39(out_38[5]), .out_40(out_38[6]), .out_41(out_38[7]), .out_42(out_38[8]), .out_43(out_38[9]),
    .out_44(out_38[10]), .out_45(out_38[11]), .out_46(out_38[12]), .out_47(out_38[13]), .out_48(out_38[14]),
    .out_49(out_38[15]), .out_50(out_38[16]), .out_51(out_38[17]), .out_52(out_38[18]), .out_53(out_38[19]),
    .out_54(out_38[20]), .out_55(out_38[21]), .out_56(out_38[22]), .out_57(out_38[23]), .out_58(out_38[24]),
    .out_59(out_38[25]), .out_60(out_38[26]), .out_61(out_38[27]), .out_62(out_38[28]), .out_63(out_38[29]),
    .out_64(out_38[30]), .out_65(out_38[31]));
  testComp testcomp_1 (.in_2(LAST_5_BITS), .in_1(_00000__0), .out_3(out_40));
  _32BITCONTROL u_32bitcontrol_2 (
    .in_1(out_38[31]), .in_2(out_38[30]), .in_3(out_38[29]), .in_4(out_38[28]), .in_5(out_38[27]),
    .in_6(out_38[26]), .in_7(out_38[25]), .in_8(out_38[24]), .in_9(out_38[23]), .in_10(out_38[22]),
    .in_11(out_38[21]), .in_12(out_38[20]), .in_13(out_38[19]), .in_14(out_38[18]), .in_15(out_38[17]),
    .in_16(out_38[16]), .in_17(out_38[15]), .in_18(out_38[14]), .in_19(out_38[13]), .in_20(out_38[12]),
    .in_21(out_38[11]), .in_22(out_38[10]), .in_23(out_38[9]), .in_24(out_38[8]), .in_25(out_38[7]),
    .in_26(out_38[6]), .in_27(out_38[5]), .in_28(out_38[4]), .in_29(out_38[3]), .in_30(out_38[2]),
    .in_31(out_38[1]), .in_32(out_38[0]), .InputFromMux(out_40), .out_34(out_41[31]), .out_35(out_41[30]),
    .out_36(out_41[29]), .out_37(out_41[28]), .out_38(out_41[27]), .out_39(out_41[26]), .out_40(out_41[25]),
    .out_41(out_41[24]), .out_42(out_41[23]), .out_43(out_41[22]), .out_44(out_41[21]), .out_45(out_41[20]),
    .out_46(out_41[19]), .out_47(out_41[18]), .out_48(out_41[17]), .out_49(out_41[16]), .out_50(out_41[15]),
    .out_51(out_41[14]), .out_52(out_41[13]), .out_53(out_41[12]), .out_54(out_41[11]), .out_55(out_41[10]),
    .out_56(out_41[9]), .out_57(out_41[8]), .out_58(out_41[7]), .out_59(out_41[6]), .out_60(out_41[5]),
    .out_61(out_41[4]), .out_62(out_41[3]), .out_63(out_41[2]), .out_64(out_41[1]), .out_65(out_41[0]));
  testComp testcomp_2 (.in_2(LAST_5_BITS), .in_1(_00001__1), .out_3(out_42));
  _32BITCONTROL u_32bitcontrol_3 (
    .in_1(rotateleft_1_rorated_output[31]), .in_2(rotateleft_1_rorated_output[30]),
    .in_3(rotateleft_1_rorated_output[29]), .in_4(rotateleft_1_rorated_output[28]),
    .in_5(rotateleft_1_rorated_output[27]), .in_6(rotateleft_1_rorated_output[26]),
    .in_7(rotateleft_1_rorated_output[25]), .in_8(rotateleft_1_rorated_output[24]),
    .in_9(rotateleft_1_rorated_output[23]), .in_10(rotateleft_1_rorated_output[22]),
    .in_11(rotateleft_1_rorated_output[21]), .in_12(rotateleft_1_rorated_output[20]),
    .in_13(rotateleft_1_rorated_output[19]), .in_14(rotateleft_1_rorated_output[18]),
    .in_15(rotateleft_1_rorated_output[17]), .in_16(rotateleft_1_rorated_output[16]),
    .in_17(rotateleft_1_rorated_output[15]), .in_18(rotateleft_1_rorated_output[14]),
    .in_19(rotateleft_1_rorated_output[13]), .in_20(rotateleft_1_rorated_output[12]),
    .in_21(rotateleft_1_rorated_output[11]), .in_22(rotateleft_1_rorated_output[10]),
    .in_23(rotateleft_1_rorated_output[9]), .in_24(rotateleft_1_rorated_output[8]),
    .in_25(rotateleft_1_rorated_output[7]), .in_26(rotateleft_1_rorated_output[6]),
    .in_27(rotateleft_1_rorated_output[5]), .in_28(rotateleft_1_rorated_output[4]),
    .in_29(rotateleft_1_rorated_output[3]), .in_30(rotateleft_1_rorated_output[2]),
    .in_31(rotateleft_1_rorated_output[1]), .in_32(rotateleft_1_rorated_output[0]), .InputFromMux(out_42),
    .out_34(out_43[31]), .out_35(out_43[30]), .out_36(out_43[29]), .out_37(out_43[28]), .out_38(out_43[27]),
    .out_39(out_43[26]), .out_40(out_43[25]), .out_41(out_43[24]), .out_42(out_43[23]), .out_43(out_43[22]),
    .out_44(out_43[21]), .out_45(out_43[20]), .out_46(out_43[19]), .out_47(out_43[18]), .out_48(out_43[17]),
    .out_49(out_43[16]), .out_50(out_43[15]), .out_51(out_43[14]), .out_52(out_43[13]), .out_53(out_43[12]),
    .out_54(out_43[11]), .out_55(out_43[10]), .out_56(out_43[9]), .out_57(out_43[8]), .out_58(out_43[7]),
    .out_59(out_43[6]), .out_60(out_43[5]), .out_61(out_43[4]), .out_62(out_43[3]), .out_63(out_43[2]),
    .out_64(out_43[1]), .out_65(out_43[0]));
  testComp testcomp_3 (.in_2(LAST_5_BITS), .in_1(_10_2), .out_3(out_44));
  testComp testcomp_4 (.in_2(LAST_5_BITS), .in_1(_11__3), .out_3(out_46));
  testComp testcomp_5 (.in_2(LAST_5_BITS), .in_1(_100__4), .out_3(out_48));
  testComp testcomp_6 (.in_2(LAST_5_BITS), .in_1(_101__5), .out_3(out_50));
  testComp testcomp_7 (.in_2(LAST_5_BITS), .in_1(_110__6), .out_3(out_52));
  testComp testcomp_8 (.in_2(LAST_5_BITS), .in_1(_111__7), .out_3(out_54));
  testComp testcomp_9 (.in_2(LAST_5_BITS), .in_1(_1000__8), .out_3(out_56));
  testComp testcomp_10 (.in_2(LAST_5_BITS), .in_1(_1001__9), .out_3(out_58));
  testComp testcomp_11 (.in_2(LAST_5_BITS), .in_1(_1010__10), .out_3(out_60));
  testComp testcomp_12 (.in_2(LAST_5_BITS), .in_1(_1011__11), .out_3(out_62));
  testComp testcomp_13 (.in_2(LAST_5_BITS), .in_1(_1100__12), .out_3(out_64));
  testComp testcomp_14 (.in_2(LAST_5_BITS), .in_1(_1101__13), .out_3(out_66));
  testComp testcomp_15 (.in_2(LAST_5_BITS), .in_1(_1110__14), .out_3(out_68));
  testComp testcomp_16 (.in_2(LAST_5_BITS), .in_1(_1111__15), .out_3(out_70));
  testComp testcomp_17 (.in_2(LAST_5_BITS), .in_1(_10000__16), .out_3(out_72));
  testComp testcomp_18 (.in_2(LAST_5_BITS), .in_1(_10001__17), .out_3(out_74));
  testComp testcomp_19 (.in_2(LAST_5_BITS), .in_1(_10010__18), .out_3(out_76));
  testComp testcomp_20 (.in_2(LAST_5_BITS), .in_1(_10011__19), .out_3(out_78));
  testComp testcomp_21 (.in_2(LAST_5_BITS), .in_1(_10100__20), .out_3(out_80));
  testComp testcomp_22 (.in_2(LAST_5_BITS), .in_1(_10101__21), .out_3(out_82));
  testComp testcomp_23 (.in_2(LAST_5_BITS), .in_1(_10110__22), .out_3(out_84));
  testComp testcomp_24 (.in_2(LAST_5_BITS), .in_1(_11000__23), .out_3(out_86));
  testComp testcomp_25 (.in_2(LAST_5_BITS), .in_1(_11000__24), .out_3(out_88));
  testComp testcomp_26 (.in_2(LAST_5_BITS), .in_1(_11001__25), .out_3(out_90));
  testComp testcomp_27 (.in_2(LAST_5_BITS), .in_1(_11010__26), .out_3(out_92));
  testComp testcomp_28 (.in_2(LAST_5_BITS), .in_1(_11011__27), .out_3(out_94));
  testComp testcomp_29 (.in_2(LAST_5_BITS), .in_1(_11100__28), .out_3(out_96));
  testComp testcomp_30 (.in_2(LAST_5_BITS), .in_1(_11101__29), .out_3(out_98));
  testComp testcomp_31 (.in_2(LAST_5_BITS), .in_1(_11110__30), .out_3(out_100));
  testComp testcomp_32 (.in_2(LAST_5_BITS), .in_1(_11111__31), .out_3(out_102));
  _32BITCONTROL u_32bitcontrol_4 (
    .in_1(rotateleft_2_rorated_output[31]), .in_2(rotateleft_2_rorated_output[30]),
    .in_3(rotateleft_2_rorated_output[29]), .in_4(rotateleft_2_rorated_output[28]),
    .in_5(rotateleft_2_rorated_output[27]), .in_6(rotateleft_2_rorated_output[26]),
    .in_7(rotateleft_2_rorated_output[25]), .in_8(rotateleft_2_rorated_output[24]),
    .in_9(rotateleft_2_rorated_output[23]), .in_10(rotateleft_2_rorated_output[22]),
    .in_11(rotateleft_2_rorated_output[21]), .in_12(rotateleft_2_rorated_output[20]),
    .in_13(rotateleft_2_rorated_output[19]), .in_14(rotateleft_2_rorated_output[18]),
    .in_15(rotateleft_2_rorated_output[17]), .in_16(rotateleft_2_rorated_output[16]),
    .in_17(rotateleft_2_rorated_output[15]), .in_18(rotateleft_2_rorated_output[14]),
    .in_19(rotateleft_2_rorated_output[13]), .in_20(rotateleft_2_rorated_output[12]),
    .in_21(rotateleft_2_rorated_output[11]), .in_22(rotateleft_2_rorated_output[10]),
    .in_23(rotateleft_2_rorated_output[9]), .in_24(rotateleft_2_rorated_output[8]),
    .in_25(rotateleft_2_rorated_output[7]), .in_26(rotateleft_2_rorated_output[6]),
    .in_27(rotateleft_2_rorated_output[5]), .in_28(rotateleft_2_rorated_output[4]),
    .in_29(rotateleft_2_rorated_output[3]), .in_30(rotateleft_2_rorated_output[2]),
    .in_31(rotateleft_2_rorated_output[1]), .in_32(rotateleft_2_rorated_output[0]), .InputFromMux(out_44),
    .out_34(out_45[31]), .out_35(out_45[30]), .out_36(out_45[29]), .out_37(out_45[28]), .out_38(out_45[27]),
    .out_39(out_45[26]), .out_40(out_45[25]), .out_41(out_45[24]), .out_42(out_45[23]), .out_43(out_45[22]),
    .out_44(out_45[21]), .out_45(out_45[20]), .out_46(out_45[19]), .out_47(out_45[18]), .out_48(out_45[17]),
    .out_49(out_45[16]), .out_50(out_45[15]), .out_51(out_45[14]), .out_52(out_45[13]), .out_53(out_45[12]),
    .out_54(out_45[11]), .out_55(out_45[10]), .out_56(out_45[9]), .out_57(out_45[8]), .out_58(out_45[7]),
    .out_59(out_45[6]), .out_60(out_45[5]), .out_61(out_45[4]), .out_62(out_45[3]), .out_63(out_45[2]),
    .out_64(out_45[1]), .out_65(out_45[0]));
  _32BITCONTROL u_32bitcontrol_5 (
    .in_1(rotateleft_3_rorated_output[31]), .in_2(rotateleft_3_rorated_output[30]),
    .in_3(rotateleft_3_rorated_output[29]), .in_4(rotateleft_3_rorated_output[28]),
    .in_5(rotateleft_3_rorated_output[27]), .in_6(rotateleft_3_rorated_output[26]),
    .in_7(rotateleft_3_rorated_output[25]), .in_8(rotateleft_3_rorated_output[24]),
    .in_9(rotateleft_3_rorated_output[23]), .in_10(rotateleft_3_rorated_output[22]),
    .in_11(rotateleft_3_rorated_output[21]), .in_12(rotateleft_3_rorated_output[20]),
    .in_13(rotateleft_3_rorated_output[19]), .in_14(rotateleft_3_rorated_output[18]),
    .in_15(rotateleft_3_rorated_output[17]), .in_16(rotateleft_3_rorated_output[16]),
    .in_17(rotateleft_3_rorated_output[15]), .in_18(rotateleft_3_rorated_output[14]),
    .in_19(rotateleft_3_rorated_output[13]), .in_20(rotateleft_3_rorated_output[12]),
    .in_21(rotateleft_3_rorated_output[11]), .in_22(rotateleft_3_rorated_output[10]),
    .in_23(rotateleft_3_rorated_output[9]), .in_24(rotateleft_3_rorated_output[8]),
    .in_25(rotateleft_3_rorated_output[7]), .in_26(rotateleft_3_rorated_output[6]),
    .in_27(rotateleft_3_rorated_output[5]), .in_28(rotateleft_3_rorated_output[4]),
    .in_29(rotateleft_3_rorated_output[3]), .in_30(rotateleft_3_rorated_output[2]),
    .in_31(rotateleft_3_rorated_output[1]), .in_32(rotateleft_3_rorated_output[0]), .InputFromMux(out_46),
    .out_34(out_47[31]), .out_35(out_47[30]), .out_36(out_47[29]), .out_37(out_47[28]), .out_38(out_47[27]),
    .out_39(out_47[26]), .out_40(out_47[25]), .out_41(out_47[24]), .out_42(out_47[23]), .out_43(out_47[22]),
    .out_44(out_47[21]), .out_45(out_47[20]), .out_46(out_47[19]), .out_47(out_47[18]), .out_48(out_47[17]),
    .out_49(out_47[16]), .out_50(out_47[15]), .out_51(out_47[14]), .out_52(out_47[13]), .out_53(out_47[12]),
    .out_54(out_47[11]), .out_55(out_47[10]), .out_56(out_47[9]), .out_57(out_47[8]), .out_58(out_47[7]),
    .out_59(out_47[6]), .out_60(out_47[5]), .out_61(out_47[4]), .out_62(out_47[3]), .out_63(out_47[2]),
    .out_64(out_47[1]), .out_65(out_47[0]));
  _32BITCONTROL u_32bitcontrol_6 (
    .in_1(rotateleft_4_rorated_output[31]), .in_2(rotateleft_4_rorated_output[30]),
    .in_3(rotateleft_4_rorated_output[29]), .in_4(rotateleft_4_rorated_output[28]),
    .in_5(rotateleft_4_rorated_output[27]), .in_6(rotateleft_4_rorated_output[26]),
    .in_7(rotateleft_4_rorated_output[25]), .in_8(rotateleft_4_rorated_output[24]),
    .in_9(rotateleft_4_rorated_output[23]), .in_10(rotateleft_4_rorated_output[22]),
    .in_11(rotateleft_4_rorated_output[21]), .in_12(rotateleft_4_rorated_output[20]),
    .in_13(rotateleft_4_rorated_output[19]), .in_14(rotateleft_4_rorated_output[18]),
    .in_15(rotateleft_4_rorated_output[17]), .in_16(rotateleft_4_rorated_output[16]),
    .in_17(rotateleft_4_rorated_output[15]), .in_18(rotateleft_4_rorated_output[14]),
    .in_19(rotateleft_4_rorated_output[13]), .in_20(rotateleft_4_rorated_output[12]),
    .in_21(rotateleft_4_rorated_output[11]), .in_22(rotateleft_4_rorated_output[10]),
    .in_23(rotateleft_4_rorated_output[9]), .in_24(rotateleft_4_rorated_output[8]),
    .in_25(rotateleft_4_rorated_output[7]), .in_26(rotateleft_4_rorated_output[6]),
    .in_27(rotateleft_4_rorated_output[5]), .in_28(rotateleft_4_rorated_output[4]),
    .in_29(rotateleft_4_rorated_output[3]), .in_30(rotateleft_4_rorated_output[2]),
    .in_31(rotateleft_4_rorated_output[1]), .in_32(rotateleft_4_rorated_output[0]), .InputFromMux(out_48),
    .out_34(out_49[31]), .out_35(out_49[30]), .out_36(out_49[29]), .out_37(out_49[28]), .out_38(out_49[27]),
    .out_39(out_49[26]), .out_40(out_49[25]), .out_41(out_49[24]), .out_42(out_49[23]), .out_43(out_49[22]),
    .out_44(out_49[21]), .out_45(out_49[20]), .out_46(out_49[19]), .out_47(out_49[18]), .out_48(out_49[17]),
    .out_49(out_49[16]), .out_50(out_49[15]), .out_51(out_49[14]), .out_52(out_49[13]), .out_53(out_49[12]),
    .out_54(out_49[11]), .out_55(out_49[10]), .out_56(out_49[9]), .out_57(out_49[8]), .out_58(out_49[7]),
    .out_59(out_49[6]), .out_60(out_49[5]), .out_61(out_49[4]), .out_62(out_49[3]), .out_63(out_49[2]),
    .out_64(out_49[1]), .out_65(out_49[0]));
  _32BITCONTROL u_32bitcontrol_7 (
    .in_1(rotateleft_5_rorated_output[31]), .in_2(rotateleft_5_rorated_output[30]),
    .in_3(rotateleft_5_rorated_output[29]), .in_4(rotateleft_5_rorated_output[28]),
    .in_5(rotateleft_5_rorated_output[27]), .in_6(rotateleft_5_rorated_output[26]),
    .in_7(rotateleft_5_rorated_output[25]), .in_8(rotateleft_5_rorated_output[24]),
    .in_9(rotateleft_5_rorated_output[23]), .in_10(rotateleft_5_rorated_output[22]),
    .in_11(rotateleft_5_rorated_output[21]), .in_12(rotateleft_5_rorated_output[20]),
    .in_13(rotateleft_5_rorated_output[19]), .in_14(rotateleft_5_rorated_output[18]),
    .in_15(rotateleft_5_rorated_output[17]), .in_16(rotateleft_5_rorated_output[16]),
    .in_17(rotateleft_5_rorated_output[15]), .in_18(rotateleft_5_rorated_output[14]),
    .in_19(rotateleft_5_rorated_output[13]), .in_20(rotateleft_5_rorated_output[12]),
    .in_21(rotateleft_5_rorated_output[11]), .in_22(rotateleft_5_rorated_output[10]),
    .in_23(rotateleft_5_rorated_output[9]), .in_24(rotateleft_5_rorated_output[8]),
    .in_25(rotateleft_5_rorated_output[7]), .in_26(rotateleft_5_rorated_output[6]),
    .in_27(rotateleft_5_rorated_output[5]), .in_28(rotateleft_5_rorated_output[4]),
    .in_29(rotateleft_5_rorated_output[3]), .in_30(rotateleft_5_rorated_output[2]),
    .in_31(rotateleft_5_rorated_output[1]), .in_32(rotateleft_5_rorated_output[0]), .InputFromMux(out_50),
    .out_34(out_51[31]), .out_35(out_51[30]), .out_36(out_51[29]), .out_37(out_51[28]), .out_38(out_51[27]),
    .out_39(out_51[26]), .out_40(out_51[25]), .out_41(out_51[24]), .out_42(out_51[23]), .out_43(out_51[22]),
    .out_44(out_51[21]), .out_45(out_51[20]), .out_46(out_51[19]), .out_47(out_51[18]), .out_48(out_51[17]),
    .out_49(out_51[16]), .out_50(out_51[15]), .out_51(out_51[14]), .out_52(out_51[13]), .out_53(out_51[12]),
    .out_54(out_51[11]), .out_55(out_51[10]), .out_56(out_51[9]), .out_57(out_51[8]), .out_58(out_51[7]),
    .out_59(out_51[6]), .out_60(out_51[5]), .out_61(out_51[4]), .out_62(out_51[3]), .out_63(out_51[2]),
    .out_64(out_51[1]), .out_65(out_51[0]));
  _32BITCONTROL u_32bitcontrol_8 (
    .in_1(rotateleft_6_rorated_output[31]), .in_2(rotateleft_6_rorated_output[30]),
    .in_3(rotateleft_6_rorated_output[29]), .in_4(rotateleft_6_rorated_output[28]),
    .in_5(rotateleft_6_rorated_output[27]), .in_6(rotateleft_6_rorated_output[26]),
    .in_7(rotateleft_6_rorated_output[25]), .in_8(rotateleft_6_rorated_output[24]),
    .in_9(rotateleft_6_rorated_output[23]), .in_10(rotateleft_6_rorated_output[22]),
    .in_11(rotateleft_6_rorated_output[21]), .in_12(rotateleft_6_rorated_output[20]),
    .in_13(rotateleft_6_rorated_output[19]), .in_14(rotateleft_6_rorated_output[18]),
    .in_15(rotateleft_6_rorated_output[17]), .in_16(rotateleft_6_rorated_output[16]),
    .in_17(rotateleft_6_rorated_output[15]), .in_18(rotateleft_6_rorated_output[14]),
    .in_19(rotateleft_6_rorated_output[13]), .in_20(rotateleft_6_rorated_output[12]),
    .in_21(rotateleft_6_rorated_output[11]), .in_22(rotateleft_6_rorated_output[10]),
    .in_23(rotateleft_6_rorated_output[9]), .in_24(rotateleft_6_rorated_output[8]),
    .in_25(rotateleft_6_rorated_output[7]), .in_26(rotateleft_6_rorated_output[6]),
    .in_27(rotateleft_6_rorated_output[5]), .in_28(rotateleft_6_rorated_output[4]),
    .in_29(rotateleft_6_rorated_output[3]), .in_30(rotateleft_6_rorated_output[2]),
    .in_31(rotateleft_6_rorated_output[1]), .in_32(rotateleft_6_rorated_output[0]), .InputFromMux(out_52),
    .out_34(out_53[31]), .out_35(out_53[30]), .out_36(out_53[29]), .out_37(out_53[28]), .out_38(out_53[27]),
    .out_39(out_53[26]), .out_40(out_53[25]), .out_41(out_53[24]), .out_42(out_53[23]), .out_43(out_53[22]),
    .out_44(out_53[21]), .out_45(out_53[20]), .out_46(out_53[19]), .out_47(out_53[18]), .out_48(out_53[17]),
    .out_49(out_53[16]), .out_50(out_53[15]), .out_51(out_53[14]), .out_52(out_53[13]), .out_53(out_53[12]),
    .out_54(out_53[11]), .out_55(out_53[10]), .out_56(out_53[9]), .out_57(out_53[8]), .out_58(out_53[7]),
    .out_59(out_53[6]), .out_60(out_53[5]), .out_61(out_53[4]), .out_62(out_53[3]), .out_63(out_53[2]),
    .out_64(out_53[1]), .out_65(out_53[0]));
  _32BITCONTROL u_32bitcontrol_9 (
    .in_1(rotateleft_7_rorated_output[31]), .in_2(rotateleft_7_rorated_output[30]),
    .in_3(rotateleft_7_rorated_output[29]), .in_4(rotateleft_7_rorated_output[28]),
    .in_5(rotateleft_7_rorated_output[27]), .in_6(rotateleft_7_rorated_output[26]),
    .in_7(rotateleft_7_rorated_output[25]), .in_8(rotateleft_7_rorated_output[24]),
    .in_9(rotateleft_7_rorated_output[23]), .in_10(rotateleft_7_rorated_output[22]),
    .in_11(rotateleft_7_rorated_output[21]), .in_12(rotateleft_7_rorated_output[20]),
    .in_13(rotateleft_7_rorated_output[19]), .in_14(rotateleft_7_rorated_output[18]),
    .in_15(rotateleft_7_rorated_output[17]), .in_16(rotateleft_7_rorated_output[16]),
    .in_17(rotateleft_7_rorated_output[15]), .in_18(rotateleft_7_rorated_output[14]),
    .in_19(rotateleft_7_rorated_output[13]), .in_20(rotateleft_7_rorated_output[12]),
    .in_21(rotateleft_7_rorated_output[11]), .in_22(rotateleft_7_rorated_output[10]),
    .in_23(rotateleft_7_rorated_output[9]), .in_24(rotateleft_7_rorated_output[8]),
    .in_25(rotateleft_7_rorated_output[7]), .in_26(rotateleft_7_rorated_output[6]),
    .in_27(rotateleft_7_rorated_output[5]), .in_28(rotateleft_7_rorated_output[4]),
    .in_29(rotateleft_7_rorated_output[3]), .in_30(rotateleft_7_rorated_output[2]),
    .in_31(rotateleft_7_rorated_output[1]), .in_32(rotateleft_7_rorated_output[0]), .InputFromMux(out_54),
    .out_34(out_55[31]), .out_35(out_55[30]), .out_36(out_55[29]), .out_37(out_55[28]), .out_38(out_55[27]),
    .out_39(out_55[26]), .out_40(out_55[25]), .out_41(out_55[24]), .out_42(out_55[23]), .out_43(out_55[22]),
    .out_44(out_55[21]), .out_45(out_55[20]), .out_46(out_55[19]), .out_47(out_55[18]), .out_48(out_55[17]),
    .out_49(out_55[16]), .out_50(out_55[15]), .out_51(out_55[14]), .out_52(out_55[13]), .out_53(out_55[12]),
    .out_54(out_55[11]), .out_55(out_55[10]), .out_56(out_55[9]), .out_57(out_55[8]), .out_58(out_55[7]),
    .out_59(out_55[6]), .out_60(out_55[5]), .out_61(out_55[4]), .out_62(out_55[3]), .out_63(out_55[2]),
    .out_64(out_55[1]), .out_65(out_55[0]));
  _32BITCONTROL u_32bitcontrol_10 (
    .in_1(rotateleft_8_rorated_output[31]), .in_2(rotateleft_8_rorated_output[30]),
    .in_3(rotateleft_8_rorated_output[29]), .in_4(rotateleft_8_rorated_output[28]),
    .in_5(rotateleft_8_rorated_output[27]), .in_6(rotateleft_8_rorated_output[26]),
    .in_7(rotateleft_8_rorated_output[25]), .in_8(rotateleft_8_rorated_output[24]),
    .in_9(rotateleft_8_rorated_output[23]), .in_10(rotateleft_8_rorated_output[22]),
    .in_11(rotateleft_8_rorated_output[21]), .in_12(rotateleft_8_rorated_output[20]),
    .in_13(rotateleft_8_rorated_output[19]), .in_14(rotateleft_8_rorated_output[18]),
    .in_15(rotateleft_8_rorated_output[17]), .in_16(rotateleft_8_rorated_output[16]),
    .in_17(rotateleft_8_rorated_output[15]), .in_18(rotateleft_8_rorated_output[14]),
    .in_19(rotateleft_8_rorated_output[13]), .in_20(rotateleft_8_rorated_output[12]),
    .in_21(rotateleft_8_rorated_output[11]), .in_22(rotateleft_8_rorated_output[10]),
    .in_23(rotateleft_8_rorated_output[9]), .in_24(rotateleft_8_rorated_output[8]),
    .in_25(rotateleft_8_rorated_output[7]), .in_26(rotateleft_8_rorated_output[6]),
    .in_27(rotateleft_8_rorated_output[5]), .in_28(rotateleft_8_rorated_output[4]),
    .in_29(rotateleft_8_rorated_output[3]), .in_30(rotateleft_8_rorated_output[2]),
    .in_31(rotateleft_8_rorated_output[1]), .in_32(rotateleft_8_rorated_output[0]), .InputFromMux(out_56),
    .out_34(out_57[31]), .out_35(out_57[30]), .out_36(out_57[29]), .out_37(out_57[28]), .out_38(out_57[27]),
    .out_39(out_57[26]), .out_40(out_57[25]), .out_41(out_57[24]), .out_42(out_57[23]), .out_43(out_57[22]),
    .out_44(out_57[21]), .out_45(out_57[20]), .out_46(out_57[19]), .out_47(out_57[18]), .out_48(out_57[17]),
    .out_49(out_57[16]), .out_50(out_57[15]), .out_51(out_57[14]), .out_52(out_57[13]), .out_53(out_57[12]),
    .out_54(out_57[11]), .out_55(out_57[10]), .out_56(out_57[9]), .out_57(out_57[8]), .out_58(out_57[7]),
    .out_59(out_57[6]), .out_60(out_57[5]), .out_61(out_57[4]), .out_62(out_57[3]), .out_63(out_57[2]),
    .out_64(out_57[1]), .out_65(out_57[0]));
  _32BITCONTROL u_32bitcontrol_11 (
    .in_1(rotateleft_9_rorated_output[31]), .in_2(rotateleft_9_rorated_output[30]),
    .in_3(rotateleft_9_rorated_output[29]), .in_4(rotateleft_9_rorated_output[28]),
    .in_5(rotateleft_9_rorated_output[27]), .in_6(rotateleft_9_rorated_output[26]),
    .in_7(rotateleft_9_rorated_output[25]), .in_8(rotateleft_9_rorated_output[24]),
    .in_9(rotateleft_9_rorated_output[23]), .in_10(rotateleft_9_rorated_output[22]),
    .in_11(rotateleft_9_rorated_output[21]), .in_12(rotateleft_9_rorated_output[20]),
    .in_13(rotateleft_9_rorated_output[19]), .in_14(rotateleft_9_rorated_output[18]),
    .in_15(rotateleft_9_rorated_output[17]), .in_16(rotateleft_9_rorated_output[16]),
    .in_17(rotateleft_9_rorated_output[15]), .in_18(rotateleft_9_rorated_output[14]),
    .in_19(rotateleft_9_rorated_output[13]), .in_20(rotateleft_9_rorated_output[12]),
    .in_21(rotateleft_9_rorated_output[11]), .in_22(rotateleft_9_rorated_output[10]),
    .in_23(rotateleft_9_rorated_output[9]), .in_24(rotateleft_9_rorated_output[8]),
    .in_25(rotateleft_9_rorated_output[7]), .in_26(rotateleft_9_rorated_output[6]),
    .in_27(rotateleft_9_rorated_output[5]), .in_28(rotateleft_9_rorated_output[4]),
    .in_29(rotateleft_9_rorated_output[3]), .in_30(rotateleft_9_rorated_output[2]),
    .in_31(rotateleft_9_rorated_output[1]), .in_32(rotateleft_9_rorated_output[0]), .InputFromMux(out_58),
    .out_34(out_59[31]), .out_35(out_59[30]), .out_36(out_59[29]), .out_37(out_59[28]), .out_38(out_59[27]),
    .out_39(out_59[26]), .out_40(out_59[25]), .out_41(out_59[24]), .out_42(out_59[23]), .out_43(out_59[22]),
    .out_44(out_59[21]), .out_45(out_59[20]), .out_46(out_59[19]), .out_47(out_59[18]), .out_48(out_59[17]),
    .out_49(out_59[16]), .out_50(out_59[15]), .out_51(out_59[14]), .out_52(out_59[13]), .out_53(out_59[12]),
    .out_54(out_59[11]), .out_55(out_59[10]), .out_56(out_59[9]), .out_57(out_59[8]), .out_58(out_59[7]),
    .out_59(out_59[6]), .out_60(out_59[5]), .out_61(out_59[4]), .out_62(out_59[3]), .out_63(out_59[2]),
    .out_64(out_59[1]), .out_65(out_59[0]));
  _32BITCONTROL u_32bitcontrol_12 (
    .in_1(rotateleft_10_rorated_output[31]), .in_2(rotateleft_10_rorated_output[30]),
    .in_3(rotateleft_10_rorated_output[29]), .in_4(rotateleft_10_rorated_output[28]),
    .in_5(rotateleft_10_rorated_output[27]), .in_6(rotateleft_10_rorated_output[26]),
    .in_7(rotateleft_10_rorated_output[25]), .in_8(rotateleft_10_rorated_output[24]),
    .in_9(rotateleft_10_rorated_output[23]), .in_10(rotateleft_10_rorated_output[22]),
    .in_11(rotateleft_10_rorated_output[21]), .in_12(rotateleft_10_rorated_output[20]),
    .in_13(rotateleft_10_rorated_output[19]), .in_14(rotateleft_10_rorated_output[18]),
    .in_15(rotateleft_10_rorated_output[17]), .in_16(rotateleft_10_rorated_output[16]),
    .in_17(rotateleft_10_rorated_output[15]), .in_18(rotateleft_10_rorated_output[14]),
    .in_19(rotateleft_10_rorated_output[13]), .in_20(rotateleft_10_rorated_output[12]),
    .in_21(rotateleft_10_rorated_output[11]), .in_22(rotateleft_10_rorated_output[10]),
    .in_23(rotateleft_10_rorated_output[9]), .in_24(rotateleft_10_rorated_output[8]),
    .in_25(rotateleft_10_rorated_output[7]), .in_26(rotateleft_10_rorated_output[6]),
    .in_27(rotateleft_10_rorated_output[5]), .in_28(rotateleft_10_rorated_output[4]),
    .in_29(rotateleft_10_rorated_output[3]), .in_30(rotateleft_10_rorated_output[2]),
    .in_31(rotateleft_10_rorated_output[1]), .in_32(rotateleft_10_rorated_output[0]), .InputFromMux(out_60),
    .out_34(out_61[31]), .out_35(out_61[30]), .out_36(out_61[29]), .out_37(out_61[28]), .out_38(out_61[27]),
    .out_39(out_61[26]), .out_40(out_61[25]), .out_41(out_61[24]), .out_42(out_61[23]), .out_43(out_61[22]),
    .out_44(out_61[21]), .out_45(out_61[20]), .out_46(out_61[19]), .out_47(out_61[18]), .out_48(out_61[17]),
    .out_49(out_61[16]), .out_50(out_61[15]), .out_51(out_61[14]), .out_52(out_61[13]), .out_53(out_61[12]),
    .out_54(out_61[11]), .out_55(out_61[10]), .out_56(out_61[9]), .out_57(out_61[8]), .out_58(out_61[7]),
    .out_59(out_61[6]), .out_60(out_61[5]), .out_61(out_61[4]), .out_62(out_61[3]), .out_63(out_61[2]),
    .out_64(out_61[1]), .out_65(out_61[0]));
  _32BITCONTROL u_32bitcontrol_13 (
    .in_1(rotateleft_11_rorated_output[31]), .in_2(rotateleft_11_rorated_output[30]),
    .in_3(rotateleft_11_rorated_output[29]), .in_4(rotateleft_11_rorated_output[28]),
    .in_5(rotateleft_11_rorated_output[27]), .in_6(rotateleft_11_rorated_output[26]),
    .in_7(rotateleft_11_rorated_output[25]), .in_8(rotateleft_11_rorated_output[24]),
    .in_9(rotateleft_11_rorated_output[23]), .in_10(rotateleft_11_rorated_output[22]),
    .in_11(rotateleft_11_rorated_output[21]), .in_12(rotateleft_11_rorated_output[20]),
    .in_13(rotateleft_11_rorated_output[19]), .in_14(rotateleft_11_rorated_output[18]),
    .in_15(rotateleft_11_rorated_output[17]), .in_16(rotateleft_11_rorated_output[16]),
    .in_17(rotateleft_11_rorated_output[15]), .in_18(rotateleft_11_rorated_output[14]),
    .in_19(rotateleft_11_rorated_output[13]), .in_20(rotateleft_11_rorated_output[12]),
    .in_21(rotateleft_11_rorated_output[11]), .in_22(rotateleft_11_rorated_output[10]),
    .in_23(rotateleft_11_rorated_output[9]), .in_24(rotateleft_11_rorated_output[8]),
    .in_25(rotateleft_11_rorated_output[7]), .in_26(rotateleft_11_rorated_output[6]),
    .in_27(rotateleft_11_rorated_output[5]), .in_28(rotateleft_11_rorated_output[4]),
    .in_29(rotateleft_11_rorated_output[3]), .in_30(rotateleft_11_rorated_output[2]),
    .in_31(rotateleft_11_rorated_output[1]), .in_32(rotateleft_11_rorated_output[0]), .InputFromMux(out_62),
    .out_34(out_63[31]), .out_35(out_63[30]), .out_36(out_63[29]), .out_37(out_63[28]), .out_38(out_63[27]),
    .out_39(out_63[26]), .out_40(out_63[25]), .out_41(out_63[24]), .out_42(out_63[23]), .out_43(out_63[22]),
    .out_44(out_63[21]), .out_45(out_63[20]), .out_46(out_63[19]), .out_47(out_63[18]), .out_48(out_63[17]),
    .out_49(out_63[16]), .out_50(out_63[15]), .out_51(out_63[14]), .out_52(out_63[13]), .out_53(out_63[12]),
    .out_54(out_63[11]), .out_55(out_63[10]), .out_56(out_63[9]), .out_57(out_63[8]), .out_58(out_63[7]),
    .out_59(out_63[6]), .out_60(out_63[5]), .out_61(out_63[4]), .out_62(out_63[3]), .out_63(out_63[2]),
    .out_64(out_63[1]), .out_65(out_63[0]));
  _32BITCONTROL u_32bitcontrol_14 (
    .in_1(rotateleft_12_rorated_output[31]), .in_2(rotateleft_12_rorated_output[30]),
    .in_3(rotateleft_12_rorated_output[29]), .in_4(rotateleft_12_rorated_output[28]),
    .in_5(rotateleft_12_rorated_output[27]), .in_6(rotateleft_12_rorated_output[26]),
    .in_7(rotateleft_12_rorated_output[25]), .in_8(rotateleft_12_rorated_output[24]),
    .in_9(rotateleft_12_rorated_output[23]), .in_10(rotateleft_12_rorated_output[22]),
    .in_11(rotateleft_12_rorated_output[21]), .in_12(rotateleft_12_rorated_output[20]),
    .in_13(rotateleft_12_rorated_output[19]), .in_14(rotateleft_12_rorated_output[18]),
    .in_15(rotateleft_12_rorated_output[17]), .in_16(rotateleft_12_rorated_output[16]),
    .in_17(rotateleft_12_rorated_output[15]), .in_18(rotateleft_12_rorated_output[14]),
    .in_19(rotateleft_12_rorated_output[13]), .in_20(rotateleft_12_rorated_output[12]),
    .in_21(rotateleft_12_rorated_output[11]), .in_22(rotateleft_12_rorated_output[10]),
    .in_23(rotateleft_12_rorated_output[9]), .in_24(rotateleft_12_rorated_output[8]),
    .in_25(rotateleft_12_rorated_output[7]), .in_26(rotateleft_12_rorated_output[6]),
    .in_27(rotateleft_12_rorated_output[5]), .in_28(rotateleft_12_rorated_output[4]),
    .in_29(rotateleft_12_rorated_output[3]), .in_30(rotateleft_12_rorated_output[2]),
    .in_31(rotateleft_12_rorated_output[1]), .in_32(rotateleft_12_rorated_output[0]), .InputFromMux(out_64),
    .out_34(out_65[31]), .out_35(out_65[30]), .out_36(out_65[29]), .out_37(out_65[28]), .out_38(out_65[27]),
    .out_39(out_65[26]), .out_40(out_65[25]), .out_41(out_65[24]), .out_42(out_65[23]), .out_43(out_65[22]),
    .out_44(out_65[21]), .out_45(out_65[20]), .out_46(out_65[19]), .out_47(out_65[18]), .out_48(out_65[17]),
    .out_49(out_65[16]), .out_50(out_65[15]), .out_51(out_65[14]), .out_52(out_65[13]), .out_53(out_65[12]),
    .out_54(out_65[11]), .out_55(out_65[10]), .out_56(out_65[9]), .out_57(out_65[8]), .out_58(out_65[7]),
    .out_59(out_65[6]), .out_60(out_65[5]), .out_61(out_65[4]), .out_62(out_65[3]), .out_63(out_65[2]),
    .out_64(out_65[1]), .out_65(out_65[0]));
  _32BITCONTROL u_32bitcontrol_15 (
    .in_1(rotateleft_13_rorated_output[31]), .in_2(rotateleft_13_rorated_output[30]),
    .in_3(rotateleft_13_rorated_output[29]), .in_4(rotateleft_13_rorated_output[28]),
    .in_5(rotateleft_13_rorated_output[27]), .in_6(rotateleft_13_rorated_output[26]),
    .in_7(rotateleft_13_rorated_output[25]), .in_8(rotateleft_13_rorated_output[24]),
    .in_9(rotateleft_13_rorated_output[23]), .in_10(rotateleft_13_rorated_output[22]),
    .in_11(rotateleft_13_rorated_output[21]), .in_12(rotateleft_13_rorated_output[20]),
    .in_13(rotateleft_13_rorated_output[19]), .in_14(rotateleft_13_rorated_output[18]),
    .in_15(rotateleft_13_rorated_output[17]), .in_16(rotateleft_13_rorated_output[16]),
    .in_17(rotateleft_13_rorated_output[15]), .in_18(rotateleft_13_rorated_output[14]),
    .in_19(rotateleft_13_rorated_output[13]), .in_20(rotateleft_13_rorated_output[12]),
    .in_21(rotateleft_13_rorated_output[11]), .in_22(rotateleft_13_rorated_output[10]),
    .in_23(rotateleft_13_rorated_output[9]), .in_24(rotateleft_13_rorated_output[8]),
    .in_25(rotateleft_13_rorated_output[7]), .in_26(rotateleft_13_rorated_output[6]),
    .in_27(rotateleft_13_rorated_output[5]), .in_28(rotateleft_13_rorated_output[4]),
    .in_29(rotateleft_13_rorated_output[3]), .in_30(rotateleft_13_rorated_output[2]),
    .in_31(rotateleft_13_rorated_output[1]), .in_32(rotateleft_13_rorated_output[0]), .InputFromMux(out_66),
    .out_34(out_67[31]), .out_35(out_67[30]), .out_36(out_67[29]), .out_37(out_67[28]), .out_38(out_67[27]),
    .out_39(out_67[26]), .out_40(out_67[25]), .out_41(out_67[24]), .out_42(out_67[23]), .out_43(out_67[22]),
    .out_44(out_67[21]), .out_45(out_67[20]), .out_46(out_67[19]), .out_47(out_67[18]), .out_48(out_67[17]),
    .out_49(out_67[16]), .out_50(out_67[15]), .out_51(out_67[14]), .out_52(out_67[13]), .out_53(out_67[12]),
    .out_54(out_67[11]), .out_55(out_67[10]), .out_56(out_67[9]), .out_57(out_67[8]), .out_58(out_67[7]),
    .out_59(out_67[6]), .out_60(out_67[5]), .out_61(out_67[4]), .out_62(out_67[3]), .out_63(out_67[2]),
    .out_64(out_67[1]), .out_65(out_67[0]));
  _32BITCONTROL u_32bitcontrol_16 (
    .in_1(rotateleft_14_rorated_output[31]), .in_2(rotateleft_14_rorated_output[30]),
    .in_3(rotateleft_14_rorated_output[29]), .in_4(rotateleft_14_rorated_output[28]),
    .in_5(rotateleft_14_rorated_output[27]), .in_6(rotateleft_14_rorated_output[26]),
    .in_7(rotateleft_14_rorated_output[25]), .in_8(rotateleft_14_rorated_output[24]),
    .in_9(rotateleft_14_rorated_output[23]), .in_10(rotateleft_14_rorated_output[22]),
    .in_11(rotateleft_14_rorated_output[21]), .in_12(rotateleft_14_rorated_output[20]),
    .in_13(rotateleft_14_rorated_output[19]), .in_14(rotateleft_14_rorated_output[18]),
    .in_15(rotateleft_14_rorated_output[17]), .in_16(rotateleft_14_rorated_output[16]),
    .in_17(rotateleft_14_rorated_output[15]), .in_18(rotateleft_14_rorated_output[14]),
    .in_19(rotateleft_14_rorated_output[13]), .in_20(rotateleft_14_rorated_output[12]),
    .in_21(rotateleft_14_rorated_output[11]), .in_22(rotateleft_14_rorated_output[10]),
    .in_23(rotateleft_14_rorated_output[9]), .in_24(rotateleft_14_rorated_output[8]),
    .in_25(rotateleft_14_rorated_output[7]), .in_26(rotateleft_14_rorated_output[6]),
    .in_27(rotateleft_14_rorated_output[5]), .in_28(rotateleft_14_rorated_output[4]),
    .in_29(rotateleft_14_rorated_output[3]), .in_30(rotateleft_14_rorated_output[2]),
    .in_31(rotateleft_14_rorated_output[1]), .in_32(rotateleft_14_rorated_output[0]), .InputFromMux(out_68),
    .out_34(out_69[31]), .out_35(out_69[30]), .out_36(out_69[29]), .out_37(out_69[28]), .out_38(out_69[27]),
    .out_39(out_69[26]), .out_40(out_69[25]), .out_41(out_69[24]), .out_42(out_69[23]), .out_43(out_69[22]),
    .out_44(out_69[21]), .out_45(out_69[20]), .out_46(out_69[19]), .out_47(out_69[18]), .out_48(out_69[17]),
    .out_49(out_69[16]), .out_50(out_69[15]), .out_51(out_69[14]), .out_52(out_69[13]), .out_53(out_69[12]),
    .out_54(out_69[11]), .out_55(out_69[10]), .out_56(out_69[9]), .out_57(out_69[8]), .out_58(out_69[7]),
    .out_59(out_69[6]), .out_60(out_69[5]), .out_61(out_69[4]), .out_62(out_69[3]), .out_63(out_69[2]),
    .out_64(out_69[1]), .out_65(out_69[0]));
  _32BITCONTROL u_32bitcontrol_17 (
    .in_1(rotateleft_15_rorated_output[31]), .in_2(rotateleft_15_rorated_output[30]),
    .in_3(rotateleft_15_rorated_output[29]), .in_4(rotateleft_15_rorated_output[28]),
    .in_5(rotateleft_15_rorated_output[27]), .in_6(rotateleft_15_rorated_output[26]),
    .in_7(rotateleft_15_rorated_output[25]), .in_8(rotateleft_15_rorated_output[24]),
    .in_9(rotateleft_15_rorated_output[23]), .in_10(rotateleft_15_rorated_output[22]),
    .in_11(rotateleft_15_rorated_output[21]), .in_12(rotateleft_15_rorated_output[20]),
    .in_13(rotateleft_15_rorated_output[19]), .in_14(rotateleft_15_rorated_output[18]),
    .in_15(rotateleft_15_rorated_output[17]), .in_16(rotateleft_15_rorated_output[16]),
    .in_17(rotateleft_15_rorated_output[15]), .in_18(rotateleft_15_rorated_output[14]),
    .in_19(rotateleft_15_rorated_output[13]), .in_20(rotateleft_15_rorated_output[12]),
    .in_21(rotateleft_15_rorated_output[11]), .in_22(rotateleft_15_rorated_output[10]),
    .in_23(rotateleft_15_rorated_output[9]), .in_24(rotateleft_15_rorated_output[8]),
    .in_25(rotateleft_15_rorated_output[7]), .in_26(rotateleft_15_rorated_output[6]),
    .in_27(rotateleft_15_rorated_output[5]), .in_28(rotateleft_15_rorated_output[4]),
    .in_29(rotateleft_15_rorated_output[3]), .in_30(rotateleft_15_rorated_output[2]),
    .in_31(rotateleft_15_rorated_output[1]), .in_32(rotateleft_15_rorated_output[0]), .InputFromMux(out_70),
    .out_34(out_71[31]), .out_35(out_71[30]), .out_36(out_71[29]), .out_37(out_71[28]), .out_38(out_71[27]),
    .out_39(out_71[26]), .out_40(out_71[25]), .out_41(out_71[24]), .out_42(out_71[23]), .out_43(out_71[22]),
    .out_44(out_71[21]), .out_45(out_71[20]), .out_46(out_71[19]), .out_47(out_71[18]), .out_48(out_71[17]),
    .out_49(out_71[16]), .out_50(out_71[15]), .out_51(out_71[14]), .out_52(out_71[13]), .out_53(out_71[12]),
    .out_54(out_71[11]), .out_55(out_71[10]), .out_56(out_71[9]), .out_57(out_71[8]), .out_58(out_71[7]),
    .out_59(out_71[6]), .out_60(out_71[5]), .out_61(out_71[4]), .out_62(out_71[3]), .out_63(out_71[2]),
    .out_64(out_71[1]), .out_65(out_71[0]));
  _32BITCONTROL u_32bitcontrol_18 (
    .in_1(rotateleft_16_rorated_output[31]), .in_2(rotateleft_16_rorated_output[30]),
    .in_3(rotateleft_16_rorated_output[29]), .in_4(rotateleft_16_rorated_output[28]),
    .in_5(rotateleft_16_rorated_output[27]), .in_6(rotateleft_16_rorated_output[26]),
    .in_7(rotateleft_16_rorated_output[25]), .in_8(rotateleft_16_rorated_output[24]),
    .in_9(rotateleft_16_rorated_output[23]), .in_10(rotateleft_16_rorated_output[22]),
    .in_11(rotateleft_16_rorated_output[21]), .in_12(rotateleft_16_rorated_output[20]),
    .in_13(rotateleft_16_rorated_output[19]), .in_14(rotateleft_16_rorated_output[18]),
    .in_15(rotateleft_16_rorated_output[17]), .in_16(rotateleft_16_rorated_output[16]),
    .in_17(rotateleft_16_rorated_output[15]), .in_18(rotateleft_16_rorated_output[14]),
    .in_19(rotateleft_16_rorated_output[13]), .in_20(rotateleft_16_rorated_output[12]),
    .in_21(rotateleft_16_rorated_output[11]), .in_22(rotateleft_16_rorated_output[10]),
    .in_23(rotateleft_16_rorated_output[9]), .in_24(rotateleft_16_rorated_output[8]),
    .in_25(rotateleft_16_rorated_output[7]), .in_26(rotateleft_16_rorated_output[6]),
    .in_27(rotateleft_16_rorated_output[5]), .in_28(rotateleft_16_rorated_output[4]),
    .in_29(rotateleft_16_rorated_output[3]), .in_30(rotateleft_16_rorated_output[2]),
    .in_31(rotateleft_16_rorated_output[1]), .in_32(rotateleft_16_rorated_output[0]), .InputFromMux(out_72),
    .out_34(out_73[31]), .out_35(out_73[30]), .out_36(out_73[29]), .out_37(out_73[28]), .out_38(out_73[27]),
    .out_39(out_73[26]), .out_40(out_73[25]), .out_41(out_73[24]), .out_42(out_73[23]), .out_43(out_73[22]),
    .out_44(out_73[21]), .out_45(out_73[20]), .out_46(out_73[19]), .out_47(out_73[18]), .out_48(out_73[17]),
    .out_49(out_73[16]), .out_50(out_73[15]), .out_51(out_73[14]), .out_52(out_73[13]), .out_53(out_73[12]),
    .out_54(out_73[11]), .out_55(out_73[10]), .out_56(out_73[9]), .out_57(out_73[8]), .out_58(out_73[7]),
    .out_59(out_73[6]), .out_60(out_73[5]), .out_61(out_73[4]), .out_62(out_73[3]), .out_63(out_73[2]),
    .out_64(out_73[1]), .out_65(out_73[0]));
  _32BITCONTROL u_32bitcontrol_19 (
    .in_1(rotateleft_17_rorated_output[31]), .in_2(rotateleft_17_rorated_output[30]),
    .in_3(rotateleft_17_rorated_output[29]), .in_4(rotateleft_17_rorated_output[28]),
    .in_5(rotateleft_17_rorated_output[27]), .in_6(rotateleft_17_rorated_output[26]),
    .in_7(rotateleft_17_rorated_output[25]), .in_8(rotateleft_17_rorated_output[24]),
    .in_9(rotateleft_17_rorated_output[23]), .in_10(rotateleft_17_rorated_output[22]),
    .in_11(rotateleft_17_rorated_output[21]), .in_12(rotateleft_17_rorated_output[20]),
    .in_13(rotateleft_17_rorated_output[19]), .in_14(rotateleft_17_rorated_output[18]),
    .in_15(rotateleft_17_rorated_output[17]), .in_16(rotateleft_17_rorated_output[16]),
    .in_17(rotateleft_17_rorated_output[15]), .in_18(rotateleft_17_rorated_output[14]),
    .in_19(rotateleft_17_rorated_output[13]), .in_20(rotateleft_17_rorated_output[12]),
    .in_21(rotateleft_17_rorated_output[11]), .in_22(rotateleft_17_rorated_output[10]),
    .in_23(rotateleft_17_rorated_output[9]), .in_24(rotateleft_17_rorated_output[8]),
    .in_25(rotateleft_17_rorated_output[7]), .in_26(rotateleft_17_rorated_output[6]),
    .in_27(rotateleft_17_rorated_output[5]), .in_28(rotateleft_17_rorated_output[4]),
    .in_29(rotateleft_17_rorated_output[3]), .in_30(rotateleft_17_rorated_output[2]),
    .in_31(rotateleft_17_rorated_output[1]), .in_32(rotateleft_17_rorated_output[0]), .InputFromMux(out_74),
    .out_34(out_75[31]), .out_35(out_75[30]), .out_36(out_75[29]), .out_37(out_75[28]), .out_38(out_75[27]),
    .out_39(out_75[26]), .out_40(out_75[25]), .out_41(out_75[24]), .out_42(out_75[23]), .out_43(out_75[22]),
    .out_44(out_75[21]), .out_45(out_75[20]), .out_46(out_75[19]), .out_47(out_75[18]), .out_48(out_75[17]),
    .out_49(out_75[16]), .out_50(out_75[15]), .out_51(out_75[14]), .out_52(out_75[13]), .out_53(out_75[12]),
    .out_54(out_75[11]), .out_55(out_75[10]), .out_56(out_75[9]), .out_57(out_75[8]), .out_58(out_75[7]),
    .out_59(out_75[6]), .out_60(out_75[5]), .out_61(out_75[4]), .out_62(out_75[3]), .out_63(out_75[2]),
    .out_64(out_75[1]), .out_65(out_75[0]));
  _32BITCONTROL u_32bitcontrol_20 (
    .in_1(rotateleft_18_rorated_output[31]), .in_2(rotateleft_18_rorated_output[30]),
    .in_3(rotateleft_18_rorated_output[29]), .in_4(rotateleft_18_rorated_output[28]),
    .in_5(rotateleft_18_rorated_output[27]), .in_6(rotateleft_18_rorated_output[26]),
    .in_7(rotateleft_18_rorated_output[25]), .in_8(rotateleft_18_rorated_output[24]),
    .in_9(rotateleft_18_rorated_output[23]), .in_10(rotateleft_18_rorated_output[22]),
    .in_11(rotateleft_18_rorated_output[21]), .in_12(rotateleft_18_rorated_output[20]),
    .in_13(rotateleft_18_rorated_output[19]), .in_14(rotateleft_18_rorated_output[18]),
    .in_15(rotateleft_18_rorated_output[17]), .in_16(rotateleft_18_rorated_output[16]),
    .in_17(rotateleft_18_rorated_output[15]), .in_18(rotateleft_18_rorated_output[14]),
    .in_19(rotateleft_18_rorated_output[13]), .in_20(rotateleft_18_rorated_output[12]),
    .in_21(rotateleft_18_rorated_output[11]), .in_22(rotateleft_18_rorated_output[10]),
    .in_23(rotateleft_18_rorated_output[9]), .in_24(rotateleft_18_rorated_output[8]),
    .in_25(rotateleft_18_rorated_output[7]), .in_26(rotateleft_18_rorated_output[6]),
    .in_27(rotateleft_18_rorated_output[5]), .in_28(rotateleft_18_rorated_output[4]),
    .in_29(rotateleft_18_rorated_output[3]), .in_30(rotateleft_18_rorated_output[2]),
    .in_31(rotateleft_18_rorated_output[1]), .in_32(rotateleft_18_rorated_output[0]), .InputFromMux(out_76),
    .out_34(out_77[31]), .out_35(out_77[30]), .out_36(out_77[29]), .out_37(out_77[28]), .out_38(out_77[27]),
    .out_39(out_77[26]), .out_40(out_77[25]), .out_41(out_77[24]), .out_42(out_77[23]), .out_43(out_77[22]),
    .out_44(out_77[21]), .out_45(out_77[20]), .out_46(out_77[19]), .out_47(out_77[18]), .out_48(out_77[17]),
    .out_49(out_77[16]), .out_50(out_77[15]), .out_51(out_77[14]), .out_52(out_77[13]), .out_53(out_77[12]),
    .out_54(out_77[11]), .out_55(out_77[10]), .out_56(out_77[9]), .out_57(out_77[8]), .out_58(out_77[7]),
    .out_59(out_77[6]), .out_60(out_77[5]), .out_61(out_77[4]), .out_62(out_77[3]), .out_63(out_77[2]),
    .out_64(out_77[1]), .out_65(out_77[0]));
  _32BITCONTROL u_32bitcontrol_21 (
    .in_1(rotateleft_19_rorated_output[31]), .in_2(rotateleft_19_rorated_output[30]),
    .in_3(rotateleft_19_rorated_output[29]), .in_4(rotateleft_19_rorated_output[28]),
    .in_5(rotateleft_19_rorated_output[27]), .in_6(rotateleft_19_rorated_output[26]),
    .in_7(rotateleft_19_rorated_output[25]), .in_8(rotateleft_19_rorated_output[24]),
    .in_9(rotateleft_19_rorated_output[23]), .in_10(rotateleft_19_rorated_output[22]),
    .in_11(rotateleft_19_rorated_output[21]), .in_12(rotateleft_19_rorated_output[20]),
    .in_13(rotateleft_19_rorated_output[19]), .in_14(rotateleft_19_rorated_output[18]),
    .in_15(rotateleft_19_rorated_output[17]), .in_16(rotateleft_19_rorated_output[16]),
    .in_17(rotateleft_19_rorated_output[15]), .in_18(rotateleft_19_rorated_output[14]),
    .in_19(rotateleft_19_rorated_output[13]), .in_20(rotateleft_19_rorated_output[12]),
    .in_21(rotateleft_19_rorated_output[11]), .in_22(rotateleft_19_rorated_output[10]),
    .in_23(rotateleft_19_rorated_output[9]), .in_24(rotateleft_19_rorated_output[8]),
    .in_25(rotateleft_19_rorated_output[7]), .in_26(rotateleft_19_rorated_output[6]),
    .in_27(rotateleft_19_rorated_output[5]), .in_28(rotateleft_19_rorated_output[4]),
    .in_29(rotateleft_19_rorated_output[3]), .in_30(rotateleft_19_rorated_output[2]),
    .in_31(rotateleft_19_rorated_output[1]), .in_32(rotateleft_19_rorated_output[0]), .InputFromMux(out_78),
    .out_34(out_79[31]), .out_35(out_79[30]), .out_36(out_79[29]), .out_37(out_79[28]), .out_38(out_79[27]),
    .out_39(out_79[26]), .out_40(out_79[25]), .out_41(out_79[24]), .out_42(out_79[23]), .out_43(out_79[22]),
    .out_44(out_79[21]), .out_45(out_79[20]), .out_46(out_79[19]), .out_47(out_79[18]), .out_48(out_79[17]),
    .out_49(out_79[16]), .out_50(out_79[15]), .out_51(out_79[14]), .out_52(out_79[13]), .out_53(out_79[12]),
    .out_54(out_79[11]), .out_55(out_79[10]), .out_56(out_79[9]), .out_57(out_79[8]), .out_58(out_79[7]),
    .out_59(out_79[6]), .out_60(out_79[5]), .out_61(out_79[4]), .out_62(out_79[3]), .out_63(out_79[2]),
    .out_64(out_79[1]), .out_65(out_79[0]));
  _32BITCONTROL u_32bitcontrol_22 (
    .in_1(rotateleft_20_rorated_output[31]), .in_2(rotateleft_20_rorated_output[30]),
    .in_3(rotateleft_20_rorated_output[29]), .in_4(rotateleft_20_rorated_output[28]),
    .in_5(rotateleft_20_rorated_output[27]), .in_6(rotateleft_20_rorated_output[26]),
    .in_7(rotateleft_20_rorated_output[25]), .in_8(rotateleft_20_rorated_output[24]),
    .in_9(rotateleft_20_rorated_output[23]), .in_10(rotateleft_20_rorated_output[22]),
    .in_11(rotateleft_20_rorated_output[21]), .in_12(rotateleft_20_rorated_output[20]),
    .in_13(rotateleft_20_rorated_output[19]), .in_14(rotateleft_20_rorated_output[18]),
    .in_15(rotateleft_20_rorated_output[17]), .in_16(rotateleft_20_rorated_output[16]),
    .in_17(rotateleft_20_rorated_output[15]), .in_18(rotateleft_20_rorated_output[14]),
    .in_19(rotateleft_20_rorated_output[13]), .in_20(rotateleft_20_rorated_output[12]),
    .in_21(rotateleft_20_rorated_output[11]), .in_22(rotateleft_20_rorated_output[10]),
    .in_23(rotateleft_20_rorated_output[9]), .in_24(rotateleft_20_rorated_output[8]),
    .in_25(rotateleft_20_rorated_output[7]), .in_26(rotateleft_20_rorated_output[6]),
    .in_27(rotateleft_20_rorated_output[5]), .in_28(rotateleft_20_rorated_output[4]),
    .in_29(rotateleft_20_rorated_output[3]), .in_30(rotateleft_20_rorated_output[2]),
    .in_31(rotateleft_20_rorated_output[1]), .in_32(rotateleft_20_rorated_output[0]), .InputFromMux(out_80),
    .out_34(out_81[31]), .out_35(out_81[30]), .out_36(out_81[29]), .out_37(out_81[28]), .out_38(out_81[27]),
    .out_39(out_81[26]), .out_40(out_81[25]), .out_41(out_81[24]), .out_42(out_81[23]), .out_43(out_81[22]),
    .out_44(out_81[21]), .out_45(out_81[20]), .out_46(out_81[19]), .out_47(out_81[18]), .out_48(out_81[17]),
    .out_49(out_81[16]), .out_50(out_81[15]), .out_51(out_81[14]), .out_52(out_81[13]), .out_53(out_81[12]),
    .out_54(out_81[11]), .out_55(out_81[10]), .out_56(out_81[9]), .out_57(out_81[8]), .out_58(out_81[7]),
    .out_59(out_81[6]), .out_60(out_81[5]), .out_61(out_81[4]), .out_62(out_81[3]), .out_63(out_81[2]),
    .out_64(out_81[1]), .out_65(out_81[0]));
  _32BITCONTROL u_32bitcontrol_23 (
    .in_1(rotateleft_21_rorated_output[31]), .in_2(rotateleft_21_rorated_output[30]),
    .in_3(rotateleft_21_rorated_output[29]), .in_4(rotateleft_21_rorated_output[28]),
    .in_5(rotateleft_21_rorated_output[27]), .in_6(rotateleft_21_rorated_output[26]),
    .in_7(rotateleft_21_rorated_output[25]), .in_8(rotateleft_21_rorated_output[24]),
    .in_9(rotateleft_21_rorated_output[23]), .in_10(rotateleft_21_rorated_output[22]),
    .in_11(rotateleft_21_rorated_output[21]), .in_12(rotateleft_21_rorated_output[20]),
    .in_13(rotateleft_21_rorated_output[19]), .in_14(rotateleft_21_rorated_output[18]),
    .in_15(rotateleft_21_rorated_output[17]), .in_16(rotateleft_21_rorated_output[16]),
    .in_17(rotateleft_21_rorated_output[15]), .in_18(rotateleft_21_rorated_output[14]),
    .in_19(rotateleft_21_rorated_output[13]), .in_20(rotateleft_21_rorated_output[12]),
    .in_21(rotateleft_21_rorated_output[11]), .in_22(rotateleft_21_rorated_output[10]),
    .in_23(rotateleft_21_rorated_output[9]), .in_24(rotateleft_21_rorated_output[8]),
    .in_25(rotateleft_21_rorated_output[7]), .in_26(rotateleft_21_rorated_output[6]),
    .in_27(rotateleft_21_rorated_output[5]), .in_28(rotateleft_21_rorated_output[4]),
    .in_29(rotateleft_21_rorated_output[3]), .in_30(rotateleft_21_rorated_output[2]),
    .in_31(rotateleft_21_rorated_output[1]), .in_32(rotateleft_21_rorated_output[0]), .InputFromMux(out_82),
    .out_34(out_83[31]), .out_35(out_83[30]), .out_36(out_83[29]), .out_37(out_83[28]), .out_38(out_83[27]),
    .out_39(out_83[26]), .out_40(out_83[25]), .out_41(out_83[24]), .out_42(out_83[23]), .out_43(out_83[22]),
    .out_44(out_83[21]), .out_45(out_83[20]), .out_46(out_83[19]), .out_47(out_83[18]), .out_48(out_83[17]),
    .out_49(out_83[16]), .out_50(out_83[15]), .out_51(out_83[14]), .out_52(out_83[13]), .out_53(out_83[12]),
    .out_54(out_83[11]), .out_55(out_83[10]), .out_56(out_83[9]), .out_57(out_83[8]), .out_58(out_83[7]),
    .out_59(out_83[6]), .out_60(out_83[5]), .out_61(out_83[4]), .out_62(out_83[3]), .out_63(out_83[2]),
    .out_64(out_83[1]), .out_65(out_83[0]));
  _32BITCONTROL u_32bitcontrol_24 (
    .in_1(rotateleft_22_rorated_output[31]), .in_2(rotateleft_22_rorated_output[30]),
    .in_3(rotateleft_22_rorated_output[29]), .in_4(rotateleft_22_rorated_output[28]),
    .in_5(rotateleft_22_rorated_output[27]), .in_6(rotateleft_22_rorated_output[26]),
    .in_7(rotateleft_22_rorated_output[25]), .in_8(rotateleft_22_rorated_output[24]),
    .in_9(rotateleft_22_rorated_output[23]), .in_10(rotateleft_22_rorated_output[22]),
    .in_11(rotateleft_22_rorated_output[21]), .in_12(rotateleft_22_rorated_output[20]),
    .in_13(rotateleft_22_rorated_output[19]), .in_14(rotateleft_22_rorated_output[18]),
    .in_15(rotateleft_22_rorated_output[17]), .in_16(rotateleft_22_rorated_output[16]),
    .in_17(rotateleft_22_rorated_output[15]), .in_18(rotateleft_22_rorated_output[14]),
    .in_19(rotateleft_22_rorated_output[13]), .in_20(rotateleft_22_rorated_output[12]),
    .in_21(rotateleft_22_rorated_output[11]), .in_22(rotateleft_22_rorated_output[10]),
    .in_23(rotateleft_22_rorated_output[9]), .in_24(rotateleft_22_rorated_output[8]),
    .in_25(rotateleft_22_rorated_output[7]), .in_26(rotateleft_22_rorated_output[6]),
    .in_27(rotateleft_22_rorated_output[5]), .in_28(rotateleft_22_rorated_output[4]),
    .in_29(rotateleft_22_rorated_output[3]), .in_30(rotateleft_22_rorated_output[2]),
    .in_31(rotateleft_22_rorated_output[1]), .in_32(rotateleft_22_rorated_output[0]), .InputFromMux(out_84),
    .out_34(out_85[31]), .out_35(out_85[30]), .out_36(out_85[29]), .out_37(out_85[28]), .out_38(out_85[27]),
    .out_39(out_85[26]), .out_40(out_85[25]), .out_41(out_85[24]), .out_42(out_85[23]), .out_43(out_85[22]),
    .out_44(out_85[21]), .out_45(out_85[20]), .out_46(out_85[19]), .out_47(out_85[18]), .out_48(out_85[17]),
    .out_49(out_85[16]), .out_50(out_85[15]), .out_51(out_85[14]), .out_52(out_85[13]), .out_53(out_85[12]),
    .out_54(out_85[11]), .out_55(out_85[10]), .out_56(out_85[9]), .out_57(out_85[8]), .out_58(out_85[7]),
    .out_59(out_85[6]), .out_60(out_85[5]), .out_61(out_85[4]), .out_62(out_85[3]), .out_63(out_85[2]),
    .out_64(out_85[1]), .out_65(out_85[0]));
  _32BITCONTROL u_32bitcontrol_25 (
    .in_1(rotateleft_23_rorated_output[31]), .in_2(rotateleft_23_rorated_output[30]),
    .in_3(rotateleft_23_rorated_output[29]), .in_4(rotateleft_23_rorated_output[28]),
    .in_5(rotateleft_23_rorated_output[27]), .in_6(rotateleft_23_rorated_output[26]),
    .in_7(rotateleft_23_rorated_output[25]), .in_8(rotateleft_23_rorated_output[24]),
    .in_9(rotateleft_23_rorated_output[23]), .in_10(rotateleft_23_rorated_output[22]),
    .in_11(rotateleft_23_rorated_output[21]), .in_12(rotateleft_23_rorated_output[20]),
    .in_13(rotateleft_23_rorated_output[19]), .in_14(rotateleft_23_rorated_output[18]),
    .in_15(rotateleft_23_rorated_output[17]), .in_16(rotateleft_23_rorated_output[16]),
    .in_17(rotateleft_23_rorated_output[15]), .in_18(rotateleft_23_rorated_output[14]),
    .in_19(rotateleft_23_rorated_output[13]), .in_20(rotateleft_23_rorated_output[12]),
    .in_21(rotateleft_23_rorated_output[11]), .in_22(rotateleft_23_rorated_output[10]),
    .in_23(rotateleft_23_rorated_output[9]), .in_24(rotateleft_23_rorated_output[8]),
    .in_25(rotateleft_23_rorated_output[7]), .in_26(rotateleft_23_rorated_output[6]),
    .in_27(rotateleft_23_rorated_output[5]), .in_28(rotateleft_23_rorated_output[4]),
    .in_29(rotateleft_23_rorated_output[3]), .in_30(rotateleft_23_rorated_output[2]),
    .in_31(rotateleft_23_rorated_output[1]), .in_32(rotateleft_23_rorated_output[0]), .InputFromMux(out_86),
    .out_34(out_87[31]), .out_35(out_87[30]), .out_36(out_87[29]), .out_37(out_87[28]), .out_38(out_87[27]),
    .out_39(out_87[26]), .out_40(out_87[25]), .out_41(out_87[24]), .out_42(out_87[23]), .out_43(out_87[22]),
    .out_44(out_87[21]), .out_45(out_87[20]), .out_46(out_87[19]), .out_47(out_87[18]), .out_48(out_87[17]),
    .out_49(out_87[16]), .out_50(out_87[15]), .out_51(out_87[14]), .out_52(out_87[13]), .out_53(out_87[12]),
    .out_54(out_87[11]), .out_55(out_87[10]), .out_56(out_87[9]), .out_57(out_87[8]), .out_58(out_87[7]),
    .out_59(out_87[6]), .out_60(out_87[5]), .out_61(out_87[4]), .out_62(out_87[3]), .out_63(out_87[2]),
    .out_64(out_87[1]), .out_65(out_87[0]));
  _32BITCONTROL u_32bitcontrol_26 (
    .in_1(rotateleft_24_rorated_output[31]), .in_2(rotateleft_24_rorated_output[30]),
    .in_3(rotateleft_24_rorated_output[29]), .in_4(rotateleft_24_rorated_output[28]),
    .in_5(rotateleft_24_rorated_output[27]), .in_6(rotateleft_24_rorated_output[26]),
    .in_7(rotateleft_24_rorated_output[25]), .in_8(rotateleft_24_rorated_output[24]),
    .in_9(rotateleft_24_rorated_output[23]), .in_10(rotateleft_24_rorated_output[22]),
    .in_11(rotateleft_24_rorated_output[21]), .in_12(rotateleft_24_rorated_output[20]),
    .in_13(rotateleft_24_rorated_output[19]), .in_14(rotateleft_24_rorated_output[18]),
    .in_15(rotateleft_24_rorated_output[17]), .in_16(rotateleft_24_rorated_output[16]),
    .in_17(rotateleft_24_rorated_output[15]), .in_18(rotateleft_24_rorated_output[14]),
    .in_19(rotateleft_24_rorated_output[13]), .in_20(rotateleft_24_rorated_output[12]),
    .in_21(rotateleft_24_rorated_output[11]), .in_22(rotateleft_24_rorated_output[10]),
    .in_23(rotateleft_24_rorated_output[9]), .in_24(rotateleft_24_rorated_output[8]),
    .in_25(rotateleft_24_rorated_output[7]), .in_26(rotateleft_24_rorated_output[6]),
    .in_27(rotateleft_24_rorated_output[5]), .in_28(rotateleft_24_rorated_output[4]),
    .in_29(rotateleft_24_rorated_output[3]), .in_30(rotateleft_24_rorated_output[2]),
    .in_31(rotateleft_24_rorated_output[1]), .in_32(rotateleft_24_rorated_output[0]), .InputFromMux(out_88),
    .out_34(out_89[31]), .out_35(out_89[30]), .out_36(out_89[29]), .out_37(out_89[28]), .out_38(out_89[27]),
    .out_39(out_89[26]), .out_40(out_89[25]), .out_41(out_89[24]), .out_42(out_89[23]), .out_43(out_89[22]),
    .out_44(out_89[21]), .out_45(out_89[20]), .out_46(out_89[19]), .out_47(out_89[18]), .out_48(out_89[17]),
    .out_49(out_89[16]), .out_50(out_89[15]), .out_51(out_89[14]), .out_52(out_89[13]), .out_53(out_89[12]),
    .out_54(out_89[11]), .out_55(out_89[10]), .out_56(out_89[9]), .out_57(out_89[8]), .out_58(out_89[7]),
    .out_59(out_89[6]), .out_60(out_89[5]), .out_61(out_89[4]), .out_62(out_89[3]), .out_63(out_89[2]),
    .out_64(out_89[1]), .out_65(out_89[0]));
  _32BITCONTROL u_32bitcontrol_27 (
    .in_1(rotateleft_25_rorated_output[31]), .in_2(rotateleft_25_rorated_output[30]),
    .in_3(rotateleft_25_rorated_output[29]), .in_4(rotateleft_25_rorated_output[28]),
    .in_5(rotateleft_25_rorated_output[27]), .in_6(rotateleft_25_rorated_output[26]),
    .in_7(rotateleft_25_rorated_output[25]), .in_8(rotateleft_25_rorated_output[24]),
    .in_9(rotateleft_25_rorated_output[23]), .in_10(rotateleft_25_rorated_output[22]),
    .in_11(rotateleft_25_rorated_output[21]), .in_12(rotateleft_25_rorated_output[20]),
    .in_13(rotateleft_25_rorated_output[19]), .in_14(rotateleft_25_rorated_output[18]),
    .in_15(rotateleft_25_rorated_output[17]), .in_16(rotateleft_25_rorated_output[16]),
    .in_17(rotateleft_25_rorated_output[15]), .in_18(rotateleft_25_rorated_output[14]),
    .in_19(rotateleft_25_rorated_output[13]), .in_20(rotateleft_25_rorated_output[12]),
    .in_21(rotateleft_25_rorated_output[11]), .in_22(rotateleft_25_rorated_output[10]),
    .in_23(rotateleft_25_rorated_output[9]), .in_24(rotateleft_25_rorated_output[8]),
    .in_25(rotateleft_25_rorated_output[7]), .in_26(rotateleft_25_rorated_output[6]),
    .in_27(rotateleft_25_rorated_output[5]), .in_28(rotateleft_25_rorated_output[4]),
    .in_29(rotateleft_25_rorated_output[3]), .in_30(rotateleft_25_rorated_output[2]),
    .in_31(rotateleft_25_rorated_output[1]), .in_32(rotateleft_25_rorated_output[0]), .InputFromMux(out_90),
    .out_34(out_91[31]), .out_35(out_91[30]), .out_36(out_91[29]), .out_37(out_91[28]), .out_38(out_91[27]),
    .out_39(out_91[26]), .out_40(out_91[25]), .out_41(out_91[24]), .out_42(out_91[23]), .out_43(out_91[22]),
    .out_44(out_91[21]), .out_45(out_91[20]), .out_46(out_91[19]), .out_47(out_91[18]), .out_48(out_91[17]),
    .out_49(out_91[16]), .out_50(out_91[15]), .out_51(out_91[14]), .out_52(out_91[13]), .out_53(out_91[12]),
    .out_54(out_91[11]), .out_55(out_91[10]), .out_56(out_91[9]), .out_57(out_91[8]), .out_58(out_91[7]),
    .out_59(out_91[6]), .out_60(out_91[5]), .out_61(out_91[4]), .out_62(out_91[3]), .out_63(out_91[2]),
    .out_64(out_91[1]), .out_65(out_91[0]));
  _32BITCONTROL u_32bitcontrol_28 (
    .in_1(rotateleft_26_rorated_output[31]), .in_2(rotateleft_26_rorated_output[30]),
    .in_3(rotateleft_26_rorated_output[29]), .in_4(rotateleft_26_rorated_output[28]),
    .in_5(rotateleft_26_rorated_output[27]), .in_6(rotateleft_26_rorated_output[26]),
    .in_7(rotateleft_26_rorated_output[25]), .in_8(rotateleft_26_rorated_output[24]),
    .in_9(rotateleft_26_rorated_output[23]), .in_10(rotateleft_26_rorated_output[22]),
    .in_11(rotateleft_26_rorated_output[21]), .in_12(rotateleft_26_rorated_output[20]),
    .in_13(rotateleft_26_rorated_output[19]), .in_14(rotateleft_26_rorated_output[18]),
    .in_15(rotateleft_26_rorated_output[17]), .in_16(rotateleft_26_rorated_output[16]),
    .in_17(rotateleft_26_rorated_output[15]), .in_18(rotateleft_26_rorated_output[14]),
    .in_19(rotateleft_26_rorated_output[13]), .in_20(rotateleft_26_rorated_output[12]),
    .in_21(rotateleft_26_rorated_output[11]), .in_22(rotateleft_26_rorated_output[10]),
    .in_23(rotateleft_26_rorated_output[9]), .in_24(rotateleft_26_rorated_output[8]),
    .in_25(rotateleft_26_rorated_output[7]), .in_26(rotateleft_26_rorated_output[6]),
    .in_27(rotateleft_26_rorated_output[5]), .in_28(rotateleft_26_rorated_output[4]),
    .in_29(rotateleft_26_rorated_output[3]), .in_30(rotateleft_26_rorated_output[2]),
    .in_31(rotateleft_26_rorated_output[1]), .in_32(rotateleft_26_rorated_output[0]), .InputFromMux(out_92),
    .out_34(out_93[31]), .out_35(out_93[30]), .out_36(out_93[29]), .out_37(out_93[28]), .out_38(out_93[27]),
    .out_39(out_93[26]), .out_40(out_93[25]), .out_41(out_93[24]), .out_42(out_93[23]), .out_43(out_93[22]),
    .out_44(out_93[21]), .out_45(out_93[20]), .out_46(out_93[19]), .out_47(out_93[18]), .out_48(out_93[17]),
    .out_49(out_93[16]), .out_50(out_93[15]), .out_51(out_93[14]), .out_52(out_93[13]), .out_53(out_93[12]),
    .out_54(out_93[11]), .out_55(out_93[10]), .out_56(out_93[9]), .out_57(out_93[8]), .out_58(out_93[7]),
    .out_59(out_93[6]), .out_60(out_93[5]), .out_61(out_93[4]), .out_62(out_93[3]), .out_63(out_93[2]),
    .out_64(out_93[1]), .out_65(out_93[0]));
  _32BITCONTROL u_32bitcontrol_29 (
    .in_1(rotateleft_27_rorated_output[31]), .in_2(rotateleft_27_rorated_output[30]),
    .in_3(rotateleft_27_rorated_output[29]), .in_4(rotateleft_27_rorated_output[28]),
    .in_5(rotateleft_27_rorated_output[27]), .in_6(rotateleft_27_rorated_output[26]),
    .in_7(rotateleft_27_rorated_output[25]), .in_8(rotateleft_27_rorated_output[24]),
    .in_9(rotateleft_27_rorated_output[23]), .in_10(rotateleft_27_rorated_output[22]),
    .in_11(rotateleft_27_rorated_output[21]), .in_12(rotateleft_27_rorated_output[20]),
    .in_13(rotateleft_27_rorated_output[19]), .in_14(rotateleft_27_rorated_output[18]),
    .in_15(rotateleft_27_rorated_output[17]), .in_16(rotateleft_27_rorated_output[16]),
    .in_17(rotateleft_27_rorated_output[15]), .in_18(rotateleft_27_rorated_output[14]),
    .in_19(rotateleft_27_rorated_output[13]), .in_20(rotateleft_27_rorated_output[12]),
    .in_21(rotateleft_27_rorated_output[11]), .in_22(rotateleft_27_rorated_output[10]),
    .in_23(rotateleft_27_rorated_output[9]), .in_24(rotateleft_27_rorated_output[8]),
    .in_25(rotateleft_27_rorated_output[7]), .in_26(rotateleft_27_rorated_output[6]),
    .in_27(rotateleft_27_rorated_output[5]), .in_28(rotateleft_27_rorated_output[4]),
    .in_29(rotateleft_27_rorated_output[3]), .in_30(rotateleft_27_rorated_output[2]),
    .in_31(rotateleft_27_rorated_output[1]), .in_32(rotateleft_27_rorated_output[0]), .InputFromMux(out_94),
    .out_34(out_95[31]), .out_35(out_95[30]), .out_36(out_95[29]), .out_37(out_95[28]), .out_38(out_95[27]),
    .out_39(out_95[26]), .out_40(out_95[25]), .out_41(out_95[24]), .out_42(out_95[23]), .out_43(out_95[22]),
    .out_44(out_95[21]), .out_45(out_95[20]), .out_46(out_95[19]), .out_47(out_95[18]), .out_48(out_95[17]),
    .out_49(out_95[16]), .out_50(out_95[15]), .out_51(out_95[14]), .out_52(out_95[13]), .out_53(out_95[12]),
    .out_54(out_95[11]), .out_55(out_95[10]), .out_56(out_95[9]), .out_57(out_95[8]), .out_58(out_95[7]),
    .out_59(out_95[6]), .out_60(out_95[5]), .out_61(out_95[4]), .out_62(out_95[3]), .out_63(out_95[2]),
    .out_64(out_95[1]), .out_65(out_95[0]));
  _32BITCONTROL u_32bitcontrol_30 (
    .in_1(rotateleft_28_rorated_output[31]), .in_2(rotateleft_28_rorated_output[30]),
    .in_3(rotateleft_28_rorated_output[29]), .in_4(rotateleft_28_rorated_output[28]),
    .in_5(rotateleft_28_rorated_output[27]), .in_6(rotateleft_28_rorated_output[26]),
    .in_7(rotateleft_28_rorated_output[25]), .in_8(rotateleft_28_rorated_output[24]),
    .in_9(rotateleft_28_rorated_output[23]), .in_10(rotateleft_28_rorated_output[22]),
    .in_11(rotateleft_28_rorated_output[21]), .in_12(rotateleft_28_rorated_output[20]),
    .in_13(rotateleft_28_rorated_output[19]), .in_14(rotateleft_28_rorated_output[18]),
    .in_15(rotateleft_28_rorated_output[17]), .in_16(rotateleft_28_rorated_output[16]),
    .in_17(rotateleft_28_rorated_output[15]), .in_18(rotateleft_28_rorated_output[14]),
    .in_19(rotateleft_28_rorated_output[13]), .in_20(rotateleft_28_rorated_output[12]),
    .in_21(rotateleft_28_rorated_output[11]), .in_22(rotateleft_28_rorated_output[10]),
    .in_23(rotateleft_28_rorated_output[9]), .in_24(rotateleft_28_rorated_output[8]),
    .in_25(rotateleft_28_rorated_output[7]), .in_26(rotateleft_28_rorated_output[6]),
    .in_27(rotateleft_28_rorated_output[5]), .in_28(rotateleft_28_rorated_output[4]),
    .in_29(rotateleft_28_rorated_output[3]), .in_30(rotateleft_28_rorated_output[2]),
    .in_31(rotateleft_28_rorated_output[1]), .in_32(rotateleft_28_rorated_output[0]), .InputFromMux(out_96),
    .out_34(out_97[31]), .out_35(out_97[30]), .out_36(out_97[29]), .out_37(out_97[28]), .out_38(out_97[27]),
    .out_39(out_97[26]), .out_40(out_97[25]), .out_41(out_97[24]), .out_42(out_97[23]), .out_43(out_97[22]),
    .out_44(out_97[21]), .out_45(out_97[20]), .out_46(out_97[19]), .out_47(out_97[18]), .out_48(out_97[17]),
    .out_49(out_97[16]), .out_50(out_97[15]), .out_51(out_97[14]), .out_52(out_97[13]), .out_53(out_97[12]),
    .out_54(out_97[11]), .out_55(out_97[10]), .out_56(out_97[9]), .out_57(out_97[8]), .out_58(out_97[7]),
    .out_59(out_97[6]), .out_60(out_97[5]), .out_61(out_97[4]), .out_62(out_97[3]), .out_63(out_97[2]),
    .out_64(out_97[1]), .out_65(out_97[0]));
  _32BITCONTROL u_32bitcontrol_31 (
    .in_1(rotateleft_29_rorated_output[31]), .in_2(rotateleft_29_rorated_output[30]),
    .in_3(rotateleft_29_rorated_output[29]), .in_4(rotateleft_29_rorated_output[28]),
    .in_5(rotateleft_29_rorated_output[27]), .in_6(rotateleft_29_rorated_output[26]),
    .in_7(rotateleft_29_rorated_output[25]), .in_8(rotateleft_29_rorated_output[24]),
    .in_9(rotateleft_29_rorated_output[23]), .in_10(rotateleft_29_rorated_output[22]),
    .in_11(rotateleft_29_rorated_output[21]), .in_12(rotateleft_29_rorated_output[20]),
    .in_13(rotateleft_29_rorated_output[19]), .in_14(rotateleft_29_rorated_output[18]),
    .in_15(rotateleft_29_rorated_output[17]), .in_16(rotateleft_29_rorated_output[16]),
    .in_17(rotateleft_29_rorated_output[15]), .in_18(rotateleft_29_rorated_output[14]),
    .in_19(rotateleft_29_rorated_output[13]), .in_20(rotateleft_29_rorated_output[12]),
    .in_21(rotateleft_29_rorated_output[11]), .in_22(rotateleft_29_rorated_output[10]),
    .in_23(rotateleft_29_rorated_output[9]), .in_24(rotateleft_29_rorated_output[8]),
    .in_25(rotateleft_29_rorated_output[7]), .in_26(rotateleft_29_rorated_output[6]),
    .in_27(rotateleft_29_rorated_output[5]), .in_28(rotateleft_29_rorated_output[4]),
    .in_29(rotateleft_29_rorated_output[3]), .in_30(rotateleft_29_rorated_output[2]),
    .in_31(rotateleft_29_rorated_output[1]), .in_32(rotateleft_29_rorated_output[0]), .InputFromMux(out_98),
    .out_34(out_99[31]), .out_35(out_99[30]), .out_36(out_99[29]), .out_37(out_99[28]), .out_38(out_99[27]),
    .out_39(out_99[26]), .out_40(out_99[25]), .out_41(out_99[24]), .out_42(out_99[23]), .out_43(out_99[22]),
    .out_44(out_99[21]), .out_45(out_99[20]), .out_46(out_99[19]), .out_47(out_99[18]), .out_48(out_99[17]),
    .out_49(out_99[16]), .out_50(out_99[15]), .out_51(out_99[14]), .out_52(out_99[13]), .out_53(out_99[12]),
    .out_54(out_99[11]), .out_55(out_99[10]), .out_56(out_99[9]), .out_57(out_99[8]), .out_58(out_99[7]),
    .out_59(out_99[6]), .out_60(out_99[5]), .out_61(out_99[4]), .out_62(out_99[3]), .out_63(out_99[2]),
    .out_64(out_99[1]), .out_65(out_99[0]));
  _32BITCONTROL u_32bitcontrol_32 (
    .in_1(rotateleft_30_rorated_output[31]), .in_2(rotateleft_30_rorated_output[30]),
    .in_3(rotateleft_30_rorated_output[29]), .in_4(rotateleft_30_rorated_output[28]),
    .in_5(rotateleft_30_rorated_output[27]), .in_6(rotateleft_30_rorated_output[26]),
    .in_7(rotateleft_30_rorated_output[25]), .in_8(rotateleft_30_rorated_output[24]),
    .in_9(rotateleft_30_rorated_output[23]), .in_10(rotateleft_30_rorated_output[22]),
    .in_11(rotateleft_30_rorated_output[21]), .in_12(rotateleft_30_rorated_output[20]),
    .in_13(rotateleft_30_rorated_output[19]), .in_14(rotateleft_30_rorated_output[18]),
    .in_15(rotateleft_30_rorated_output[17]), .in_16(rotateleft_30_rorated_output[16]),
    .in_17(rotateleft_30_rorated_output[15]), .in_18(rotateleft_30_rorated_output[14]),
    .in_19(rotateleft_30_rorated_output[13]), .in_20(rotateleft_30_rorated_output[12]),
    .in_21(rotateleft_30_rorated_output[11]), .in_22(rotateleft_30_rorated_output[10]),
    .in_23(rotateleft_30_rorated_output[9]), .in_24(rotateleft_30_rorated_output[8]),
    .in_25(rotateleft_30_rorated_output[7]), .in_26(rotateleft_30_rorated_output[6]),
    .in_27(rotateleft_30_rorated_output[5]), .in_28(rotateleft_30_rorated_output[4]),
    .in_29(rotateleft_30_rorated_output[3]), .in_30(rotateleft_30_rorated_output[2]),
    .in_31(rotateleft_30_rorated_output[1]), .in_32(rotateleft_30_rorated_output[0]), .InputFromMux(out_100),
    .out_34(out_101[31]), .out_35(out_101[30]), .out_36(out_101[29]), .out_37(out_101[28]),
    .out_38(out_101[27]), .out_39(out_101[26]), .out_40(out_101[25]), .out_41(out_101[24]),
    .out_42(out_101[23]), .out_43(out_101[22]), .out_44(out_101[21]), .out_45(out_101[20]),
    .out_46(out_101[19]), .out_47(out_101[18]), .out_48(out_101[17]), .out_49(out_101[16]),
    .out_50(out_101[15]), .out_51(out_101[14]), .out_52(out_101[13]), .out_53(out_101[12]),
    .out_54(out_101[11]), .out_55(out_101[10]), .out_56(out_101[9]), .out_57(out_101[8]),
    .out_58(out_101[7]), .out_59(out_101[6]), .out_60(out_101[5]), .out_61(out_101[4]), .out_62(out_101[3]),
    .out_63(out_101[2]), .out_64(out_101[1]), .out_65(out_101[0]));
  _32BITCONTROL u_32bitcontrol_33 (
    .in_1(rotateleft_31_rorated_output[31]), .in_2(rotateleft_31_rorated_output[30]),
    .in_3(rotateleft_31_rorated_output[29]), .in_4(rotateleft_31_rorated_output[28]),
    .in_5(rotateleft_31_rorated_output[27]), .in_6(rotateleft_31_rorated_output[26]),
    .in_7(rotateleft_31_rorated_output[25]), .in_8(rotateleft_31_rorated_output[24]),
    .in_9(rotateleft_31_rorated_output[23]), .in_10(rotateleft_31_rorated_output[22]),
    .in_11(rotateleft_31_rorated_output[21]), .in_12(rotateleft_31_rorated_output[20]),
    .in_13(rotateleft_31_rorated_output[19]), .in_14(rotateleft_31_rorated_output[18]),
    .in_15(rotateleft_31_rorated_output[17]), .in_16(rotateleft_31_rorated_output[16]),
    .in_17(rotateleft_31_rorated_output[15]), .in_18(rotateleft_31_rorated_output[14]),
    .in_19(rotateleft_31_rorated_output[13]), .in_20(rotateleft_31_rorated_output[12]),
    .in_21(rotateleft_31_rorated_output[11]), .in_22(rotateleft_31_rorated_output[10]),
    .in_23(rotateleft_31_rorated_output[9]), .in_24(rotateleft_31_rorated_output[8]),
    .in_25(rotateleft_31_rorated_output[7]), .in_26(rotateleft_31_rorated_output[6]),
    .in_27(rotateleft_31_rorated_output[5]), .in_28(rotateleft_31_rorated_output[4]),
    .in_29(rotateleft_31_rorated_output[3]), .in_30(rotateleft_31_rorated_output[2]),
    .in_31(rotateleft_31_rorated_output[1]), .in_32(rotateleft_31_rorated_output[0]), .InputFromMux(out_102),
    .out_34(out_103[31]), .out_35(out_103[30]), .out_36(out_103[29]), .out_37(out_103[28]),
    .out_38(out_103[27]), .out_39(out_103[26]), .out_40(out_103[25]), .out_41(out_103[24]),
    .out_42(out_103[23]), .out_43(out_103[22]), .out_44(out_103[21]), .out_45(out_103[20]),
    .out_46(out_103[19]), .out_47(out_103[18]), .out_48(out_103[17]), .out_49(out_103[16]),
    .out_50(out_103[15]), .out_51(out_103[14]), .out_52(out_103[13]), .out_53(out_103[12]),
    .out_54(out_103[11]), .out_55(out_103[10]), .out_56(out_103[9]), .out_57(out_103[8]),
    .out_58(out_103[7]), .out_59(out_103[6]), .out_60(out_103[5]), .out_61(out_103[4]), .out_62(out_103[3]),
    .out_63(out_103[2]), .out_64(out_103[1]), .out_65(out_103[0]));
  _32BITCONTROL u_32bitcontrol_34 (
    .in_1(_32_Bit_Input_2[0]), .in_2(_32_Bit_Input_2[1]), .in_3(_32_Bit_Input_2[2]),
    .in_4(_32_Bit_Input_2[3]), .in_5(_32_Bit_Input_2[4]), .in_6(_32_Bit_Input_2[5]),
    .in_7(_32_Bit_Input_2[6]), .in_8(_32_Bit_Input_2[7]), .in_9(_32_Bit_Input_2[8]),
    .in_10(_32_Bit_Input_2[9]), .in_11(_32_Bit_Input_2[10]), .in_12(_32_Bit_Input_2[11]),
    .in_13(_32_Bit_Input_2[12]), .in_14(_32_Bit_Input_2[13]), .in_15(_32_Bit_Input_2[14]),
    .in_16(_32_Bit_Input_2[15]), .in_17(_32_Bit_Input_2[16]), .in_18(_32_Bit_Input_2[17]),
    .in_19(_32_Bit_Input_2[18]), .in_20(_32_Bit_Input_2[19]), .in_21(_32_Bit_Input_2[20]),
    .in_22(_32_Bit_Input_2[21]), .in_23(_32_Bit_Input_2[22]), .in_24(_32_Bit_Input_2[23]),
    .in_25(_32_Bit_Input_2[24]), .in_26(_32_Bit_Input_2[25]), .in_27(_32_Bit_Input_2[26]),
    .in_28(_32_Bit_Input_2[27]), .in_29(_32_Bit_Input_2[28]), .in_30(_32_Bit_Input_2[29]),
    .in_31(_32_Bit_Input_2[30]), .in_32(_32_Bit_Input_2[31]), .InputFromMux(mux_for_finalexam_1_out_17),
    .out_34(LAST_5_BITS[0]), .out_35(LAST_5_BITS[1]), .out_36(LAST_5_BITS[2]), .out_37(LAST_5_BITS[3]),
    .out_38(LAST_5_BITS[4]), .out_39(n32bitcontrol_34_out_39[5]), .out_40(n32bitcontrol_34_out_39[6]),
    .out_41(n32bitcontrol_34_out_39[7]), .out_42(n32bitcontrol_34_out_39[8]),
    .out_43(n32bitcontrol_34_out_39[9]), .out_44(n32bitcontrol_34_out_39[10]),
    .out_45(n32bitcontrol_34_out_39[11]), .out_46(n32bitcontrol_34_out_39[12]),
    .out_47(n32bitcontrol_34_out_39[13]), .out_48(n32bitcontrol_34_out_39[14]),
    .out_49(n32bitcontrol_34_out_39[15]), .out_50(n32bitcontrol_34_out_39[16]),
    .out_51(n32bitcontrol_34_out_39[17]), .out_52(n32bitcontrol_34_out_39[18]),
    .out_53(n32bitcontrol_34_out_39[19]), .out_54(n32bitcontrol_34_out_39[20]),
    .out_55(n32bitcontrol_34_out_39[21]), .out_56(n32bitcontrol_34_out_39[22]),
    .out_57(n32bitcontrol_34_out_39[23]), .out_58(n32bitcontrol_34_out_39[24]),
    .out_59(n32bitcontrol_34_out_39[25]), .out_60(n32bitcontrol_34_out_39[26]),
    .out_61(n32bitcontrol_34_out_39[27]), .out_62(n32bitcontrol_34_out_39[28]),
    .out_63(n32bitcontrol_34_out_39[29]), .out_64(n32bitcontrol_34_out_39[30]),
    .out_65(n32bitcontrol_34_out_39[31]));
  assign _32_BIT_OUTPUT = out_41 | out_43 | out_45 | out_47 | out_49 | out_51 | out_53 | out_55 | out_57 | out_59 | out_61 | out_63 | out_65 | out_67 | out_69 | out_71 | out_73 | out_75 | out_77 | out_79 | out_81 | out_83 | out_85 | out_87 | out_89 | out_91 | out_93 | out_95 | out_97 | out_99 | out_101 | out_103;  // OR_Gate or_1, 32 bits wide

  assign out_37 = LAST_5_BITS;

  // Notes on the sheet:
  //   16 Bit Code: 0001-1101-0000-1111
endmodule

// Control 32BIT by BASU
module _32BITCONTROL (
  input  in_1,
  input  in_2,
  input  in_3,
  input  in_4,
  input  in_5,
  input  in_6,
  input  in_7,
  input  in_8,
  input  in_9,
  input  in_10,
  input  in_11,
  input  in_12,
  input  in_13,
  input  in_14,
  input  in_15,
  input  in_16,
  input  in_17,
  input  in_18,
  input  in_19,
  input  in_20,
  input  in_21,
  input  in_22,
  input  in_23,
  input  in_24,
  input  in_25,
  input  in_26,
  input  in_27,
  input  in_28,
  input  in_29,
  input  in_30,
  input  in_31,
  input  in_32,
  input  InputFromMux,
  output out_34,
  output out_35,
  output out_36,
  output out_37,
  output out_38,
  output out_39,
  output out_40,
  output out_41,
  output out_42,
  output out_43,
  output out_44,
  output out_45,
  output out_46,
  output out_47,
  output out_48,
  output out_49,
  output out_50,
  output out_51,
  output out_52,
  output out_53,
  output out_54,
  output out_55,
  output out_56,
  output out_57,
  output out_58,
  output out_59,
  output out_60,
  output out_61,
  output out_62,
  output out_63,
  output out_64,
  output out_65
);

  and and_1 (out_64, InputFromMux, in_31);
  and and_2 (out_65, InputFromMux, in_32);
  and and_3 (out_63, InputFromMux, in_30);
  and and_4 (out_62, InputFromMux, in_29);
  and and_5 (out_61, InputFromMux, in_28);
  and and_6 (out_60, InputFromMux, in_27);
  and and_7 (out_58, InputFromMux, in_25);
  and and_8 (out_59, InputFromMux, in_26);
  and and_9 (out_57, InputFromMux, in_24);
  and and_10 (out_55, InputFromMux, in_22);
  and and_11 (out_54, InputFromMux, in_21);
  and and_12 (out_56, InputFromMux, in_23);
  and and_13 (out_53, InputFromMux, in_20);
  and and_14 (out_52, InputFromMux, in_19);
  and and_15 (out_51, InputFromMux, in_18);
  and and_16 (out_50, InputFromMux, in_17);
  and and_17 (out_49, InputFromMux, in_16);
  and and_18 (out_48, InputFromMux, in_15);
  and and_19 (out_47, InputFromMux, in_14);
  and and_20 (out_46, InputFromMux, in_13);
  and and_21 (out_45, InputFromMux, in_12);
  and and_22 (out_43, InputFromMux, in_10);
  and and_23 (out_44, InputFromMux, in_11);
  and and_24 (out_42, InputFromMux, in_9);
  and and_25 (out_41, InputFromMux, in_8);
  and and_26 (out_40, InputFromMux, in_7);
  and and_27 (out_39, InputFromMux, in_6);
  and and_28 (out_37, InputFromMux, in_4);
  and and_29 (out_38, InputFromMux, in_5);
  and and_30 (out_35, InputFromMux, in_2);
  and and_31 (out_36, InputFromMux, in_3);
  and and_32 (out_34, InputFromMux, in_1);
endmodule

module _32BitControlBasuWithAnd (
  input  in_1
);
endmodule

// 16 BIT MUX for FINAL
module MUX_FOR_FINALEXAM (
  input  LS,
  input  in_2,
  input  in_3,
  input  in_4,
  input  in_5,
  input  in_6,
  input  in_7,
  input  in_8,
  input  in_9,
  input  in_10,
  input  in_11,
  input  in_12,
  input  in_13,
  input  in_14,
  input  in_15,
  input  MS,
  output out_17
);

  wire not_1_out, not_2_out, not_3_out, not_4_out, not_5_out, not_6_out, not_7_out, not_8_out;

  LED led_1 (.in(MS));
  LED led_2 (.in(in_8));
  not not_1 (not_1_out, MS);
  not not_2 (not_2_out, in_14);
  not not_3 (not_3_out, in_10);
  not not_4 (not_4_out, in_8);
  not not_5 (not_5_out, in_7);
  not not_6 (not_6_out, in_5);
  not not_7 (not_7_out, in_15);
  not not_8 (not_8_out, in_6);
  and and_1 (out_17, not_1_out, not_7_out, not_2_out, in_13, in_12, in_11, not_3_out, in_9, not_5_out, not_8_out, not_6_out, in_4, in_3, in_2, LS);

  // Notes on the sheet:
  //   16 Bit Code: 0001-1101-0000-1111
endmodule

// Comp
module TestCircuitCompaRison (
  input  [4:0] in_1,
  input  [4:0] in_2,
  output [4:0] out_3
);

  assign out_3 = ~(in_1 ^ in_2);  // XNOR_Gate xnor_1, 5 bits wide
endmodule

// COM
module testComp (
  input  [4:0] in_1,
  input  [4:0] in_2,
  output out_3
);

  wire [4:0] xnor_1_out;

  assign xnor_1_out = ~(in_1 ^ in_2);  // XNOR_Gate xnor_1, 5 bits wide
  and and_1 (out_3, xnor_1_out[0], xnor_1_out[1], xnor_1_out[2], xnor_1_out[3], xnor_1_out[4]);
endmodule

// RO
module RotateLeft (
  input  [31:0] INPUT,
  output [31:0] Rorated_Output
);


  assign Rorated_Output = {INPUT[30:0], INPUT[31]};
endmodule
