// Logisim project MUX_4_14_2015.circ as structural Verilog: 1 circuit, main circuit main
module main (
  input  in_1,
  input  in_2,
  input  in_3,
  input  in_4,
  input  in_5,
  input  in_6,
  input  in_7,
  input  in_8,
  input  in_9,
  input  in_10,
  input  in_11,
  input  in_12,
  input  in_13,
  input  in_14,
  input  in_15,
  input  in_16,
  input  in_17,
  input  in_18,
  output out_19,
  output out_20,
  output out_21,
  output out_22,
  output out_23,
  output out_24,
  output out_25,
  output out_26,
  output out_27,
  output out_28,
  output out_29,
  output out_30,
  output out_31,
  output out_32,
  output out_33,
  output out_34,
  output out_35,
  output out_36,
  output out_37,
  output out_38,
  output out_39,
  output out_40,
  output out_41,
  output out_42,
  output out_43,
  output out_44,
  output out_45,
  output out_46,
  output out_47,
  output out_48,
  output out_49,
  output out_50,
  output out_51,
  output out_52,
  output out_53,
  output out_54,
  output out_55,
  output out_56,
  output out_57,
  output out_58,
  output out_59,
  output out_60,
  output out_61,
  output out_62,
  output out_63,
  output out_64,
  output out_65,
  output out_66,
  output out_67,
  output out_68,
  output out_69,
  output out_70,
  output out_71,
  output out_72,
  output out_73,
  output out_74,
  output out_75,
  output out_76,
  output out_77,
  output out_78,
  output out_79,
  output out_80,
  output out_81,
  output out_82,
  output out_83,
  output out_84,
  output out_85,
  output out_86
);

  LED led_1 (.in(in_3));
  LED led_2 (.in(in_11));
  not not_1 (out_20, in_4);
  not not_2 (out_22, in_6);
  not not_3 (out_26, in_10);
  not not_4 (out_31, in_14);
  not not_5 (out_34, in_17);
  not not_6 (out_36, in_3);
  not not_7 (out_37, in_4);
  not not_8 (out_38, in_5);
  not not_9 (out_39, in_6);
  not not_10 (out_41, in_8);
  not not_11 (out_42, in_9);
  not not_12 (out_43, in_10);
  not not_13 (out_50, in_16);
  not not_14 (out_51, in_17);
  not not_15 (out_55, in_5);
  not not_16 (out_56, in_6);
  not not_17 (out_57, in_7);
  not not_18 (out_60, in_10);
  not not_19 (out_61, in_11);
  not not_20 (out_63, in_12);
  not not_21 (out_64, in_13);
  not not_22 (out_69, in_18);
  not not_23 (out_70, in_3);
  not not_24 (out_72, in_5);
  not not_25 (out_73, in_6);
  not not_26 (out_75, in_8);
  not not_27 (out_77, in_10);
  not not_28 (out_78, in_11);
  not not_29 (out_81, in_13);
  not not_30 (out_83, in_15);
  not not_31 (out_84, in_16);
  not not_32 (out_86, in_18);
  LED led_3 (.in(out_28));
  and and_1 (out_28, in_3, out_20, in_5, out_22, in_7, in_8, in_9, out_26, in_12, in_13, out_31, in_15, in_16, out_34, in_18);
  and and_2 (out_45, out_36, out_37, out_38, out_39, in_7, out_41, out_42, out_43, in_12, in_13, in_14, in_15, out_50, out_51, in_18);
  LED led_4 (.in(out_45));
  and and_3 (out_62, in_3, in_4, out_55, out_56, out_57, in_8, in_9, out_60, out_63, out_64, in_14, in_15, in_16, in_17, out_69);
  LED led_5 (.in(out_62));
  and and_4 (out_79, out_70, in_4, out_72, out_73, in_7, out_75, in_9, out_77, in_12, out_81, in_14, out_83, out_84, in_17, out_86);
  LED led_6 (.in(out_79));

  assign out_19 = in_3;
  assign out_21 = in_5;
  assign out_23 = in_7;
  assign out_24 = in_8;
  assign out_25 = in_9;
  assign out_27 = in_11;
  assign out_29 = in_12;
  assign out_30 = in_13;
  assign out_32 = in_15;
  assign out_33 = in_16;
  assign out_35 = in_18;
  assign out_40 = in_7;
  assign out_44 = in_11;
  assign out_46 = in_12;
  assign out_47 = in_13;
  assign out_48 = in_14;
  assign out_49 = in_15;
  assign out_52 = in_18;
  assign out_53 = in_3;
  assign out_54 = in_4;
  assign out_58 = in_8;
  assign out_59 = in_9;
  assign out_65 = in_14;
  assign out_66 = in_15;
  assign out_67 = in_16;
  assign out_68 = in_17;
  assign out_71 = in_4;
  assign out_74 = in_7;
  assign out_76 = in_9;
  assign out_80 = in_12;
  assign out_82 = in_14;
  assign out_85 = in_17;

  // Notes on the sheet:
  //   ADD
  //   SUB
  //   MUL
  //   DIV
endmodule
