// Logisim project MUX_4_14_2015_t1.circ as structural Verilog: 1 circuit, main circuit main
module main (
  input  in_1,
  input  in_2,
  input  in_3,
  input  in_4,
  input  in_5,
  input  in_6,
  input  in_7,
  input  in_8,
  input  in_9,
  input  in_10,
  input  in_11,
  input  in_12,
  input  in_13,
  input  in_14,
  input  in_15,
  input  in_16,
  input  in_17,
  input  in_18,
  input  in_19,
  input  in_20,
  input  in_21,
  input  in_22,
  input  in_23,
  input  in_24,
  input  in_25,
  input  in_26,
  input  in_27,
  input  in_28,
  input  in_29,
  input  in_30,
  input  in_31,
  input  in_32,
  input  in_33,
  input  in_34,
  output out_35,
  output out_36,
  output out_37,
  output out_38,
  output out_39,
  output out_40,
  output out_41,
  output out_42,
  output out_43,
  output out_44,
  output out_45,
  output out_46,
  output out_47,
  output out_48,
  output out_49,
  output out_50,
  output out_51,
  output out_52,
  output out_53,
  output out_54,
  output out_55,
  output out_56,
  output out_57,
  output out_58,
  output SUB,
  output out_60,
  output out_61,
  output out_62,
  output out_63,
  output out_64,
  output out_65,
  output out_66,
  output out_67,
  output out_68,
  output out_69,
  output out_70,
  output out_71,
  output out_72,
  output out_73,
  output out_74,
  output out_75,
  output MUL,
  output out_77,
  output out_78,
  output out_79,
  output out_80,
  output out_81,
  output out_82,
  output out_83,
  output out_84,
  output out_85,
  output out_86,
  output out_87,
  output out_88,
  output out_89,
  output out_90,
  output out_91,
  output out_92,
  output DIV,
  output out_94,
  output out_95,
  output out_96,
  output out_97,
  output out_98,
  output out_99,
  output out_100,
  output out_101,
  output out_102
);

  wire and_5_out, and_6_out, and_7_out, and_17_out, and_18_out, and_25_out, and_26_out, and_27_out,
       and_37_out, and_38_out, and_39_out, and_49_out, and_51_out, undriven, undriven_2, undriven_3,
       undriven_4, undriven_5, undriven_6, undriven_7, undriven_8, undriven_9, undriven_10, undriven_11,
       undriven_12, undriven_13, undriven_14, undriven_15, undriven_16;

  LED led_1 (.in(in_19));
  LED led_2 (.in(in_27));
  not not_1 (out_36, in_20);
  not not_2 (out_38, in_22);
  not not_3 (out_43, in_26);
  not not_4 (out_47, in_30);
  not not_5 (out_50, in_33);
  not not_6 (out_52, in_19);
  not not_7 (out_53, in_20);
  not not_8 (out_54, in_21);
  not not_9 (out_55, in_22);
  not not_10 (out_57, in_24);
  not not_11 (out_58, in_25);
  not not_12 (out_60, in_26);
  not not_13 (out_66, in_32);
  not not_14 (out_67, in_33);
  not not_15 (out_71, in_21);
  not not_16 (out_72, in_22);
  not not_17 (out_73, in_23);
  not not_18 (out_77, in_26);
  not not_19 (out_78, in_27);
  not not_20 (out_79, in_28);
  not not_21 (out_80, in_29);
  not not_22 (out_85, in_34);
  not not_23 (out_86, in_19);
  not not_24 (out_88, in_21);
  not not_25 (out_89, in_22);
  not not_26 (out_91, in_24);
  not not_27 (out_94, in_26);
  not not_28 (out_95, in_27);
  not not_29 (out_97, in_29);
  not not_30 (out_99, in_31);
  not not_31 (out_100, in_32);
  not not_32 (out_102, in_34);
  LED led_3 (.in(out_42));
  and and_1 (out_42, in_19, out_36, in_21, out_38, in_23, in_24, in_25, out_43, in_28, in_29, out_47, in_31, in_32, out_50, in_34);
  and and_2 (SUB, out_52, out_53, out_54, out_55, in_23, out_57, out_58, out_60, in_28, in_29, in_30, in_31, out_66, out_67, in_34);
  LED led_4 (.in(SUB));
  LED led_5 (.in(MUL));
  and and_3 (MUL, in_19, in_20, out_71, out_72, out_73, in_24, in_25, out_77, out_79, out_80, in_30, in_31, in_32, in_33, out_85);
  and and_4 (in_2, out_86, in_20, out_88, out_89, in_23, out_91, in_25, out_94, in_28, out_97, in_30, out_99, out_100, in_33, out_102);
  LED led_6 (.in(in_2));
  and and_5 (and_5_out, out_42, in_2);
  and and_6 (and_6_out, out_42, in_2);
  and and_7 (and_7_out, out_42, in_2);
  // AND_Gate and_8 has open pins: in0=SUB, in1=in_2, out=open
  // AND_Gate and_9 has open pins: in0=SUB, in1=in_2, out=open
  // AND_Gate and_10 has open pins: in0=SUB, in1=in_2, out=open
  // AND_Gate and_11 has open pins: in0=MUL, in1=in_2, out=open
  // AND_Gate and_12 has open pins: in0=MUL, in1=in_2, out=open
  // AND_Gate and_13 has open pins: in0=MUL, in1=in_2, out=open
  // AND_Gate and_14 has open pins: in0=in_2, in1=in_2, out=open
  // AND_Gate and_15 has open pins: in0=in_2, in1=in_2, out=open
  // AND_Gate and_16 has open pins: in0=in_2, in1=in_2, out=open
  and and_17 (and_17_out, out_42, in_2);
  and and_18 (and_18_out, out_42, in_2);
  // AND_Gate and_19 has open pins: in0=SUB, in1=in_2, out=open
  // AND_Gate and_20 has open pins: in0=SUB, in1=in_2, out=open
  // AND_Gate and_21 has open pins: in0=MUL, in1=in_2, out=open
  // AND_Gate and_22 has open pins: in0=MUL, in1=in_2, out=open
  // AND_Gate and_23 has open pins: in0=in_2, in1=in_2, out=open
  // AND_Gate and_24 has open pins: in0=in_2, in1=in_2, out=open
  and and_25 (and_25_out, out_42, in_2);
  and and_26 (and_26_out, out_42, in_2);
  and and_27 (and_27_out, out_42, in_2);
  // AND_Gate and_28 has open pins: in0=SUB, in1=in_2, out=open
  // AND_Gate and_29 has open pins: in0=SUB, in1=in_2, out=open
  // AND_Gate and_30 has open pins: in0=SUB, in1=in_2, out=open
  // AND_Gate and_31 has open pins: in0=MUL, in1=in_2, out=open
  // AND_Gate and_32 has open pins: in0=MUL, in1=in_2, out=open
  // AND_Gate and_33 has open pins: in0=MUL, in1=in_2, out=open
  // AND_Gate and_34 has open pins: in0=in_2, in1=in_2, out=open
  // AND_Gate and_35 has open pins: in0=in_2, in1=in_2, out=open
  // AND_Gate and_36 has open pins: in0=in_2, in1=in_2, out=open
  and and_37 (and_37_out, out_42, in_10);
  and and_38 (and_38_out, out_42, in_11);
  and and_39 (and_39_out, out_42, in_12);
  // AND_Gate and_40 has open pins: in0=SUB, in1=undriven_5, out=open
  // AND_Gate and_41 has open pins: in0=SUB, in1=undriven, out=open
  // AND_Gate and_42 has open pins: in0=SUB, in1=undriven_3, out=open
  // AND_Gate and_43 has open pins: in0=MUL, in1=undriven_6, out=open
  // AND_Gate and_44 has open pins: in0=MUL, in1=undriven_2, out=open
  // AND_Gate and_45 has open pins: in0=MUL, in1=undriven_4, out=open
  // AND_Gate and_46 has open pins: in0=in_2, in1=in_2, out=open
  // AND_Gate and_47 has open pins: in0=in_2, in1=in_2, out=open
  // AND_Gate and_48 has open pins: in0=in_2, in1=in_2, out=open
  and and_49 (and_49_out, out_42, in_13);
  // AND_Gate and_50 has open pins: in0=out_42, in1=in_15, out=open
  and and_51 (and_51_out, out_42, in_14);
  // AND_Gate and_52 has open pins: in0=SUB, in1=undriven_7, out=open
  // AND_Gate and_53 has open pins: in0=SUB, in1=undriven_11, out=open
  // AND_Gate and_54 has open pins: in0=SUB, in1=undriven_9, out=open
  // AND_Gate and_55 has open pins: in0=MUL, in1=undriven_8, out=open
  // AND_Gate and_56 has open pins: in0=MUL, in1=undriven_10, out=open
  // AND_Gate and_57 has open pins: in0=MUL, in1=undriven_12, out=open
  // AND_Gate and_58 has open pins: in0=in_2, in1=in_2, out=open
  // AND_Gate and_59 has open pins: in0=in_2, in1=in_2, out=open
  // AND_Gate and_60 has open pins: in0=in_2, in1=in_2, out=open
  // AND_Gate and_61 has open pins: in0=out_42, in1=in_16, out=open
  // AND_Gate and_62 has open pins: in0=out_42, in1=in_17, out=open
  // AND_Gate and_63 has open pins: in0=SUB, in1=undriven_13, out=open
  // AND_Gate and_64 has open pins: in0=SUB, in1=undriven_15, out=open
  // AND_Gate and_65 has open pins: in0=MUL, in1=undriven_16, out=open
  // AND_Gate and_66 has open pins: in0=MUL, in1=undriven_14, out=open
  // AND_Gate and_67 has open pins: in0=in_2, in1=in_2, out=open
  // AND_Gate and_68 has open pins: in0=in_2, in1=in_2, out=open

  assign DIV = in_2;
  assign in_3 = in_2;
  assign in_4 = in_2;
  assign in_5 = in_2;
  assign in_6 = in_2;
  assign in_7 = in_2;
  assign in_8 = in_2;
  assign in_9 = in_2;
  assign out_35 = in_19;
  assign out_37 = in_21;
  assign out_39 = in_23;
  assign out_40 = in_24;
  assign out_41 = in_25;
  assign out_44 = in_27;
  assign out_45 = in_28;
  assign out_46 = in_29;
  assign out_48 = in_31;
  assign out_49 = in_32;
  assign out_51 = in_34;
  assign out_56 = in_23;
  assign out_61 = in_27;
  assign out_62 = in_28;
  assign out_63 = in_29;
  assign out_64 = in_30;
  assign out_65 = in_31;
  assign out_68 = in_34;
  assign out_69 = in_19;
  assign out_70 = in_20;
  assign out_74 = in_24;
  assign out_75 = in_25;
  assign out_81 = in_30;
  assign out_82 = in_31;
  assign out_83 = in_32;
  assign out_84 = in_33;
  assign out_87 = in_20;
  assign out_90 = in_23;
  assign out_92 = in_25;
  assign out_96 = in_28;
  assign out_98 = in_30;
  assign out_101 = in_33;

  // Notes on the sheet:
  //   ADD
  //   A
  //   B
endmodule
