// Logisim project MUX_4_14_2015_t4.circ as structural Verilog: 2 circuits, main circuit main
module main (
  input  in_1,
  input  in_2,
  input  in_3,
  input  in_4,
  input  in_5,
  input  in_6,
  input  in_7,
  input  in_8,
  input  in_9,
  input  in_10,
  input  in_11,
  input  in_12,
  input  in_13,
  input  in_14,
  input  in_15,
  input  in_16,
  input  in_17,
  input  in_18,
  input  in_19,
  input  in_20,
  input  in_21,
  input  in_22,
  input  in_23,
  input  in_24,
  input  in_25,
  input  in_26,
  input  in_27,
  input  in_28,
  input  in_29,
  input  in_30,
  input  in_31,
  input  in_32,
  input  in_33,
  input  in_34,
  input  B1,
  input  in_36,
  input  B8,
  input  B7,
  input  B6,
  input  B5,
  input  B4,
  input  B3,
  input  B2,
  input  in_44,
  input  in_45,
  input  in_46,
  input  in_47,
  input  in_48,
  input  in_49,
  input  in_50,
  input  in_51,
  output out_52,
  output out_53,
  output out_54,
  output out_55,
  output out_56,
  output out_57,
  output out_58,
  output out_59,
  output out_60,
  output out_61,
  output out_62,
  output out_63,
  output out_64,
  output out_65,
  output out_66,
  output out_67,
  output out_68,
  output out_69,
  output out_70,
  output out_71,
  output out_72,
  output out_73,
  output out_74,
  output out_75,
  output SUB,
  output out_77,
  output out_78,
  output out_79,
  output out_80,
  output out_81,
  output out_82,
  output out_83,
  output out_84,
  output out_85,
  output out_86,
  output out_87,
  output out_88,
  output out_89,
  output out_90,
  output out_91,
  output out_92,
  output MUL,
  output out_94,
  output out_95,
  output out_96,
  output out_97,
  output out_98,
  output out_99,
  output out_100,
  output out_101,
  output out_102,
  output out_103,
  output out_104,
  output out_105,
  output out_106,
  output out_107,
  output out_108,
  output out_109,
  output DIV,
  output out_111,
  output out_112,
  output out_113,
  output out_114,
  output out_115,
  output out_116,
  output out_117,
  output out_118,
  output out_119,
  output out_120,
  output out_121,
  output out_122,
  output out_123,
  output out_124,
  output out_125,
  output out_126,
  output out_127,
  output out_128,
  output out_129,
  output out_130,
  output out_131,
  output out_132,
  output out_133,
  output out_134,
  output out_135,
  output out_136,
  output out_137,
  output out_138,
  output out_139,
  output out_140,
  output out_141,
  output out_142,
  output out_143
);

  wire _001_1_2_out, _001_1_3_out, _001_1_4_out, _001_1_5_out, _001_1_6_out, _001_1_7_out, _001_1_out,
       _010_1_2_out, _010_1_3_out, _010_1_4_out, _010_1_5_out, _010_1_6_out, _010_1_7_out, _010_1_out,
       _011_2_2_out, _011_2_3_out, _011_2_4_out, _011_2_5_out, _011_2_6_out, _011_2_7_out, _011_2_out,
       _100_1_2_out, _100_1_3_out, _100_1_4_out, _100_1_5_out, _100_1_6_out, _100_1_7_out, _100_1_out,
       _101_2_2_out, _101_2_3_out, _101_2_4_out, _101_2_5_out, _101_2_6_out, _101_2_7_out, _101_2_out,
       _110_2_2_out, _110_2_3_out, _110_2_4_out, _110_2_5_out, _110_2_6_out, _110_2_7_out, _110_2_out,
       _111_3_2_out, _111_3_3_out, _111_3_4_out, _111_3_5_out, _111_3_6_out, _111_3_7_out, _111_3_out,
       and_5_out, and_6_out, and_7_out, and_8_out, and_9_out, and_10_out, and_11_out, and_12_out, and_13_out,
       and_14_out, and_15_out, and_16_out, and_17_out, and_18_out, and_19_out, and_20_out, and_21_out,
       and_22_out, and_23_out, and_24_out, and_25_out, and_26_out, and_27_out, and_28_out, and_29_out,
       and_30_out, and_31_out, and_32_out, and_33_out, and_34_out, and_35_out, and_36_out, and_37_out,
       and_38_out, and_39_out, and_40_out, and_41_out, and_42_out, and_43_out, and_44_out, and_45_out,
       and_46_out, and_47_out, and_48_out, and_49_out, and_50_out, and_51_out, and_52_out, and_53_out,
       and_54_out, and_55_out, and_56_out, and_57_out, and_58_out, and_59_out, and_60_out, and_61_out,
       and_62_out, and_63_out, and_64_out, and_65_out, and_66_out, and_67_out, and_68_out, Carry_1_out,
       Carry_2_out, Carry_2_out_2, Carry_3_out, Carry_3_out_2, Carry_4_out, Carry_4_out_2, Carry_5_out,
       Carry_5_out_2, Carry_6_out, Carry_6_out_2, Carry_7_out, Carry_7_out_2, Carry_8_out, Carry_8_out_2,
       Carry_out, not_41_out, not_42_out, not_43_out, not_44_out, not_45_out, not_46_out, not_47_out,
       not_48_out, not_49_out, not_50_out, not_51_out, not_52_out, not_53_out, not_54_out, not_55_out,
       not_56_out, not_57_out, not_58_out, not_59_out, not_60_out, not_61_out, not_62_out, not_63_out,
       not_64_out, not_65_out, not_66_out, not_67_out, not_68_out, not_69_out, not_70_out, not_71_out,
       not_72_out, not_73_out, not_74_out, not_75_out, not_76_out, not_77_out, not_78_out, not_79_out,
       not_80_out, not_81_out, not_82_out, not_83_out, not_84_out, not_85_out, not_86_out, not_87_out,
       not_88_out, not_89_out, not_90_out, not_91_out, not_92_out, not_93_out, not_94_out, not_95_out,
       not_96_out, not_97_out, not_98_out, not_99_out, not_100_out, not_101_out, not_102_out, not_103_out;

  LED led_1 (.in(in_19));
  LED led_2 (.in(in_27));
  not not_1 (out_53, in_20);
  not not_2 (out_55, in_22);
  not not_3 (out_60, in_26);
  not not_4 (out_64, in_30);
  not not_5 (out_67, in_33);
  not not_6 (out_69, in_19);
  not not_7 (out_70, in_20);
  not not_8 (out_71, in_21);
  not not_9 (out_72, in_22);
  not not_10 (out_74, in_24);
  not not_11 (out_75, in_25);
  not not_12 (out_77, in_26);
  not not_13 (out_83, in_32);
  not not_14 (out_84, in_33);
  not not_15 (out_88, in_21);
  not not_16 (out_89, in_22);
  not not_17 (out_90, in_23);
  not not_18 (out_94, in_26);
  not not_19 (out_95, in_27);
  not not_20 (out_96, in_28);
  not not_21 (out_97, in_29);
  not not_22 (out_102, in_34);
  not not_23 (out_103, in_19);
  not not_24 (out_105, in_21);
  not not_25 (out_106, in_22);
  not not_26 (out_108, in_24);
  not not_27 (out_111, in_26);
  not not_28 (out_112, in_27);
  not not_29 (out_114, in_29);
  not not_30 (out_116, in_31);
  not not_31 (out_117, in_32);
  not not_32 (out_119, in_34);
  LED led_3 (.in(out_59));
  and and_1 (out_59, in_19, out_53, in_21, out_55, in_23, in_24, in_25, out_60, in_28, in_29, out_64, in_31, in_32, out_67, in_34);
  LED led_4 (.in(SUB));
  and and_2 (SUB, out_69, out_70, out_71, out_72, in_23, out_74, out_75, out_77, in_28, in_29, in_30, in_31, out_83, out_84, in_34);
  LED led_5 (.in(MUL));
  and and_3 (MUL, in_19, in_20, out_88, out_89, out_90, in_24, in_25, out_94, out_96, out_97, in_30, in_31, in_32, in_33, out_102);
  and and_4 (DIV, out_103, in_20, out_105, out_106, in_23, out_108, in_25, out_111, in_28, out_114, in_30, out_116, out_117, in_33, out_119);
  LED led_6 (.in(DIV));
  and and_5 (and_5_out, out_59, in_4);
  and and_6 (and_6_out, out_59, in_2);
  and and_7 (and_7_out, out_59, in_3);
  and and_8 (and_8_out, SUB, in_4);
  and and_9 (and_9_out, SUB, in_2);
  and and_10 (and_10_out, SUB, in_3);
  and and_11 (and_11_out, MUL, in_2);
  and and_12 (and_12_out, MUL, in_3);
  and and_13 (and_13_out, MUL, in_4);
  and and_14 (and_14_out, DIV, in_4);
  and and_15 (and_15_out, DIV, in_2);
  and and_16 (and_16_out, DIV, in_3);
  and and_17 (and_17_out, out_59, in_6);
  and and_18 (and_18_out, out_59, in_5);
  and and_19 (and_19_out, SUB, in_5);
  and and_20 (and_20_out, SUB, in_6);
  and and_21 (and_21_out, MUL, in_6);
  and and_22 (and_22_out, MUL, in_5);
  and and_23 (and_23_out, DIV, in_6);
  and and_24 (and_24_out, DIV, in_5);
  and and_25 (and_25_out, out_59, in_7);
  and and_26 (and_26_out, out_59, in_9);
  and and_27 (and_27_out, out_59, in_8);
  and and_28 (and_28_out, SUB, in_7);
  and and_29 (and_29_out, SUB, in_9);
  and and_30 (and_30_out, SUB, in_8);
  and and_31 (and_31_out, MUL, in_8);
  and and_32 (and_32_out, MUL, in_7);
  and and_33 (and_33_out, MUL, in_9);
  and and_34 (and_34_out, DIV, in_8);
  and and_35 (and_35_out, DIV, in_7);
  and and_36 (and_36_out, DIV, in_9);
  and and_37 (and_37_out, out_59, in_10);
  and and_38 (and_38_out, SUB, in_10);
  and and_39 (and_39_out, MUL, in_10);
  and and_40 (and_40_out, DIV, in_10);
  and and_41 (and_41_out, out_59, in_12);
  and and_42 (and_42_out, out_59, in_11);
  and and_43 (and_43_out, out_59, in_13);
  and and_44 (and_44_out, SUB, in_13);
  and and_45 (and_45_out, SUB, in_12);
  and and_46 (and_46_out, SUB, in_11);
  and and_47 (and_47_out, MUL, in_13);
  and and_48 (and_48_out, MUL, in_11);
  and and_49 (and_49_out, MUL, in_12);
  and and_50 (and_50_out, DIV, in_12);
  and and_51 (and_51_out, DIV, in_13);
  and and_52 (and_52_out, DIV, in_11);
  and and_53 (and_53_out, out_59, in_16);
  and and_54 (and_54_out, out_59, in_14);
  and and_55 (and_55_out, out_59, in_15);
  and and_56 (and_56_out, SUB, in_16);
  and and_57 (and_57_out, SUB, in_15);
  and and_58 (and_58_out, SUB, in_14);
  and and_59 (and_59_out, MUL, in_15);
  and and_60 (and_60_out, MUL, in_16);
  and and_61 (and_61_out, MUL, in_14);
  and and_62 (and_62_out, DIV, in_15);
  and and_63 (and_63_out, DIV, in_16);
  and and_64 (and_64_out, DIV, in_14);
  and and_65 (and_65_out, out_59, in_17);
  and and_66 (and_66_out, SUB, in_17);
  and and_67 (and_67_out, MUL, in_17);
  and and_68 (and_68_out, DIV, in_17);
  not not_33 (out_120, in_44);
  not not_34 (out_121, in_45);
  not not_35 (out_122, in_46);
  not not_36 (out_123, in_47);
  and Carry (Carry_out, out_120, Carry_3_out);
  not not_37 (out_124, in_48);
  and Carry_2 (Carry_2_out, out_122, Carry_4_out);
  xor Sum (out_137, out_121, Carry_2_out);
  and Carry_3 (Carry_3_out, out_121, Carry_2_out);
  xor Sum_2 (out_136, out_120, Carry_3_out);
  not not_38 (out_125, in_49);
  and Carry_4 (Carry_4_out, out_123, Carry_6_out);
  xor Sum_3 (out_138, out_122, Carry_4_out);
  not not_39 (out_127, in_51);
  not not_40 (out_126, in_50);
  and Carry_5 (Carry_5_out, out_125, Carry_7_out);
  and Carry_6 (Carry_6_out, out_124, Carry_5_out);
  xor Sum_4 (out_140, out_124, Carry_5_out);
  xor Sum_5 (out_139, out_123, Carry_6_out);
  and Carry_7 (Carry_7_out, out_126, Carry_8_out);
  xor Sum_6 (out_141, out_125, Carry_7_out);
  xor Sum_7 (out_143, out_127, in_36);
  and Carry_8 (Carry_8_out, out_127, in_36);
  xor Sum_8 (out_142, out_126, Carry_8_out);
  and Carry_1 (Carry_1_out, B1, out_143);
  not not_41 (not_41_out, out_142);
  and _010_1 (_010_1_out, not_41_out, B2, not_42_out);
  not not_42 (not_42_out, Carry_1_out);
  not not_43 (not_43_out, out_142);
  not not_44 (not_44_out, B2);
  and _001_1 (_001_1_out, not_43_out, not_44_out, Carry_1_out);
  and _100_1 (_100_1_out, out_142, not_45_out, not_46_out);
  not not_45 (not_45_out, B2);
  not not_46 (not_46_out, Carry_1_out);
  and _111_3 (_111_3_out, out_142, B2, Carry_1_out);
  not not_47 (not_47_out, out_142);
  and _011_2 (_011_2_out, not_47_out, B2, Carry_1_out);
  and _110_2 (_110_2_out, out_142, B2, not_48_out);
  not not_48 (not_48_out, Carry_1_out);
  and _101_2 (_101_2_out, out_142, not_49_out, Carry_1_out);
  not not_49 (not_49_out, B2);
  not not_50 (not_50_out, out_141);
  and _010_1_2 (_010_1_2_out, not_50_out, B3, not_51_out);
  not not_51 (not_51_out, Carry_2_out_2);
  not not_52 (not_52_out, out_141);
  not not_53 (not_53_out, B3);
  and _001_1_2 (_001_1_2_out, not_52_out, not_53_out, Carry_2_out_2);
  not not_54 (not_54_out, B3);
  and _100_1_2 (_100_1_2_out, out_141, not_54_out, not_55_out);
  not not_55 (not_55_out, Carry_2_out_2);
  and _111_3_2 (_111_3_2_out, out_141, B3, Carry_2_out_2);
  not not_56 (not_56_out, out_141);
  and _011_2_2 (_011_2_2_out, not_56_out, B3, Carry_2_out_2);
  and _110_2_2 (_110_2_2_out, out_141, B3, not_57_out);
  not not_57 (not_57_out, Carry_2_out_2);
  and _101_2_2 (_101_2_2_out, out_141, not_58_out, Carry_2_out_2);
  not not_58 (not_58_out, B3);
  not not_59 (not_59_out, out_140);
  and _010_1_3 (_010_1_3_out, not_59_out, B4, not_60_out);
  not not_60 (not_60_out, Carry_3_out_2);
  not not_61 (not_61_out, out_140);
  and _001_1_3 (_001_1_3_out, not_61_out, not_62_out, Carry_3_out_2);
  not not_62 (not_62_out, B4);
  not not_63 (not_63_out, B4);
  and _100_1_3 (_100_1_3_out, out_140, not_63_out, not_64_out);
  not not_64 (not_64_out, Carry_3_out_2);
  and _111_3_3 (_111_3_3_out, out_140, B4, Carry_3_out_2);
  not not_65 (not_65_out, out_140);
  and _011_2_3 (_011_2_3_out, not_65_out, B4, Carry_3_out_2);
  and _110_2_3 (_110_2_3_out, out_140, B4, not_66_out);
  not not_66 (not_66_out, Carry_3_out_2);
  and _101_2_3 (_101_2_3_out, out_140, not_67_out, Carry_3_out_2);
  not not_67 (not_67_out, B4);
  not not_68 (not_68_out, out_139);
  and _010_1_4 (_010_1_4_out, not_68_out, B5, not_69_out);
  not not_69 (not_69_out, Carry_4_out_2);
  not not_70 (not_70_out, out_139);
  and _001_1_4 (_001_1_4_out, not_70_out, not_71_out, Carry_4_out_2);
  not not_71 (not_71_out, B5);
  and _100_1_4 (_100_1_4_out, out_139, not_72_out, not_73_out);
  not not_72 (not_72_out, B5);
  not not_73 (not_73_out, Carry_4_out_2);
  and _111_3_4 (_111_3_4_out, out_139, B5, Carry_4_out_2);
  not not_74 (not_74_out, out_139);
  and _011_2_4 (_011_2_4_out, not_74_out, B5, Carry_4_out_2);
  and _110_2_4 (_110_2_4_out, out_139, B5, not_75_out);
  not not_75 (not_75_out, Carry_4_out_2);
  and _101_2_4 (_101_2_4_out, out_139, not_76_out, Carry_4_out_2);
  not not_76 (not_76_out, B5);
  not not_77 (not_77_out, out_138);
  and _010_1_5 (_010_1_5_out, not_77_out, B6, not_78_out);
  not not_78 (not_78_out, Carry_5_out_2);
  not not_79 (not_79_out, out_138);
  not not_80 (not_80_out, out_138);
  and _001_1_5 (_001_1_5_out, not_79_out, not_80_out, Carry_5_out_2);
  and _100_1_5 (_100_1_5_out, out_138, not_81_out, not_82_out);
  not not_81 (not_81_out, B6);
  not not_82 (not_82_out, Carry_5_out_2);
  and _111_3_5 (_111_3_5_out, out_138, B6, Carry_5_out_2);
  not not_83 (not_83_out, out_138);
  and _011_2_5 (_011_2_5_out, not_83_out, B6, Carry_5_out_2);
  and _110_2_5 (_110_2_5_out, out_138, B6, not_84_out);
  not not_84 (not_84_out, Carry_5_out_2);
  not not_85 (not_85_out, B6);
  and _101_2_5 (_101_2_5_out, out_138, not_85_out, Carry_5_out_2);
  not not_86 (not_86_out, out_137);
  and _010_1_6 (_010_1_6_out, not_86_out, B7, not_87_out);
  not not_87 (not_87_out, Carry_6_out_2);
  not not_88 (not_88_out, out_137);
  not not_89 (not_89_out, B7);
  and _001_1_6 (_001_1_6_out, not_88_out, not_89_out, Carry_6_out_2);
  not not_90 (not_90_out, B7);
  and _100_1_6 (_100_1_6_out, out_137, not_90_out, not_91_out);
  not not_91 (not_91_out, Carry_6_out_2);
  and _111_3_6 (_111_3_6_out, out_137, B7, Carry_6_out_2);
  not not_92 (not_92_out, out_137);
  and _011_2_6 (_011_2_6_out, not_92_out, B7, Carry_6_out_2);
  and _110_2_6 (_110_2_6_out, out_137, B7, not_93_out);
  not not_93 (not_93_out, Carry_6_out_2);
  not not_94 (not_94_out, B7);
  and _101_2_6 (_101_2_6_out, out_137, not_94_out, Carry_6_out_2);
  not not_95 (not_95_out, out_136);
  and _010_1_7 (_010_1_7_out, not_95_out, B8, not_96_out);
  not not_96 (not_96_out, Carry_7_out_2);
  not not_97 (not_97_out, out_136);
  and _001_1_7 (_001_1_7_out, not_97_out, not_98_out, Carry_7_out_2);
  not not_98 (not_98_out, B8);
  and _100_1_7 (_100_1_7_out, out_136, not_99_out, not_100_out);
  not not_99 (not_99_out, B8);
  not not_100 (not_100_out, Carry_7_out_2);
  and _111_3_7 (_111_3_7_out, out_136, B8, Carry_7_out_2);
  not not_101 (not_101_out, out_136);
  and _011_2_7 (_011_2_7_out, not_101_out, B8, Carry_7_out_2);
  and _110_2_7 (_110_2_7_out, out_136, B8, not_102_out);
  not not_102 (not_102_out, Carry_7_out_2);
  not not_103 (not_103_out, B8);
  and _101_2_7 (_101_2_7_out, out_136, not_103_out, Carry_7_out_2);
  xor Output_1 (out_135, B1, out_143);
  or Output_2 (out_134, _010_1_out, _001_1_out, _100_1_out, _111_3_out);
  or Carry_2_dup2 (Carry_2_out_2, _111_3_out, _011_2_out, _110_2_out, _101_2_out);
  or Output_3 (out_133, _010_1_2_out, _001_1_2_out, _100_1_2_out, _111_3_2_out);
  or Carry_3_dup2 (Carry_3_out_2, _111_3_2_out, _011_2_2_out, _110_2_2_out, _101_2_2_out);
  or Output_4 (out_132, _010_1_3_out, _001_1_3_out, _100_1_3_out, _111_3_3_out);
  or Carry_4_dup2 (Carry_4_out_2, _111_3_3_out, _011_2_3_out, _110_2_3_out, _101_2_3_out);
  or Output_5 (out_131, _010_1_4_out, _001_1_4_out, _100_1_4_out, _111_3_4_out);
  or Carry_5_dup2 (Carry_5_out_2, _111_3_4_out, _011_2_4_out, _110_2_4_out, _101_2_4_out);
  or Output_6 (out_130, _010_1_5_out, _001_1_5_out, _100_1_5_out, _111_3_5_out);
  or Carry_6_dup2 (Carry_6_out_2, _111_3_5_out, _011_2_5_out, _110_2_5_out, _101_2_5_out);
  or Output_7 (out_129, _010_1_6_out, _001_1_6_out, _100_1_6_out, _111_3_6_out);
  or Carry_7_dup2 (Carry_7_out_2, _111_3_6_out, _011_2_6_out, _110_2_6_out, _101_2_6_out);
  or Output_8 (out_128, _010_1_7_out, _001_1_7_out, _100_1_7_out, _111_3_7_out);
  or Carry_8_dup2 (Carry_8_out_2, _111_3_7_out, _011_2_7_out, _110_2_7_out, _101_2_7_out);

  assign out_52 = in_19;
  assign out_54 = in_21;
  assign out_56 = in_23;
  assign out_57 = in_24;
  assign out_58 = in_25;
  assign out_61 = in_27;
  assign out_62 = in_28;
  assign out_63 = in_29;
  assign out_65 = in_31;
  assign out_66 = in_32;
  assign out_68 = in_34;
  assign out_73 = in_23;
  assign out_78 = in_27;
  assign out_79 = in_28;
  assign out_80 = in_29;
  assign out_81 = in_30;
  assign out_82 = in_31;
  assign out_85 = in_34;
  assign out_86 = in_19;
  assign out_87 = in_20;
  assign out_91 = in_24;
  assign out_92 = in_25;
  assign out_98 = in_30;
  assign out_99 = in_31;
  assign out_100 = in_32;
  assign out_101 = in_33;
  assign out_104 = in_20;
  assign out_107 = in_23;
  assign out_109 = in_25;
  assign out_113 = in_28;
  assign out_115 = in_30;
  assign out_118 = in_33;

  // Notes on the sheet:
  //   ADD: 1010  1110  1110  1101 
  //   SUB: 0000  1000  1111 1001
  //   MUL: 1100  0110  0001 1110
  //   DIV: 0100  1010 0101 0010 
  //   ADD
  //   A
  //   B
  //   Subtraction
endmodule

module FullAdder (
  input  A,
  input  B,
  input  Cin,
  output Cout,
  output S
);

  wire and_1_out, and_2_out, xor_2_out;

  or or_1 (Cout, and_1_out, and_2_out);
  and and_1 (and_1_out, Cin, B);
  and and_2 (and_2_out, A, xor_2_out);
  xor xor_1 (S, A, xor_2_out);
  xor xor_2 (xor_2_out, B, Cin);

  // Notes on the sheet:
  //   Full Adder
endmodule
