// Logisim project Multiplication.circ as structural Verilog: 1 circuit, main circuit main
module main (
  input  in_1,
  input  in_2,
  input  in_3,
  input  in_4,
  input  in_5,
  input  in_6,
  input  in_7,
  input  in_8,
  output out_9,
  output out_10,
  output out_11,
  output out_12,
  output out_13,
  output out_14,
  output out_15,
  output out_16,
  output out_17,
  output out_18,
  output out_19,
  output out_20,
  output out_21,
  output out_22,
  output out_23,
  output out_24,
  output out_25,
  output out_26,
  output out_27,
  output out_28,
  output out_29,
  output out_30,
  output out_31,
  output out_32,
  output out_33,
  output out_34,
  output out_35,
  output out_36,
  output out_37,
  output out_38,
  output out_39,
  output out_40,
  output out_41,
  output out_42,
  output out_43,
  output out_44,
  output out_45,
  output out_46,
  output out_47,
  output out_48,
  output out_49,
  output out_50,
  output out_51,
  output out_52,
  output out_53,
  output out_54,
  output out_55,
  output out_56,
  output out_57,
  output out_58,
  output out_59,
  output out_60,
  output out_61,
  output out_62,
  output out_63,
  output out_64,
  output out_65,
  output out_66,
  output out_67,
  output out_68,
  output out_69,
  output out_70,
  output out_71,
  output out_72,
  output out_73,
  output out_74,
  output out_75,
  output out_76,
  output out_77,
  output out_78,
  output out_79,
  output out_80,
  output out_81,
  output out_82,
  output out_83,
  output out_84,
  output out_85,
  output out_86,
  output out_87,
  output out_88,
  output out_89,
  output out_90,
  output out_91,
  output out_92,
  output out_93,
  output out_94,
  output out_95,
  output out_96,
  output out_97,
  output out_98,
  output out_99,
  output out_100,
  output out_101,
  output out_102,
  output out_103,
  output out_104,
  output out_105,
  output out_106,
  output out_107,
  output out_108,
  output out_109,
  output out_110,
  output out_111,
  output out_112,
  output out_113,
  output out_114,
  output out_115,
  output out_116,
  output out_117,
  output out_118,
  output out_119,
  output out_120,
  output out_121,
  output out_122,
  output out_123,
  output out_124,
  output out_125,
  output out_126,
  output out_127,
  output out_128,
  output out_129,
  output out_130,
  output out_131,
  output out_132,
  output out_133,
  output out_134,
  output out_135,
  output out_136
);


  assign out_17 = in_1;
  assign out_18 = in_2;
  assign out_19 = in_3;
  assign out_20 = in_4;
  assign out_21 = in_5;
  assign out_22 = in_6;
  assign out_23 = in_7;
  assign out_24 = in_8;
  assign out_32 = in_1;
  assign out_33 = in_2;
  assign out_34 = in_3;
  assign out_35 = in_4;
  assign out_36 = in_5;
  assign out_37 = in_6;
  assign out_38 = in_7;
  assign out_39 = in_8;
  assign out_47 = in_1;
  assign out_48 = in_2;
  assign out_49 = in_3;
  assign out_50 = in_4;
  assign out_51 = in_5;
  assign out_52 = in_6;
  assign out_53 = in_7;
  assign out_54 = in_8;
  assign out_62 = in_1;
  assign out_63 = in_2;
  assign out_64 = in_3;
  assign out_65 = in_4;
  assign out_66 = in_5;
  assign out_67 = in_6;
  assign out_68 = in_7;
  assign out_69 = in_8;
  assign out_77 = in_1;
  assign out_78 = in_2;
  assign out_79 = in_3;
  assign out_80 = in_4;
  assign out_81 = in_5;
  assign out_82 = in_6;
  assign out_83 = in_7;
  assign out_84 = in_8;
  assign out_92 = in_1;
  assign out_93 = in_2;
  assign out_94 = in_3;
  assign out_95 = in_4;
  assign out_96 = in_5;
  assign out_97 = in_6;
  assign out_98 = in_7;
  assign out_99 = in_8;
  assign out_107 = in_1;
  assign out_108 = in_2;
  assign out_109 = in_3;
  assign out_110 = in_4;
  assign out_111 = in_5;
  assign out_112 = in_6;
  assign out_113 = in_7;
  assign out_114 = in_8;
  assign out_122 = in_1;
  assign out_123 = in_2;
  assign out_124 = in_3;
  assign out_125 = in_4;
  assign out_126 = in_5;
  assign out_127 = in_6;
  assign out_128 = in_7;
  assign out_129 = in_8;
endmodule
