// Logisim project MultiplierUsingAndGates.circ as structural Verilog: 1 circuit, main circuit main
module main (
  input  a8,
  input  a7,
  input  a6,
  input  a5,
  input  a4,
  input  a3,
  input  a2,
  input  a1,
  input  b1,
  input  b2,
  output out_11,
  output out_12,
  output out_13,
  output out_14,
  output out_15,
  output out_16,
  output out_17,
  output out_18,
  output out_19,
  output out_20,
  output out_21,
  output out_22,
  output out_23,
  output out_24,
  output out_25,
  output out_26
);

  and a8b2 (out_19, a8, b2);
  and a8b1 (out_11, a8, b1);
  and a7b2 (out_20, a7, b2);
  and a7b1 (out_12, a7, b1);
  and a6b2 (out_21, a6, b2);
  and a6b1 (out_13, a6, b1);
  and a5b2 (out_22, a5, b2);
  and a5b1 (out_14, a5, b1);
  and a4b2 (out_23, a4, b2);
  and a4b1 (out_15, a4, b1);
  and a3b2 (out_24, a3, b2);
  and a3b1 (out_16, a3, b1, b1);
  and a2_b2 (out_25, b1, b2);
  and a2_b1 (out_17, b1, a2);
  and a1_b2 (out_26, a1, b2);
  and a1_b1 (out_18, a1, b1);

  // Notes on the sheet:
  //   b2
  //   b1
endmodule
