// Logisim project MultiplierUsingAndGatesFinal_AB_4_28_2015.circ as structural Verilog: 3 circuits, main circuit main
module main (
  input  in_1,
  input  in_2,
  input  in_3,
  input  in_4,
  input  a5,
  input  a6,
  input  a7,
  input  a8,
  input  b1,
  input  b2,
  input  b3,
  input  b4,
  input  b5,
  input  b6,
  input  b7,
  input  b8,
  output out_17,
  output out_18,
  output out_19,
  output out_20,
  output out_21,
  output out_22,
  output out_23,
  output out_24,
  output out_25,
  output out_26,
  output out_27,
  output out_28,
  output out_29,
  output out_30,
  output out_31,
  output out_32
);

  wire a1_b2_out, a1_b3_out, a1_b4_out, a1_b5_out, a1_b6_out, a1_b7_out, a1_b8_out, a2_b1_out, a2_b2_out,
       a2_b3_out, a2_b4_out, a2_b5_out, a2_b6_out, a2_b7_out, a2_b8_out, a3b1_out, a3b2_out, a3b3_out,
       a3b4_out, a3b5_out, a3b6_out, a3b7_out, a3b8_out, a4b1_out, a4b2_out, a4b3_out, a4b4_out, a4b5_out,
       a4b6_out, a4b7_out, a4b8_out, a5b1_out, a5b2_out, a5b3_out, a5b4_out, a5b5_out, a5b6_out, a5b7_out,
       a5b8_out, a6b1_out, a6b2_out, a6b3_out, a6b4_out, a6b5_out, a6b6_out, a6b7_out, a6b8_out, a7b1_out,
       a7b2_out, a7b3_out, a7b4_out, a7b5_out, a7b6_out, a7b7_out, a7b8_out, a8b1_out, a8b2_out, a8b3_out,
       a8b4_out, a8b5_out, a8b6_out, a8b7_out, a8b8_out, fadder_2_cout, fadder_2_s, fadder_3_cout,
       fadder_4_cout, fadder_4_s, fadder_5_cout, fadder_5_s, fadder_6_cout, fadder_7_cout, fadder_7_s,
       fadder_8_cout, fadder_8_s, fadder_9_cout, fadder_9_s, fadder_10_cout, fadder_11_cout, fadder_11_s,
       fadder_12_cout, fadder_12_s, fadder_13_cout, fadder_13_s, fadder_14_cout, fadder_14_s, fadder_15_cout,
       fadder_16_cout, fadder_16_s, fadder_17_cout, fadder_17_s, fadder_18_cout, fadder_18_s, fadder_19_cout,
       fadder_19_s, fadder_20_cout, fadder_20_s, fadder_21_cout, fadder_21_s, fadder_22_cout, fadder_23_cout,
       fadder_23_s, fadder_24_cout, fadder_24_s, fadder_25_cout, fadder_25_s, fadder_26_cout, fadder_26_s,
       fadder_27_cout, fadder_27_s, fadder_28_cout, fadder_28_s, fadder_29_cout, fadder_30_cout, fadder_30_s,
       fadder_31_cout, fadder_31_s, fadder_32_cout, fadder_32_s, fadder_33_cout, fadder_33_s, fadder_34_cout,
       fadder_34_s, fadder_35_cout, fadder_36_cout, fadder_36_s, fadder_37_cout, fadder_37_s, fadder_38_cout,
       fadder_38_s, fadder_39_cout, fadder_39_s, fadder_40_cout, fadder_40_s, fadder_41_cout, fadder_42_cout,
       fadder_42_s, fadder_43_cout, fadder_43_s, fadder_44_cout, fadder_44_s, fadder_45_cout, fadder_45_s,
       fadder_46_cout, fadder_46_s, fadder_47_cout, fadder_47_s, fadder_48_cout, fadder_48_s, fadder_49_cout,
       fadder_50_cout, fadder_51_cout, fadder_51_s, fadder_52_cout, fadder_52_s, fadder_53_cout,
       fadder_54_cout, fadder_54_s, fadder_55_cout, fadder_56_cout, not_1_out, not_2_out, not_3_out,
       not_4_out, not_5_out, not_6_out, not_7_out, not_8_out;

  and a8b8 (a8b8_out, a8, b8);
  LED led_1 (.in(out_17));
  and a8b7 (a8b7_out, a8, b7);
  LED led_2 (.in(fadder_2_cout));
  FAdder fadder_1 (.Cout(out_17), .Cin(fadder_3_cout), .A(fadder_2_cout), .B(a8b8_out), .S(out_18));
  LED led_3 (.in(out_18));
  LED led_4 (.in(fadder_4_cout));
  FAdder fadder_2 (.Cout(fadder_2_cout), .Cin(fadder_5_cout), .A(fadder_4_cout), .B(a8b7_out), .S(fadder_2_s));
  LED led_5 (.in(fadder_2_s));
  and a7b8 (a7b8_out, a7, b8);
  FAdder fadder_3 (.Cout(fadder_3_cout), .Cin(fadder_6_cout), .A(fadder_2_s), .B(a7b8_out), .S(out_19));
  LED led_6 (.in(out_19));
  and a8b5 (a8b5_out, a8, b5);
  LED led_7 (.in(fadder_7_cout));
  and a8b6 (a8b6_out, a8, b6);
  FAdder fadder_4 (.Cout(fadder_4_cout), .Cin(fadder_8_cout), .A(fadder_7_cout), .B(a8b6_out), .S(fadder_4_s));
  LED led_8 (.in(fadder_4_s));
  and a7b7 (a7b7_out, a7, b7);
  FAdder fadder_5 (.Cout(fadder_5_cout), .Cin(fadder_9_cout), .A(fadder_4_s), .B(a7b7_out), .S(fadder_5_s));
  LED led_9 (.in(fadder_5_s));
  and a6b8 (a6b8_out, a6, b8);
  FAdder fadder_6 (.Cout(fadder_6_cout), .Cin(fadder_10_cout), .A(fadder_5_s), .B(a6b8_out), .S(out_20));
  LED led_10 (.in(out_20));
  and a8b4 (a8b4_out, a8, b4);
  LED led_11 (.in(fadder_11_cout));
  FAdder fadder_7 (.Cout(fadder_7_cout), .Cin(fadder_12_cout), .A(fadder_11_cout), .B(a8b5_out), .S(fadder_7_s));
  LED led_12 (.in(fadder_7_s));
  and a7b6 (a7b6_out, a7, b6);
  FAdder fadder_8 (.Cout(fadder_8_cout), .Cin(fadder_13_cout), .A(fadder_7_s), .B(a7b6_out), .S(fadder_8_s));
  LED led_13 (.in(fadder_8_s));
  and a6b7 (a6b7_out, a6, b7);
  FAdder fadder_9 (.Cout(fadder_9_cout), .Cin(fadder_14_cout), .A(fadder_8_s), .B(a6b7_out), .S(fadder_9_s));
  LED led_14 (.in(fadder_9_s));
  and a5b8 (a5b8_out, a5, b8);
  FAdder fadder_10 (.Cout(fadder_10_cout), .Cin(fadder_15_cout), .A(fadder_9_s), .B(a5b8_out), .S(out_21));
  LED led_15 (.in(out_21));
  not not_1 (not_1_out, 1'b1);
  LED led_16 (.in(fadder_16_cout));
  LED led_17 (.in(fadder_16_cout));
  LED led_18 (.in(fadder_17_cout));
  FAdder fadder_11 (.Cout(fadder_11_cout), .Cin(fadder_18_cout), .A(fadder_17_cout), .B(a8b4_out), .S(fadder_11_s));
  LED led_19 (.in(fadder_11_s));
  and a7b5 (a7b5_out, a7, b5);
  FAdder fadder_12 (.Cout(fadder_12_cout), .Cin(fadder_19_cout), .A(fadder_11_s), .B(a7b5_out), .S(fadder_12_s));
  LED led_20 (.in(fadder_12_s));
  and a6b6 (a6b6_out, a6, b6);
  FAdder fadder_13 (.Cout(fadder_13_cout), .Cin(fadder_20_cout), .A(fadder_12_s), .B(a6b6_out), .S(fadder_13_s));
  LED led_21 (.in(fadder_13_s));
  and a5b7 (a5b7_out, a5, b7);
  FAdder fadder_14 (.Cout(fadder_14_cout), .Cin(fadder_21_cout), .A(fadder_13_s), .B(a5b7_out), .S(fadder_14_s));
  LED led_22 (.in(fadder_14_s));
  and a4b8 (a4b8_out, in_4, b8);
  FAdder fadder_15 (.Cout(fadder_15_cout), .Cin(fadder_22_cout), .A(fadder_14_s), .B(a4b8_out), .S(out_22));
  LED led_23 (.in(out_22));
  and a8b2 (a8b2_out, a8, b2);
  FAdder fadder_16 (.Cout(fadder_16_cout), .Cin(fadder_23_cout), .A(not_1_out), .B(a8b2_out), .S(fadder_16_s));
  LED led_24 (.in(fadder_16_cout));
  LED led_25 (.in(fadder_16_s));
  and a8b3 (a8b3_out, a8, b3);
  FAdder fadder_17 (.Cout(fadder_17_cout), .Cin(fadder_24_cout), .A(fadder_16_cout), .B(a8b3_out), .S(fadder_17_s));
  LED led_26 (.in(fadder_17_s));
  and a7b4 (a7b4_out, a7, b4);
  FAdder fadder_18 (.Cout(fadder_18_cout), .Cin(fadder_25_cout), .A(fadder_17_s), .B(a7b4_out), .S(fadder_18_s));
  LED led_27 (.in(fadder_18_s));
  and a6b5 (a6b5_out, a6, b5);
  FAdder fadder_19 (.Cout(fadder_19_cout), .Cin(fadder_26_cout), .A(fadder_18_s), .B(a6b5_out), .S(fadder_19_s));
  LED led_28 (.in(fadder_19_s));
  and a5b6 (a5b6_out, a5, b6);
  FAdder fadder_20 (.Cout(fadder_20_cout), .Cin(fadder_27_cout), .A(fadder_19_s), .B(a5b6_out), .S(fadder_20_s));
  LED led_29 (.in(fadder_20_s));
  and a4b7 (a4b7_out, in_4, b7);
  FAdder fadder_21 (.Cout(fadder_21_cout), .Cin(fadder_28_cout), .A(fadder_20_s), .B(a4b7_out), .S(fadder_21_s));
  LED led_30 (.in(fadder_21_s));
  and a3b8 (a3b8_out, in_3, b8);
  FAdder fadder_22 (.Cout(fadder_22_cout), .Cin(fadder_29_cout), .A(fadder_21_s), .B(a3b8_out), .S(out_23));
  LED led_31 (.in(out_23));
  and a8b1 (a8b1_out, a8, b1);
  and a7b2 (a7b2_out, a7, b2);
  FAdder fadder_23 (.Cout(fadder_23_cout), .Cin(fadder_36_cout), .A(a8b1_out), .B(a7b2_out), .S(fadder_23_s));
  and a7b3 (a7b3_out, a7, b3);
  FAdder fadder_24 (.Cout(fadder_24_cout), .Cin(fadder_30_cout), .A(fadder_16_s), .B(a7b3_out), .S(fadder_24_s));
  LED led_32 (.in(fadder_24_s));
  and a6b4 (a6b4_out, a6, b4);
  FAdder fadder_25 (.Cout(fadder_25_cout), .Cin(fadder_31_cout), .A(fadder_24_s), .B(a6b4_out), .S(fadder_25_s));
  LED led_33 (.in(fadder_25_s));
  and a5b5 (a5b5_out, a5, b5);
  FAdder fadder_26 (.Cout(fadder_26_cout), .Cin(fadder_32_cout), .A(fadder_25_s), .B(a5b5_out), .S(fadder_26_s));
  LED led_34 (.in(fadder_26_s));
  and a4b6 (a4b6_out, in_4, b6);
  FAdder fadder_27 (.Cout(fadder_27_cout), .Cin(fadder_33_cout), .A(fadder_26_s), .B(a4b6_out), .S(fadder_27_s));
  LED led_35 (.in(fadder_27_s));
  and a3b7 (a3b7_out, in_3, b7);
  FAdder fadder_28 (.Cout(fadder_28_cout), .Cin(fadder_34_cout), .A(fadder_27_s), .B(a3b7_out), .S(fadder_28_s));
  LED led_36 (.in(fadder_28_s));
  and a2_b8 (a2_b8_out, in_2, b8);
  FAdder fadder_29 (.Cout(fadder_29_cout), .Cin(fadder_35_cout), .A(fadder_28_s), .B(a2_b8_out), .S(out_32));
  and a7b1 (a7b1_out, a7, b1);
  LED led_37 (.in(fadder_23_s));
  and a6b3 (a6b3_out, a6, b3);
  FAdder fadder_30 (.Cout(fadder_30_cout), .Cin(fadder_37_cout), .A(fadder_23_s), .B(a6b3_out), .S(fadder_30_s));
  LED led_38 (.in(fadder_30_s));
  and a5b4 (a5b4_out, a5, b4);
  FAdder fadder_31 (.Cout(fadder_31_cout), .Cin(fadder_38_cout), .A(fadder_30_s), .B(a5b4_out), .S(fadder_31_s));
  LED led_39 (.in(fadder_31_s));
  and a4b5 (a4b5_out, in_4, b5);
  FAdder fadder_32 (.Cout(fadder_32_cout), .Cin(fadder_39_cout), .A(fadder_31_s), .B(a4b5_out), .S(fadder_32_s));
  LED led_40 (.in(fadder_32_s));
  and a3b6 (a3b6_out, in_3, b6);
  FAdder fadder_33 (.Cout(fadder_33_cout), .Cin(fadder_40_cout), .A(fadder_32_s), .B(a3b6_out), .S(fadder_33_s));
  LED led_41 (.in(fadder_33_s));
  and a2_b7 (a2_b7_out, in_2, b7);
  FAdder fadder_34 (.Cout(fadder_34_cout), .Cin(fadder_41_cout), .A(fadder_33_s), .B(a2_b7_out), .S(fadder_34_s));
  and a1_b8 (a1_b8_out, in_1, b8);
  FAdder fadder_35 (.Cout(fadder_35_cout), .Cin(not_2_out), .A(fadder_34_s), .B(a1_b8_out), .S(out_24));
  LED led_42 (.in(out_32));
  and a6b2 (a6b2_out, a6, b2);
  FAdder fadder_36 (.Cout(fadder_36_cout), .Cin(fadder_42_cout), .A(a7b1_out), .B(a6b2_out), .S(fadder_36_s));
  LED led_43 (.in(fadder_36_s));
  and a5b3 (a5b3_out, a5, b3);
  FAdder fadder_37 (.Cout(fadder_37_cout), .Cin(fadder_43_cout), .A(fadder_36_s), .B(a5b3_out), .S(fadder_37_s));
  LED led_44 (.in(fadder_37_s));
  and a4b4 (a4b4_out, in_4, b4);
  FAdder fadder_38 (.Cout(fadder_38_cout), .Cin(fadder_44_cout), .A(fadder_37_s), .B(a4b4_out), .S(fadder_38_s));
  LED led_45 (.in(fadder_38_s));
  and a3b5 (a3b5_out, in_3, b5);
  FAdder fadder_39 (.Cout(fadder_39_cout), .Cin(fadder_45_cout), .A(fadder_38_s), .B(a3b5_out), .S(fadder_39_s));
  LED led_46 (.in(fadder_39_s));
  FAdder fadder_40 (.Cout(fadder_40_cout), .Cin(fadder_50_cout), .A(fadder_39_s), .B(a2_b6_out), .S(fadder_40_s));
  and a1_b7 (a1_b7_out, in_1, b7);
  FAdder fadder_41 (.Cout(fadder_41_cout), .Cin(not_3_out), .A(fadder_40_s), .B(a1_b7_out), .S(out_25));
  LED led_47 (.in(fadder_34_s));
  not not_2 (not_2_out, 1'b1);
  LED led_48 (.in(out_24));
  and a6b1 (a6b1_out, a6, b1);
  and a5b2 (a5b2_out, a5, b2);
  FAdder fadder_42 (.Cout(fadder_42_cout), .Cin(fadder_46_cout), .A(a6b1_out), .B(a5b2_out), .S(fadder_42_s));
  LED led_49 (.in(fadder_42_s));
  and a4b3 (a4b3_out, in_4, in_4, b3);
  FAdder fadder_43 (.Cout(fadder_43_cout), .Cin(fadder_47_cout), .A(fadder_42_s), .B(a4b3_out), .S(fadder_43_s));
  LED led_50 (.in(fadder_43_s));
  and a3b4 (a3b4_out, in_3, b4);
  FAdder fadder_44 (.Cout(fadder_44_cout), .Cin(fadder_48_cout), .A(fadder_43_s), .B(a3b4_out), .S(fadder_44_s));
  LED led_51 (.in(fadder_44_s));
  and a2_b5 (a2_b5_out, in_2, b5);
  FAdder fadder_45 (.Cout(fadder_45_cout), .Cin(fadder_49_cout), .A(fadder_44_s), .B(a2_b5_out), .S(fadder_45_s));
  and a2_b6 (a2_b6_out, in_2, b6);
  LED led_52 (.in(fadder_40_s));
  not not_3 (not_3_out, 1'b1);
  LED led_53 (.in(out_25));
  LED led_54 (.in(out_25));
  and a5b1 (a5b1_out, a5, b1);
  and a4b2 (a4b2_out, in_4, b2);
  FAdder fadder_46 (.Cout(fadder_46_cout), .Cin(fadder_51_cout), .A(a5b1_out), .B(a4b2_out), .S(fadder_46_s));
  LED led_55 (.in(fadder_46_s));
  and a3b3 (a3b3_out, in_3, b3);
  FAdder fadder_47 (.Cout(fadder_47_cout), .Cin(fadder_52_cout), .A(fadder_46_s), .B(a3b3_out), .S(fadder_47_s));
  LED led_56 (.in(fadder_47_s));
  and a2_b4 (a2_b4_out, in_2, in_2, in_2, b4);
  FAdder fadder_48 (.Cout(fadder_48_cout), .Cin(fadder_53_cout), .A(fadder_47_s), .B(a2_b4_out), .S(fadder_48_s));
  and a1_b5 (a1_b5_out, in_1, b5);
  FAdder fadder_49 (.Cout(fadder_49_cout), .Cin(not_5_out), .A(fadder_48_s), .B(a1_b5_out), .S(out_27));
  LED led_57 (.in(fadder_45_s));
  and a1_b6 (a1_b6_out, in_1, b6);
  not not_4 (not_4_out, 1'b1);
  FAdder fadder_50 (.Cout(fadder_50_cout), .Cin(not_4_out), .A(fadder_45_s), .B(a1_b6_out), .S(out_26));
  LED led_58 (.in(out_26));
  LED led_59 (.in(out_26));
  LED led_60 (.in(out_26));
  and a4b1 (a4b1_out, in_4, b1);
  and a3b2 (a3b2_out, in_3, b2);
  FAdder fadder_51 (.Cout(fadder_51_cout), .Cin(fadder_54_cout), .A(a4b1_out), .B(a3b2_out), .S(fadder_51_s));
  LED led_61 (.in(fadder_51_s));
  and a2_b3 (a2_b3_out, in_2, in_2, b3);
  FAdder fadder_52 (.Cout(fadder_52_cout), .Cin(fadder_56_cout), .A(fadder_51_s), .B(a2_b3_out), .S(fadder_52_s));
  and a1_b4 (a1_b4_out, in_1, b4);
  FAdder fadder_53 (.Cout(fadder_53_cout), .Cin(not_6_out), .A(fadder_52_s), .B(a1_b4_out), .S(out_28));
  LED led_62 (.in(fadder_48_s));
  not not_5 (not_5_out, 1'b1);
  LED led_63 (.in(out_27));
  LED led_64 (.in(out_27));
  LED led_65 (.in(out_27));
  LED led_66 (.in(out_27));
  and a3b1 (a3b1_out, in_3, b1, b1);
  and a2_b2 (a2_b2_out, in_2, b2);
  FAdder fadder_54 (.Cout(fadder_54_cout), .Cin(fadder_55_cout), .A(a3b1_out), .B(a2_b2_out), .S(fadder_54_s));
  LED led_67 (.in(fadder_54_s));
  LED led_68 (.in(fadder_52_s));
  not not_6 (not_6_out, 1'b1);
  LED led_69 (.in(out_28));
  LED led_70 (.in(out_28));
  LED led_71 (.in(out_28));
  LED led_72 (.in(out_28));
  LED led_73 (.in(out_28));
  and a2_b1 (a2_b1_out, b1, in_2);
  and a1_b2 (a1_b2_out, in_1, b2);
  FAdder fadder_55 (.Cout(fadder_55_cout), .Cin(not_8_out), .A(a2_b1_out), .B(a1_b2_out), .S(out_30));
  LED led_74 (.in(out_30));
  and a1_b3 (a1_b3_out, in_1, b3);
  not not_7 (not_7_out, 1'b1);
  FAdder fadder_56 (.Cout(fadder_56_cout), .Cin(not_7_out), .A(fadder_54_s), .B(a1_b3_out), .S(out_29));
  LED led_75 (.in(out_29));
  LED led_76 (.in(out_29));
  LED led_77 (.in(out_29));
  LED led_78 (.in(out_29));
  LED led_79 (.in(out_29));
  LED led_80 (.in(out_29));
  and a1_b1 (out_31, in_1, b1);
  not not_8 (not_8_out, 1'b1);
  LED led_81 (.in(out_31));
  LED led_82 (.in(out_30));
  LED led_83 (.in(out_31));
  LED led_84 (.in(out_31));
  LED led_85 (.in(out_30));
  LED led_86 (.in(out_31));
  LED led_87 (.in(out_30));
  LED led_88 (.in(out_30));
  LED led_89 (.in(out_31));
  LED led_90 (.in(out_31));
  LED led_91 (.in(out_30));
  LED led_92 (.in(out_31));
  LED led_93 (.in(out_30));
  LED led_94 (.in(out_31));
  LED led_95 (.in(out_30));

  // Notes on the sheet:
  //   b2
  //   e
  //   b1
  //   a4
  //   a3
  //   a2
  //   a1
endmodule

module FAdder (
  input  A,
  input  B,
  input  Cin,
  output Cout,
  output S
);

  wire and_1_out, and_2_out, xor_2_out;

  or or_1 (Cout, and_1_out, and_2_out);
  and and_1 (and_1_out, Cin, B);
  and and_2 (and_2_out, A, xor_2_out);
  xor xor_1 (S, A, xor_2_out);
  xor xor_2 (xor_2_out, B, Cin);

  // Notes on the sheet:
  //   Full Adder
endmodule

module Division (
  input  in_1,
  input  in_2,
  input  in_3,
  input  in_4,
  input  in_5,
  input  in_6,
  input  in_7,
  input  in_8,
  input  in_9,
  input  in_10,
  input  in_11,
  input  in_12,
  input  in_13,
  input  in_14,
  input  in_15,
  input  in_16,
  input  in_17,
  input  in_18,
  input  in_19,
  input  in_20,
  input  in_21,
  input  in_22,
  input  in_23,
  input  in_24,
  input  in_25,
  input  in_26,
  input  in_27,
  input  in_28,
  input  in_29,
  input  in_30,
  input  in_31,
  input  in_32
);

  wire main_1_out_17, main_1_out_18, main_1_out_19, main_1_out_20, main_1_out_21, main_1_out_22,
       main_1_out_23, main_1_out_24, main_1_out_25, main_1_out_26, main_1_out_27, main_1_out_28,
       main_1_out_29, main_1_out_30, main_1_out_31, main_1_out_32, main_2_out_17, main_2_out_18,
       main_2_out_19, main_2_out_20, main_2_out_21, main_2_out_22, main_2_out_23, main_2_out_24,
       main_2_out_25, main_2_out_26, main_2_out_27, main_2_out_28, main_2_out_29, main_2_out_30,
       main_2_out_31, main_2_out_32, not_1_out;

  not not_1 (not_1_out, 1'b1);
  main main_1 (
    .in_1(in_17), .in_2(in_19), .in_3(in_21), .in_4(in_23), .a5(in_25), .a6(in_27), .a7(in_29), .a8(in_31),
    .out_17(main_1_out_17), .out_18(main_1_out_18), .out_19(main_1_out_19), .out_20(main_1_out_20),
    .out_21(main_1_out_21), .out_22(main_1_out_22), .out_23(main_1_out_23), .out_32(main_1_out_32),
    .out_24(main_1_out_24), .out_25(main_1_out_25), .out_26(main_1_out_26), .out_27(main_1_out_27),
    .out_28(main_1_out_28), .out_29(main_1_out_29), .out_30(main_1_out_30), .out_31(main_1_out_31),
    .b1(in_18), .b2(in_20), .b3(in_22), .b4(in_24), .b5(in_26), .b6(in_28), .b7(in_30), .b8(in_32));
  main main_2 (
    .in_1(in_1), .in_2(in_3), .in_3(in_5), .in_4(in_7), .a5(in_9), .a6(in_11), .a7(in_13), .a8(in_15),
    .out_17(main_2_out_17), .out_18(main_2_out_18), .out_19(main_2_out_19), .out_20(main_2_out_20),
    .out_21(main_2_out_21), .out_22(main_2_out_22), .out_23(main_2_out_23), .out_32(main_2_out_32),
    .out_24(main_2_out_24), .out_25(main_2_out_25), .out_26(main_2_out_26), .out_27(main_2_out_27),
    .out_28(main_2_out_28), .out_29(main_2_out_29), .out_30(main_2_out_30), .out_31(main_2_out_31),
    .b1(in_2), .b2(in_4), .b3(in_6), .b4(in_8), .b5(in_10), .b6(in_12), .b7(in_14), .b8(in_16));
endmodule
