// Logisim project MultiplierUsingAndGates_3.circ as structural Verilog: 2 circuits, main circuit main
module main (
  input  a8,
  input  a7,
  input  a6,
  input  a5,
  input  a4,
  input  a3,
  input  a2,
  input  a1,
  input  b1,
  input  b2,
  input  e,
  input  in_12,
  input  b2_2,
  input  e_2,
  input  in_15,
  output out_16,
  output out_17,
  output out_18,
  output out_19,
  output out_20,
  output out_21,
  output out_22,
  output out_23,
  output out_24,
  output out_25,
  output out_26,
  output out_27,
  output out_28,
  output out_29,
  output out_30,
  output out_31,
  output out_32,
  output out_33,
  output out_34,
  output out_35,
  output out_36,
  output out_37,
  output out_38,
  output out_39,
  output out_40,
  output out_41,
  output out_42,
  output out_43,
  output out_44,
  output out_45,
  output out_46,
  output out_47,
  output out_48,
  output out_49,
  output out_50,
  output out_51,
  output out_52,
  output out_53,
  output out_54,
  output out_55,
  output out_56,
  output out_57,
  output out_58,
  output out_59,
  output out_60
);

  wire fadder_4_cout, fadder_5_cout, fadder_6_cout, fadder_7_cout, fadder_8_cout, fadder_9_cout,
       fadder_10_cout, fadder_11_cout, fadder_12_cout, fadder_13_cout, fadder_14_cout, fadder_15_cout,
       fadder_16_cout;

  and a8b2 (out_24, a8, b2);
  FAdder fadder_1 (.Cout(out_32), .Cin(out_33), .A(e), .B(out_24), .S(out_33));
  LED led_1 (.in(out_32));
  and a8b3 (out_42, a8, b2_2);
  FAdder fadder_2 (.Cout(out_55), .Cin(fadder_4_cout), .A(e_2), .B(out_42), .S(out_56));
  and a8b1 (out_16, a8, b1);
  and a7b2 (out_25, a7, b2);
  FAdder fadder_3 (.Cout(out_33), .Cin(fadder_6_cout), .A(out_16), .B(out_25), .S(out_34));
  LED led_2 (.in(out_33));
  and a7b3 (out_43, out_33, b2_2);
  FAdder fadder_4 (.Cout(fadder_4_cout), .Cin(fadder_5_cout), .A(out_33), .B(out_43), .S(out_57));
  and a7b1 (out_17, a7, b1);
  LED led_3 (.in(out_34));
  and a6b3 (out_44, a6, b2_2);
  FAdder fadder_5 (.Cout(fadder_5_cout), .Cin(fadder_7_cout), .A(out_34), .B(out_44), .S(out_58));
  and a6b2 (out_26, a6, b2);
  FAdder fadder_6 (.Cout(fadder_6_cout), .Cin(fadder_8_cout), .A(out_17), .B(out_26), .S(out_35));
  LED led_4 (.in(out_35));
  and a5b3 (out_45, a5, b2_2);
  FAdder fadder_7 (.Cout(fadder_7_cout), .Cin(fadder_9_cout), .A(out_35), .B(out_45), .S(out_59));
  and a6b1 (out_18, a6, b1);
  and a5b2 (out_27, a5, b2);
  FAdder fadder_8 (.Cout(fadder_8_cout), .Cin(fadder_10_cout), .A(out_18), .B(out_27), .S(out_36));
  LED led_5 (.in(out_36));
  and a4b3 (out_46, a4, a4, b2_2);
  FAdder fadder_9 (.Cout(fadder_9_cout), .Cin(fadder_11_cout), .A(out_36), .B(out_46), .S(out_60));
  and a5b1 (out_19, a5, b1);
  and a4b2 (out_28, a4, b2);
  FAdder fadder_10 (.Cout(fadder_10_cout), .Cin(fadder_12_cout), .A(out_19), .B(out_28), .S(out_37));
  LED led_6 (.in(out_37));
  and a3b3 (out_47, a3, b2_2);
  FAdder fadder_11 (.Cout(fadder_11_cout), .Cin(fadder_13_cout), .A(out_37), .B(out_47), .S(out_50));
  and a4b1 (out_20, a4, b1);
  and a3b2 (out_29, a3, b2);
  FAdder fadder_12 (.Cout(fadder_12_cout), .Cin(fadder_14_cout), .A(out_20), .B(out_29), .S(out_38));
  LED led_7 (.in(out_38));
  and a2_b3 (out_48, b1, b1, b2_2);
  FAdder fadder_13 (.Cout(fadder_13_cout), .Cin(fadder_16_cout), .A(out_38), .B(out_48), .S(out_51));
  and a3b1 (out_21, a3, b1, b1);
  and a2_b2 (out_30, b1, b2);
  FAdder fadder_14 (.Cout(fadder_14_cout), .Cin(fadder_15_cout), .A(out_21), .B(out_30), .S(out_39));
  LED led_8 (.in(out_39));
  and a2_b1 (out_22, b1, a2);
  and a1_b2 (out_31, a1, b2);
  FAdder fadder_15 (.Cout(fadder_15_cout), .Cin(in_12), .A(out_22), .B(out_31), .S(out_40));
  LED led_9 (.in(out_40));
  and a1_b3 (out_49, a1, b2_2);
  FAdder fadder_16 (.Cout(fadder_16_cout), .Cin(in_15), .A(out_39), .B(out_49), .S(out_52));
  and a1_b1 (out_23, a1, b1);
  LED led_10 (.in(out_23));
  LED led_11 (.in(out_23));
  LED led_12 (.in(out_40));
  LED led_13 (.in(out_23));

  assign out_41 = out_23;
  assign out_53 = out_40;
  assign out_54 = out_23;

  // Notes on the sheet:
  //   b2
  //   b1
endmodule

module FAdder (
  input  A,
  input  B,
  input  Cin,
  output Cout,
  output S
);

  wire and_1_out, and_2_out, xor_2_out;

  or or_1 (Cout, and_1_out, and_2_out);
  and and_1 (and_1_out, Cin, B);
  and and_2 (and_2_out, A, xor_2_out);
  xor xor_1 (S, A, xor_2_out);
  xor xor_2 (xor_2_out, B, Cin);

  // Notes on the sheet:
  //   Full Adder
endmodule
