// Logisim project MultiplierUsingAndGates_5.circ as structural Verilog: 2 circuits, main circuit main
module main (
  input  a8,
  input  a7,
  input  a6,
  input  a5,
  input  a4,
  input  a3,
  input  a2,
  input  a1,
  input  b1,
  input  b2,
  input  e,
  input  in_12,
  input  b3,
  input  in_14,
  input  b4,
  input  in_16,
  input  b5,
  input  in_18,
  output out_19,
  output out_20,
  output out_21,
  output out_22,
  output out_23,
  output out_24,
  output out_25,
  output out_26,
  output out_27,
  output out_28,
  output out_29,
  output out_30,
  output out_31,
  output out_32,
  output out_33,
  output out_34,
  output out_35,
  output out_36,
  output out_37,
  output out_38,
  output out_39,
  output out_40,
  output out_41,
  output out_42,
  output out_43,
  output out_44,
  output out_45,
  output out_46,
  output out_47,
  output out_48,
  output out_49,
  output out_50,
  output out_51,
  output out_52,
  output out_53,
  output out_54,
  output out_55,
  output out_56,
  output out_57,
  output out_58,
  output out_59,
  output out_60,
  output out_61,
  output out_62,
  output out_63,
  output out_64,
  output out_65,
  output out_66,
  output out_67,
  output out_68,
  output out_69,
  output out_70,
  output out_71,
  output out_72,
  output out_73,
  output out_74,
  output out_75,
  output out_76,
  output out_77,
  output out_78,
  output out_79,
  output out_80,
  output out_81,
  output out_82,
  output out_83,
  output out_84,
  output out_85,
  output out_86,
  output out_87,
  output out_88,
  output out_89,
  output out_90,
  output out_91,
  output out_92,
  output out_93,
  output out_94,
  output out_95,
  output out_96,
  output out_97,
  output out_98,
  output out_99,
  output out_100,
  output out_101,
  output out_102,
  output out_103,
  output out_104,
  output out_105
);

  wire fadder_3_cout, fadder_6_cout, fadder_7_cout, fadder_8_cout, fadder_9_cout, fadder_10_cout,
       fadder_11_cout, fadder_12_cout, fadder_13_cout, fadder_14_cout, fadder_15_cout, fadder_16_cout,
       fadder_17_cout, fadder_18_cout, fadder_19_cout, fadder_20_cout, fadder_21_cout, fadder_22_cout,
       fadder_23_cout, fadder_24_cout, fadder_25_cout, fadder_26_cout, fadder_27_cout, fadder_28_cout,
       fadder_29_cout, fadder_30_cout, fadder_31_cout, fadder_32_cout;

  and a8b5 (out_85, a8, b5);
  LED led_1 (.in(out_93));
  and a8b4 (out_65, a8, b4);
  LED led_2 (.in(out_73));
  FAdder fadder_1 (.Cout(out_93), .Cin(fadder_3_cout), .A(out_73), .B(out_85), .S(out_94));
  LED led_3 (.in(out_94));
  LED led_4 (.in(out_36));
  LED led_5 (.in(out_36));
  LED led_6 (.in(out_54));
  FAdder fadder_2 (.Cout(out_73), .Cin(fadder_6_cout), .A(out_54), .B(out_65), .S(out_74));
  LED led_7 (.in(out_74));
  and a7b5 (out_86, a7, b5);
  FAdder fadder_3 (.Cout(fadder_3_cout), .Cin(fadder_7_cout), .A(out_74), .B(out_86), .S(out_95));
  LED led_8 (.in(out_95));
  and a8b2 (out_28, a8, b2);
  FAdder fadder_4 (.Cout(out_36), .Cin(fadder_8_cout), .A(e), .B(out_28), .S(out_45));
  LED led_9 (.in(out_36));
  LED led_10 (.in(out_45));
  and a8b3 (out_46, a8, b3);
  FAdder fadder_5 (.Cout(out_54), .Cin(fadder_9_cout), .A(out_36), .B(out_46), .S(out_55));
  LED led_11 (.in(out_55));
  and a7b4 (out_66, a7, b4);
  FAdder fadder_6 (.Cout(fadder_6_cout), .Cin(fadder_10_cout), .A(out_55), .B(out_66), .S(out_75));
  LED led_12 (.in(out_75));
  and a6b5 (out_87, a6, b5);
  FAdder fadder_7 (.Cout(fadder_7_cout), .Cin(fadder_11_cout), .A(out_75), .B(out_87), .S(out_96));
  LED led_13 (.in(out_96));
  and a8b1 (out_19, a8, b1);
  and a7b2 (out_29, a7, b2);
  FAdder fadder_8 (.Cout(fadder_8_cout), .Cin(fadder_15_cout), .A(out_19), .B(out_29), .S(out_37));
  and a7b3 (out_47, a7, b3);
  FAdder fadder_9 (.Cout(fadder_9_cout), .Cin(fadder_12_cout), .A(out_45), .B(out_47), .S(out_56));
  LED led_14 (.in(out_56));
  and a6b4 (out_67, a6, b4);
  FAdder fadder_10 (.Cout(fadder_10_cout), .Cin(fadder_13_cout), .A(out_56), .B(out_67), .S(out_76));
  LED led_15 (.in(out_76));
  and a5b5 (out_88, a5, b5);
  FAdder fadder_11 (.Cout(fadder_11_cout), .Cin(fadder_14_cout), .A(out_76), .B(out_88), .S(out_97));
  LED led_16 (.in(out_97));
  and a7b1 (out_20, a7, b1);
  LED led_17 (.in(out_37));
  and a6b3 (out_48, a6, b3);
  FAdder fadder_12 (.Cout(fadder_12_cout), .Cin(fadder_16_cout), .A(out_37), .B(out_48), .S(out_57));
  LED led_18 (.in(out_57));
  and a5b4 (out_68, a5, b4);
  FAdder fadder_13 (.Cout(fadder_13_cout), .Cin(fadder_17_cout), .A(out_57), .B(out_68), .S(out_77));
  LED led_19 (.in(out_77));
  and a4b5 (out_89, a4, b5);
  FAdder fadder_14 (.Cout(fadder_14_cout), .Cin(fadder_18_cout), .A(out_77), .B(out_89), .S(out_98));
  LED led_20 (.in(out_98));
  and a6b2 (out_30, a6, b2);
  FAdder fadder_15 (.Cout(fadder_15_cout), .Cin(fadder_19_cout), .A(out_20), .B(out_30), .S(out_38));
  LED led_21 (.in(out_38));
  and a5b3 (out_49, a5, b3);
  FAdder fadder_16 (.Cout(fadder_16_cout), .Cin(fadder_20_cout), .A(out_38), .B(out_49), .S(out_58));
  LED led_22 (.in(out_58));
  and a4b4 (out_69, a4, b4);
  FAdder fadder_17 (.Cout(fadder_17_cout), .Cin(fadder_21_cout), .A(out_58), .B(out_69), .S(out_78));
  LED led_23 (.in(out_78));
  and a3b5 (out_90, a3, b5);
  FAdder fadder_18 (.Cout(fadder_18_cout), .Cin(fadder_22_cout), .A(out_78), .B(out_90), .S(out_99));
  LED led_24 (.in(out_99));
  and a6b1 (out_21, a6, b1);
  and a5b2 (out_31, a5, b2);
  FAdder fadder_19 (.Cout(fadder_19_cout), .Cin(fadder_23_cout), .A(out_21), .B(out_31), .S(out_39));
  LED led_25 (.in(out_39));
  and a4b3 (out_50, a4, a4, b3);
  FAdder fadder_20 (.Cout(fadder_20_cout), .Cin(fadder_24_cout), .A(out_39), .B(out_50), .S(out_59));
  LED led_26 (.in(out_59));
  and a3b4 (out_70, a3, b4);
  FAdder fadder_21 (.Cout(fadder_21_cout), .Cin(fadder_25_cout), .A(out_59), .B(out_70), .S(out_79));
  LED led_27 (.in(out_79));
  and a2_b5 (out_91, a2, a2, a2, b5);
  FAdder fadder_22 (.Cout(fadder_22_cout), .Cin(fadder_26_cout), .A(out_79), .B(out_91), .S(out_100));
  and a5b1 (out_22, a5, b1);
  and a4b2 (out_32, a4, b2);
  FAdder fadder_23 (.Cout(fadder_23_cout), .Cin(fadder_27_cout), .A(out_22), .B(out_32), .S(out_40));
  LED led_28 (.in(out_40));
  and a3b3 (out_51, a3, b3);
  FAdder fadder_24 (.Cout(fadder_24_cout), .Cin(fadder_28_cout), .A(out_40), .B(out_51), .S(out_60));
  LED led_29 (.in(out_60));
  and a2_b4 (out_71, a2, a2, a2, b4);
  FAdder fadder_25 (.Cout(fadder_25_cout), .Cin(fadder_29_cout), .A(out_60), .B(out_71), .S(out_80));
  and a1_b5 (out_92, a1, b5);
  FAdder fadder_26 (.Cout(fadder_26_cout), .Cin(in_18), .A(out_80), .B(out_92), .S(out_101));
  LED led_30 (.in(out_100));
  and a4b1 (out_23, a4, b1);
  and a3b2 (out_33, a3, b2);
  FAdder fadder_27 (.Cout(fadder_27_cout), .Cin(fadder_30_cout), .A(out_23), .B(out_33), .S(out_41));
  LED led_31 (.in(out_41));
  and a2_b3 (out_52, a2, a2, b3);
  FAdder fadder_28 (.Cout(fadder_28_cout), .Cin(fadder_32_cout), .A(out_41), .B(out_52), .S(out_61));
  and a1_b4 (out_72, a1, b4);
  FAdder fadder_29 (.Cout(fadder_29_cout), .Cin(in_16), .A(out_61), .B(out_72), .S(out_81));
  LED led_32 (.in(out_80));
  LED led_33 (.in(out_101));
  and a3b1 (out_24, a3, b1, b1);
  and a2_b2 (out_34, a2, b2);
  FAdder fadder_30 (.Cout(fadder_30_cout), .Cin(fadder_31_cout), .A(out_24), .B(out_34), .S(out_42));
  LED led_34 (.in(out_42));
  LED led_35 (.in(out_61));
  LED led_36 (.in(out_81));
  LED led_37 (.in(out_81));
  and a2_b1 (out_25, b1, a2);
  and a1_b2 (out_35, a1, b2);
  FAdder fadder_31 (.Cout(fadder_31_cout), .Cin(in_12), .A(out_25), .B(out_35), .S(out_43));
  LED led_38 (.in(out_43));
  and a1_b3 (out_53, a1, b3);
  FAdder fadder_32 (.Cout(fadder_32_cout), .Cin(in_14), .A(out_42), .B(out_53), .S(out_62));
  LED led_39 (.in(out_62));
  LED led_40 (.in(out_62));
  LED led_41 (.in(out_62));
  and a1_b1 (out_26, a1, b1);
  LED led_42 (.in(out_26));
  LED led_43 (.in(out_43));
  LED led_44 (.in(out_26));
  LED led_45 (.in(out_26));
  LED led_46 (.in(out_43));
  LED led_47 (.in(out_43));
  LED led_48 (.in(out_26));
  LED led_49 (.in(out_43));
  LED led_50 (.in(out_26));

  assign out_27 = out_19;
  assign out_44 = out_26;
  assign out_63 = out_43;
  assign out_64 = out_26;
  assign out_82 = out_62;
  assign out_83 = out_43;
  assign out_84 = out_26;
  assign out_102 = out_81;
  assign out_103 = out_62;
  assign out_104 = out_43;
  assign out_105 = out_26;

  // Notes on the sheet:
  //   b2
  //   b1
endmodule

module FAdder (
  input  A,
  input  B,
  input  Cin,
  output Cout,
  output S
);

  wire and_1_out, and_2_out, xor_2_out;

  or or_1 (Cout, and_1_out, and_2_out);
  and and_1 (and_1_out, Cin, B);
  and and_2 (and_2_out, A, xor_2_out);
  xor xor_1 (S, A, xor_2_out);
  xor xor_2 (xor_2_out, B, Cin);

  // Notes on the sheet:
  //   Full Adder
endmodule
