// Logisim project MultiplierUsingAndGates_6.circ as structural Verilog: 2 circuits, main circuit main
module main (
  input  a8,
  input  a7,
  input  a6,
  input  a5,
  input  a4,
  input  a3,
  input  a2,
  input  a1,
  input  b1,
  input  b2,
  input  e,
  input  in_12,
  input  b3,
  input  in_14,
  input  b4,
  input  in_16,
  input  b5,
  input  in_18,
  input  b6,
  input  in_20,
  output out_21,
  output out_22,
  output out_23,
  output out_24,
  output out_25,
  output out_26,
  output out_27,
  output out_28,
  output out_29,
  output out_30,
  output out_31,
  output out_32,
  output out_33,
  output out_34,
  output out_35,
  output out_36,
  output out_37,
  output out_38,
  output out_39,
  output out_40,
  output out_41,
  output out_42,
  output out_43,
  output out_44,
  output out_45,
  output out_46,
  output out_47,
  output out_48,
  output out_49,
  output out_50,
  output out_51,
  output out_52,
  output out_53,
  output out_54,
  output out_55,
  output out_56,
  output out_57,
  output out_58,
  output out_59,
  output out_60,
  output out_61,
  output out_62,
  output out_63,
  output out_64,
  output out_65,
  output out_66,
  output out_67,
  output out_68,
  output out_69,
  output out_70,
  output out_71,
  output out_72,
  output out_73,
  output out_74,
  output out_75,
  output out_76,
  output out_77,
  output out_78,
  output out_79,
  output out_80,
  output out_81,
  output out_82,
  output out_83,
  output out_84,
  output out_85,
  output out_86,
  output out_87,
  output out_88,
  output out_89,
  output out_90,
  output out_91,
  output out_92,
  output out_93,
  output out_94,
  output out_95,
  output out_96,
  output out_97,
  output out_98,
  output out_99,
  output out_100,
  output out_101,
  output out_102,
  output out_103,
  output out_104,
  output out_105,
  output out_106,
  output out_107,
  output out_108,
  output out_109,
  output out_110,
  output out_111,
  output out_112,
  output out_113,
  output out_114,
  output out_115,
  output out_116,
  output out_117,
  output out_118,
  output out_119,
  output out_120,
  output out_121,
  output out_122,
  output out_123,
  output out_124,
  output out_125,
  output out_126,
  output out_127,
  output out_128,
  output out_129
);

  wire fadder_3_cout, fadder_5_cout, fadder_6_cout, fadder_9_cout, fadder_10_cout, fadder_11_cout,
       fadder_12_cout, fadder_13_cout, fadder_14_cout, fadder_15_cout, fadder_16_cout, fadder_17_cout,
       fadder_18_cout, fadder_19_cout, fadder_20_cout, fadder_21_cout, fadder_22_cout, fadder_23_cout,
       fadder_24_cout, fadder_25_cout, fadder_26_cout, fadder_27_cout, fadder_28_cout, fadder_29_cout,
       fadder_30_cout, fadder_31_cout, fadder_32_cout, fadder_33_cout, fadder_34_cout, fadder_35_cout,
       fadder_36_cout, fadder_37_cout, fadder_38_cout, fadder_39_cout, fadder_40_cout;

  LED led_1 (.in(out_116));
  and a8b5 (out_87, a8, b5);
  LED led_2 (.in(out_95));
  and a8b5_2 (out_108, a8, b6);
  FAdder fadder_1 (.Cout(out_116), .Cin(fadder_3_cout), .A(out_95), .B(out_108), .S(out_117));
  LED led_3 (.in(out_117));
  and a8b4 (out_67, a8, b4);
  LED led_4 (.in(out_75));
  FAdder fadder_2 (.Cout(out_95), .Cin(fadder_5_cout), .A(out_75), .B(out_87), .S(out_96));
  LED led_5 (.in(out_96));
  and a7b5 (out_109, a7, b6);
  FAdder fadder_3 (.Cout(fadder_3_cout), .Cin(fadder_6_cout), .A(out_96), .B(out_109), .S(out_118));
  LED led_6 (.in(out_118));
  LED led_7 (.in(out_38));
  LED led_8 (.in(out_38));
  LED led_9 (.in(out_56));
  FAdder fadder_4 (.Cout(out_75), .Cin(fadder_9_cout), .A(out_56), .B(out_67), .S(out_76));
  LED led_10 (.in(out_76));
  and a7b5_2 (out_88, a7, b5);
  FAdder fadder_5 (.Cout(fadder_5_cout), .Cin(fadder_10_cout), .A(out_76), .B(out_88), .S(out_97));
  LED led_11 (.in(out_97));
  and a6b5 (out_110, a6, b6);
  FAdder fadder_6 (.Cout(fadder_6_cout), .Cin(fadder_11_cout), .A(out_97), .B(out_110), .S(out_119));
  LED led_12 (.in(out_119));
  and a8b2 (out_30, a8, b2);
  FAdder fadder_7 (.Cout(out_38), .Cin(fadder_12_cout), .A(e), .B(out_30), .S(out_47));
  LED led_13 (.in(out_38));
  LED led_14 (.in(out_47));
  and a8b3 (out_48, a8, b3);
  FAdder fadder_8 (.Cout(out_56), .Cin(fadder_13_cout), .A(out_38), .B(out_48), .S(out_57));
  LED led_15 (.in(out_57));
  and a7b4 (out_68, a7, b4);
  FAdder fadder_9 (.Cout(fadder_9_cout), .Cin(fadder_14_cout), .A(out_57), .B(out_68), .S(out_77));
  LED led_16 (.in(out_77));
  and a6b5_2 (out_89, a6, b5);
  FAdder fadder_10 (.Cout(fadder_10_cout), .Cin(fadder_15_cout), .A(out_77), .B(out_89), .S(out_98));
  LED led_17 (.in(out_98));
  and a5b5 (out_111, a5, b6);
  FAdder fadder_11 (.Cout(fadder_11_cout), .Cin(fadder_16_cout), .A(out_98), .B(out_111), .S(out_120));
  LED led_18 (.in(out_120));
  and a8b1 (out_21, a8, b1);
  and a7b2 (out_31, a7, b2);
  FAdder fadder_12 (.Cout(fadder_12_cout), .Cin(fadder_21_cout), .A(out_21), .B(out_31), .S(out_39));
  and a7b3 (out_49, a7, b3);
  FAdder fadder_13 (.Cout(fadder_13_cout), .Cin(fadder_17_cout), .A(out_47), .B(out_49), .S(out_58));
  LED led_19 (.in(out_58));
  and a6b4 (out_69, a6, b4);
  FAdder fadder_14 (.Cout(fadder_14_cout), .Cin(fadder_18_cout), .A(out_58), .B(out_69), .S(out_78));
  LED led_20 (.in(out_78));
  and a5b5_2 (out_90, a5, b5);
  FAdder fadder_15 (.Cout(fadder_15_cout), .Cin(fadder_19_cout), .A(out_78), .B(out_90), .S(out_99));
  LED led_21 (.in(out_99));
  and a4b5 (out_112, a4, b6);
  FAdder fadder_16 (.Cout(fadder_16_cout), .Cin(fadder_20_cout), .A(out_99), .B(out_112), .S(out_121));
  LED led_22 (.in(out_121));
  and a7b1 (out_22, a7, b1);
  LED led_23 (.in(out_39));
  and a6b3 (out_50, a6, b3);
  FAdder fadder_17 (.Cout(fadder_17_cout), .Cin(fadder_22_cout), .A(out_39), .B(out_50), .S(out_59));
  LED led_24 (.in(out_59));
  and a5b4 (out_70, a5, b4);
  FAdder fadder_18 (.Cout(fadder_18_cout), .Cin(fadder_23_cout), .A(out_59), .B(out_70), .S(out_79));
  LED led_25 (.in(out_79));
  and a4b5_2 (out_91, a4, b5);
  FAdder fadder_19 (.Cout(fadder_19_cout), .Cin(fadder_24_cout), .A(out_79), .B(out_91), .S(out_100));
  LED led_26 (.in(out_100));
  and a3b5 (out_113, a3, b6);
  FAdder fadder_20 (.Cout(fadder_20_cout), .Cin(fadder_25_cout), .A(out_100), .B(out_113), .S(out_122));
  LED led_27 (.in(out_122));
  and a6b2 (out_32, a6, b2);
  FAdder fadder_21 (.Cout(fadder_21_cout), .Cin(fadder_26_cout), .A(out_22), .B(out_32), .S(out_40));
  LED led_28 (.in(out_40));
  and a5b3 (out_51, a5, b3);
  FAdder fadder_22 (.Cout(fadder_22_cout), .Cin(fadder_27_cout), .A(out_40), .B(out_51), .S(out_60));
  LED led_29 (.in(out_60));
  and a4b4 (out_71, a4, b4);
  FAdder fadder_23 (.Cout(fadder_23_cout), .Cin(fadder_28_cout), .A(out_60), .B(out_71), .S(out_80));
  LED led_30 (.in(out_80));
  and a3b5_2 (out_92, a3, b5);
  FAdder fadder_24 (.Cout(fadder_24_cout), .Cin(fadder_29_cout), .A(out_80), .B(out_92), .S(out_101));
  LED led_31 (.in(out_101));
  and a2_b5 (out_114, a2, b6);
  FAdder fadder_25 (.Cout(fadder_25_cout), .Cin(fadder_34_cout), .A(out_101), .B(out_114), .S(out_123));
  and a6b1 (out_23, a6, b1);
  and a5b2 (out_33, a5, b2);
  FAdder fadder_26 (.Cout(fadder_26_cout), .Cin(fadder_30_cout), .A(out_23), .B(out_33), .S(out_41));
  LED led_32 (.in(out_41));
  and a4b3 (out_52, a4, a4, b3);
  FAdder fadder_27 (.Cout(fadder_27_cout), .Cin(fadder_31_cout), .A(out_41), .B(out_52), .S(out_61));
  LED led_33 (.in(out_61));
  and a3b4 (out_72, a3, b4);
  FAdder fadder_28 (.Cout(fadder_28_cout), .Cin(fadder_32_cout), .A(out_61), .B(out_72), .S(out_81));
  LED led_34 (.in(out_81));
  and a2_b5_2 (out_93, a2, b5);
  FAdder fadder_29 (.Cout(fadder_29_cout), .Cin(fadder_33_cout), .A(out_81), .B(out_93), .S(out_102));
  LED led_35 (.in(out_123));
  and a5b1 (out_24, a5, b1);
  and a4b2 (out_34, a4, b2);
  FAdder fadder_30 (.Cout(fadder_30_cout), .Cin(fadder_35_cout), .A(out_24), .B(out_34), .S(out_42));
  LED led_36 (.in(out_42));
  and a3b3 (out_53, a3, b3);
  FAdder fadder_31 (.Cout(fadder_31_cout), .Cin(fadder_36_cout), .A(out_42), .B(out_53), .S(out_62));
  LED led_37 (.in(out_62));
  and a2_b4 (out_73, a2, a2, a2, b4);
  FAdder fadder_32 (.Cout(fadder_32_cout), .Cin(fadder_37_cout), .A(out_62), .B(out_73), .S(out_82));
  and a1_b5 (out_94, a1, b5);
  FAdder fadder_33 (.Cout(fadder_33_cout), .Cin(in_18), .A(out_82), .B(out_94), .S(out_103));
  LED led_38 (.in(out_102));
  and a1_b5_2 (out_115, a1, b6);
  FAdder fadder_34 (.Cout(fadder_34_cout), .Cin(in_20), .A(out_102), .B(out_115), .S(out_124));
  LED led_39 (.in(out_124));
  and a4b1 (out_25, a4, b1);
  and a3b2 (out_35, a3, b2);
  FAdder fadder_35 (.Cout(fadder_35_cout), .Cin(fadder_38_cout), .A(out_25), .B(out_35), .S(out_43));
  LED led_40 (.in(out_43));
  and a2_b3 (out_54, a2, a2, b3);
  FAdder fadder_36 (.Cout(fadder_36_cout), .Cin(fadder_40_cout), .A(out_43), .B(out_54), .S(out_63));
  and a1_b4 (out_74, a1, b4);
  FAdder fadder_37 (.Cout(fadder_37_cout), .Cin(in_16), .A(out_63), .B(out_74), .S(out_83));
  LED led_41 (.in(out_82));
  LED led_42 (.in(out_103));
  LED led_43 (.in(out_103));
  and a3b1 (out_26, a3, b1, b1);
  and a2_b2 (out_36, a2, b2);
  FAdder fadder_38 (.Cout(fadder_38_cout), .Cin(fadder_39_cout), .A(out_26), .B(out_36), .S(out_44));
  LED led_44 (.in(out_44));
  LED led_45 (.in(out_63));
  LED led_46 (.in(out_83));
  LED led_47 (.in(out_83));
  LED led_48 (.in(out_83));
  and a2_b1 (out_27, b1, a2);
  and a1_b2 (out_37, a1, b2);
  FAdder fadder_39 (.Cout(fadder_39_cout), .Cin(in_12), .A(out_27), .B(out_37), .S(out_45));
  LED led_49 (.in(out_45));
  and a1_b3 (out_55, a1, b3);
  FAdder fadder_40 (.Cout(fadder_40_cout), .Cin(in_14), .A(out_44), .B(out_55), .S(out_64));
  LED led_50 (.in(out_64));
  LED led_51 (.in(out_64));
  LED led_52 (.in(out_64));
  LED led_53 (.in(out_64));
  and a1_b1 (out_28, a1, b1);
  LED led_54 (.in(out_28));
  LED led_55 (.in(out_28));
  LED led_56 (.in(out_45));
  LED led_57 (.in(out_28));
  LED led_58 (.in(out_45));
  LED led_59 (.in(out_28));
  LED led_60 (.in(out_45));
  LED led_61 (.in(out_28));
  LED led_62 (.in(out_45));
  LED led_63 (.in(out_45));
  LED led_64 (.in(out_28));

  assign out_29 = out_21;
  assign out_46 = out_28;
  assign out_65 = out_45;
  assign out_66 = out_28;
  assign out_84 = out_64;
  assign out_85 = out_45;
  assign out_86 = out_28;
  assign out_104 = out_83;
  assign out_105 = out_64;
  assign out_106 = out_45;
  assign out_107 = out_28;
  assign out_125 = out_103;
  assign out_126 = out_83;
  assign out_127 = out_64;
  assign out_128 = out_45;
  assign out_129 = out_28;

  // Notes on the sheet:
  //   b2
  //   b1
endmodule

module FAdder (
  input  A,
  input  B,
  input  Cin,
  output Cout,
  output S
);

  wire and_1_out, and_2_out, xor_2_out;

  or or_1 (Cout, and_1_out, and_2_out);
  and and_1 (and_1_out, Cin, B);
  and and_2 (and_2_out, A, xor_2_out);
  xor xor_1 (S, A, xor_2_out);
  xor xor_2 (xor_2_out, B, Cin);

  // Notes on the sheet:
  //   Full Adder
endmodule
