// Logisim project MultiplierUsingAndGates_8.circ as structural Verilog: 2 circuits, main circuit main
module main (
  input  a8,
  input  a7,
  input  a6,
  input  a5,
  input  a4,
  input  a3,
  input  a2,
  input  a1,
  input  b1,
  input  b2,
  input  e,
  input  in_12,
  input  b3,
  input  in_14,
  input  b4,
  input  in_16,
  input  b5,
  input  in_18,
  input  b6,
  input  in_20,
  input  b7,
  input  in_22,
  input  b8,
  input  in_24,
  output out_25,
  output out_26,
  output out_27,
  output out_28,
  output out_29,
  output out_30,
  output out_31,
  output out_32,
  output out_33,
  output out_34,
  output out_35,
  output out_36,
  output out_37,
  output out_38,
  output out_39,
  output out_40,
  output out_41,
  output out_42,
  output out_43,
  output out_44,
  output out_45,
  output out_46,
  output out_47,
  output out_48,
  output out_49,
  output out_50,
  output out_51,
  output out_52,
  output out_53,
  output out_54,
  output out_55,
  output out_56,
  output out_57,
  output out_58,
  output out_59,
  output out_60,
  output out_61,
  output out_62,
  output out_63,
  output out_64,
  output out_65,
  output out_66,
  output out_67,
  output out_68,
  output out_69,
  output out_70,
  output out_71,
  output out_72,
  output out_73,
  output out_74,
  output out_75,
  output out_76,
  output out_77,
  output out_78,
  output out_79,
  output out_80,
  output out_81,
  output out_82,
  output out_83,
  output out_84,
  output out_85,
  output out_86,
  output out_87,
  output out_88,
  output out_89,
  output out_90,
  output out_91,
  output out_92,
  output out_93,
  output out_94,
  output out_95,
  output out_96,
  output out_97,
  output out_98,
  output out_99,
  output out_100,
  output out_101,
  output out_102,
  output out_103,
  output out_104,
  output out_105,
  output out_106,
  output out_107,
  output out_108,
  output out_109,
  output out_110,
  output out_111,
  output out_112,
  output out_113,
  output out_114,
  output out_115,
  output out_116,
  output out_117,
  output out_118,
  output out_119,
  output out_120,
  output out_121,
  output out_122,
  output out_123,
  output out_124,
  output out_125,
  output out_126,
  output out_127,
  output out_128,
  output out_129,
  output out_130,
  output out_131,
  output out_132,
  output out_133,
  output out_134,
  output out_135,
  output out_136,
  output out_137,
  output out_138,
  output out_139,
  output out_140,
  output out_141,
  output out_142,
  output out_143,
  output out_144,
  output out_145,
  output out_146,
  output out_147,
  output out_148,
  output out_149,
  output out_150,
  output out_151,
  output out_152,
  output out_153,
  output out_154,
  output out_155,
  output out_156,
  output out_157,
  output out_158,
  output out_159,
  output out_160,
  output out_161,
  output out_162,
  output out_163,
  output out_164,
  output out_165,
  output out_166,
  output out_167,
  output out_168,
  output out_169,
  output out_170,
  output out_171,
  output out_172,
  output out_173,
  output out_174,
  output out_175,
  output out_176,
  output out_177,
  output out_178,
  output out_179,
  output out_180
);

  wire fadder_3_cout, fadder_5_cout, fadder_6_cout, fadder_8_cout, fadder_9_cout, fadder_10_cout,
       fadder_12_cout, fadder_13_cout, fadder_14_cout, fadder_15_cout, fadder_18_cout, fadder_19_cout,
       fadder_20_cout, fadder_21_cout, fadder_22_cout, fadder_23_cout, fadder_24_cout, fadder_25_cout,
       fadder_26_cout, fadder_27_cout, fadder_28_cout, fadder_29_cout, fadder_30_cout, fadder_31_cout,
       fadder_32_cout, fadder_33_cout, fadder_34_cout, fadder_35_cout, fadder_36_cout, fadder_37_cout,
       fadder_38_cout, fadder_39_cout, fadder_40_cout, fadder_41_cout, fadder_42_cout, fadder_43_cout,
       fadder_44_cout, fadder_45_cout, fadder_46_cout, fadder_47_cout, fadder_48_cout, fadder_49_cout,
       fadder_50_cout, fadder_51_cout, fadder_52_cout, fadder_53_cout, fadder_54_cout, fadder_55_cout,
       fadder_56_cout;

  and a8b8 (out_157, a8, b8);
  LED led_1 (.in(out_165));
  and a8b7 (out_134, a8, b7);
  LED led_2 (.in(out_142));
  FAdder fadder_1 (.Cout(out_165), .Cin(fadder_3_cout), .A(out_142), .B(out_157), .S(out_166));
  LED led_3 (.in(out_166));
  LED led_4 (.in(out_120));
  FAdder fadder_2 (.Cout(out_142), .Cin(fadder_5_cout), .A(out_120), .B(out_134), .S(out_143));
  LED led_5 (.in(out_143));
  and a7b8 (out_158, a7, b8);
  FAdder fadder_3 (.Cout(fadder_3_cout), .Cin(fadder_6_cout), .A(out_143), .B(out_158), .S(out_167));
  LED led_6 (.in(out_167));
  and a8b5 (out_91, a8, b5);
  LED led_7 (.in(out_99));
  and a8b6 (out_112, a8, b6);
  FAdder fadder_4 (.Cout(out_120), .Cin(fadder_8_cout), .A(out_99), .B(out_112), .S(out_121));
  LED led_8 (.in(out_121));
  and a7b7 (out_135, a7, b7);
  FAdder fadder_5 (.Cout(fadder_5_cout), .Cin(fadder_9_cout), .A(out_121), .B(out_135), .S(out_144));
  LED led_9 (.in(out_144));
  and a6b8 (out_159, a6, b8);
  FAdder fadder_6 (.Cout(fadder_6_cout), .Cin(fadder_10_cout), .A(out_144), .B(out_159), .S(out_168));
  LED led_10 (.in(out_168));
  and a8b4 (out_71, a8, b4);
  LED led_11 (.in(out_79));
  FAdder fadder_7 (.Cout(out_99), .Cin(fadder_12_cout), .A(out_79), .B(out_91), .S(out_100));
  LED led_12 (.in(out_100));
  and a7b6 (out_113, a7, b6);
  FAdder fadder_8 (.Cout(fadder_8_cout), .Cin(fadder_13_cout), .A(out_100), .B(out_113), .S(out_122));
  LED led_13 (.in(out_122));
  and a6b7 (out_136, a6, b7);
  FAdder fadder_9 (.Cout(fadder_9_cout), .Cin(fadder_14_cout), .A(out_122), .B(out_136), .S(out_145));
  LED led_14 (.in(out_145));
  and a5b8 (out_160, a5, b8);
  FAdder fadder_10 (.Cout(fadder_10_cout), .Cin(fadder_15_cout), .A(out_145), .B(out_160), .S(out_169));
  LED led_15 (.in(out_169));
  LED led_16 (.in(out_42));
  LED led_17 (.in(out_42));
  LED led_18 (.in(out_60));
  FAdder fadder_11 (.Cout(out_79), .Cin(fadder_18_cout), .A(out_60), .B(out_71), .S(out_80));
  LED led_19 (.in(out_80));
  and a7b5 (out_92, a7, b5);
  FAdder fadder_12 (.Cout(fadder_12_cout), .Cin(fadder_19_cout), .A(out_80), .B(out_92), .S(out_101));
  LED led_20 (.in(out_101));
  and a6b6 (out_114, a6, b6);
  FAdder fadder_13 (.Cout(fadder_13_cout), .Cin(fadder_20_cout), .A(out_101), .B(out_114), .S(out_123));
  LED led_21 (.in(out_123));
  and a5b7 (out_137, a5, b7);
  FAdder fadder_14 (.Cout(fadder_14_cout), .Cin(fadder_21_cout), .A(out_123), .B(out_137), .S(out_146));
  LED led_22 (.in(out_146));
  and a4b8 (out_161, a4, b8);
  FAdder fadder_15 (.Cout(fadder_15_cout), .Cin(fadder_22_cout), .A(out_146), .B(out_161), .S(out_170));
  LED led_23 (.in(out_170));
  and a8b2 (out_34, a8, b2);
  FAdder fadder_16 (.Cout(out_42), .Cin(fadder_23_cout), .A(e), .B(out_34), .S(out_51));
  LED led_24 (.in(out_42));
  LED led_25 (.in(out_51));
  and a8b3 (out_52, a8, b3);
  FAdder fadder_17 (.Cout(out_60), .Cin(fadder_24_cout), .A(out_42), .B(out_52), .S(out_61));
  LED led_26 (.in(out_61));
  and a7b4 (out_72, a7, b4);
  FAdder fadder_18 (.Cout(fadder_18_cout), .Cin(fadder_25_cout), .A(out_61), .B(out_72), .S(out_81));
  LED led_27 (.in(out_81));
  and a6b5 (out_93, a6, b5);
  FAdder fadder_19 (.Cout(fadder_19_cout), .Cin(fadder_26_cout), .A(out_81), .B(out_93), .S(out_102));
  LED led_28 (.in(out_102));
  and a5b6 (out_115, a5, b6);
  FAdder fadder_20 (.Cout(fadder_20_cout), .Cin(fadder_27_cout), .A(out_102), .B(out_115), .S(out_124));
  LED led_29 (.in(out_124));
  and a4b7 (out_138, a4, b7);
  FAdder fadder_21 (.Cout(fadder_21_cout), .Cin(fadder_28_cout), .A(out_124), .B(out_138), .S(out_147));
  LED led_30 (.in(out_147));
  and a3b8 (out_162, a3, b8);
  FAdder fadder_22 (.Cout(fadder_22_cout), .Cin(fadder_29_cout), .A(out_147), .B(out_162), .S(out_171));
  LED led_31 (.in(out_171));
  and a8b1 (out_25, a8, b1);
  and a7b2 (out_35, a7, b2);
  FAdder fadder_23 (.Cout(fadder_23_cout), .Cin(fadder_36_cout), .A(out_25), .B(out_35), .S(out_43));
  and a7b3 (out_53, a7, b3);
  FAdder fadder_24 (.Cout(fadder_24_cout), .Cin(fadder_30_cout), .A(out_51), .B(out_53), .S(out_62));
  LED led_32 (.in(out_62));
  and a6b4 (out_73, a6, b4);
  FAdder fadder_25 (.Cout(fadder_25_cout), .Cin(fadder_31_cout), .A(out_62), .B(out_73), .S(out_82));
  LED led_33 (.in(out_82));
  and a5b5 (out_94, a5, b5);
  FAdder fadder_26 (.Cout(fadder_26_cout), .Cin(fadder_32_cout), .A(out_82), .B(out_94), .S(out_103));
  LED led_34 (.in(out_103));
  and a4b6 (out_116, a4, b6);
  FAdder fadder_27 (.Cout(fadder_27_cout), .Cin(fadder_33_cout), .A(out_103), .B(out_116), .S(out_125));
  LED led_35 (.in(out_125));
  and a3b7 (out_139, a3, b7);
  FAdder fadder_28 (.Cout(fadder_28_cout), .Cin(fadder_34_cout), .A(out_125), .B(out_139), .S(out_148));
  LED led_36 (.in(out_148));
  and a2_b8 (out_163, a2, b8);
  FAdder fadder_29 (.Cout(fadder_29_cout), .Cin(fadder_35_cout), .A(out_148), .B(out_163), .S(out_172));
  and a7b1 (out_26, a7, b1);
  LED led_37 (.in(out_43));
  and a6b3 (out_54, a6, b3);
  FAdder fadder_30 (.Cout(fadder_30_cout), .Cin(fadder_37_cout), .A(out_43), .B(out_54), .S(out_63));
  LED led_38 (.in(out_63));
  and a5b4 (out_74, a5, b4);
  FAdder fadder_31 (.Cout(fadder_31_cout), .Cin(fadder_38_cout), .A(out_63), .B(out_74), .S(out_83));
  LED led_39 (.in(out_83));
  and a4b5 (out_95, a4, b5);
  FAdder fadder_32 (.Cout(fadder_32_cout), .Cin(fadder_39_cout), .A(out_83), .B(out_95), .S(out_104));
  LED led_40 (.in(out_104));
  and a3b6 (out_117, a3, b6);
  FAdder fadder_33 (.Cout(fadder_33_cout), .Cin(fadder_40_cout), .A(out_104), .B(out_117), .S(out_126));
  LED led_41 (.in(out_126));
  and a2_b7 (out_140, a2, b7);
  FAdder fadder_34 (.Cout(fadder_34_cout), .Cin(fadder_41_cout), .A(out_126), .B(out_140), .S(out_149));
  and a1_b8 (out_164, a1, b8);
  FAdder fadder_35 (.Cout(fadder_35_cout), .Cin(in_24), .A(out_149), .B(out_164), .S(out_173));
  LED led_42 (.in(out_172));
  and a6b2 (out_36, a6, b2);
  FAdder fadder_36 (.Cout(fadder_36_cout), .Cin(fadder_42_cout), .A(out_26), .B(out_36), .S(out_44));
  LED led_43 (.in(out_44));
  and a5b3 (out_55, a5, b3);
  FAdder fadder_37 (.Cout(fadder_37_cout), .Cin(fadder_43_cout), .A(out_44), .B(out_55), .S(out_64));
  LED led_44 (.in(out_64));
  and a4b4 (out_75, a4, b4);
  FAdder fadder_38 (.Cout(fadder_38_cout), .Cin(fadder_44_cout), .A(out_64), .B(out_75), .S(out_84));
  LED led_45 (.in(out_84));
  and a3b5 (out_96, a3, b5);
  FAdder fadder_39 (.Cout(fadder_39_cout), .Cin(fadder_45_cout), .A(out_84), .B(out_96), .S(out_105));
  LED led_46 (.in(out_105));
  FAdder fadder_40 (.Cout(fadder_40_cout), .Cin(fadder_50_cout), .A(out_105), .B(out_118), .S(out_127));
  and a1_b7 (out_141, a1, b7);
  FAdder fadder_41 (.Cout(fadder_41_cout), .Cin(in_22), .A(out_127), .B(out_141), .S(out_150));
  LED led_47 (.in(out_149));
  LED led_48 (.in(out_173));
  and a6b1 (out_27, a6, b1);
  and a5b2 (out_37, a5, b2);
  FAdder fadder_42 (.Cout(fadder_42_cout), .Cin(fadder_46_cout), .A(out_27), .B(out_37), .S(out_45));
  LED led_49 (.in(out_45));
  and a4b3 (out_56, a4, a4, b3);
  FAdder fadder_43 (.Cout(fadder_43_cout), .Cin(fadder_47_cout), .A(out_45), .B(out_56), .S(out_65));
  LED led_50 (.in(out_65));
  and a3b4 (out_76, a3, b4);
  FAdder fadder_44 (.Cout(fadder_44_cout), .Cin(fadder_48_cout), .A(out_65), .B(out_76), .S(out_85));
  LED led_51 (.in(out_85));
  and a2_b5 (out_97, a2, b5);
  FAdder fadder_45 (.Cout(fadder_45_cout), .Cin(fadder_49_cout), .A(out_85), .B(out_97), .S(out_106));
  and a2_b6 (out_118, a2, b6);
  LED led_52 (.in(out_127));
  LED led_53 (.in(out_150));
  LED led_54 (.in(out_150));
  and a5b1 (out_28, a5, b1);
  and a4b2 (out_38, a4, b2);
  FAdder fadder_46 (.Cout(fadder_46_cout), .Cin(fadder_51_cout), .A(out_28), .B(out_38), .S(out_46));
  LED led_55 (.in(out_46));
  and a3b3 (out_57, a3, b3);
  FAdder fadder_47 (.Cout(fadder_47_cout), .Cin(fadder_52_cout), .A(out_46), .B(out_57), .S(out_66));
  LED led_56 (.in(out_66));
  and a2_b4 (out_77, a2, a2, a2, b4);
  FAdder fadder_48 (.Cout(fadder_48_cout), .Cin(fadder_53_cout), .A(out_66), .B(out_77), .S(out_86));
  and a1_b5 (out_98, a1, b5);
  FAdder fadder_49 (.Cout(fadder_49_cout), .Cin(in_18), .A(out_86), .B(out_98), .S(out_107));
  LED led_57 (.in(out_106));
  and a1_b6 (out_119, a1, b6);
  FAdder fadder_50 (.Cout(fadder_50_cout), .Cin(in_20), .A(out_106), .B(out_119), .S(out_128));
  LED led_58 (.in(out_128));
  LED led_59 (.in(out_128));
  LED led_60 (.in(out_128));
  and a4b1 (out_29, a4, b1);
  and a3b2 (out_39, a3, b2);
  FAdder fadder_51 (.Cout(fadder_51_cout), .Cin(fadder_54_cout), .A(out_29), .B(out_39), .S(out_47));
  LED led_61 (.in(out_47));
  and a2_b3 (out_58, a2, a2, b3);
  FAdder fadder_52 (.Cout(fadder_52_cout), .Cin(fadder_56_cout), .A(out_47), .B(out_58), .S(out_67));
  and a1_b4 (out_78, a1, b4);
  FAdder fadder_53 (.Cout(fadder_53_cout), .Cin(in_16), .A(out_67), .B(out_78), .S(out_87));
  LED led_62 (.in(out_86));
  LED led_63 (.in(out_107));
  LED led_64 (.in(out_107));
  LED led_65 (.in(out_107));
  LED led_66 (.in(out_107));
  and a3b1 (out_30, a3, b1, b1);
  and a2_b2 (out_40, a2, b2);
  FAdder fadder_54 (.Cout(fadder_54_cout), .Cin(fadder_55_cout), .A(out_30), .B(out_40), .S(out_48));
  LED led_67 (.in(out_48));
  LED led_68 (.in(out_67));
  LED led_69 (.in(out_87));
  LED led_70 (.in(out_87));
  LED led_71 (.in(out_87));
  LED led_72 (.in(out_87));
  LED led_73 (.in(out_87));
  and a2_b1 (out_31, b1, a2);
  and a1_b2 (out_41, a1, b2);
  FAdder fadder_55 (.Cout(fadder_55_cout), .Cin(in_12), .A(out_31), .B(out_41), .S(out_49));
  LED led_74 (.in(out_49));
  and a1_b3 (out_59, a1, b3);
  FAdder fadder_56 (.Cout(fadder_56_cout), .Cin(in_14), .A(out_48), .B(out_59), .S(out_68));
  LED led_75 (.in(out_68));
  LED led_76 (.in(out_68));
  LED led_77 (.in(out_68));
  LED led_78 (.in(out_68));
  LED led_79 (.in(out_68));
  LED led_80 (.in(out_68));
  and a1_b1 (out_32, a1, b1);
  LED led_81 (.in(out_32));
  LED led_82 (.in(out_49));
  LED led_83 (.in(out_32));
  LED led_84 (.in(out_32));
  LED led_85 (.in(out_49));
  LED led_86 (.in(out_32));
  LED led_87 (.in(out_49));
  LED led_88 (.in(out_32));
  LED led_89 (.in(out_49));
  LED led_90 (.in(out_49));
  LED led_91 (.in(out_32));
  LED led_92 (.in(out_32));
  LED led_93 (.in(out_49));
  LED led_94 (.in(out_49));
  LED led_95 (.in(out_32));

  assign out_33 = out_25;
  assign out_50 = out_32;
  assign out_69 = out_49;
  assign out_70 = out_32;
  assign out_88 = out_68;
  assign out_89 = out_49;
  assign out_90 = out_32;
  assign out_108 = out_87;
  assign out_109 = out_68;
  assign out_110 = out_49;
  assign out_111 = out_32;
  assign out_129 = out_107;
  assign out_130 = out_87;
  assign out_131 = out_68;
  assign out_132 = out_49;
  assign out_133 = out_32;
  assign out_151 = out_128;
  assign out_152 = out_107;
  assign out_153 = out_87;
  assign out_154 = out_68;
  assign out_155 = out_49;
  assign out_156 = out_32;
  assign out_174 = out_150;
  assign out_175 = out_128;
  assign out_176 = out_107;
  assign out_177 = out_87;
  assign out_178 = out_68;
  assign out_179 = out_49;
  assign out_180 = out_32;

  // Notes on the sheet:
  //   b2
  //   b1
endmodule

module FAdder (
  input  A,
  input  B,
  input  Cin,
  output Cout,
  output S
);

  wire and_1_out, and_2_out, xor_2_out;

  or or_1 (Cout, and_1_out, and_2_out);
  and and_1 (and_1_out, Cin, B);
  and and_2 (and_2_out, A, xor_2_out);
  xor xor_1 (S, A, xor_2_out);
  xor xor_2 (xor_2_out, B, Cin);

  // Notes on the sheet:
  //   Full Adder
endmodule
