// Logisim project Subtraction.circ as structural Verilog: 1 circuit, main circuit main
module main (
  input  B1,
  input  in_2,
  input  B8,
  input  B7,
  input  B6,
  input  B5,
  input  B4,
  input  B3,
  input  B2,
  input  in_10,
  input  in_11,
  input  in_12,
  input  in_13,
  input  in_14,
  input  in_15,
  input  in_16,
  input  in_17,
  output out_18,
  output out_19,
  output out_20,
  output out_21,
  output out_22,
  output out_23,
  output out_24,
  output out_25,
  output out_26,
  output out_27,
  output out_28,
  output out_29,
  output out_30,
  output out_31,
  output out_32,
  output out_33,
  output out_34,
  output out_35,
  output out_36,
  output out_37,
  output out_38,
  output out_39,
  output out_40,
  output out_41
);

  wire _001_1_2_out, _001_1_3_out, _001_1_4_out, _001_1_5_out, _001_1_6_out, _001_1_7_out, _001_1_out,
       _010_1_2_out, _010_1_3_out, _010_1_4_out, _010_1_5_out, _010_1_6_out, _010_1_7_out, _010_1_out,
       _011_2_2_out, _011_2_3_out, _011_2_4_out, _011_2_5_out, _011_2_6_out, _011_2_7_out, _011_2_out,
       _100_1_2_out, _100_1_3_out, _100_1_4_out, _100_1_5_out, _100_1_6_out, _100_1_7_out, _100_1_out,
       _101_2_2_out, _101_2_3_out, _101_2_4_out, _101_2_5_out, _101_2_6_out, _101_2_7_out, _101_2_out,
       _110_2_2_out, _110_2_3_out, _110_2_4_out, _110_2_5_out, _110_2_6_out, _110_2_7_out, _110_2_out,
       _111_3_2_out, _111_3_3_out, _111_3_4_out, _111_3_5_out, _111_3_6_out, _111_3_7_out, _111_3_out,
       Carry_1_out, Carry_2_out, Carry_2_out_2, Carry_3_out, Carry_3_out_2, Carry_4_out, Carry_4_out_2,
       Carry_5_out, Carry_5_out_2, Carry_6_out, Carry_6_out_2, Carry_7_out, Carry_7_out_2, Carry_8_out,
       Carry_8_out_2, Carry_out, not_9_out, not_10_out, not_11_out, not_12_out, not_13_out, not_14_out,
       not_15_out, not_16_out, not_17_out, not_18_out, not_19_out, not_20_out, not_21_out, not_22_out,
       not_23_out, not_24_out, not_25_out, not_26_out, not_27_out, not_28_out, not_29_out, not_30_out,
       not_31_out, not_32_out, not_33_out, not_34_out, not_35_out, not_36_out, not_37_out, not_38_out,
       not_39_out, not_40_out, not_41_out, not_42_out, not_43_out, not_44_out, not_45_out, not_46_out,
       not_47_out, not_48_out, not_49_out, not_50_out, not_51_out, not_52_out, not_53_out, not_54_out,
       not_55_out, not_56_out, not_57_out, not_58_out, not_59_out, not_60_out, not_61_out, not_62_out,
       not_63_out, not_64_out, not_65_out, not_66_out, not_67_out, not_68_out, not_69_out, not_70_out,
       not_71_out;

  not not_1 (out_18, in_10);
  not not_2 (out_19, in_11);
  not not_3 (out_20, in_12);
  not not_4 (out_21, in_13);
  and Carry (Carry_out, out_18, Carry_3_out);
  not not_5 (out_22, in_14);
  and Carry_2 (Carry_2_out, out_20, Carry_4_out);
  and Carry_3 (Carry_3_out, out_19, Carry_2_out);
  xor Sum (out_35, out_19, Carry_2_out);
  xor Sum_2 (out_34, out_18, Carry_3_out);
  not not_6 (out_23, in_15);
  and Carry_4 (Carry_4_out, out_21, Carry_6_out);
  xor Sum_3 (out_36, out_20, Carry_4_out);
  not not_7 (out_24, in_16);
  not not_8 (out_25, in_17);
  and Carry_5 (Carry_5_out, out_23, Carry_7_out);
  and Carry_6 (Carry_6_out, out_22, Carry_5_out);
  xor Sum_4 (out_38, out_22, Carry_5_out);
  xor Sum_5 (out_37, out_21, Carry_6_out);
  and Carry_7 (Carry_7_out, out_24, Carry_8_out);
  xor Sum_6 (out_39, out_23, Carry_7_out);
  and Carry_8 (Carry_8_out, out_25, in_2);
  xor Sum_7 (out_41, out_25, in_2);
  xor Sum_8 (out_40, out_24, Carry_8_out);
  and Carry_1 (Carry_1_out, B1, out_41);
  not not_9 (not_9_out, out_40);
  and _010_1 (_010_1_out, not_9_out, B2, not_10_out);
  not not_10 (not_10_out, Carry_1_out);
  not not_11 (not_11_out, out_40);
  and _001_1 (_001_1_out, not_11_out, not_12_out, Carry_1_out);
  not not_12 (not_12_out, B2);
  not not_13 (not_13_out, B2);
  and _100_1 (_100_1_out, out_40, not_13_out, not_14_out);
  not not_14 (not_14_out, Carry_1_out);
  and _111_3 (_111_3_out, out_40, B2, Carry_1_out);
  not not_15 (not_15_out, out_40);
  and _011_2 (_011_2_out, not_15_out, B2, Carry_1_out);
  and _110_2 (_110_2_out, out_40, B2, not_16_out);
  not not_16 (not_16_out, Carry_1_out);
  not not_17 (not_17_out, B2);
  and _101_2 (_101_2_out, out_40, not_17_out, Carry_1_out);
  not not_18 (not_18_out, out_39);
  and _010_1_2 (_010_1_2_out, not_18_out, B3, not_19_out);
  not not_19 (not_19_out, Carry_2_out_2);
  not not_20 (not_20_out, out_39);
  and _001_1_2 (_001_1_2_out, not_20_out, not_21_out, Carry_2_out_2);
  not not_21 (not_21_out, B3);
  and _100_1_2 (_100_1_2_out, out_39, not_22_out, not_23_out);
  not not_22 (not_22_out, B3);
  not not_23 (not_23_out, Carry_2_out_2);
  and _111_3_2 (_111_3_2_out, out_39, B3, Carry_2_out_2);
  not not_24 (not_24_out, out_39);
  and _011_2_2 (_011_2_2_out, not_24_out, B3, Carry_2_out_2);
  and _110_2_2 (_110_2_2_out, out_39, B3, not_25_out);
  not not_25 (not_25_out, Carry_2_out_2);
  not not_26 (not_26_out, B3);
  and _101_2_2 (_101_2_2_out, out_39, not_26_out, Carry_2_out_2);
  not not_27 (not_27_out, out_38);
  and _010_1_3 (_010_1_3_out, not_27_out, B4, not_28_out);
  not not_28 (not_28_out, Carry_3_out_2);
  not not_29 (not_29_out, out_38);
  not not_30 (not_30_out, B4);
  and _001_1_3 (_001_1_3_out, not_29_out, not_30_out, Carry_3_out_2);
  not not_31 (not_31_out, B4);
  and _100_1_3 (_100_1_3_out, out_38, not_31_out, not_32_out);
  not not_32 (not_32_out, Carry_3_out_2);
  and _111_3_3 (_111_3_3_out, out_38, B4, Carry_3_out_2);
  not not_33 (not_33_out, out_38);
  and _011_2_3 (_011_2_3_out, not_33_out, B4, Carry_3_out_2);
  and _110_2_3 (_110_2_3_out, out_38, B4, not_34_out);
  not not_34 (not_34_out, Carry_3_out_2);
  not not_35 (not_35_out, B4);
  and _101_2_3 (_101_2_3_out, out_38, not_35_out, Carry_3_out_2);
  not not_36 (not_36_out, out_37);
  and _010_1_4 (_010_1_4_out, not_36_out, B5, not_37_out);
  not not_37 (not_37_out, Carry_4_out_2);
  not not_38 (not_38_out, out_37);
  not not_39 (not_39_out, B5);
  and _001_1_4 (_001_1_4_out, not_38_out, not_39_out, Carry_4_out_2);
  not not_40 (not_40_out, B5);
  and _100_1_4 (_100_1_4_out, out_37, not_40_out, not_41_out);
  not not_41 (not_41_out, Carry_4_out_2);
  and _111_3_4 (_111_3_4_out, out_37, B5, Carry_4_out_2);
  not not_42 (not_42_out, out_37);
  and _011_2_4 (_011_2_4_out, not_42_out, B5, Carry_4_out_2);
  and _110_2_4 (_110_2_4_out, out_37, B5, not_43_out);
  not not_43 (not_43_out, Carry_4_out_2);
  and _101_2_4 (_101_2_4_out, out_37, not_44_out, Carry_4_out_2);
  not not_44 (not_44_out, B5);
  not not_45 (not_45_out, out_36);
  and _010_1_5 (_010_1_5_out, not_45_out, B6, not_46_out);
  not not_46 (not_46_out, Carry_5_out_2);
  not not_47 (not_47_out, out_36);
  and _001_1_5 (_001_1_5_out, not_47_out, not_48_out, Carry_5_out_2);
  not not_48 (not_48_out, out_36);
  not not_49 (not_49_out, B6);
  and _100_1_5 (_100_1_5_out, out_36, not_49_out, not_50_out);
  not not_50 (not_50_out, Carry_5_out_2);
  and _111_3_5 (_111_3_5_out, out_36, B6, Carry_5_out_2);
  not not_51 (not_51_out, out_36);
  and _011_2_5 (_011_2_5_out, not_51_out, B6, Carry_5_out_2);
  and _110_2_5 (_110_2_5_out, out_36, B6, not_52_out);
  not not_52 (not_52_out, Carry_5_out_2);
  not not_53 (not_53_out, B6);
  and _101_2_5 (_101_2_5_out, out_36, not_53_out, Carry_5_out_2);
  not not_54 (not_54_out, out_35);
  and _010_1_6 (_010_1_6_out, not_54_out, B7, not_55_out);
  not not_55 (not_55_out, Carry_6_out_2);
  not not_56 (not_56_out, out_35);
  not not_57 (not_57_out, B7);
  and _001_1_6 (_001_1_6_out, not_56_out, not_57_out, Carry_6_out_2);
  not not_58 (not_58_out, B7);
  and _100_1_6 (_100_1_6_out, out_35, not_58_out, not_59_out);
  not not_59 (not_59_out, Carry_6_out_2);
  and _111_3_6 (_111_3_6_out, out_35, B7, Carry_6_out_2);
  not not_60 (not_60_out, out_35);
  and _011_2_6 (_011_2_6_out, not_60_out, B7, Carry_6_out_2);
  and _110_2_6 (_110_2_6_out, out_35, B7, not_61_out);
  not not_61 (not_61_out, Carry_6_out_2);
  and _101_2_6 (_101_2_6_out, out_35, not_62_out, Carry_6_out_2);
  not not_62 (not_62_out, B7);
  not not_63 (not_63_out, out_34);
  and _010_1_7 (_010_1_7_out, not_63_out, B8, not_64_out);
  not not_64 (not_64_out, Carry_7_out_2);
  not not_65 (not_65_out, out_34);
  and _001_1_7 (_001_1_7_out, not_65_out, not_66_out, Carry_7_out_2);
  not not_66 (not_66_out, B8);
  and _100_1_7 (_100_1_7_out, out_34, not_67_out, not_68_out);
  not not_67 (not_67_out, B8);
  not not_68 (not_68_out, Carry_7_out_2);
  and _111_3_7 (_111_3_7_out, out_34, B8, Carry_7_out_2);
  not not_69 (not_69_out, out_34);
  and _011_2_7 (_011_2_7_out, not_69_out, B8, Carry_7_out_2);
  and _110_2_7 (_110_2_7_out, out_34, B8, not_70_out);
  not not_70 (not_70_out, Carry_7_out_2);
  not not_71 (not_71_out, B8);
  and _101_2_7 (_101_2_7_out, out_34, not_71_out, Carry_7_out_2);
  xor Output_1 (out_33, B1, out_41);
  or Output_2 (out_32, _010_1_out, _001_1_out, _100_1_out, _111_3_out);
  or Carry_2_dup2 (Carry_2_out_2, _111_3_out, _011_2_out, _110_2_out, _101_2_out);
  or Output_3 (out_31, _010_1_2_out, _001_1_2_out, _100_1_2_out, _111_3_2_out);
  or Carry_3_dup2 (Carry_3_out_2, _111_3_2_out, _011_2_2_out, _110_2_2_out, _101_2_2_out);
  or Output_4 (out_30, _010_1_3_out, _001_1_3_out, _100_1_3_out, _111_3_3_out);
  or Carry_4_dup2 (Carry_4_out_2, _111_3_3_out, _011_2_3_out, _110_2_3_out, _101_2_3_out);
  or Output_5 (out_29, _010_1_4_out, _001_1_4_out, _100_1_4_out, _111_3_4_out);
  or Carry_5_dup2 (Carry_5_out_2, _111_3_4_out, _011_2_4_out, _110_2_4_out, _101_2_4_out);
  or Output_6 (out_28, _010_1_5_out, _001_1_5_out, _100_1_5_out, _111_3_5_out);
  or Carry_6_dup2 (Carry_6_out_2, _111_3_5_out, _011_2_5_out, _110_2_5_out, _101_2_5_out);
  or Output_7 (out_27, _010_1_6_out, _001_1_6_out, _100_1_6_out, _111_3_6_out);
  or Carry_7_dup2 (Carry_7_out_2, _111_3_6_out, _011_2_6_out, _110_2_6_out, _101_2_6_out);
  or Output_8 (out_26, _010_1_7_out, _001_1_7_out, _100_1_7_out, _111_3_7_out);
  or Carry_8_dup2 (Carry_8_out_2, _111_3_7_out, _011_2_7_out, _110_2_7_out, _101_2_7_out);
endmodule
