// Logisim project Twos_Compliment.circ as structural Verilog: 1 circuit, main circuit main
module main (
  input  in_1,
  input  in_2,
  input  in_3,
  input  in_4,
  input  in_5,
  input  in_6,
  input  in_7,
  input  in_8,
  input  in_9,
  output out_10,
  output out_11,
  output out_12,
  output out_13,
  output out_14,
  output out_15,
  output out_16,
  output out_17,
  output out_18,
  output out_19,
  output out_20,
  output out_21,
  output out_22,
  output out_23,
  output out_24,
  output out_25
);

  wire Carry_2_out, Carry_3_out, Carry_4_out, Carry_5_out, Carry_6_out, Carry_7_out, Carry_8_out, Carry_out;

  not not_1 (out_10, in_2);
  not not_2 (out_11, in_3);
  not not_3 (out_12, in_4);
  and Carry (Carry_out, out_10, Carry_2_out);
  not not_4 (out_14, in_6);
  not not_5 (out_13, in_5);
  and Carry_2 (Carry_2_out, out_11, Carry_4_out);
  xor Sum (out_18, out_10, Carry_2_out);
  not not_6 (out_15, in_7);
  and Carry_3 (Carry_3_out, out_13, Carry_5_out);
  and Carry_4 (Carry_4_out, out_12, Carry_3_out);
  xor Sum_2 (out_20, out_12, Carry_3_out);
  xor Sum_3 (out_19, out_11, Carry_4_out);
  not not_7 (out_16, in_8);
  and Carry_5 (Carry_5_out, out_14, Carry_7_out);
  xor Sum_4 (out_21, out_13, Carry_5_out);
  not not_8 (out_17, in_9);
  and Carry_6 (Carry_6_out, out_16, Carry_8_out);
  and Carry_7 (Carry_7_out, out_15, Carry_6_out);
  xor Sum_5 (out_23, out_15, Carry_6_out);
  xor Sum_6 (out_22, out_14, Carry_7_out);
  and Carry_8 (Carry_8_out, out_17, in_1);
  xor Sum_7 (out_24, out_16, Carry_8_out);
  xor Sum_8 (out_25, out_17, in_1);
endmodule
